// Logisim project LambdaCalculus.circ as structural Verilog: 20 circuits, main circuit main
module main (
  input  [21:0] in_1,
  output [21:0] out_2,
  output [21:0] out_3,
  output [21:0] out_4,
  output [21:0] out_5,
  output [21:0] out_6,
  output [21:0] out_7,
  output [21:0] out_8,
  output [21:0] out_9,
  output [21:0] out_10,
  output [21:0] out_11,
  output [21:0] out_12,
  output [21:0] out_13,
  output [21:0] out_14,
  output [21:0] out_15,
  output [21:0] out_16,
  output out_17,
  output [2:0] out_18,
  output out_19,
  output [2:0] out_20,
  output out_21,
  output [2:0] out_22,
  output out_23,
  output [2:0] out_24,
  output out_25,
  output [2:0] out_26,
  output out_27,
  output [2:0] out_28,
  output out_29,
  output [2:0] out_30,
  output out_31,
  output [2:0] out_32,
  output out_33,
  output [2:0] out_34,
  output out_35,
  output [2:0] out_36,
  output out_37,
  output [2:0] out_38,
  output out_39,
  output [2:0] out_40,
  output out_41,
  output [2:0] out_42,
  output out_43,
  output [2:0] out_44,
  output out_45,
  output [2:0] out_46,
  output out_47,
  output [2:0] out_48,
  output [3:0] out_49
);

  wire clock_1_out, selector_1_ramwriet, selector_2_ramwriet, selector_3_ramwriet, selector_4_ramwriet,
       selector_5_ramwriet, selector_6_ramwriet, selector_7_ramwriet, selector_8_ramwriet,
       selector_9_ramwriet, selector_10_ramwriet, selector_11_ramwriet, selector_12_ramwriet,
       selector_13_ramwriet, selector_14_ramwriet, selector_15_ramwriet, selector_16_ramwriet;
  wire [3:0] ram_1_dout, ram_2_dout, ram_9_dout, ram_10_dout, selector_1_ram, selector_1_ramin,
       selector_1_ramloc, selector_2_ram, selector_2_ramloc, selector_3_ram, selector_3_ramin,
       selector_3_ramloc, selector_4_ram, selector_4_ramin, selector_4_ramloc, selector_5_ram,
       selector_5_ramin, selector_5_ramloc, selector_6_ram, selector_6_ramin, selector_6_ramloc,
       selector_7_ram, selector_7_ramin, selector_7_ramloc, selector_8_ram, selector_8_ramin,
       selector_8_ramloc, selector_9_ram, selector_9_ramloc, selector_10_ram, selector_10_ramloc,
       selector_11_ram, selector_11_ramin, selector_11_ramloc, selector_12_ram, selector_12_ramin,
       selector_12_ramloc, selector_13_ram, selector_13_ramin, selector_13_ramloc, selector_14_ram,
       selector_14_ramin, selector_14_ramloc, selector_15_ram, selector_15_ramin, selector_15_ramloc,
       selector_16_ram, selector_16_ramin, selector_16_ramloc;
  wire [15:0] selector_1_newnoderequest, selector_1_stackclear;
  wire [21:0] Bus6In, Bus6Out, Bus9In, Bus9Out, Bus10In, Bus10Out, Bus11In, Bus11Out, Bus12In, Bus12Out,
       Bus13In, Bus13Out, Bus14In, Bus14Out, Bus15In, Bus15Out;

  Clock clock_1 (.out(clock_1_out));
  RAM #(.addrWidth(4), .dataWidth(4), .databus("bibus")) ram_1 (
    .addr(selector_1_ramloc), .we(selector_1_ramwriet), .oe(1'b1), .clk(clock_1_out), .din(selector_1_ram),
    .dout(ram_1_dout));
  Selector selector_1 (
    .IN1(out_5), .OUT1(out_4), .IN2(out_7), .OUT2(out_6), .IN3(out_9), .OUT3(out_8), .IN4(out_11),
    .OUT4(out_10), .IN5(out_15), .OUT5(out_12), .IN6(Bus6Out), .OUT6(Bus6In), .IN7(out_14), .OUT7(out_13),
    .IN8(out_3), .OUT8(out_2), .IN9(Bus9Out), .OUT9(Bus9In), .IN10(Bus10Out), .OUT10(Bus10In),
    .IN11(Bus11Out), .OUT11(Bus11In), .IN12(Bus12Out), .OUT12(Bus12In), .IN13(Bus13Out), .OUT13(Bus13In),
    .IN14(Bus14Out), .OUT14(Bus14In), .IN15(Bus15Out), .OUT15(Bus15In), .SelfBusInput(in_1),
    .CurrentResolveState(out_17), .CurrentExpressionType(out_18),
    .NewNodeRequest(selector_1_newnoderequest[0]), .StackClear(selector_1_stackclear[0]),
    .NewNodeReturn(out_49), .SelfBusOutput(out_16), .CLK(clock_1_out), .NodeID(4'b0000),
    .RAMWriet(selector_1_ramwriet), .RAMLoc(selector_1_ramloc), .RAM(selector_1_ram),
    .RAMIn(selector_1_ramin), .IN1_2(out_5), .OUT1_2(out_4), .IN2_2(out_7), .OUT2_2(out_6), .IN3_2(out_9),
    .OUT3_2(out_8), .IN4_2(out_11), .OUT4_2(out_10), .IN5_2(out_15), .OUT5_2(out_12), .IN6_2(Bus6Out),
    .OUT6_2(Bus6In), .IN7_2(out_14), .OUT7_2(out_13), .IN8_2(out_3), .OUT8_2(out_2), .IN9_2(Bus9Out),
    .OUT9_2(Bus9In), .IN10_2(Bus10Out), .OUT10_2(Bus10In), .IN11_2(Bus11Out), .OUT11_2(Bus11In),
    .IN12_2(Bus12Out), .OUT12_2(Bus12In), .IN13_2(Bus13Out), .OUT13_2(Bus13In), .IN14_2(Bus14Out),
    .OUT14_2(Bus14In), .IN15_2(Bus15Out), .OUT15_2(Bus15In));
  RAM #(.addrWidth(4), .dataWidth(4), .databus("bibus")) ram_2 (
    .addr(selector_2_ramloc), .we(selector_2_ramwriet), .oe(1'b1), .clk(clock_1_out), .din(selector_2_ram),
    .dout(ram_2_dout));
  Selector selector_2 (
    .IN1(out_5), .OUT1(out_4), .IN2(out_7), .OUT2(out_6), .IN3(out_9), .OUT3(out_8), .IN4(out_11),
    .OUT4(out_10), .IN5(out_15), .OUT5(out_12), .IN6(Bus6Out), .OUT6(Bus6In), .IN7(out_14), .OUT7(out_13),
    .IN8(out_3), .OUT8(out_2), .IN9(Bus9Out), .OUT9(Bus9In), .IN10(Bus10Out), .OUT10(Bus10In),
    .IN11(Bus11Out), .OUT11(Bus11In), .IN12(Bus12Out), .OUT12(Bus12In), .IN13(Bus13Out), .OUT13(Bus13In),
    .IN14(Bus14Out), .OUT14(Bus14In), .IN15(Bus15Out), .OUT15(Bus15In), .SelfBusInput(out_4),
    .CurrentResolveState(out_19), .CurrentExpressionType(out_20),
    .NewNodeRequest(selector_1_newnoderequest[1]), .StackClear(selector_1_stackclear[1]),
    .NewNodeReturn(out_49), .SelfBusOutput(out_5), .CLK(clock_1_out), .NodeID(4'b0001),
    .RAMWriet(selector_2_ramwriet), .RAMLoc(selector_2_ramloc), .RAM(selector_2_ram), .RAMIn(ram_2_dout),
    .IN1_2(out_5), .OUT1_2(out_4), .IN2_2(out_7), .OUT2_2(out_6), .IN3_2(out_9), .OUT3_2(out_8),
    .IN4_2(out_11), .OUT4_2(out_10), .IN5_2(out_15), .OUT5_2(out_12), .IN6_2(Bus6Out), .OUT6_2(Bus6In),
    .IN7_2(out_14), .OUT7_2(out_13), .IN8_2(out_3), .OUT8_2(out_2), .IN9_2(Bus9Out), .OUT9_2(Bus9In),
    .IN10_2(Bus10Out), .OUT10_2(Bus10In), .IN11_2(Bus11Out), .OUT11_2(Bus11In), .IN12_2(Bus12Out),
    .OUT12_2(Bus12In), .IN13_2(Bus13Out), .OUT13_2(Bus13In), .IN14_2(Bus14Out), .OUT14_2(Bus14In),
    .IN15_2(Bus15Out), .OUT15_2(Bus15In));
  Selector selector_3 (
    .IN1(out_5), .OUT1(out_4), .IN2(out_7), .OUT2(out_6), .IN3(out_9), .OUT3(out_8), .IN4(out_11),
    .OUT4(out_10), .IN5(out_15), .OUT5(out_12), .IN6(Bus6Out), .OUT6(Bus6In), .IN7(out_14), .OUT7(out_13),
    .IN8(out_3), .OUT8(out_2), .IN9(Bus9Out), .OUT9(Bus9In), .IN10(Bus10Out), .OUT10(Bus10In),
    .IN11(Bus11Out), .OUT11(Bus11In), .IN12(Bus12Out), .OUT12(Bus12In), .IN13(Bus13Out), .OUT13(Bus13In),
    .IN14(Bus14Out), .OUT14(Bus14In), .IN15(Bus15Out), .OUT15(Bus15In), .SelfBusInput(out_6),
    .CurrentResolveState(out_21), .CurrentExpressionType(out_22),
    .NewNodeRequest(selector_1_newnoderequest[2]), .StackClear(selector_1_stackclear[2]),
    .NewNodeReturn(out_49), .SelfBusOutput(out_7), .CLK(clock_1_out), .NodeID(4'b0010),
    .RAMWriet(selector_3_ramwriet), .RAMLoc(selector_3_ramloc), .RAM(selector_3_ram),
    .RAMIn(selector_3_ramin), .IN1_2(out_5), .OUT1_2(out_4), .IN2_2(out_7), .OUT2_2(out_6), .IN3_2(out_9),
    .OUT3_2(out_8), .IN4_2(out_11), .OUT4_2(out_10), .IN5_2(out_15), .OUT5_2(out_12), .IN6_2(Bus6Out),
    .OUT6_2(Bus6In), .IN7_2(out_14), .OUT7_2(out_13), .IN8_2(out_3), .OUT8_2(out_2), .IN9_2(Bus9Out),
    .OUT9_2(Bus9In), .IN10_2(Bus10Out), .OUT10_2(Bus10In), .IN11_2(Bus11Out), .OUT11_2(Bus11In),
    .IN12_2(Bus12Out), .OUT12_2(Bus12In), .IN13_2(Bus13Out), .OUT13_2(Bus13In), .IN14_2(Bus14Out),
    .OUT14_2(Bus14In), .IN15_2(Bus15Out), .OUT15_2(Bus15In));
  RAM #(.addrWidth(4), .dataWidth(4), .databus("bibus")) ram_3 (
    .addr(selector_3_ramloc), .we(selector_3_ramwriet), .oe(1'b1), .clk(clock_1_out), .din(selector_3_ram),
    .dout(selector_3_ramin));
  Selector selector_4 (
    .IN1(out_5), .OUT1(out_4), .IN2(out_7), .OUT2(out_6), .IN3(out_9), .OUT3(out_8), .IN4(out_11),
    .OUT4(out_10), .IN5(out_15), .OUT5(out_12), .IN6(Bus6Out), .OUT6(Bus6In), .IN7(out_14), .OUT7(out_13),
    .IN8(out_3), .OUT8(out_2), .IN9(Bus9Out), .OUT9(Bus9In), .IN10(Bus10Out), .OUT10(Bus10In),
    .IN11(Bus11Out), .OUT11(Bus11In), .IN12(Bus12Out), .OUT12(Bus12In), .IN13(Bus13Out), .OUT13(Bus13In),
    .IN14(Bus14Out), .OUT14(Bus14In), .IN15(Bus15Out), .OUT15(Bus15In), .SelfBusInput(out_8),
    .CurrentResolveState(out_23), .CurrentExpressionType(out_24),
    .NewNodeRequest(selector_1_newnoderequest[3]), .StackClear(selector_1_stackclear[3]),
    .NewNodeReturn(out_49), .SelfBusOutput(out_9), .CLK(clock_1_out), .NodeID(4'b0011),
    .RAMWriet(selector_4_ramwriet), .RAMLoc(selector_4_ramloc), .RAM(selector_4_ram),
    .RAMIn(selector_4_ramin), .IN1_2(out_5), .OUT1_2(out_4), .IN2_2(out_7), .OUT2_2(out_6), .IN3_2(out_9),
    .OUT3_2(out_8), .IN4_2(out_11), .OUT4_2(out_10), .IN5_2(out_15), .OUT5_2(out_12), .IN6_2(Bus6Out),
    .OUT6_2(Bus6In), .IN7_2(out_14), .OUT7_2(out_13), .IN8_2(out_3), .OUT8_2(out_2), .IN9_2(Bus9Out),
    .OUT9_2(Bus9In), .IN10_2(Bus10Out), .OUT10_2(Bus10In), .IN11_2(Bus11Out), .OUT11_2(Bus11In),
    .IN12_2(Bus12Out), .OUT12_2(Bus12In), .IN13_2(Bus13Out), .OUT13_2(Bus13In), .IN14_2(Bus14Out),
    .OUT14_2(Bus14In), .IN15_2(Bus15Out), .OUT15_2(Bus15In));
  RAM #(.addrWidth(4), .dataWidth(4), .databus("bibus")) ram_4 (
    .addr(selector_4_ramloc), .we(selector_4_ramwriet), .oe(1'b1), .clk(clock_1_out), .din(selector_4_ram),
    .dout(selector_4_ramin));
  Selector selector_5 (
    .IN1(out_5), .OUT1(out_4), .IN2(out_7), .OUT2(out_6), .IN3(out_9), .OUT3(out_8), .IN4(out_11),
    .OUT4(out_10), .IN5(out_15), .OUT5(out_12), .IN6(Bus6Out), .OUT6(Bus6In), .IN7(out_14), .OUT7(out_13),
    .IN8(out_3), .OUT8(out_2), .IN9(Bus9Out), .OUT9(Bus9In), .IN10(Bus10Out), .OUT10(Bus10In),
    .IN11(Bus11Out), .OUT11(Bus11In), .IN12(Bus12Out), .OUT12(Bus12In), .IN13(Bus13Out), .OUT13(Bus13In),
    .IN14(Bus14Out), .OUT14(Bus14In), .IN15(Bus15Out), .OUT15(Bus15In), .SelfBusInput(out_10),
    .CurrentResolveState(out_25), .CurrentExpressionType(out_26),
    .NewNodeRequest(selector_1_newnoderequest[4]), .StackClear(selector_1_stackclear[4]),
    .NewNodeReturn(out_49), .SelfBusOutput(out_11), .CLK(clock_1_out), .NodeID(4'b0100),
    .RAMWriet(selector_5_ramwriet), .RAMLoc(selector_5_ramloc), .RAM(selector_5_ram),
    .RAMIn(selector_5_ramin), .IN1_2(out_5), .OUT1_2(out_4), .IN2_2(out_7), .OUT2_2(out_6), .IN3_2(out_9),
    .OUT3_2(out_8), .IN4_2(out_11), .OUT4_2(out_10), .IN5_2(out_15), .OUT5_2(out_12), .IN6_2(Bus6Out),
    .OUT6_2(Bus6In), .IN7_2(out_14), .OUT7_2(out_13), .IN8_2(out_3), .OUT8_2(out_2), .IN9_2(Bus9Out),
    .OUT9_2(Bus9In), .IN10_2(Bus10Out), .OUT10_2(Bus10In), .IN11_2(Bus11Out), .OUT11_2(Bus11In),
    .IN12_2(Bus12Out), .OUT12_2(Bus12In), .IN13_2(Bus13Out), .OUT13_2(Bus13In), .IN14_2(Bus14Out),
    .OUT14_2(Bus14In), .IN15_2(Bus15Out), .OUT15_2(Bus15In));
  RAM #(.addrWidth(4), .dataWidth(4), .databus("bibus")) ram_5 (
    .addr(selector_5_ramloc), .we(selector_5_ramwriet), .oe(1'b1), .clk(clock_1_out), .din(selector_5_ram),
    .dout(selector_5_ramin));
  Selector selector_6 (
    .IN1(out_5), .OUT1(out_4), .IN2(out_7), .OUT2(out_6), .IN3(out_9), .OUT3(out_8), .IN4(out_11),
    .OUT4(out_10), .IN5(out_15), .OUT5(out_12), .IN6(Bus6Out), .OUT6(Bus6In), .IN7(out_14), .OUT7(out_13),
    .IN8(out_3), .OUT8(out_2), .IN9(Bus9Out), .OUT9(Bus9In), .IN10(Bus10Out), .OUT10(Bus10In),
    .IN11(Bus11Out), .OUT11(Bus11In), .IN12(Bus12Out), .OUT12(Bus12In), .IN13(Bus13Out), .OUT13(Bus13In),
    .IN14(Bus14Out), .OUT14(Bus14In), .IN15(Bus15Out), .OUT15(Bus15In), .SelfBusInput(out_12),
    .CurrentResolveState(out_27), .CurrentExpressionType(out_28),
    .NewNodeRequest(selector_1_newnoderequest[5]), .StackClear(selector_1_stackclear[5]),
    .NewNodeReturn(out_49), .SelfBusOutput(out_15), .CLK(clock_1_out), .NodeID(4'b0101),
    .RAMWriet(selector_6_ramwriet), .RAMLoc(selector_6_ramloc), .RAM(selector_6_ram),
    .RAMIn(selector_6_ramin), .IN1_2(out_5), .OUT1_2(out_4), .IN2_2(out_7), .OUT2_2(out_6), .IN3_2(out_9),
    .OUT3_2(out_8), .IN4_2(out_11), .OUT4_2(out_10), .IN5_2(out_15), .OUT5_2(out_12), .IN6_2(Bus6Out),
    .OUT6_2(Bus6In), .IN7_2(out_14), .OUT7_2(out_13), .IN8_2(out_3), .OUT8_2(out_2), .IN9_2(Bus9Out),
    .OUT9_2(Bus9In), .IN10_2(Bus10Out), .OUT10_2(Bus10In), .IN11_2(Bus11Out), .OUT11_2(Bus11In),
    .IN12_2(Bus12Out), .OUT12_2(Bus12In), .IN13_2(Bus13Out), .OUT13_2(Bus13In), .IN14_2(Bus14Out),
    .OUT14_2(Bus14In), .IN15_2(Bus15Out), .OUT15_2(Bus15In));
  RAM #(.addrWidth(4), .dataWidth(4), .databus("bibus")) ram_6 (
    .addr(selector_6_ramloc), .we(selector_6_ramwriet), .oe(1'b1), .clk(clock_1_out), .din(selector_6_ram),
    .dout(selector_6_ramin));
  Selector selector_7 (
    .IN1(out_5), .OUT1(out_4), .IN2(out_7), .OUT2(out_6), .IN3(out_9), .OUT3(out_8), .IN4(out_11),
    .OUT4(out_10), .IN5(out_15), .OUT5(out_12), .IN6(Bus6Out), .OUT6(Bus6In), .IN7(out_14), .OUT7(out_13),
    .IN8(out_3), .OUT8(out_2), .IN9(Bus9Out), .OUT9(Bus9In), .IN10(Bus10Out), .OUT10(Bus10In),
    .IN11(Bus11Out), .OUT11(Bus11In), .IN12(Bus12Out), .OUT12(Bus12In), .IN13(Bus13Out), .OUT13(Bus13In),
    .IN14(Bus14Out), .OUT14(Bus14In), .IN15(Bus15Out), .OUT15(Bus15In), .SelfBusInput(Bus6In),
    .CurrentResolveState(out_29), .CurrentExpressionType(out_30),
    .NewNodeRequest(selector_1_newnoderequest[6]), .StackClear(selector_1_stackclear[6]),
    .NewNodeReturn(out_49), .SelfBusOutput(Bus6Out), .CLK(clock_1_out), .NodeID(4'b0110),
    .RAMWriet(selector_7_ramwriet), .RAMLoc(selector_7_ramloc), .RAM(selector_7_ram),
    .RAMIn(selector_7_ramin), .IN1_2(out_5), .OUT1_2(out_4), .IN2_2(out_7), .OUT2_2(out_6), .IN3_2(out_9),
    .OUT3_2(out_8), .IN4_2(out_11), .OUT4_2(out_10), .IN5_2(out_15), .OUT5_2(out_12), .IN6_2(Bus6Out),
    .OUT6_2(Bus6In), .IN7_2(out_14), .OUT7_2(out_13), .IN8_2(out_3), .OUT8_2(out_2), .IN9_2(Bus9Out),
    .OUT9_2(Bus9In), .IN10_2(Bus10Out), .OUT10_2(Bus10In), .IN11_2(Bus11Out), .OUT11_2(Bus11In),
    .IN12_2(Bus12Out), .OUT12_2(Bus12In), .IN13_2(Bus13Out), .OUT13_2(Bus13In), .IN14_2(Bus14Out),
    .OUT14_2(Bus14In), .IN15_2(Bus15Out), .OUT15_2(Bus15In));
  RAM #(.addrWidth(4), .dataWidth(4), .databus("bibus")) ram_7 (
    .addr(selector_7_ramloc), .we(selector_7_ramwriet), .oe(1'b1), .clk(clock_1_out), .din(selector_7_ram),
    .dout(selector_7_ramin));
  Selector selector_8 (
    .IN1(out_5), .OUT1(out_4), .IN2(out_7), .OUT2(out_6), .IN3(out_9), .OUT3(out_8), .IN4(out_11),
    .OUT4(out_10), .IN5(out_15), .OUT5(out_12), .IN6(Bus6Out), .OUT6(Bus6In), .IN7(out_14), .OUT7(out_13),
    .IN8(out_3), .OUT8(out_2), .IN9(Bus9Out), .OUT9(Bus9In), .IN10(Bus10Out), .OUT10(Bus10In),
    .IN11(Bus11Out), .OUT11(Bus11In), .IN12(Bus12Out), .OUT12(Bus12In), .IN13(Bus13Out), .OUT13(Bus13In),
    .IN14(Bus14Out), .OUT14(Bus14In), .IN15(Bus15Out), .OUT15(Bus15In), .SelfBusInput(out_13),
    .CurrentResolveState(out_31), .CurrentExpressionType(out_32),
    .NewNodeRequest(selector_1_newnoderequest[7]), .StackClear(selector_1_stackclear[7]),
    .NewNodeReturn(out_49), .SelfBusOutput(out_14), .CLK(clock_1_out), .NodeID(4'b0111),
    .RAMWriet(selector_8_ramwriet), .RAMLoc(selector_8_ramloc), .RAM(selector_8_ram),
    .RAMIn(selector_8_ramin), .IN1_2(out_5), .OUT1_2(out_4), .IN2_2(out_7), .OUT2_2(out_6), .IN3_2(out_9),
    .OUT3_2(out_8), .IN4_2(out_11), .OUT4_2(out_10), .IN5_2(out_15), .OUT5_2(out_12), .IN6_2(Bus6Out),
    .OUT6_2(Bus6In), .IN7_2(out_14), .OUT7_2(out_13), .IN8_2(out_3), .OUT8_2(out_2), .IN9_2(Bus9Out),
    .OUT9_2(Bus9In), .IN10_2(Bus10Out), .OUT10_2(Bus10In), .IN11_2(Bus11Out), .OUT11_2(Bus11In),
    .IN12_2(Bus12Out), .OUT12_2(Bus12In), .IN13_2(Bus13Out), .OUT13_2(Bus13In), .IN14_2(Bus14Out),
    .OUT14_2(Bus14In), .IN15_2(Bus15Out), .OUT15_2(Bus15In));
  RAM #(.addrWidth(4), .dataWidth(4), .databus("bibus")) ram_8 (
    .addr(selector_8_ramloc), .we(selector_8_ramwriet), .oe(1'b1), .clk(clock_1_out), .din(selector_8_ram),
    .dout(selector_8_ramin));
  RAM #(.addrWidth(4), .dataWidth(4), .databus("bibus")) ram_9 (
    .addr(selector_9_ramloc), .we(selector_9_ramwriet), .oe(1'b1), .clk(clock_1_out), .din(selector_9_ram),
    .dout(ram_9_dout));
  Selector selector_9 (
    .IN1(out_5), .OUT1(out_4), .IN2(out_7), .OUT2(out_6), .IN3(out_9), .OUT3(out_8), .IN4(out_11),
    .OUT4(out_10), .IN5(out_15), .OUT5(out_12), .IN6(Bus6Out), .OUT6(Bus6In), .IN7(out_14), .OUT7(out_13),
    .IN8(out_3), .OUT8(out_2), .IN9(Bus9Out), .OUT9(Bus9In), .IN10(Bus10Out), .OUT10(Bus10In),
    .IN11(Bus11Out), .OUT11(Bus11In), .IN12(Bus12Out), .OUT12(Bus12In), .IN13(Bus13Out), .OUT13(Bus13In),
    .IN14(Bus14Out), .OUT14(Bus14In), .IN15(Bus15Out), .OUT15(Bus15In), .SelfBusInput(out_2),
    .CurrentResolveState(out_33), .CurrentExpressionType(out_34),
    .NewNodeRequest(selector_1_newnoderequest[8]), .StackClear(selector_1_stackclear[8]),
    .NewNodeReturn(out_49), .SelfBusOutput(out_3), .CLK(clock_1_out), .NodeID(4'b1000),
    .RAMWriet(selector_9_ramwriet), .RAMLoc(selector_9_ramloc), .RAM(selector_9_ram), .RAMIn(ram_9_dout),
    .IN1_2(out_5), .OUT1_2(out_4), .IN2_2(out_7), .OUT2_2(out_6), .IN3_2(out_9), .OUT3_2(out_8),
    .IN4_2(out_11), .OUT4_2(out_10), .IN5_2(out_15), .OUT5_2(out_12), .IN6_2(Bus6Out), .OUT6_2(Bus6In),
    .IN7_2(out_14), .OUT7_2(out_13), .IN8_2(out_3), .OUT8_2(out_2), .IN9_2(Bus9Out), .OUT9_2(Bus9In),
    .IN10_2(Bus10Out), .OUT10_2(Bus10In), .IN11_2(Bus11Out), .OUT11_2(Bus11In), .IN12_2(Bus12Out),
    .OUT12_2(Bus12In), .IN13_2(Bus13Out), .OUT13_2(Bus13In), .IN14_2(Bus14Out), .OUT14_2(Bus14In),
    .IN15_2(Bus15Out), .OUT15_2(Bus15In));
  RAM #(.addrWidth(4), .dataWidth(4), .databus("bibus")) ram_10 (
    .addr(selector_10_ramloc), .we(selector_10_ramwriet), .oe(1'b1), .clk(clock_1_out),
    .din(selector_10_ram), .dout(ram_10_dout));
  Selector selector_10 (
    .IN1(out_5), .OUT1(out_4), .IN2(out_7), .OUT2(out_6), .IN3(out_9), .OUT3(out_8), .IN4(out_11),
    .OUT4(out_10), .IN5(out_15), .OUT5(out_12), .IN6(Bus6Out), .OUT6(Bus6In), .IN7(out_14), .OUT7(out_13),
    .IN8(out_3), .OUT8(out_2), .IN9(Bus9Out), .OUT9(Bus9In), .IN10(Bus10Out), .OUT10(Bus10In),
    .IN11(Bus11Out), .OUT11(Bus11In), .IN12(Bus12Out), .OUT12(Bus12In), .IN13(Bus13Out), .OUT13(Bus13In),
    .IN14(Bus14Out), .OUT14(Bus14In), .IN15(Bus15Out), .OUT15(Bus15In), .SelfBusInput(Bus9In),
    .CurrentResolveState(out_35), .CurrentExpressionType(out_36),
    .NewNodeRequest(selector_1_newnoderequest[9]), .StackClear(selector_1_stackclear[9]),
    .NewNodeReturn(out_49), .SelfBusOutput(Bus9Out), .CLK(clock_1_out), .NodeID(4'b1001),
    .RAMWriet(selector_10_ramwriet), .RAMLoc(selector_10_ramloc), .RAM(selector_10_ram), .RAMIn(ram_10_dout),
    .IN1_2(out_5), .OUT1_2(out_4), .IN2_2(out_7), .OUT2_2(out_6), .IN3_2(out_9), .OUT3_2(out_8),
    .IN4_2(out_11), .OUT4_2(out_10), .IN5_2(out_15), .OUT5_2(out_12), .IN6_2(Bus6Out), .OUT6_2(Bus6In),
    .IN7_2(out_14), .OUT7_2(out_13), .IN8_2(out_3), .OUT8_2(out_2), .IN9_2(Bus9Out), .OUT9_2(Bus9In),
    .IN10_2(Bus10Out), .OUT10_2(Bus10In), .IN11_2(Bus11Out), .OUT11_2(Bus11In), .IN12_2(Bus12Out),
    .OUT12_2(Bus12In), .IN13_2(Bus13Out), .OUT13_2(Bus13In), .IN14_2(Bus14Out), .OUT14_2(Bus14In),
    .IN15_2(Bus15Out), .OUT15_2(Bus15In));
  Selector selector_11 (
    .IN1(out_5), .OUT1(out_4), .IN2(out_7), .OUT2(out_6), .IN3(out_9), .OUT3(out_8), .IN4(out_11),
    .OUT4(out_10), .IN5(out_15), .OUT5(out_12), .IN6(Bus6Out), .OUT6(Bus6In), .IN7(out_14), .OUT7(out_13),
    .IN8(out_3), .OUT8(out_2), .IN9(Bus9Out), .OUT9(Bus9In), .IN10(Bus10Out), .OUT10(Bus10In),
    .IN11(Bus11Out), .OUT11(Bus11In), .IN12(Bus12Out), .OUT12(Bus12In), .IN13(Bus13Out), .OUT13(Bus13In),
    .IN14(Bus14Out), .OUT14(Bus14In), .IN15(Bus15Out), .OUT15(Bus15In), .SelfBusInput(Bus10In),
    .CurrentResolveState(out_37), .CurrentExpressionType(out_38),
    .NewNodeRequest(selector_1_newnoderequest[10]), .StackClear(selector_1_stackclear[10]),
    .NewNodeReturn(out_49), .SelfBusOutput(Bus10Out), .CLK(clock_1_out), .NodeID(4'b1010),
    .RAMWriet(selector_11_ramwriet), .RAMLoc(selector_11_ramloc), .RAM(selector_11_ram),
    .RAMIn(selector_11_ramin), .IN1_2(out_5), .OUT1_2(out_4), .IN2_2(out_7), .OUT2_2(out_6), .IN3_2(out_9),
    .OUT3_2(out_8), .IN4_2(out_11), .OUT4_2(out_10), .IN5_2(out_15), .OUT5_2(out_12), .IN6_2(Bus6Out),
    .OUT6_2(Bus6In), .IN7_2(out_14), .OUT7_2(out_13), .IN8_2(out_3), .OUT8_2(out_2), .IN9_2(Bus9Out),
    .OUT9_2(Bus9In), .IN10_2(Bus10Out), .OUT10_2(Bus10In), .IN11_2(Bus11Out), .OUT11_2(Bus11In),
    .IN12_2(Bus12Out), .OUT12_2(Bus12In), .IN13_2(Bus13Out), .OUT13_2(Bus13In), .IN14_2(Bus14Out),
    .OUT14_2(Bus14In), .IN15_2(Bus15Out), .OUT15_2(Bus15In));
  RAM #(.addrWidth(4), .dataWidth(4), .databus("bibus")) ram_11 (
    .addr(selector_11_ramloc), .we(selector_11_ramwriet), .oe(1'b1), .clk(clock_1_out),
    .din(selector_11_ram), .dout(selector_11_ramin));
  Selector selector_12 (
    .IN1(out_5), .OUT1(out_4), .IN2(out_7), .OUT2(out_6), .IN3(out_9), .OUT3(out_8), .IN4(out_11),
    .OUT4(out_10), .IN5(out_15), .OUT5(out_12), .IN6(Bus6Out), .OUT6(Bus6In), .IN7(out_14), .OUT7(out_13),
    .IN8(out_3), .OUT8(out_2), .IN9(Bus9Out), .OUT9(Bus9In), .IN10(Bus10Out), .OUT10(Bus10In),
    .IN11(Bus11Out), .OUT11(Bus11In), .IN12(Bus12Out), .OUT12(Bus12In), .IN13(Bus13Out), .OUT13(Bus13In),
    .IN14(Bus14Out), .OUT14(Bus14In), .IN15(Bus15Out), .OUT15(Bus15In), .SelfBusInput(Bus11In),
    .CurrentResolveState(out_39), .CurrentExpressionType(out_40),
    .NewNodeRequest(selector_1_newnoderequest[11]), .StackClear(selector_1_stackclear[11]),
    .NewNodeReturn(out_49), .SelfBusOutput(Bus11Out), .CLK(clock_1_out), .NodeID(4'b1011),
    .RAMWriet(selector_12_ramwriet), .RAMLoc(selector_12_ramloc), .RAM(selector_12_ram),
    .RAMIn(selector_12_ramin), .IN1_2(out_5), .OUT1_2(out_4), .IN2_2(out_7), .OUT2_2(out_6), .IN3_2(out_9),
    .OUT3_2(out_8), .IN4_2(out_11), .OUT4_2(out_10), .IN5_2(out_15), .OUT5_2(out_12), .IN6_2(Bus6Out),
    .OUT6_2(Bus6In), .IN7_2(out_14), .OUT7_2(out_13), .IN8_2(out_3), .OUT8_2(out_2), .IN9_2(Bus9Out),
    .OUT9_2(Bus9In), .IN10_2(Bus10Out), .OUT10_2(Bus10In), .IN11_2(Bus11Out), .OUT11_2(Bus11In),
    .IN12_2(Bus12Out), .OUT12_2(Bus12In), .IN13_2(Bus13Out), .OUT13_2(Bus13In), .IN14_2(Bus14Out),
    .OUT14_2(Bus14In), .IN15_2(Bus15Out), .OUT15_2(Bus15In));
  RAM #(.addrWidth(4), .dataWidth(4), .databus("bibus")) ram_12 (
    .addr(selector_12_ramloc), .we(selector_12_ramwriet), .oe(1'b1), .clk(clock_1_out),
    .din(selector_12_ram), .dout(selector_12_ramin));
  Selector selector_13 (
    .IN1(out_5), .OUT1(out_4), .IN2(out_7), .OUT2(out_6), .IN3(out_9), .OUT3(out_8), .IN4(out_11),
    .OUT4(out_10), .IN5(out_15), .OUT5(out_12), .IN6(Bus6Out), .OUT6(Bus6In), .IN7(out_14), .OUT7(out_13),
    .IN8(out_3), .OUT8(out_2), .IN9(Bus9Out), .OUT9(Bus9In), .IN10(Bus10Out), .OUT10(Bus10In),
    .IN11(Bus11Out), .OUT11(Bus11In), .IN12(Bus12Out), .OUT12(Bus12In), .IN13(Bus13Out), .OUT13(Bus13In),
    .IN14(Bus14Out), .OUT14(Bus14In), .IN15(Bus15Out), .OUT15(Bus15In), .SelfBusInput(Bus12In),
    .CurrentResolveState(out_41), .CurrentExpressionType(out_42),
    .NewNodeRequest(selector_1_newnoderequest[12]), .StackClear(selector_1_stackclear[12]),
    .NewNodeReturn(out_49), .SelfBusOutput(Bus12Out), .CLK(clock_1_out), .NodeID(4'b1100),
    .RAMWriet(selector_13_ramwriet), .RAMLoc(selector_13_ramloc), .RAM(selector_13_ram),
    .RAMIn(selector_13_ramin), .IN1_2(out_5), .OUT1_2(out_4), .IN2_2(out_7), .OUT2_2(out_6), .IN3_2(out_9),
    .OUT3_2(out_8), .IN4_2(out_11), .OUT4_2(out_10), .IN5_2(out_15), .OUT5_2(out_12), .IN6_2(Bus6Out),
    .OUT6_2(Bus6In), .IN7_2(out_14), .OUT7_2(out_13), .IN8_2(out_3), .OUT8_2(out_2), .IN9_2(Bus9Out),
    .OUT9_2(Bus9In), .IN10_2(Bus10Out), .OUT10_2(Bus10In), .IN11_2(Bus11Out), .OUT11_2(Bus11In),
    .IN12_2(Bus12Out), .OUT12_2(Bus12In), .IN13_2(Bus13Out), .OUT13_2(Bus13In), .IN14_2(Bus14Out),
    .OUT14_2(Bus14In), .IN15_2(Bus15Out), .OUT15_2(Bus15In));
  RAM #(.addrWidth(4), .dataWidth(4), .databus("bibus")) ram_13 (
    .addr(selector_13_ramloc), .we(selector_13_ramwriet), .oe(1'b1), .clk(clock_1_out),
    .din(selector_13_ram), .dout(selector_13_ramin));
  Selector selector_14 (
    .IN1(out_5), .OUT1(out_4), .IN2(out_7), .OUT2(out_6), .IN3(out_9), .OUT3(out_8), .IN4(out_11),
    .OUT4(out_10), .IN5(out_15), .OUT5(out_12), .IN6(Bus6Out), .OUT6(Bus6In), .IN7(out_14), .OUT7(out_13),
    .IN8(out_3), .OUT8(out_2), .IN9(Bus9Out), .OUT9(Bus9In), .IN10(Bus10Out), .OUT10(Bus10In),
    .IN11(Bus11Out), .OUT11(Bus11In), .IN12(Bus12Out), .OUT12(Bus12In), .IN13(Bus13Out), .OUT13(Bus13In),
    .IN14(Bus14Out), .OUT14(Bus14In), .IN15(Bus15Out), .OUT15(Bus15In), .SelfBusInput(Bus13In),
    .CurrentResolveState(out_43), .CurrentExpressionType(out_44),
    .NewNodeRequest(selector_1_newnoderequest[13]), .StackClear(selector_1_stackclear[13]),
    .NewNodeReturn(out_49), .SelfBusOutput(Bus13Out), .CLK(clock_1_out), .NodeID(4'b1101),
    .RAMWriet(selector_14_ramwriet), .RAMLoc(selector_14_ramloc), .RAM(selector_14_ram),
    .RAMIn(selector_14_ramin), .IN1_2(out_5), .OUT1_2(out_4), .IN2_2(out_7), .OUT2_2(out_6), .IN3_2(out_9),
    .OUT3_2(out_8), .IN4_2(out_11), .OUT4_2(out_10), .IN5_2(out_15), .OUT5_2(out_12), .IN6_2(Bus6Out),
    .OUT6_2(Bus6In), .IN7_2(out_14), .OUT7_2(out_13), .IN8_2(out_3), .OUT8_2(out_2), .IN9_2(Bus9Out),
    .OUT9_2(Bus9In), .IN10_2(Bus10Out), .OUT10_2(Bus10In), .IN11_2(Bus11Out), .OUT11_2(Bus11In),
    .IN12_2(Bus12Out), .OUT12_2(Bus12In), .IN13_2(Bus13Out), .OUT13_2(Bus13In), .IN14_2(Bus14Out),
    .OUT14_2(Bus14In), .IN15_2(Bus15Out), .OUT15_2(Bus15In));
  RAM #(.addrWidth(4), .dataWidth(4), .databus("bibus")) ram_14 (
    .addr(selector_14_ramloc), .we(selector_14_ramwriet), .oe(1'b1), .clk(clock_1_out),
    .din(selector_14_ram), .dout(selector_14_ramin));
  Selector selector_15 (
    .IN1(out_5), .OUT1(out_4), .IN2(out_7), .OUT2(out_6), .IN3(out_9), .OUT3(out_8), .IN4(out_11),
    .OUT4(out_10), .IN5(out_15), .OUT5(out_12), .IN6(Bus6Out), .OUT6(Bus6In), .IN7(out_14), .OUT7(out_13),
    .IN8(out_3), .OUT8(out_2), .IN9(Bus9Out), .OUT9(Bus9In), .IN10(Bus10Out), .OUT10(Bus10In),
    .IN11(Bus11Out), .OUT11(Bus11In), .IN12(Bus12Out), .OUT12(Bus12In), .IN13(Bus13Out), .OUT13(Bus13In),
    .IN14(Bus14Out), .OUT14(Bus14In), .IN15(Bus15Out), .OUT15(Bus15In), .SelfBusInput(Bus14In),
    .CurrentResolveState(out_45), .CurrentExpressionType(out_46),
    .NewNodeRequest(selector_1_newnoderequest[14]), .StackClear(selector_1_stackclear[14]),
    .NewNodeReturn(out_49), .SelfBusOutput(Bus14Out), .CLK(clock_1_out), .NodeID(4'b1110),
    .RAMWriet(selector_15_ramwriet), .RAMLoc(selector_15_ramloc), .RAM(selector_15_ram),
    .RAMIn(selector_15_ramin), .IN1_2(out_5), .OUT1_2(out_4), .IN2_2(out_7), .OUT2_2(out_6), .IN3_2(out_9),
    .OUT3_2(out_8), .IN4_2(out_11), .OUT4_2(out_10), .IN5_2(out_15), .OUT5_2(out_12), .IN6_2(Bus6Out),
    .OUT6_2(Bus6In), .IN7_2(out_14), .OUT7_2(out_13), .IN8_2(out_3), .OUT8_2(out_2), .IN9_2(Bus9Out),
    .OUT9_2(Bus9In), .IN10_2(Bus10Out), .OUT10_2(Bus10In), .IN11_2(Bus11Out), .OUT11_2(Bus11In),
    .IN12_2(Bus12Out), .OUT12_2(Bus12In), .IN13_2(Bus13Out), .OUT13_2(Bus13In), .IN14_2(Bus14Out),
    .OUT14_2(Bus14In), .IN15_2(Bus15Out), .OUT15_2(Bus15In));
  RAM #(.addrWidth(4), .dataWidth(4), .databus("bibus")) ram_15 (
    .addr(selector_15_ramloc), .we(selector_15_ramwriet), .oe(1'b1), .clk(clock_1_out),
    .din(selector_15_ram), .dout(selector_15_ramin));
  Selector selector_16 (
    .IN1(out_5), .OUT1(out_4), .IN2(out_7), .OUT2(out_6), .IN3(out_9), .OUT3(out_8), .IN4(out_11),
    .OUT4(out_10), .IN5(out_15), .OUT5(out_12), .IN6(Bus6Out), .OUT6(Bus6In), .IN7(out_14), .OUT7(out_13),
    .IN8(out_3), .OUT8(out_2), .IN9(Bus9Out), .OUT9(Bus9In), .IN10(Bus10Out), .OUT10(Bus10In),
    .IN11(Bus11Out), .OUT11(Bus11In), .IN12(Bus12Out), .OUT12(Bus12In), .IN13(Bus13Out), .OUT13(Bus13In),
    .IN14(Bus14Out), .OUT14(Bus14In), .IN15(Bus15Out), .OUT15(Bus15In), .SelfBusInput(Bus15In),
    .CurrentResolveState(out_47), .CurrentExpressionType(out_48),
    .NewNodeRequest(selector_1_newnoderequest[15]), .StackClear(selector_1_stackclear[15]),
    .NewNodeReturn(out_49), .SelfBusOutput(Bus15Out), .CLK(clock_1_out), .NodeID(4'b1111),
    .RAMWriet(selector_16_ramwriet), .RAMLoc(selector_16_ramloc), .RAM(selector_16_ram),
    .RAMIn(selector_16_ramin), .IN1_2(out_5), .OUT1_2(out_4), .IN2_2(out_7), .OUT2_2(out_6), .IN3_2(out_9),
    .OUT3_2(out_8), .IN4_2(out_11), .OUT4_2(out_10), .IN5_2(out_15), .OUT5_2(out_12), .IN6_2(Bus6Out),
    .OUT6_2(Bus6In), .IN7_2(out_14), .OUT7_2(out_13), .IN8_2(out_3), .OUT8_2(out_2), .IN9_2(Bus9Out),
    .OUT9_2(Bus9In), .IN10_2(Bus10Out), .OUT10_2(Bus10In), .IN11_2(Bus11Out), .OUT11_2(Bus11In),
    .IN12_2(Bus12Out), .OUT12_2(Bus12In), .IN13_2(Bus13Out), .OUT13_2(Bus13In), .IN14_2(Bus14Out),
    .OUT14_2(Bus14In), .IN15_2(Bus15Out), .OUT15_2(Bus15In));
  RAM #(.addrWidth(4), .dataWidth(4), .databus("bibus")) ram_16 (
    .addr(selector_16_ramloc), .we(selector_16_ramwriet), .oe(1'b1), .clk(clock_1_out),
    .din(selector_16_ram), .dout(selector_16_ramin));
  NewNodeTracker newnodetracker_1 (
    .N0Clear(selector_1_stackclear[0]), .N1Clear(selector_1_stackclear[1]),
    .N2Clear(selector_1_stackclear[2]), .N3Clear(selector_1_stackclear[3]),
    .N4Clear(selector_1_stackclear[4]), .N5Clear(selector_1_stackclear[5]),
    .N6Clear(selector_1_stackclear[6]), .N7Clear(selector_1_stackclear[7]),
    .N8Clear(selector_1_stackclear[8]), .N9Clear(selector_1_stackclear[9]),
    .NaClear(selector_1_stackclear[10]), .NbClear(selector_1_stackclear[11]),
    .NcClear(selector_1_stackclear[12]), .NdClear(selector_1_stackclear[13]),
    .NeClear(selector_1_stackclear[14]), .NfClear(selector_1_stackclear[15]),
    .N0Request(selector_1_newnoderequest[0]), .N1Request(selector_1_newnoderequest[1]),
    .N2Request(selector_1_newnoderequest[2]), .N3Request(selector_1_newnoderequest[3]),
    .N4Request(selector_1_newnoderequest[4]), .N5Request(selector_1_newnoderequest[5]),
    .N6Request(selector_1_newnoderequest[6]), .N7Request(selector_1_newnoderequest[7]),
    .N8Request(selector_1_newnoderequest[8]), .N9Request(selector_1_newnoderequest[9]),
    .NaRequest(selector_1_newnoderequest[10]), .NbRequest(selector_1_newnoderequest[11]),
    .NcRequest(selector_1_newnoderequest[12]), .NdRequest(selector_1_newnoderequest[13]),
    .NeRequest(selector_1_newnoderequest[14]), .NfRequest(selector_1_newnoderequest[15]), .N1Exp(out_20),
    .N2Exp(out_22), .N3Exp(out_24), .N4Exp(out_26), .N5Exp(out_28), .N6Exp(out_30), .N7Exp(out_32),
    .N8Exp(out_34), .N9Exp(out_36), .NaExp(out_38), .NbExp(out_40), .NcExp(out_42), .NdExp(out_44),
    .NeExp(out_46), .NfExp(out_48), .NewNode(out_49), .Clock(clock_1_out));
  // also tied to GND on the sheet: {selector_1_ramin[0], selector_1_ramin[2], selector_1_ramin[3]}
  // also tied to VCC on the sheet: selector_1_ramin[1]

  // Other names for the same wires on the sheet: Bus1In[21:0] = out_4; Bus1Out[21:0] = out_5; Bus2In[21:0] = out_6;
  //   Bus2Out[21:0] = out_7; Bus3In[21:0] = out_8; Bus3Out[21:0] = out_9; Bus4In[21:0] = out_10;
  //   Bus4Out[21:0] = out_11; Bus5In[21:0] = out_12; Bus5Out[21:0] = out_15; Bus7In[21:0] = out_13;
  //   Bus7Out[21:0] = out_14; Bus8In[21:0] = out_2; Bus8Out[21:0] = out_3; N1Exp[2:0] = out_20; N2Exp[2:0] = out_22;
  //   N3Exp[2:0] = out_24; N4Exp[2:0] = out_26; N5Exp[2:0] = out_28; N6Exp[2:0] = out_30; N7Exp[2:0] = out_32;
  //   N8Exp[2:0] = out_34; N9Exp[2:0] = out_36; NaExp[2:0] = out_38; NbExp[2:0] = out_40; NcExp[2:0] = out_42;
  //   NdExp[2:0] = out_44; NeExp[2:0] = out_46; NfExp[2:0] = out_48

  // Notes on the sheet:
  //   22-bit bus
  //   Instruction Data: [Instruction, Address Contents]
  //   Reduce Flag: [Flag State]
  //   Resolve Flag: [Flag State]
  //   Expression Type
  //   Undefined: 000
  //   Name: 001
  //   Application: 010
  //   Function: 011
  //   Goto: 100
  //   Expression Data: [Resolve Flag, Expression Type, Child Left, Child right]
  //   4,4
  //   [1-bit]
  //   [1-bit]
  //   [Reduce Flag, Resolve Flag, Instructiom Expression]
  //   1,3,4,4
  //   [8-bit]
  //   [12-bit]
endmodule

module Selector (
  input  [21:0] SelfBusInput,
  input  [3:0] NewNodeReturn,
  input  CLK,
  input  [3:0] NodeID,
  input  [21:0] IN1,
  input  [21:0] IN1_2,
  input  [21:0] IN2,
  input  [21:0] IN2_2,
  input  [21:0] IN3,
  input  [21:0] IN3_2,
  input  [21:0] IN4,
  input  [21:0] IN4_2,
  input  [21:0] IN5,
  input  [21:0] IN5_2,
  input  [21:0] IN6,
  input  [21:0] IN6_2,
  input  [21:0] IN7,
  input  [21:0] IN7_2,
  input  [21:0] IN8,
  input  [21:0] IN8_2,
  input  [21:0] IN9,
  input  [21:0] IN9_2,
  input  [21:0] IN10,
  input  [21:0] IN10_2,
  input  [21:0] IN11,
  input  [21:0] IN11_2,
  input  [21:0] IN12,
  input  [21:0] IN12_2,
  input  [21:0] IN13,
  input  [21:0] IN13_2,
  input  [21:0] IN14,
  input  [21:0] IN14_2,
  input  [21:0] IN15,
  input  [21:0] IN15_2,
  output NewNodeRequest,
  output [21:0] SelfBusOutput,
  output [2:0] CurrentExpressionType,
  output StackClear,
  output CurrentResolveState,
  output [3:0] RAMIn,
  output [3:0] RAMLoc,
  output RAMWriet,
  output [3:0] RAM,
  output [21:0] OUT1,
  output [21:0] OUT1_2,
  output [21:0] OUT2,
  output [21:0] OUT2_2,
  output [21:0] OUT3,
  output [21:0] OUT3_2,
  output [21:0] OUT4,
  output [21:0] OUT4_2,
  output [21:0] OUT5,
  output [21:0] OUT5_2,
  output [21:0] OUT6,
  output [21:0] OUT6_2,
  output [21:0] OUT7,
  output [21:0] OUT7_2,
  output [21:0] OUT8,
  output [21:0] OUT8_2,
  output [21:0] OUT9,
  output [21:0] OUT9_2,
  output [21:0] OUT10,
  output [21:0] OUT10_2,
  output [21:0] OUT11,
  output [21:0] OUT11_2,
  output [21:0] OUT12,
  output [21:0] OUT12_2,
  output [21:0] OUT13,
  output [21:0] OUT13_2,
  output [21:0] OUT14,
  output [21:0] OUT14_2,
  output [21:0] OUT15,
  output [21:0] OUT15_2
);

  wire decoder_1_out1, decoder_1_out2, decoder_1_out3, decoder_1_out4, decoder_1_out5, decoder_1_out6,
       decoder_1_out7, decoder_1_out8, decoder_1_out9, decoder_1_out10, decoder_1_out11, decoder_1_out12,
       decoder_1_out13, decoder_1_out14, decoder_1_out15;
  wire [3:0] node_1_childleftpointerout, node_1_childrightpointerout;
  wire [15:0] decoder_2_out15;
  wire [21:0] controlled_buffer_1_out, controlled_buffer_31_out, node_1_childleftout, node_1_childrightout;

  assign controlled_buffer_1_out = decoder_1_out1 ? IN1 : 22'bz;  // Controlled_Buffer controlled_buffer_1
  assign OUT1 = decoder_1_out1 ? node_1_childleftout : 22'bz;  // Controlled_Buffer controlled_buffer_2
  assign controlled_buffer_1_out = decoder_1_out2 ? IN2 : 22'bz;  // Controlled_Buffer controlled_buffer_3
  assign OUT2 = decoder_1_out2 ? node_1_childleftout : 22'bz;  // Controlled_Buffer controlled_buffer_4
  assign controlled_buffer_1_out = decoder_1_out3 ? IN3 : 22'bz;  // Controlled_Buffer controlled_buffer_5
  assign OUT3 = decoder_1_out3 ? node_1_childleftout : 22'bz;  // Controlled_Buffer controlled_buffer_6
  assign controlled_buffer_1_out = decoder_1_out4 ? IN4 : 22'bz;  // Controlled_Buffer controlled_buffer_7
  assign OUT4 = decoder_1_out4 ? node_1_childleftout : 22'bz;  // Controlled_Buffer controlled_buffer_8
  Decoder #(.select(4)) decoder_1 (
    .out1(decoder_1_out1), .out2(decoder_1_out2), .out3(decoder_1_out3), .out4(decoder_1_out4),
    .out5(decoder_1_out5), .out6(decoder_1_out6), .out7(decoder_1_out7), .out8(decoder_1_out8),
    .out9(decoder_1_out9), .out10(decoder_1_out10), .out11(decoder_1_out11), .out12(decoder_1_out12),
    .out13(decoder_1_out13), .out14(decoder_1_out14), .out15(decoder_1_out15),
    .sel(node_1_childleftpointerout));  // open: out0, en
  assign controlled_buffer_1_out = decoder_1_out5 ? IN5 : 22'bz;  // Controlled_Buffer controlled_buffer_9
  assign OUT5 = decoder_1_out5 ? node_1_childleftout : 22'bz;  // Controlled_Buffer controlled_buffer_10
  assign controlled_buffer_1_out = decoder_1_out6 ? IN6 : 22'bz;  // Controlled_Buffer controlled_buffer_11
  assign OUT6 = decoder_1_out6 ? node_1_childleftout : 22'bz;  // Controlled_Buffer controlled_buffer_12
  assign controlled_buffer_1_out = decoder_1_out7 ? IN7 : 22'bz;  // Controlled_Buffer controlled_buffer_13
  assign OUT7 = decoder_1_out7 ? node_1_childleftout : 22'bz;  // Controlled_Buffer controlled_buffer_14
  assign controlled_buffer_1_out = decoder_1_out8 ? IN8 : 22'bz;  // Controlled_Buffer controlled_buffer_15
  assign OUT8 = decoder_1_out8 ? node_1_childleftout : 22'bz;  // Controlled_Buffer controlled_buffer_16
  assign controlled_buffer_1_out = decoder_1_out9 ? IN9 : 22'bz;  // Controlled_Buffer controlled_buffer_17
  assign OUT9 = decoder_1_out9 ? node_1_childleftout : 22'bz;  // Controlled_Buffer controlled_buffer_18
  assign controlled_buffer_1_out = decoder_1_out10 ? IN10 : 22'bz;  // Controlled_Buffer controlled_buffer_19
  assign OUT10 = decoder_1_out10 ? node_1_childleftout : 22'bz;  // Controlled_Buffer controlled_buffer_20
  assign controlled_buffer_1_out = decoder_1_out11 ? IN11 : 22'bz;  // Controlled_Buffer controlled_buffer_21
  assign OUT11 = decoder_1_out11 ? node_1_childleftout : 22'bz;  // Controlled_Buffer controlled_buffer_22
  assign controlled_buffer_1_out = decoder_1_out12 ? IN12 : 22'bz;  // Controlled_Buffer controlled_buffer_23
  assign OUT12 = decoder_1_out12 ? node_1_childleftout : 22'bz;  // Controlled_Buffer controlled_buffer_24
  assign controlled_buffer_1_out = decoder_1_out13 ? IN13 : 22'bz;  // Controlled_Buffer controlled_buffer_25
  assign OUT13 = decoder_1_out13 ? node_1_childleftout : 22'bz;  // Controlled_Buffer controlled_buffer_26
  assign controlled_buffer_1_out = decoder_1_out14 ? IN14 : 22'bz;  // Controlled_Buffer controlled_buffer_27
  assign OUT14 = decoder_1_out14 ? node_1_childleftout : 22'bz;  // Controlled_Buffer controlled_buffer_28
  assign controlled_buffer_1_out = decoder_1_out15 ? IN15 : 22'bz;  // Controlled_Buffer controlled_buffer_29
  assign OUT15 = decoder_1_out15 ? node_1_childleftout : 22'bz;  // Controlled_Buffer controlled_buffer_30
  Node node_1 (
    .ChildLeftIn(controlled_buffer_1_out), .ChildLeftOut(node_1_childleftout),
    .ChildLeftPointerOut(node_1_childleftpointerout), .ParentIn(SelfBusInput),
    .CurrentResolveState(CurrentResolveState), .CurrentExpressionType(CurrentExpressionType),
    .NewNodeRequest(NewNodeRequest), .StackClear(StackClear), .NewID(NewNodeReturn),
    .ParentOut(SelfBusOutput), .Clock(CLK), .UniqueNodeID(NodeID), .RAMWrite(RAMWriet), .RAM(RAM),
    .RAMLoc(RAMLoc), .RAMIn(RAMIn), .ChildRightIn(controlled_buffer_31_out),
    .ChildRightOut(node_1_childrightout), .ChildRightPointerOut(node_1_childrightpointerout));
  Decoder #(.select(4)) decoder_2 (
    .out0(decoder_2_out15[15]), .out1(decoder_2_out15[14]), .out2(decoder_2_out15[13]),
    .out3(decoder_2_out15[12]), .out4(decoder_2_out15[11]), .out5(decoder_2_out15[10]),
    .out6(decoder_2_out15[9]), .out7(decoder_2_out15[8]), .out8(decoder_2_out15[7]),
    .out9(decoder_2_out15[6]), .out10(decoder_2_out15[5]), .out11(decoder_2_out15[4]),
    .out12(decoder_2_out15[3]), .out13(decoder_2_out15[2]), .out14(decoder_2_out15[1]),
    .out15(decoder_2_out15[0]), .sel(node_1_childrightpointerout));  // open: en
  assign controlled_buffer_31_out = decoder_2_out15[1] ? IN14_2 : 22'bz;  // Controlled_Buffer controlled_buffer_31
  assign OUT14_2 = decoder_2_out15[1] ? node_1_childrightout : 22'bz;  // Controlled_Buffer controlled_buffer_32
  assign controlled_buffer_31_out = decoder_2_out15[0] ? IN15_2 : 22'bz;  // Controlled_Buffer controlled_buffer_33
  assign OUT15_2 = decoder_2_out15[0] ? node_1_childrightout : 22'bz;  // Controlled_Buffer controlled_buffer_34
  assign controlled_buffer_31_out = decoder_2_out15[3] ? IN12_2 : 22'bz;  // Controlled_Buffer controlled_buffer_35
  assign OUT12_2 = decoder_2_out15[3] ? node_1_childrightout : 22'bz;  // Controlled_Buffer controlled_buffer_36
  assign controlled_buffer_31_out = decoder_2_out15[2] ? IN13_2 : 22'bz;  // Controlled_Buffer controlled_buffer_37
  assign OUT13_2 = decoder_2_out15[2] ? node_1_childrightout : 22'bz;  // Controlled_Buffer controlled_buffer_38
  assign controlled_buffer_31_out = decoder_2_out15[5] ? IN10_2 : 22'bz;  // Controlled_Buffer controlled_buffer_39
  assign OUT10_2 = decoder_2_out15[5] ? node_1_childrightout : 22'bz;  // Controlled_Buffer controlled_buffer_40
  assign controlled_buffer_31_out = decoder_2_out15[4] ? IN11_2 : 22'bz;  // Controlled_Buffer controlled_buffer_41
  assign OUT11_2 = decoder_2_out15[4] ? node_1_childrightout : 22'bz;  // Controlled_Buffer controlled_buffer_42
  assign controlled_buffer_31_out = decoder_2_out15[7] ? IN8_2 : 22'bz;  // Controlled_Buffer controlled_buffer_43
  assign OUT8_2 = decoder_2_out15[7] ? node_1_childrightout : 22'bz;  // Controlled_Buffer controlled_buffer_44
  assign controlled_buffer_31_out = decoder_2_out15[6] ? IN9_2 : 22'bz;  // Controlled_Buffer controlled_buffer_45
  assign OUT9_2 = decoder_2_out15[6] ? node_1_childrightout : 22'bz;  // Controlled_Buffer controlled_buffer_46
  assign controlled_buffer_31_out = decoder_2_out15[9] ? IN6_2 : 22'bz;  // Controlled_Buffer controlled_buffer_47
  assign OUT6_2 = decoder_2_out15[9] ? node_1_childrightout : 22'bz;  // Controlled_Buffer controlled_buffer_48
  assign controlled_buffer_31_out = decoder_2_out15[8] ? IN7_2 : 22'bz;  // Controlled_Buffer controlled_buffer_49
  assign OUT7_2 = decoder_2_out15[8] ? node_1_childrightout : 22'bz;  // Controlled_Buffer controlled_buffer_50
  assign controlled_buffer_31_out = decoder_2_out15[11] ? IN4_2 : 22'bz;  // Controlled_Buffer controlled_buffer_51
  assign OUT4_2 = decoder_2_out15[11] ? node_1_childrightout : 22'bz;  // Controlled_Buffer controlled_buffer_52
  assign controlled_buffer_31_out = decoder_2_out15[10] ? IN5_2 : 22'bz;  // Controlled_Buffer controlled_buffer_53
  assign OUT5_2 = decoder_2_out15[10] ? node_1_childrightout : 22'bz;  // Controlled_Buffer controlled_buffer_54
  assign controlled_buffer_31_out = decoder_2_out15[13] ? IN2_2 : 22'bz;  // Controlled_Buffer controlled_buffer_55
  assign OUT2_2 = decoder_2_out15[13] ? node_1_childrightout : 22'bz;  // Controlled_Buffer controlled_buffer_56
  assign controlled_buffer_31_out = decoder_2_out15[12] ? IN3_2 : 22'bz;  // Controlled_Buffer controlled_buffer_57
  assign OUT3_2 = decoder_2_out15[12] ? node_1_childrightout : 22'bz;  // Controlled_Buffer controlled_buffer_58
  assign controlled_buffer_31_out = decoder_2_out15[14] ? IN1_2 : 22'bz;  // Controlled_Buffer controlled_buffer_59
  assign OUT1_2 = decoder_2_out15[14] ? node_1_childrightout : 22'bz;  // Controlled_Buffer controlled_buffer_60
endmodule

module Node (
  input  [21:0] ParentIn,
  input  [3:0] NewID,
  input  [21:0] ChildLeftIn,
  input  [21:0] ChildRightIn,
  input  [3:0] RAMIn,
  input  Clock,
  input  [3:0] UniqueNodeID,
  output CurrentResolveState,
  output NewNodeRequest,
  output [2:0] CurrentExpressionType,
  output StackClear,
  output [21:0] ParentOut,
  output RAMWrite,
  output [3:0] RAM,
  output [3:0] RAMLoc,
  output [21:0] ChildLeftOut,
  output [21:0] ChildRightOut,
  output [3:0] ChildRightPointerOut,
  output [3:0] ChildLeftPointerOut
);

  wire and_1_out, and_2_out, and_3_out, and_4_out, and_5_out, and_6_out, and_7_out, and_8_out, and_9_out,
       and_10_out, d_ff_1_q, d_ff_2_q, d_ff_3_q, functionexpression_1_resolveflagoveride,
       nameexpression_1_backstack, nameexpression_1_bufferwrite, nameexpression_1_clearchidlren,
       nameexpression_1_expwrite, nameexpression_1_frontstack, nameexpression_1_nametogglechildren,
       nameexpression_1_ramselect, not_1_out, not_2_out, not_4_out, not_8_out, not_9_out, or_1_out, or_2_out,
       or_4_out, or_5_out, or_6_out, or_7_out;
  wire [2:0] nameexpression_1_newnode_2_3, not_3_out, not_5_out, not_6_out, not_7_out, register_4_q,
       xor_1_out, xor_2_out, xor_3_out, xor_4_out;
  wire [3:0] ChildL, ChildR, nameexpression_1_newnode_2, nameexpression_1_newnode_2_2, NewNode, register_5_q,
       register_6_q;
  wire [7:4] nameexpression_1_generaloutput;
  wire [11:11] nameexpression_1_newnode_2_4;

  Register #(.width(4)) register_1 (
    .D(nameexpression_1_newnode_2), .en(nameexpression_1_expwrite), .clk(Clock), .Q(ChildR),
    .clr(nameexpression_1_clearchidlren));
  Register #(.width(4)) register_2 (
    .D(nameexpression_1_newnode_2_2), .en(nameexpression_1_expwrite), .clk(Clock), .Q(ChildL),
    .clr(nameexpression_1_clearchidlren));
  Register #(.width(3)) register_3 (
    .D(nameexpression_1_newnode_2_3), .en(nameexpression_1_expwrite), .clk(Clock), .Q(CurrentExpressionType));  // open: clr
  and and_1 (and_1_out, nameexpression_1_expwrite, nameexpression_1_newnode_2_4[11]);
  not not_1 (not_1_out, nameexpression_1_expwrite);
  and and_2 (and_2_out, not_1_out, and_3_out);
  and and_3 (and_3_out, functionexpression_1_resolveflagoveride, or_4_out);
  assign ChildLeftPointerOut = not_2_out ? ChildL : 4'bz;  // Controlled_Buffer controlled_buffer_1
  not not_2 (not_2_out, or_6_out);
  assign ChildLeftPointerOut = or_6_out ? 4'b0000 : 4'bz;  // Controlled_Buffer controlled_buffer_2
  assign xor_1_out = 3'b011 ^ CurrentExpressionType;  // XOR_Gate xor_1, 3 bits wide
  assign not_3_out = ~xor_1_out;  // NOT_Gate not_3, 3 bits wide
  D_Flip_Flop d_ff_1 (.D(or_1_out), .clk(Clock), .Q(d_ff_1_q));  // open: Qn, preset, reset
  or or_1 (or_1_out, and_1_out, and_2_out);
  or or_2 (or_2_out, d_ff_2_q, nameexpression_1_nametogglechildren);
  and and_4 (and_4_out, not_3_out[0], not_3_out[1], not_3_out[2]);
  or or_3 (CurrentResolveState, and_7_out, and_5_out);
  and and_5 (and_5_out, d_ff_1_q, or_4_out);
  D_Flip_Flop d_ff_2 (.D(or_2_out), .clk(Clock), .Q(d_ff_2_q), .reset(StackClear));  // open: Qn, preset
  Register #(.width(3)) register_4 (
    .D(RAM[2:0]), .en(nameexpression_1_bufferwrite), .clk(Clock), .Q(register_4_q));  // open: clr
  and and_6 (and_6_out, ChildLeftIn[20], ChildRightIn[20]);
  D_Flip_Flop d_ff_3 (.D(ParentIn[21]), .clk(Clock), .Q(d_ff_3_q));  // open: Qn, preset, reset
  or or_4 (or_4_out, and_6_out, or_5_out);
  or or_5 (or_5_out, and_9_out, ChildRightIn[20]);
  assign xor_2_out = 3'b001 ^ CurrentExpressionType;  // XOR_Gate xor_2, 3 bits wide
  and and_7 (and_7_out, not_5_out[0], not_5_out[1], not_5_out[2]);
  not not_4 (not_4_out, d_ff_2_q);
  and and_8 (and_8_out, not_4_out, and_10_out);
  or or_6 (or_6_out, and_8_out, and_9_out);
  or or_7 (or_7_out, and_4_out, ParentIn[21]);
  or or_8 (ChildRightOut[21], or_7_out, d_ff_3_q);
  assign not_5_out = ~xor_2_out;  // NOT_Gate not_5, 3 bits wide
  NameExpression nameexpression_1 (
    .PEB(ParentIn[11:0]), .PIB(ParentIn[19:12]), .CRE(ChildRightIn[11:0]), .CRI(ChildRightIn[19:12]),
    .CLE(ChildLeftIn[11:0]), .CLI(ChildLeftIn[19:12]), .SFS(register_5_q), .SBS(register_6_q), .RAM(RAMIn),
    .InternalExpression({CurrentResolveState, CurrentExpressionType, ChildL, ChildR}), .Buffer(register_4_q),
    .EXPWrite(nameexpression_1_expwrite), .RamSelect(nameexpression_1_ramselect),
    .FrontStack(nameexpression_1_frontstack), .BackStack(nameexpression_1_backstack), .RAMwrite(RAMWrite),
    .NewNode(NewNodeRequest), .Clock(Clock), .NewNodeID(NewNode), .UniqueNodeID(UniqueNodeID),
    .BufferWrite(nameexpression_1_bufferwrite), .NameToggleChildren(nameexpression_1_nametogglechildren),
    .ClearChidlren(nameexpression_1_clearchidlren), .StackClear(StackClear), .PEB_2(ParentOut[11:0]),
    .PIB_2(ParentOut[19:12]), .CRE_2(ChildRightOut[11:0]), .CRI_2(ChildRightOut[19:12]),
    .CLE_2(ChildLeftOut[11:0]), .CLI_2(ChildLeftOut[19:12]),
    .NewNode_2({nameexpression_1_newnode_2_4[11], nameexpression_1_newnode_2_3, nameexpression_1_newnode_2_2, nameexpression_1_newnode_2}),
    .GeneralOutput({nameexpression_1_generaloutput, RAM}));
  and and_9 (and_9_out, not_6_out[0], not_6_out[1], not_6_out[2]);
  and and_10 (and_10_out, not_7_out[0], not_7_out[1], not_7_out[2]);
  assign xor_3_out = CurrentExpressionType ^ 3'b100;  // XOR_Gate xor_3, 3 bits wide
  assign not_6_out = ~xor_3_out;  // NOT_Gate not_6, 3 bits wide
  assign xor_4_out = CurrentExpressionType ^ 3'b001;  // XOR_Gate xor_4, 3 bits wide
  assign not_7_out = ~xor_4_out;  // NOT_Gate not_7, 3 bits wide
  UndefinedExpression undefinedexpression_1 (
    .PEB(ParentIn[11:0]), .PIB(ParentIn[19:12]), .CRE(ChildRightIn[11:0]), .CRI(ChildRightIn[19:12]),
    .CLE(ChildLeftIn[11:0]), .CLI(ChildLeftIn[19:12]), .SFS(RAMIn), .SBS(register_6_q), .RAM(RAMIn),
    .InternalExpression({CurrentResolveState, CurrentExpressionType, ChildL, ChildR}), .Buffer(register_4_q),
    .EXPWrite(nameexpression_1_expwrite), .RamSelect(nameexpression_1_ramselect),
    .FrontStack(nameexpression_1_frontstack), .BackStack(nameexpression_1_backstack), .RAMwrite(RAMWrite),
    .NewNode(NewNodeRequest), .Clock(Clock), .NewNodeID(NewNode), .UniqueNodeID(UniqueNodeID),
    .ClearChidlren(nameexpression_1_clearchidlren), .StackClear(StackClear), .PEB_2(ParentOut[11:0]),
    .PIB_2(ParentOut[19:12]), .CRE_2(ChildRightOut[11:0]), .CRI_2(ChildRightOut[19:12]),
    .CLE_2(ChildLeftOut[11:0]), .CLI_2(ChildLeftOut[19:12]),
    .NewNode_2({nameexpression_1_newnode_2_4[11], nameexpression_1_newnode_2_3, nameexpression_1_newnode_2_2, nameexpression_1_newnode_2}),
    .GeneralOutput({nameexpression_1_generaloutput, RAM}));
  GoToExpression gotoexpression_1 (
    .PEB(ParentIn[11:0]), .PIB(ParentIn[19:12]), .CRE(ChildRightIn[11:0]), .CRI(ChildRightIn[19:12]),
    .CLE(ChildLeftIn[11:0]), .CLI(ChildLeftIn[19:12]), .SFS(RAMIn), .SBS(register_6_q), .RAM(RAMIn),
    .InternalExpression({CurrentResolveState, CurrentExpressionType, ChildL, ChildR}), .Buffer(register_4_q),
    .EXPWrite(nameexpression_1_expwrite), .RamSelect(nameexpression_1_ramselect),
    .FrontStack(nameexpression_1_frontstack), .BackStack(nameexpression_1_backstack), .RAMwrite(RAMWrite),
    .NewNode(NewNodeRequest), .Clock(Clock), .NewNodeID(NewNode), .UniqueNodeID(UniqueNodeID),
    .ClearChidlren(nameexpression_1_clearchidlren), .StackClear(StackClear), .PEB_2(ParentOut[11:0]),
    .PIB_2(ParentOut[19:12]), .CRE_2(ChildRightOut[11:0]), .CRI_2(ChildRightOut[19:12]),
    .CLE_2(ChildLeftOut[11:0]), .CLI_2(ChildLeftOut[19:12]),
    .NewNode_2({nameexpression_1_newnode_2_4[11], nameexpression_1_newnode_2_3, nameexpression_1_newnode_2_2, nameexpression_1_newnode_2}),
    .GeneralOutput({nameexpression_1_generaloutput, RAM}));
  ApplicationExpression applicationexpression_1 (
    .PEB(ParentIn[11:0]), .PIB(ParentIn[19:12]), .CRE(ChildRightIn[11:0]), .CRI(ChildRightIn[19:12]),
    .CLE(ChildLeftIn[11:0]), .CLI(ChildLeftIn[19:12]), .SFS(RAMIn), .SBS(register_6_q), .RAM(RAMIn),
    .InternalExpression({CurrentResolveState, CurrentExpressionType, ChildL, ChildR}), .Buffer(register_4_q),
    .EXPWrite(nameexpression_1_expwrite), .RamSelect(nameexpression_1_ramselect),
    .FrontStack(nameexpression_1_frontstack), .BackStack(nameexpression_1_backstack), .RAMwrite(RAMWrite),
    .NewNode(NewNodeRequest), .Clock(Clock), .NewNodeID(NewNode), .UniqueNodeID(UniqueNodeID),
    .ClearChidlren(nameexpression_1_clearchidlren), .StackClear(StackClear), .PEB_2(ParentOut[11:0]),
    .PIB_2(ParentOut[19:12]), .CRE_2(ChildRightOut[11:0]), .CRI_2(ChildRightOut[19:12]),
    .CLE_2(ChildLeftOut[11:0]), .CLI_2(ChildLeftOut[19:12]),
    .NewNode_2({nameexpression_1_newnode_2_4[11], nameexpression_1_newnode_2_3, nameexpression_1_newnode_2_2, nameexpression_1_newnode_2}),
    .GeneralOutput({nameexpression_1_generaloutput, RAM}));
  FunctionExpression functionexpression_1 (
    .PEB(ParentIn[11:0]), .PIB(ParentIn[19:12]), .CRE(ChildRightIn[11:0]), .CRI(ChildRightIn[19:12]),
    .CLE(ChildLeftIn[11:0]), .CLI(ChildLeftIn[19:12]), .SFS(register_5_q), .SBS(register_6_q), .RAM(RAMIn),
    .InternalExpression({CurrentResolveState, CurrentExpressionType, ChildL, ChildR}),
    .UnreduceFlag(ParentIn[21]), .EXPWrite(nameexpression_1_expwrite),
    .RamSelect(nameexpression_1_ramselect), .FrontStack(nameexpression_1_frontstack),
    .BackStack(nameexpression_1_backstack), .RAMwrite(RAMWrite), .NewNode(NewNodeRequest), .Clock(Clock),
    .NewNodeID(NewNode), .UniqueNodeID(UniqueNodeID),
    .ResolveFlagOveride(functionexpression_1_resolveflagoveride),
    .ClearChidlren(nameexpression_1_clearchidlren), .StackClear(StackClear), .PEB_2(ParentOut[11:0]),
    .PIB_2(ParentOut[19:12]), .CRE_2(ChildRightOut[11:0]), .CRI_2(ChildRightOut[19:12]),
    .CLE_2(ChildLeftOut[11:0]), .CLI_2(ChildLeftOut[19:12]),
    .NewNode_2({nameexpression_1_newnode_2_4[11], nameexpression_1_newnode_2_3, nameexpression_1_newnode_2_2, nameexpression_1_newnode_2}),
    .GeneralOutput({nameexpression_1_generaloutput, RAM}));
  Register #(.width(4)) register_5 (
    .D(RAM), .en(nameexpression_1_frontstack), .clk(Clock), .Q(register_5_q), .clr(StackClear));
  not not_8 (not_8_out, and_8_out);
  Register #(.width(4)) NewNodeID (.D(NewID), .en(Clock), .clk(NewNodeRequest), .Q(NewNode));  // open: clr
  assign RAMLoc = nameexpression_1_ramselect ? register_5_q : 4'bz;  // Controlled_Buffer controlled_buffer_3
  assign ChildRightPointerOut = not_8_out ? ChildR : 4'bz;  // Controlled_Buffer controlled_buffer_4
  assign ChildRightPointerOut = and_8_out ? 4'b0000 : 4'bz;  // Controlled_Buffer controlled_buffer_5
  Register #(.width(4)) register_6 (
    .D(RAM), .en(nameexpression_1_backstack), .clk(Clock), .Q(register_6_q), .clr(StackClear));
  assign RAMLoc = not_9_out ? register_6_q : 4'bz;  // Controlled_Buffer controlled_buffer_6
  not not_9 (not_9_out, nameexpression_1_ramselect);

  assign ChildLeftOut[21:20] = 2'b00;
  assign ChildRightOut[20] = 1'b0;
  assign ParentOut[21:20] = {ChildRightOut[21], CurrentResolveState};

  // Other names for the same wires on the sheet: Expres[2:0] = CurrentExpressionType

  // Notes on the sheet:
  //   Resolve Flag
  //   Reduce Flag
  //   FrontStack
  //   BackStack
endmodule

module UndefinedExpression (
  input  [11:0] PEB,
  input  [7:0] PIB,
  input  [11:0] CRE,
  input  [7:0] CRI,
  input  [11:0] CLE,
  input  [7:0] CLI,
  input  [3:0] SFS,
  input  [3:0] SBS,
  input  [3:0] RAM,
  input  [11:0] InternalExpression,
  input  [2:0] Buffer,
  input  Clock,
  input  [3:0] NewNodeID,
  input  [3:0] UniqueNodeID,
  output EXPWrite,
  output RamSelect,
  output FrontStack,
  output BackStack,
  output RAMwrite,
  output NewNode,
  output [11:0] PEB_2,
  output [7:0] PIB_2,
  output [11:0] CRE_2,
  output [7:0] CRI_2,
  output [11:0] CLE_2,
  output [7:0] CLI_2,
  output [11:0] NewNode_2,
  output [7:0] GeneralOutput,
  output ClearChidlren,
  output StackClear
);

  wire and_1_out, decoder_1_out2, decoder_1_out3, decoder_1_out4, not_2_out, not_3_out, not_4_out, not_5_out,
       not_6_out, or_1_out, or_2_out, or_3_out, or_4_out, or_5_out, or_6_out, or_7_out, or_8_out, or_9_out,
       or_10_out, or_11_out, or_12_out, or_13_out, or_14_out, or_15_out, updateexpression_1_updcle,
       updateexpression_1_updcli, updateexpression_1_updcre, updateexpression_1_updcri,
       updateexpression_1_updexp, updateexpression_1_updstackclear, updatepointerleft_1_updcle,
       updatepointerleft_1_updcli, updatepointerleft_1_updcre, updatepointerleft_1_updcri,
       updatepointerleft_1_updexp, updatepointerright_1_updcle, updatepointerright_1_updcli,
       updatepointerright_1_updcre, updatepointerright_1_updcri, updatepointerright_1_updexp;
  wire [2:0] not_1_out, xor_1_out;
  wire [7:0] controlled_buffer_2_out, controlled_buffer_4_out, updateexpression_1_cli,
       updateexpression_1_cri, updatepointerleft_1_cli, updatepointerleft_1_cri, updatepointerright_1_cli,
       updatepointerright_1_cri;
  wire [11:0] controlled_buffer_1_out, controlled_buffer_3_out, controlled_buffer_5_out,
       updateexpression_1_cle, updateexpression_1_cre, updateexpression_1_newvalue, updatepointerleft_1_cle,
       updatepointerleft_1_cre, updatepointerleft_1_newvalue, updatepointerright_1_cli_2,
       updatepointerright_1_cri_2, updatepointerright_1_newvalue;

  Decoder #(.select(4)) decoder_1 (
    .out2(decoder_1_out2), .out3(decoder_1_out3), .out4(decoder_1_out4), .sel(PIB[7:4]));  // open: out0, out1, out5, out6, out7, out8, out9, out10, out11, out12, out13, out14, out15, en
  assign xor_1_out = InternalExpression[10:8] ^ 3'b000;  // XOR_Gate xor_1, 3 bits wide
  assign controlled_buffer_1_out = updateexpression_1_updcre ? updateexpression_1_cre : 12'bz;  // Controlled_Buffer controlled_buffer_1
  buf or_1 (or_1_out, updateexpression_1_updcri);  // OR_Gate
  assign controlled_buffer_2_out = updateexpression_1_updcri ? updateexpression_1_cri : 8'bz;  // Controlled_Buffer controlled_buffer_2
  UpdateExpression updateexpression_1 (
    .ActivationSignal(decoder_1_out2), .Clock(Clock), .UniqueNodeID(UniqueNodeID), .PIB(PIB), .PEB(PEB),
    .UpdCLE(updateexpression_1_updcle), .UpdCRE(updateexpression_1_updcre),
    .UpdCLI(updateexpression_1_updcli), .UpdCRI(updateexpression_1_updcri),
    .UpdStackClear(updateexpression_1_updstackclear), .UpdEXP(updateexpression_1_updexp),
    .CRI(updateexpression_1_cri), .CLI(updateexpression_1_cli), .CRE(updateexpression_1_cre),
    .CLE(updateexpression_1_cle), .NewValue(updateexpression_1_newvalue));
  assign not_1_out = ~xor_1_out;  // NOT_Gate not_1, 3 bits wide
  assign controlled_buffer_3_out = updateexpression_1_updcle ? updateexpression_1_cle : 12'bz;  // Controlled_Buffer controlled_buffer_3
  buf or_2 (or_2_out, updateexpression_1_updcli);  // OR_Gate
  assign controlled_buffer_4_out = updateexpression_1_updcli ? updateexpression_1_cli : 8'bz;  // Controlled_Buffer controlled_buffer_4
  buf or_3 (or_3_out, updateexpression_1_updexp);  // OR_Gate
  assign controlled_buffer_5_out = updateexpression_1_updexp ? updateexpression_1_newvalue : 12'bz;  // Controlled_Buffer controlled_buffer_5
  and and_1 (and_1_out, not_1_out[0], not_1_out[1], not_1_out[2]);
  or or_4 (or_4_out, updateexpression_1_updexp, updatepointerleft_1_updexp);
  assign controlled_buffer_1_out = updatepointerleft_1_updcre ? updatepointerleft_1_cre : 12'bz;  // Controlled_Buffer controlled_buffer_6
  UpdatePointerLeft updatepointerleft_1 (
    .ActivationSignal(decoder_1_out3), .Clock(Clock), .UniqueNodeID(UniqueNodeID), .PIB(PIB),
    .InternalExpression(InternalExpression), .PEB(PEB), .UpdCLE(updatepointerleft_1_updcle),
    .UpdCRE(updatepointerleft_1_updcre), .UpdCLI(updatepointerleft_1_updcli),
    .UpdCRI(updatepointerleft_1_updcri), .UpdEXP(updatepointerleft_1_updexp), .CRI(updatepointerleft_1_cri),
    .CLI(updatepointerleft_1_cli), .CRE(updatepointerleft_1_cre), .CLE(updatepointerleft_1_cle),
    .NewValue(updatepointerleft_1_newvalue));
  or or_5 (or_5_out, updateexpression_1_updcre, updatepointerleft_1_updcre);
  or or_6 (or_6_out, or_1_out, updatepointerleft_1_updcri);
  assign controlled_buffer_2_out = updatepointerleft_1_updcri ? updatepointerleft_1_cri : 8'bz;  // Controlled_Buffer controlled_buffer_7
  or or_7 (or_7_out, updateexpression_1_updcle, updatepointerleft_1_updcle);
  assign controlled_buffer_3_out = updatepointerleft_1_updcle ? updatepointerleft_1_cle : 12'bz;  // Controlled_Buffer controlled_buffer_8
  or or_8 (or_8_out, or_2_out, updatepointerleft_1_updcli);
  assign controlled_buffer_4_out = updatepointerleft_1_updcli ? updatepointerleft_1_cli : 8'bz;  // Controlled_Buffer controlled_buffer_9
  or or_9 (or_9_out, or_3_out, updatepointerleft_1_updexp);
  assign controlled_buffer_5_out = updatepointerleft_1_updexp ? updatepointerleft_1_newvalue : 12'bz;  // Controlled_Buffer controlled_buffer_10
  UpdatePointerRight updatepointerright_1 (
    .ActivationSignal(decoder_1_out4), .Clock(Clock), .UniqueNodeID(UniqueNodeID), .PIB(PIB),
    .InternalExpression(InternalExpression), .PEB(PEB), .UpdCLE(updatepointerright_1_updcle),
    .UpdCRE(updatepointerright_1_updcre), .UpdCLI(updatepointerright_1_updcli),
    .UpdCRI(updatepointerright_1_updcri), .UpdEXP(updatepointerright_1_updexp),
    .CRI(updatepointerright_1_cri), .CLI(updatepointerright_1_cli), .CRI_2(updatepointerright_1_cri_2),
    .CLI_2(updatepointerright_1_cli_2), .NewValue(updatepointerright_1_newvalue));
  or or_10 (or_10_out, or_4_out, updatepointerright_1_updexp);
  or or_11 (or_11_out, or_5_out, updatepointerright_1_updcre);
  assign controlled_buffer_1_out = updatepointerright_1_updcre ? updatepointerright_1_cri_2 : 12'bz;  // Controlled_Buffer controlled_buffer_11
  or or_12 (or_12_out, or_6_out, updatepointerright_1_updcri);
  assign controlled_buffer_2_out = updatepointerright_1_updcri ? updatepointerright_1_cri : 8'bz;  // Controlled_Buffer controlled_buffer_12
  or or_13 (or_13_out, or_7_out, updatepointerright_1_updcle);
  assign controlled_buffer_3_out = updatepointerright_1_updcle ? updatepointerright_1_cli_2 : 12'bz;  // Controlled_Buffer controlled_buffer_13
  or or_14 (or_14_out, or_8_out, updatepointerright_1_updcli);
  assign controlled_buffer_4_out = updatepointerright_1_updcli ? updatepointerright_1_cli : 8'bz;  // Controlled_Buffer controlled_buffer_14
  or or_15 (or_15_out, or_9_out, updatepointerright_1_updexp);
  assign controlled_buffer_5_out = updatepointerright_1_updexp ? updatepointerright_1_newvalue : 12'bz;  // Controlled_Buffer controlled_buffer_15
  assign RamSelect = and_1_out ? 1'b0 : 1'bz;  // Controlled_Buffer controlled_buffer_16
  assign BackStack = and_1_out ? 1'b0 : 1'bz;  // Controlled_Buffer controlled_buffer_17
  assign FrontStack = and_1_out ? 1'b0 : 1'bz;  // Controlled_Buffer controlled_buffer_18
  assign RAMwrite = and_1_out ? 1'b0 : 1'bz;  // Controlled_Buffer controlled_buffer_19
  assign EXPWrite = and_1_out ? or_10_out : 1'bz;  // Controlled_Buffer controlled_buffer_20
  assign NewNode = and_1_out ? 1'b0 : 1'bz;  // Controlled_Buffer controlled_buffer_21
  not not_2 (not_2_out, or_11_out);
  assign controlled_buffer_1_out = not_2_out ? {12{1'b0}} : 12'bz;  // Controlled_Buffer controlled_buffer_22
  not not_3 (not_3_out, or_12_out);
  assign controlled_buffer_2_out = not_3_out ? {8{1'b0}} : 8'bz;  // Controlled_Buffer controlled_buffer_23
  not not_4 (not_4_out, or_13_out);
  assign controlled_buffer_3_out = not_4_out ? {12{1'b0}} : 12'bz;  // Controlled_Buffer controlled_buffer_24
  not not_5 (not_5_out, or_14_out);
  assign controlled_buffer_4_out = not_5_out ? {8{1'b0}} : 8'bz;  // Controlled_Buffer controlled_buffer_25
  not not_6 (not_6_out, or_15_out);
  assign controlled_buffer_5_out = not_6_out ? {12{1'b0}} : 12'bz;  // Controlled_Buffer controlled_buffer_26
  assign ClearChidlren = and_1_out ? 1'b0 : 1'bz;  // Controlled_Buffer controlled_buffer_27
  assign PEB_2 = and_1_out ? {12{1'b0}} : 12'bz;  // Controlled_Buffer controlled_buffer_28
  assign PIB_2 = and_1_out ? {8{1'b0}} : 8'bz;  // Controlled_Buffer controlled_buffer_29
  assign CRE_2 = and_1_out ? controlled_buffer_1_out : 12'bz;  // Controlled_Buffer controlled_buffer_30
  assign CRI_2 = and_1_out ? controlled_buffer_2_out : 8'bz;  // Controlled_Buffer controlled_buffer_31
  assign CLE_2 = and_1_out ? controlled_buffer_3_out : 12'bz;  // Controlled_Buffer controlled_buffer_32
  assign CLI_2 = and_1_out ? controlled_buffer_4_out : 8'bz;  // Controlled_Buffer controlled_buffer_33
  assign NewNode_2 = and_1_out ? controlled_buffer_5_out : 12'bz;  // Controlled_Buffer controlled_buffer_34
  assign GeneralOutput = and_1_out ? {8{1'b0}} : 8'bz;  // Controlled_Buffer controlled_buffer_35
  assign StackClear = and_1_out ? updateexpression_1_updstackclear : 1'bz;  // Controlled_Buffer controlled_buffer_36

  // Notes on the sheet:
  //   Input
  //   0 == Backstack / 1 == Frontstack
  //   Output
endmodule

module NameExpression (
  input  [11:0] PEB,
  input  [7:0] PIB,
  input  [11:0] CRE,
  input  [7:0] CRI,
  input  [11:0] CLE,
  input  [7:0] CLI,
  input  [3:0] SFS,
  input  [3:0] SBS,
  input  [3:0] RAM,
  input  [11:0] InternalExpression,
  input  [2:0] Buffer,
  input  Clock,
  input  [3:0] NewNodeID,
  input  [3:0] UniqueNodeID,
  output EXPWrite,
  output RamSelect,
  output FrontStack,
  output BackStack,
  output RAMwrite,
  output NewNode,
  output [11:0] PEB_2,
  output [7:0] PIB_2,
  output [11:0] CRE_2,
  output [7:0] CRI_2,
  output [11:0] CLE_2,
  output [7:0] CLI_2,
  output [11:0] NewNode_2,
  output [7:0] GeneralOutput,
  output BufferWrite,
  output NameToggleChildren,
  output ClearChidlren,
  output StackClear
);

  wire and_1_out, comparevalue_1_comcle, comparevalue_1_comcli, comparevalue_1_comcre, comparevalue_1_comcri,
       comparevalue_1_compib, comparevalue_1_markfortransformation, decoder_1_out1, decoder_1_out2,
       decoder_1_out3, decoder_1_out4, decoder_1_out5, decoder_1_out6, decoder_1_out7, decoder_1_out8,
       decoder_1_out9, immediateresolution_1_immpib, not_2_out, not_3_out, not_4_out, not_5_out, not_6_out,
       not_7_out, not_8_out, not_9_out, nullification_1_nullcli, nullification_1_nullcri,
       nullification_1_nullexp, nullification_1_nullstackclear, or_1_out, or_2_out, or_3_out, or_4_out,
       or_5_out, or_6_out, or_7_out, or_8_out, or_9_out, or_10_out, or_11_out, or_12_out, or_13_out,
       or_14_out, or_15_out, or_16_out, or_17_out, or_18_out, or_19_out, or_20_out, or_21_out, or_22_out,
       or_23_out, or_24_out, or_25_out, or_26_out, or_27_out, or_28_out, or_29_out, or_30_out, or_31_out,
       or_32_out, or_33_out, or_34_out, or_35_out, or_36_out, or_37_out, or_38_out, or_39_out, or_40_out,
       or_41_out, or_42_out, or_43_out, or_44_out, or_45_out,
       preparefortransformationasancestorinput_1_ptacli, preparefortransformationasancestorinput_1_ptacri,
       preparefortransformationasancestorinput_1_ptapeb, preparefortransformationasancestorinput_1_ptapib,
       preparefortransformationasancestorinput_1_ptaram, preparefortransformationasancestorinput_1_ptasbs,
       preparefortransformationasancestorinput_1_ptasel, preparefortransformationasancestorinput_1_ptasfs,
       preparefortransformationasancestorinput_1_ptastackclear,
       preparefortransformationasdecendantinput_1_ptdclc, preparefortransformationasdecendantinput_1_ptdcle,
       preparefortransformationasdecendantinput_1_ptdcli,
       preparefortransformationasdecendantinput_1_ptdcomparevalueclear,
       preparefortransformationasdecendantinput_1_ptdcre, preparefortransformationasdecendantinput_1_ptdcri,
       preparefortransformationasdecendantinput_1_ptdexp, preparefortransformationasdecendantinput_1_ptdnew,
       preparefortransformationasdecendantinput_1_ptdpib, preparefortransformationasdecendantinput_1_ptdram,
       preparefortransformationasdecendantinput_1_ptdsbs, preparefortransformationasdecendantinput_1_ptdsel,
       preparefortransformationasdecendantinput_1_ptdsfs,
       preparefortransformationasdecendantinput_1_ptdstackclear, returnexpression_1_retcli,
       returnexpression_1_retcri, returnexpression_1_retpeb, returnexpression_1_retpib,
       updateexpression_1_updcle, updateexpression_1_updcli, updateexpression_1_updcre,
       updateexpression_1_updcri, updateexpression_1_updexp, updateexpression_1_updstackclear,
       updatepointerleft_1_updcle, updatepointerleft_1_updcli, updatepointerleft_1_updcre,
       updatepointerleft_1_updcri, updatepointerleft_1_updexp, updatepointerright_1_updcle,
       updatepointerright_1_updcli, updatepointerright_1_updcre, updatepointerright_1_updcri,
       updatepointerright_1_updexp;
  wire [2:0] not_1_out, xor_1_out;
  wire [7:0] comparevalue_1_cli_2, comparevalue_1_cri_2, comparevalue_1_pib_2, controlled_buffer_1_out,
       controlled_buffer_2_out, controlled_buffer_20_out, controlled_buffer_33_out,
       immediateresolution_1_out_3, nullification_1_cli, nullification_1_cri,
       preparefortransformationasancestorinput_1_cli_2, preparefortransformationasancestorinput_1_cri_2,
       preparefortransformationasancestorinput_1_generalouput, preparefortransformationasancestorinput_1_pib,
       preparefortransformationasdecendantinput_1_cli_2, preparefortransformationasdecendantinput_1_cri_2,
       preparefortransformationasdecendantinput_1_output, preparefortransformationasdecendantinput_1_pib_2,
       returnexpression_1_cli_2, returnexpression_1_cri_2, returnexpression_1_pib_2, updateexpression_1_cli,
       updateexpression_1_cri, updatepointerleft_1_cli, updatepointerleft_1_cri, updatepointerright_1_cli,
       updatepointerright_1_cri;
  wire [11:0] comparevalue_1_cle, comparevalue_1_cre, controlled_buffer_3_out, controlled_buffer_4_out,
       controlled_buffer_6_out, controlled_buffer_19_out, nullification_1_newvalue,
       preparefortransformationasancestorinput_1_peb, preparefortransformationasdecendantinput_1_cle,
       preparefortransformationasdecendantinput_1_cre,
       preparefortransformationasdecendantinput_1_newexpression, returnexpression_1_peb,
       updateexpression_1_cle, updateexpression_1_cre, updateexpression_1_newvalue, updatepointerleft_1_cle,
       updatepointerleft_1_cre, updatepointerleft_1_newvalue, updatepointerright_1_cli_2,
       updatepointerright_1_cri_2, updatepointerright_1_newvalue;

  Decoder #(.select(4)) decoder_1 (
    .out1(decoder_1_out1), .out2(decoder_1_out2), .out3(decoder_1_out3), .out4(decoder_1_out4),
    .out5(decoder_1_out5), .out6(decoder_1_out6), .out7(decoder_1_out7), .out8(decoder_1_out8),
    .out9(decoder_1_out9), .sel(PIB[7:4]));  // open: out0, out10, out11, out12, out13, out14, out15, en
  Nullification nullification_1 (
    .ActivationSignal(decoder_1_out1), .Clock(Clock), .NullCLI(nullification_1_nullcli),
    .NullCRI(nullification_1_nullcri), .NullStackClear(nullification_1_nullstackclear),
    .NullEXP(nullification_1_nullexp), .CRI(nullification_1_cri), .CLI(nullification_1_cli),
    .NewValue(nullification_1_newvalue));
  assign controlled_buffer_1_out = nullification_1_nullcli ? nullification_1_cri : 8'bz;  // Controlled_Buffer controlled_buffer_1
  assign controlled_buffer_2_out = nullification_1_nullcri ? nullification_1_cli : 8'bz;  // Controlled_Buffer controlled_buffer_2
  assign controlled_buffer_3_out = nullification_1_nullexp ? nullification_1_newvalue : 12'bz;  // Controlled_Buffer controlled_buffer_3
  UpdateExpression updateexpression_1 (
    .ActivationSignal(decoder_1_out2), .Clock(Clock), .UniqueNodeID(UniqueNodeID), .PIB(PIB), .PEB(PEB),
    .UpdCLE(updateexpression_1_updcle), .UpdCRE(updateexpression_1_updcre),
    .UpdCLI(updateexpression_1_updcli), .UpdCRI(updateexpression_1_updcri),
    .UpdStackClear(updateexpression_1_updstackclear), .UpdEXP(updateexpression_1_updexp),
    .CRI(updateexpression_1_cri), .CLI(updateexpression_1_cli), .CRE(updateexpression_1_cre),
    .CLE(updateexpression_1_cle), .NewValue(updateexpression_1_newvalue));
  assign not_1_out = ~xor_1_out;  // NOT_Gate not_1, 3 bits wide
  assign xor_1_out = InternalExpression[10:8] ^ 3'b001;  // XOR_Gate xor_1, 3 bits wide
  or or_1 (or_1_out, nullification_1_nullexp, updateexpression_1_updexp);
  assign controlled_buffer_4_out = updateexpression_1_updcre ? updateexpression_1_cre : 12'bz;  // Controlled_Buffer controlled_buffer_4
  or or_2 (or_2_out, nullification_1_nullcli, updateexpression_1_updcri);
  assign controlled_buffer_1_out = updateexpression_1_updcri ? updateexpression_1_cri : 8'bz;  // Controlled_Buffer controlled_buffer_5
  assign controlled_buffer_6_out = updateexpression_1_updcle ? updateexpression_1_cle : 12'bz;  // Controlled_Buffer controlled_buffer_6
  or or_3 (or_3_out, nullification_1_nullcri, updateexpression_1_updcli);
  assign controlled_buffer_2_out = updateexpression_1_updcli ? updateexpression_1_cli : 8'bz;  // Controlled_Buffer controlled_buffer_7
  or or_4 (or_4_out, nullification_1_nullexp, updateexpression_1_updexp);
  assign controlled_buffer_3_out = updateexpression_1_updexp ? updateexpression_1_newvalue : 12'bz;  // Controlled_Buffer controlled_buffer_8
  or or_5 (or_5_out, nullification_1_nullstackclear, updateexpression_1_updstackclear);
  and and_1 (and_1_out, not_1_out[0], not_1_out[1], not_1_out[2]);
  UpdatePointerLeft updatepointerleft_1 (
    .ActivationSignal(decoder_1_out3), .Clock(Clock), .UniqueNodeID(UniqueNodeID), .PIB(PIB),
    .InternalExpression(InternalExpression), .PEB(PEB), .UpdCLE(updatepointerleft_1_updcle),
    .UpdCRE(updatepointerleft_1_updcre), .UpdCLI(updatepointerleft_1_updcli),
    .UpdCRI(updatepointerleft_1_updcri), .UpdEXP(updatepointerleft_1_updexp), .CRI(updatepointerleft_1_cri),
    .CLI(updatepointerleft_1_cli), .CRE(updatepointerleft_1_cre), .CLE(updatepointerleft_1_cle),
    .NewValue(updatepointerleft_1_newvalue));
  or or_6 (or_6_out, or_1_out, updatepointerleft_1_updexp);
  or or_7 (or_7_out, updateexpression_1_updcre, updatepointerleft_1_updcre);
  assign controlled_buffer_4_out = updatepointerleft_1_updcre ? updatepointerleft_1_cre : 12'bz;  // Controlled_Buffer controlled_buffer_9
  or or_8 (or_8_out, or_2_out, updatepointerleft_1_updcri);
  assign controlled_buffer_1_out = updatepointerleft_1_updcri ? updatepointerleft_1_cri : 8'bz;  // Controlled_Buffer controlled_buffer_10
  or or_9 (or_9_out, updateexpression_1_updcle, updatepointerleft_1_updcle);
  assign controlled_buffer_6_out = updatepointerleft_1_updcle ? updatepointerleft_1_cle : 12'bz;  // Controlled_Buffer controlled_buffer_11
  or or_10 (or_10_out, or_3_out, updatepointerleft_1_updcli);
  assign controlled_buffer_2_out = updatepointerleft_1_updcli ? updatepointerleft_1_cli : 8'bz;  // Controlled_Buffer controlled_buffer_12
  or or_11 (or_11_out, or_4_out, updatepointerleft_1_updexp);
  assign controlled_buffer_3_out = updatepointerleft_1_updexp ? updatepointerleft_1_newvalue : 12'bz;  // Controlled_Buffer controlled_buffer_13
  UpdatePointerRight updatepointerright_1 (
    .ActivationSignal(decoder_1_out4), .Clock(Clock), .UniqueNodeID(UniqueNodeID), .PIB(PIB),
    .InternalExpression(InternalExpression), .PEB(PEB), .UpdCLE(updatepointerright_1_updcle),
    .UpdCRE(updatepointerright_1_updcre), .UpdCLI(updatepointerright_1_updcli),
    .UpdCRI(updatepointerright_1_updcri), .UpdEXP(updatepointerright_1_updexp),
    .CRI(updatepointerright_1_cri), .CLI(updatepointerright_1_cli), .CRI_2(updatepointerright_1_cri_2),
    .CLI_2(updatepointerright_1_cli_2), .NewValue(updatepointerright_1_newvalue));
  or or_12 (or_12_out, or_6_out, updatepointerright_1_updexp);
  or or_13 (or_13_out, or_7_out, updatepointerright_1_updcre);
  assign controlled_buffer_4_out = updatepointerright_1_updcre ? updatepointerright_1_cri_2 : 12'bz;  // Controlled_Buffer controlled_buffer_14
  or or_14 (or_14_out, or_8_out, updatepointerright_1_updcri);
  assign controlled_buffer_1_out = updatepointerright_1_updcri ? updatepointerright_1_cri : 8'bz;  // Controlled_Buffer controlled_buffer_15
  or or_15 (or_15_out, or_9_out, updatepointerright_1_updcle);
  assign controlled_buffer_6_out = updatepointerright_1_updcle ? updatepointerright_1_cli_2 : 12'bz;  // Controlled_Buffer controlled_buffer_16
  or or_16 (or_16_out, or_10_out, updatepointerright_1_updcli);
  assign controlled_buffer_2_out = updatepointerright_1_updcli ? updatepointerright_1_cli : 8'bz;  // Controlled_Buffer controlled_buffer_17
  or or_17 (or_17_out, or_11_out, updatepointerright_1_updexp);
  assign controlled_buffer_3_out = updatepointerright_1_updexp ? updatepointerright_1_newvalue : 12'bz;  // Controlled_Buffer controlled_buffer_18
  assign controlled_buffer_19_out = returnexpression_1_retpeb ? returnexpression_1_peb : 12'bz;  // Controlled_Buffer controlled_buffer_19
  assign controlled_buffer_20_out = returnexpression_1_retpib ? returnexpression_1_pib_2 : 8'bz;  // Controlled_Buffer controlled_buffer_20
  or or_18 (or_18_out, or_14_out, returnexpression_1_retcri);
  assign controlled_buffer_1_out = returnexpression_1_retcri ? returnexpression_1_cri_2 : 8'bz;  // Controlled_Buffer controlled_buffer_21
  ReturnExpression returnexpression_1 (
    .ActivationSignal(decoder_1_out5), .UniqueNodeID(UniqueNodeID), .PIB(PIB), .CLI(CLI), .CRI(CRI),
    .CRE(CRE), .CLE(CLE), .InternalExpression(InternalExpression), .RetCLI(returnexpression_1_retcli),
    .RetCRI(returnexpression_1_retcri), .RetPIB(returnexpression_1_retpib),
    .RetPEB(returnexpression_1_retpeb), .CRI_2(returnexpression_1_cri_2), .CLI_2(returnexpression_1_cli_2),
    .PEB(returnexpression_1_peb), .PIB_2(returnexpression_1_pib_2));
  or or_19 (or_19_out, or_16_out, returnexpression_1_retcli);
  assign controlled_buffer_2_out = returnexpression_1_retcli ? returnexpression_1_cli_2 : 8'bz;  // Controlled_Buffer controlled_buffer_22
  CompareValue comparevalue_1 (
    .ActivationSignal(decoder_1_out6), .Clock(Clock),
    .Clear(preparefortransformationasdecendantinput_1_ptdstackclear), .InternalValue(InternalExpression),
    .PEB(PEB), .PIB(PIB), .CRI(CRI), .CLI(CLI), .ComCLI(comparevalue_1_comcli),
    .ComCLE(comparevalue_1_comcle), .ComCRI(comparevalue_1_comcri), .ComCRE(comparevalue_1_comcre),
    .ComPIB(comparevalue_1_compib), .MarkForTransformation(comparevalue_1_markfortransformation),
    .CLI_2(comparevalue_1_cli_2), .CRI_2(comparevalue_1_cri_2), .CLE(comparevalue_1_cle),
    .CRE(comparevalue_1_cre), .PIB_2(comparevalue_1_pib_2));
  or or_20 (or_20_out, returnexpression_1_retpib, comparevalue_1_compib);
  assign controlled_buffer_20_out = comparevalue_1_compib ? comparevalue_1_pib_2 : 8'bz;  // Controlled_Buffer controlled_buffer_23
  or or_21 (or_21_out, or_13_out, comparevalue_1_comcre);
  assign controlled_buffer_4_out = comparevalue_1_comcre ? comparevalue_1_cre : 12'bz;  // Controlled_Buffer controlled_buffer_24
  or or_22 (or_22_out, or_18_out, comparevalue_1_comcri);
  assign controlled_buffer_1_out = comparevalue_1_comcri ? comparevalue_1_cri_2 : 8'bz;  // Controlled_Buffer controlled_buffer_25
  or or_23 (or_23_out, or_15_out, comparevalue_1_comcle);
  assign controlled_buffer_6_out = comparevalue_1_comcle ? comparevalue_1_cle : 12'bz;  // Controlled_Buffer controlled_buffer_26
  or or_24 (or_24_out, or_19_out, comparevalue_1_comcli);
  assign controlled_buffer_2_out = comparevalue_1_comcli ? comparevalue_1_cli_2 : 8'bz;  // Controlled_Buffer controlled_buffer_27
  or or_25 (or_25_out, or_20_out, immediateresolution_1_immpib);
  assign controlled_buffer_20_out = immediateresolution_1_immpib ? immediateresolution_1_out_3 : 8'bz;  // Controlled_Buffer controlled_buffer_28
  ImmediateResolution immediateresolution_1 (
    .ActivationSignal(decoder_1_out7), .ImmPIB(immediateresolution_1_immpib),
    .out_3(immediateresolution_1_out_3));
  PrepareForTransformationAsAncestorInput preparefortransformationasancestorinput_1 (
    .ActivationSignal(decoder_1_out8), .Clock(Clock), .SFS(SFS), .SBS(SBS), .RAM(RAM),
    .UniqueNodeID(UniqueNodeID), .CLI(CLI), .CRI(CRI), .CLE(CLE), .CRE(CRE),
    .InternalExpression(InternalExpression), .ptaRAM(preparefortransformationasancestorinput_1_ptaram),
    .ptaSFS(preparefortransformationasancestorinput_1_ptasfs),
    .ptaCLI(preparefortransformationasancestorinput_1_ptacli),
    .ptaCRI(preparefortransformationasancestorinput_1_ptacri),
    .ptaPEB(preparefortransformationasancestorinput_1_ptapeb),
    .ptaSEL(preparefortransformationasancestorinput_1_ptasel),
    .ptaSBS(preparefortransformationasancestorinput_1_ptasbs),
    .ptaStackClear(preparefortransformationasancestorinput_1_ptastackclear),
    .ptaPIB(preparefortransformationasancestorinput_1_ptapib),
    .GeneralOuput(preparefortransformationasancestorinput_1_generalouput),
    .PEB(preparefortransformationasancestorinput_1_peb),
    .CLI_2(preparefortransformationasancestorinput_1_cli_2),
    .CRI_2(preparefortransformationasancestorinput_1_cri_2),
    .PIB(preparefortransformationasancestorinput_1_pib));
  or or_26 (or_26_out, returnexpression_1_retpeb, preparefortransformationasancestorinput_1_ptapeb);
  assign controlled_buffer_19_out = preparefortransformationasancestorinput_1_ptapeb ? preparefortransformationasancestorinput_1_peb : 12'bz;  // Controlled_Buffer controlled_buffer_29
  or or_27 (or_27_out, or_25_out, preparefortransformationasancestorinput_1_ptapib);
  assign controlled_buffer_20_out = preparefortransformationasancestorinput_1_ptapib ? preparefortransformationasancestorinput_1_pib : 8'bz;  // Controlled_Buffer controlled_buffer_30
  or or_28 (or_28_out, or_22_out, preparefortransformationasancestorinput_1_ptacri);
  assign controlled_buffer_1_out = preparefortransformationasancestorinput_1_ptacri ? preparefortransformationasancestorinput_1_cri_2 : 8'bz;  // Controlled_Buffer controlled_buffer_31
  or or_29 (or_29_out, or_24_out, preparefortransformationasancestorinput_1_ptacli);
  assign controlled_buffer_2_out = preparefortransformationasancestorinput_1_ptacli ? preparefortransformationasancestorinput_1_cli_2 : 8'bz;  // Controlled_Buffer controlled_buffer_32
  or or_30 (or_30_out, or_5_out, preparefortransformationasancestorinput_1_ptastackclear);
  or or_31 (or_31_out, preparefortransformationasancestorinput_1_ptaram, preparefortransformationasancestorinput_1_ptasfs, preparefortransformationasancestorinput_1_ptasbs);
  assign controlled_buffer_33_out = or_31_out ? preparefortransformationasancestorinput_1_generalouput : 8'bz;  // Controlled_Buffer controlled_buffer_33
  or or_32 (or_32_out, preparefortransformationasancestorinput_1_ptasel, preparefortransformationasdecendantinput_1_ptdsel);
  or or_33 (or_33_out, preparefortransformationasancestorinput_1_ptasbs, preparefortransformationasdecendantinput_1_ptdsbs);
  or or_34 (or_34_out, preparefortransformationasancestorinput_1_ptasfs, preparefortransformationasdecendantinput_1_ptdsfs);
  or or_35 (or_35_out, preparefortransformationasancestorinput_1_ptaram, preparefortransformationasdecendantinput_1_ptdram);
  or or_36 (or_36_out, or_12_out, preparefortransformationasdecendantinput_1_ptdexp);
  PrepareForTransformationAsDecendantInput preparefortransformationasdecendantinput_1 (
    .ActivationSignal(decoder_1_out9), .Clock(Clock), .TransformMark(comparevalue_1_markfortransformation),
    .InExp(InternalExpression), .SFS(SFS), .SBS(SBS), .UniqueNodeID(UniqueNodeID), .RAM(RAM),
    .NewNodeID(NewNodeID), .PIB(PIB), .Buffer(Buffer), .PEB(PEB), .CLI(CLI), .CRI(CRI),
    .ptdCLC(preparefortransformationasdecendantinput_1_ptdclc),
    .ptdRAM(preparefortransformationasdecendantinput_1_ptdram),
    .ptdSFS(preparefortransformationasdecendantinput_1_ptdsfs), .PtdToggleChildren(NameToggleChildren),
    .ptdSEL(preparefortransformationasdecendantinput_1_ptdsel),
    .ptdNEW(preparefortransformationasdecendantinput_1_ptdnew), .PtdBUF(BufferWrite),
    .ptdCRI(preparefortransformationasdecendantinput_1_ptdcri),
    .ptdCLI(preparefortransformationasdecendantinput_1_ptdcli),
    .ptdCRE(preparefortransformationasdecendantinput_1_ptdcre),
    .ptdCLE(preparefortransformationasdecendantinput_1_ptdcle),
    .PtdEXP(preparefortransformationasdecendantinput_1_ptdexp),
    .ptdSBS(preparefortransformationasdecendantinput_1_ptdsbs),
    .ptdPIB(preparefortransformationasdecendantinput_1_ptdpib),
    .ptdCompareValueClear(preparefortransformationasdecendantinput_1_ptdcomparevalueclear),
    .ptdStackclear(preparefortransformationasdecendantinput_1_ptdstackclear),
    .Output(preparefortransformationasdecendantinput_1_output),
    .CLI_2(preparefortransformationasdecendantinput_1_cli_2),
    .CLE(preparefortransformationasdecendantinput_1_cle),
    .CRI_2(preparefortransformationasdecendantinput_1_cri_2),
    .CRE(preparefortransformationasdecendantinput_1_cre),
    .PIB_2(preparefortransformationasdecendantinput_1_pib_2),
    .NewExpression(preparefortransformationasdecendantinput_1_newexpression));
  assign RamSelect = and_1_out ? or_32_out : 1'bz;  // Controlled_Buffer controlled_buffer_34
  assign BackStack = and_1_out ? or_33_out : 1'bz;  // Controlled_Buffer controlled_buffer_35
  assign FrontStack = and_1_out ? or_34_out : 1'bz;  // Controlled_Buffer controlled_buffer_36
  assign RAMwrite = and_1_out ? or_35_out : 1'bz;  // Controlled_Buffer controlled_buffer_37
  assign EXPWrite = and_1_out ? or_36_out : 1'bz;  // Controlled_Buffer controlled_buffer_38
  assign NewNode = and_1_out ? preparefortransformationasdecendantinput_1_ptdnew : 1'bz;  // Controlled_Buffer controlled_buffer_39
  or or_37 (or_37_out, or_27_out, preparefortransformationasdecendantinput_1_ptdpib);
  assign controlled_buffer_20_out = preparefortransformationasdecendantinput_1_ptdpib ? preparefortransformationasdecendantinput_1_pib_2 : 8'bz;  // Controlled_Buffer controlled_buffer_40
  or or_38 (or_38_out, or_21_out, preparefortransformationasdecendantinput_1_ptdcre);
  assign controlled_buffer_4_out = preparefortransformationasdecendantinput_1_ptdcre ? preparefortransformationasdecendantinput_1_cre : 12'bz;  // Controlled_Buffer controlled_buffer_41
  or or_39 (or_39_out, or_28_out, preparefortransformationasdecendantinput_1_ptdcri);
  assign controlled_buffer_1_out = preparefortransformationasdecendantinput_1_ptdcri ? preparefortransformationasdecendantinput_1_cri_2 : 8'bz;  // Controlled_Buffer controlled_buffer_42
  or or_40 (or_40_out, or_23_out, preparefortransformationasdecendantinput_1_ptdcle);
  assign controlled_buffer_6_out = preparefortransformationasdecendantinput_1_ptdcle ? preparefortransformationasdecendantinput_1_cle : 12'bz;  // Controlled_Buffer controlled_buffer_43
  or or_41 (or_41_out, or_29_out, preparefortransformationasdecendantinput_1_ptdcli);
  assign controlled_buffer_2_out = preparefortransformationasdecendantinput_1_ptdcli ? preparefortransformationasdecendantinput_1_cli_2 : 8'bz;  // Controlled_Buffer controlled_buffer_44
  or or_42 (or_42_out, or_17_out, preparefortransformationasdecendantinput_1_ptdexp);
  assign controlled_buffer_3_out = preparefortransformationasdecendantinput_1_ptdexp ? preparefortransformationasdecendantinput_1_newexpression : 12'bz;  // Controlled_Buffer controlled_buffer_45
  or or_43 (or_43_out, or_30_out, preparefortransformationasdecendantinput_1_ptdcomparevalueclear);
  or or_44 (or_44_out, preparefortransformationasdecendantinput_1_ptdram, preparefortransformationasdecendantinput_1_ptdsfs, preparefortransformationasdecendantinput_1_ptdsbs, BufferWrite);
  not not_2 (not_2_out, or_26_out);
  not not_3 (not_3_out, or_37_out);
  not not_4 (not_4_out, or_38_out);
  not not_5 (not_5_out, or_39_out);
  not not_6 (not_6_out, or_40_out);
  not not_7 (not_7_out, or_41_out);
  not not_8 (not_8_out, or_42_out);
  or or_45 (or_45_out, or_31_out, or_44_out);
  assign controlled_buffer_33_out = or_44_out ? preparefortransformationasdecendantinput_1_output : 8'bz;  // Controlled_Buffer controlled_buffer_46
  assign controlled_buffer_19_out = not_2_out ? InternalExpression : 12'bz;  // Controlled_Buffer controlled_buffer_47
  assign controlled_buffer_20_out = not_3_out ? {8{1'b0}} : 8'bz;  // Controlled_Buffer controlled_buffer_48
  assign controlled_buffer_4_out = not_4_out ? {12{1'b0}} : 12'bz;  // Controlled_Buffer controlled_buffer_49
  assign controlled_buffer_1_out = not_5_out ? {8{1'b0}} : 8'bz;  // Controlled_Buffer controlled_buffer_50
  assign controlled_buffer_6_out = not_6_out ? {12{1'b0}} : 12'bz;  // Controlled_Buffer controlled_buffer_51
  assign controlled_buffer_2_out = not_7_out ? {8{1'b0}} : 8'bz;  // Controlled_Buffer controlled_buffer_52
  assign controlled_buffer_3_out = not_8_out ? {12{1'b0}} : 12'bz;  // Controlled_Buffer controlled_buffer_53
  not not_9 (not_9_out, or_45_out);
  assign controlled_buffer_33_out = not_9_out ? {8{1'b0}} : 8'bz;  // Controlled_Buffer controlled_buffer_54
  assign ClearChidlren = and_1_out ? preparefortransformationasdecendantinput_1_ptdclc : 1'bz;  // Controlled_Buffer controlled_buffer_55
  assign PEB_2 = and_1_out ? controlled_buffer_19_out : 12'bz;  // Controlled_Buffer controlled_buffer_56
  assign PIB_2 = and_1_out ? controlled_buffer_20_out : 8'bz;  // Controlled_Buffer controlled_buffer_57
  assign CRE_2 = and_1_out ? controlled_buffer_4_out : 12'bz;  // Controlled_Buffer controlled_buffer_58
  assign CRI_2 = and_1_out ? controlled_buffer_1_out : 8'bz;  // Controlled_Buffer controlled_buffer_59
  assign CLE_2 = and_1_out ? controlled_buffer_6_out : 12'bz;  // Controlled_Buffer controlled_buffer_60
  assign CLI_2 = and_1_out ? controlled_buffer_2_out : 8'bz;  // Controlled_Buffer controlled_buffer_61
  assign NewNode_2 = and_1_out ? controlled_buffer_3_out : 12'bz;  // Controlled_Buffer controlled_buffer_62
  assign GeneralOutput = and_1_out ? controlled_buffer_33_out : 8'bz;  // Controlled_Buffer controlled_buffer_63
  assign StackClear = and_1_out ? or_43_out : 1'bz;  // Controlled_Buffer controlled_buffer_64

  // Notes on the sheet:
  //   Input
  //   0 == Backstack / 1 == Frontstack
  //   Output
endmodule
module GoToExpression (
  input  [11:0] PEB,
  input  [7:0] PIB,
  input  [11:0] CRE,
  input  [7:0] CRI,
  input  [11:0] CLE,
  input  [7:0] CLI,
  input  [3:0] SFS,
  input  [3:0] SBS,
  input  [3:0] RAM,
  input  [11:0] InternalExpression,
  input  [2:0] Buffer,
  input  Clock,
  input  [3:0] NewNodeID,
  input  [3:0] UniqueNodeID,
  output EXPWrite,
  output RamSelect,
  output FrontStack,
  output BackStack,
  output RAMwrite,
  output NewNode,
  output [11:0] PEB_2,
  output [7:0] PIB_2,
  output [11:0] CRE_2,
  output [7:0] CRI_2,
  output [11:0] CLE_2,
  output [7:0] CLI_2,
  output [11:0] NewNode_2,
  output [7:0] GeneralOutput,
  output ClearChidlren,
  output StackClear
);

  wire and_1_out, decoder_1_out1, decoder_1_out2, decoder_1_out3, decoder_1_out4, decoder_1_out5, not_2_out,
       not_3_out, not_4_out, not_5_out, not_6_out, not_7_out, not_8_out, nullification_1_nullcli,
       nullification_1_nullcri, nullification_1_nullexp, nullification_1_nullstackclear, or_1_out, or_2_out,
       or_3_out, or_4_out, or_5_out, or_6_out, or_7_out, or_8_out, or_9_out, or_10_out, or_11_out, or_12_out,
       or_13_out, or_14_out, or_15_out, or_16_out, or_17_out, or_18_out, or_19_out,
       returnexpression_1_retcli, returnexpression_1_retcri, returnexpression_1_retpeb,
       returnexpression_1_retpib, updateexpression_1_updcle, updateexpression_1_updcli,
       updateexpression_1_updcre, updateexpression_1_updcri, updateexpression_1_updexp,
       updateexpression_1_updstackclear, updatepointerleft_1_updcle, updatepointerleft_1_updcli,
       updatepointerleft_1_updcre, updatepointerleft_1_updcri, updatepointerleft_1_updexp,
       updatepointerright_1_updcle, updatepointerright_1_updcli, updatepointerright_1_updcre,
       updatepointerright_1_updcri, updatepointerright_1_updexp;
  wire [2:0] not_1_out, xor_1_out;
  wire [7:0] controlled_buffer_1_out, controlled_buffer_2_out, controlled_buffer_20_out, nullification_1_cli,
       nullification_1_cri, returnexpression_1_cli_2, returnexpression_1_cri_2, returnexpression_1_pib_2,
       updateexpression_1_cli, updateexpression_1_cri, updatepointerleft_1_cli, updatepointerleft_1_cri,
       updatepointerright_1_cli, updatepointerright_1_cri;
  wire [11:0] controlled_buffer_3_out, controlled_buffer_4_out, controlled_buffer_6_out,
       controlled_buffer_19_out, nullification_1_newvalue, returnexpression_1_peb, updateexpression_1_cle,
       updateexpression_1_cre, updateexpression_1_newvalue, updatepointerleft_1_cle, updatepointerleft_1_cre,
       updatepointerleft_1_newvalue, updatepointerright_1_cli_2, updatepointerright_1_cri_2,
       updatepointerright_1_newvalue;

  Decoder #(.select(4)) decoder_1 (
    .out1(decoder_1_out1), .out2(decoder_1_out2), .out3(decoder_1_out3), .out4(decoder_1_out4),
    .out5(decoder_1_out5), .sel(PIB[7:4]));  // open: out0, out6, out7, out8, out9, out10, out11, out12, out13, out14, out15, en
  Nullification nullification_1 (
    .ActivationSignal(decoder_1_out1), .Clock(Clock), .NullCLI(nullification_1_nullcli),
    .NullCRI(nullification_1_nullcri), .NullStackClear(nullification_1_nullstackclear),
    .NullEXP(nullification_1_nullexp), .CRI(nullification_1_cri), .CLI(nullification_1_cli),
    .NewValue(nullification_1_newvalue));
  assign controlled_buffer_1_out = nullification_1_nullcli ? nullification_1_cri : 8'bz;  // Controlled_Buffer controlled_buffer_1
  assign controlled_buffer_2_out = nullification_1_nullcri ? nullification_1_cli : 8'bz;  // Controlled_Buffer controlled_buffer_2
  assign controlled_buffer_3_out = nullification_1_nullexp ? nullification_1_newvalue : 12'bz;  // Controlled_Buffer controlled_buffer_3
  UpdateExpression updateexpression_1 (
    .ActivationSignal(decoder_1_out2), .Clock(Clock), .UniqueNodeID(UniqueNodeID), .PIB(PIB), .PEB(PEB),
    .UpdCLE(updateexpression_1_updcle), .UpdCRE(updateexpression_1_updcre),
    .UpdCLI(updateexpression_1_updcli), .UpdCRI(updateexpression_1_updcri),
    .UpdStackClear(updateexpression_1_updstackclear), .UpdEXP(updateexpression_1_updexp),
    .CRI(updateexpression_1_cri), .CLI(updateexpression_1_cli), .CRE(updateexpression_1_cre),
    .CLE(updateexpression_1_cle), .NewValue(updateexpression_1_newvalue));
  assign not_1_out = ~xor_1_out;  // NOT_Gate not_1, 3 bits wide
  assign xor_1_out = InternalExpression[10:8] ^ 3'b100;  // XOR_Gate xor_1, 3 bits wide
  or or_1 (or_1_out, nullification_1_nullexp, updateexpression_1_updexp);
  assign controlled_buffer_4_out = updateexpression_1_updcre ? updateexpression_1_cre : 12'bz;  // Controlled_Buffer controlled_buffer_4
  or or_2 (or_2_out, nullification_1_nullcli, updateexpression_1_updcri);
  assign controlled_buffer_1_out = updateexpression_1_updcri ? updateexpression_1_cri : 8'bz;  // Controlled_Buffer controlled_buffer_5
  assign controlled_buffer_6_out = updateexpression_1_updcle ? updateexpression_1_cle : 12'bz;  // Controlled_Buffer controlled_buffer_6
  or or_3 (or_3_out, nullification_1_nullcri, updateexpression_1_updcli);
  assign controlled_buffer_2_out = updateexpression_1_updcli ? updateexpression_1_cli : 8'bz;  // Controlled_Buffer controlled_buffer_7
  or or_4 (or_4_out, nullification_1_nullexp, updateexpression_1_updexp);
  assign controlled_buffer_3_out = updateexpression_1_updexp ? updateexpression_1_newvalue : 12'bz;  // Controlled_Buffer controlled_buffer_8
  or or_5 (or_5_out, nullification_1_nullstackclear, updateexpression_1_updstackclear);
  and and_1 (and_1_out, not_1_out[0], not_1_out[1], not_1_out[2]);
  UpdatePointerLeft updatepointerleft_1 (
    .ActivationSignal(decoder_1_out3), .Clock(Clock), .UniqueNodeID(UniqueNodeID), .PIB(PIB),
    .InternalExpression(InternalExpression), .PEB(PEB), .UpdCLE(updatepointerleft_1_updcle),
    .UpdCRE(updatepointerleft_1_updcre), .UpdCLI(updatepointerleft_1_updcli),
    .UpdCRI(updatepointerleft_1_updcri), .UpdEXP(updatepointerleft_1_updexp), .CRI(updatepointerleft_1_cri),
    .CLI(updatepointerleft_1_cli), .CRE(updatepointerleft_1_cre), .CLE(updatepointerleft_1_cle),
    .NewValue(updatepointerleft_1_newvalue));
  or or_6 (or_6_out, or_1_out, updatepointerleft_1_updexp);
  or or_7 (or_7_out, updateexpression_1_updcre, updatepointerleft_1_updcre);
  assign controlled_buffer_4_out = updatepointerleft_1_updcre ? updatepointerleft_1_cre : 12'bz;  // Controlled_Buffer controlled_buffer_9
  or or_8 (or_8_out, or_2_out, updatepointerleft_1_updcri);
  assign controlled_buffer_1_out = updatepointerleft_1_updcri ? updatepointerleft_1_cri : 8'bz;  // Controlled_Buffer controlled_buffer_10
  or or_9 (or_9_out, updateexpression_1_updcle, updatepointerleft_1_updcle);
  assign controlled_buffer_6_out = updatepointerleft_1_updcle ? updatepointerleft_1_cle : 12'bz;  // Controlled_Buffer controlled_buffer_11
  or or_10 (or_10_out, or_3_out, updatepointerleft_1_updcli);
  assign controlled_buffer_2_out = updatepointerleft_1_updcli ? updatepointerleft_1_cli : 8'bz;  // Controlled_Buffer controlled_buffer_12
  or or_11 (or_11_out, or_4_out, updatepointerleft_1_updexp);
  assign controlled_buffer_3_out = updatepointerleft_1_updexp ? updatepointerleft_1_newvalue : 12'bz;  // Controlled_Buffer controlled_buffer_13
  UpdatePointerRight updatepointerright_1 (
    .ActivationSignal(decoder_1_out4), .Clock(Clock), .UniqueNodeID(UniqueNodeID), .PIB(PIB),
    .InternalExpression(InternalExpression), .PEB(PEB), .UpdCLE(updatepointerright_1_updcle),
    .UpdCRE(updatepointerright_1_updcre), .UpdCLI(updatepointerright_1_updcli),
    .UpdCRI(updatepointerright_1_updcri), .UpdEXP(updatepointerright_1_updexp),
    .CRI(updatepointerright_1_cri), .CLI(updatepointerright_1_cli), .CRI_2(updatepointerright_1_cri_2),
    .CLI_2(updatepointerright_1_cli_2), .NewValue(updatepointerright_1_newvalue));
  or or_12 (or_12_out, or_6_out, updatepointerright_1_updexp);
  or or_13 (or_13_out, or_7_out, updatepointerright_1_updcre);
  assign controlled_buffer_4_out = updatepointerright_1_updcre ? updatepointerright_1_cri_2 : 12'bz;  // Controlled_Buffer controlled_buffer_14
  or or_14 (or_14_out, or_8_out, updatepointerright_1_updcri);
  assign controlled_buffer_1_out = updatepointerright_1_updcri ? updatepointerright_1_cri : 8'bz;  // Controlled_Buffer controlled_buffer_15
  or or_15 (or_15_out, or_9_out, updatepointerright_1_updcle);
  assign controlled_buffer_6_out = updatepointerright_1_updcle ? updatepointerright_1_cli_2 : 12'bz;  // Controlled_Buffer controlled_buffer_16
  or or_16 (or_16_out, or_10_out, updatepointerright_1_updcli);
  assign controlled_buffer_2_out = updatepointerright_1_updcli ? updatepointerright_1_cli : 8'bz;  // Controlled_Buffer controlled_buffer_17
  or or_17 (or_17_out, or_11_out, updatepointerright_1_updexp);
  assign controlled_buffer_3_out = updatepointerright_1_updexp ? updatepointerright_1_newvalue : 12'bz;  // Controlled_Buffer controlled_buffer_18
  assign controlled_buffer_19_out = returnexpression_1_retpeb ? returnexpression_1_peb : 12'bz;  // Controlled_Buffer controlled_buffer_19
  assign controlled_buffer_20_out = returnexpression_1_retpib ? returnexpression_1_pib_2 : 8'bz;  // Controlled_Buffer controlled_buffer_20
  or or_18 (or_18_out, or_14_out, returnexpression_1_retcri);
  assign controlled_buffer_1_out = returnexpression_1_retcri ? returnexpression_1_cri_2 : 8'bz;  // Controlled_Buffer controlled_buffer_21
  ReturnExpression returnexpression_1 (
    .ActivationSignal(decoder_1_out5), .UniqueNodeID(UniqueNodeID), .PIB(PIB), .CLI(CLI), .CRI(CRI),
    .CRE(CRE), .CLE(CLE), .InternalExpression(InternalExpression), .RetCLI(returnexpression_1_retcli),
    .RetCRI(returnexpression_1_retcri), .RetPIB(returnexpression_1_retpib),
    .RetPEB(returnexpression_1_retpeb), .CRI_2(returnexpression_1_cri_2), .CLI_2(returnexpression_1_cli_2),
    .PEB(returnexpression_1_peb), .PIB_2(returnexpression_1_pib_2));
  assign RamSelect = and_1_out ? 1'b0 : 1'bz;  // Controlled_Buffer controlled_buffer_22
  assign BackStack = and_1_out ? 1'b0 : 1'bz;  // Controlled_Buffer controlled_buffer_23
  assign FrontStack = and_1_out ? 1'b0 : 1'bz;  // Controlled_Buffer controlled_buffer_24
  assign RAMwrite = and_1_out ? 1'b0 : 1'bz;  // Controlled_Buffer controlled_buffer_25
  assign EXPWrite = and_1_out ? or_12_out : 1'bz;  // Controlled_Buffer controlled_buffer_26
  assign NewNode = and_1_out ? 1'b0 : 1'bz;  // Controlled_Buffer controlled_buffer_27
  or or_19 (or_19_out, or_16_out, returnexpression_1_retcli);
  assign controlled_buffer_2_out = returnexpression_1_retcli ? returnexpression_1_cli_2 : 8'bz;  // Controlled_Buffer controlled_buffer_28
  not not_2 (not_2_out, returnexpression_1_retpeb);
  assign controlled_buffer_19_out = not_2_out ? CRE : 12'bz;  // Controlled_Buffer controlled_buffer_29
  not not_3 (not_3_out, returnexpression_1_retpib);
  assign controlled_buffer_20_out = not_3_out ? CRI : 8'bz;  // Controlled_Buffer controlled_buffer_30
  not not_4 (not_4_out, or_13_out);
  assign controlled_buffer_4_out = not_4_out ? PEB : 12'bz;  // Controlled_Buffer controlled_buffer_31
  not not_5 (not_5_out, or_18_out);
  assign controlled_buffer_1_out = not_5_out ? PIB : 8'bz;  // Controlled_Buffer controlled_buffer_32
  not not_6 (not_6_out, or_15_out);
  assign controlled_buffer_6_out = not_6_out ? {12{1'b0}} : 12'bz;  // Controlled_Buffer controlled_buffer_33
  not not_7 (not_7_out, or_19_out);
  assign controlled_buffer_2_out = not_7_out ? {8{1'b0}} : 8'bz;  // Controlled_Buffer controlled_buffer_34
  not not_8 (not_8_out, or_17_out);
  assign controlled_buffer_3_out = not_8_out ? {12{1'b0}} : 12'bz;  // Controlled_Buffer controlled_buffer_35
  assign ClearChidlren = and_1_out ? 1'b0 : 1'bz;  // Controlled_Buffer controlled_buffer_36
  assign StackClear = and_1_out ? or_5_out : 1'bz;  // Controlled_Buffer controlled_buffer_37
  assign PEB_2 = and_1_out ? controlled_buffer_19_out : 12'bz;  // Controlled_Buffer controlled_buffer_38
  assign PIB_2 = and_1_out ? controlled_buffer_20_out : 8'bz;  // Controlled_Buffer controlled_buffer_39
  assign CRE_2 = and_1_out ? controlled_buffer_4_out : 12'bz;  // Controlled_Buffer controlled_buffer_40
  assign CRI_2 = and_1_out ? controlled_buffer_1_out : 8'bz;  // Controlled_Buffer controlled_buffer_41
  assign CLE_2 = and_1_out ? controlled_buffer_6_out : 12'bz;  // Controlled_Buffer controlled_buffer_42
  assign CLI_2 = and_1_out ? controlled_buffer_2_out : 8'bz;  // Controlled_Buffer controlled_buffer_43
  assign NewNode_2 = and_1_out ? controlled_buffer_3_out : 12'bz;  // Controlled_Buffer controlled_buffer_44
  assign GeneralOutput = and_1_out ? {8{1'b0}} : 8'bz;  // Controlled_Buffer controlled_buffer_45

  // Notes on the sheet:
  //   Input
  //   0 == Backstack / 1 == Frontstack
  //   Output
endmodule

module ApplicationExpression (
  input  [11:0] PEB,
  input  [7:0] PIB,
  input  [11:0] CRE,
  input  [7:0] CRI,
  input  [11:0] CLE,
  input  [7:0] CLI,
  input  [3:0] SFS,
  input  [3:0] SBS,
  input  [3:0] RAM,
  input  [11:0] InternalExpression,
  input  [2:0] Buffer,
  input  Clock,
  input  [3:0] NewNodeID,
  input  [3:0] UniqueNodeID,
  output EXPWrite,
  output RamSelect,
  output FrontStack,
  output BackStack,
  output RAMwrite,
  output NewNode,
  output [11:0] PEB_2,
  output [7:0] PIB_2,
  output [11:0] CRE_2,
  output [7:0] CRI_2,
  output [11:0] CLE_2,
  output [7:0] CLI_2,
  output [11:0] NewNode_2,
  output [7:0] GeneralOutput,
  output ClearChidlren,
  output StackClear
);

  wire and_1_out, branchchop_1_branew, comparevalue_1_comcle, comparevalue_1_comcli, comparevalue_1_comcre,
       comparevalue_1_comcri, comparevalue_1_compib, comparevalue_1_markfortransformation, decoder_1_out1,
       decoder_1_out2, decoder_1_out3, decoder_1_out4, decoder_1_out5, decoder_1_out6, decoder_1_out9,
       not_2_out, not_3_out, not_4_out, not_5_out, not_6_out, not_7_out, not_8_out, not_9_out,
       nullification_1_nullcli, nullification_1_nullcri, nullification_1_nullexp,
       nullification_1_nullstackclear, or_1_out, or_2_out, or_3_out, or_4_out, or_5_out, or_6_out, or_7_out,
       or_8_out, or_9_out, or_10_out, or_11_out, or_12_out, or_13_out, or_14_out, or_15_out, or_16_out,
       or_17_out, or_18_out, or_19_out, or_20_out, or_21_out, or_22_out, or_23_out, or_24_out, or_25_out,
       or_26_out, or_27_out, or_28_out, or_29_out, or_30_out, or_31_out, or_32_out, or_33_out, or_34_out,
       preparefortransformationasdecendantinput_1_ptdbuf, preparefortransformationasdecendantinput_1_ptdclc,
       preparefortransformationasdecendantinput_1_ptdcle, preparefortransformationasdecendantinput_1_ptdcli,
       preparefortransformationasdecendantinput_1_ptdcomparevalueclear,
       preparefortransformationasdecendantinput_1_ptdcre, preparefortransformationasdecendantinput_1_ptdcri,
       preparefortransformationasdecendantinput_1_ptdexp, preparefortransformationasdecendantinput_1_ptdnew,
       preparefortransformationasdecendantinput_1_ptdpib, preparefortransformationasdecendantinput_1_ptdram,
       preparefortransformationasdecendantinput_1_ptdsbs, preparefortransformationasdecendantinput_1_ptdsel,
       preparefortransformationasdecendantinput_1_ptdsfs,
       preparefortransformationasdecendantinput_1_ptdstackclear, returnexpression_1_retcli,
       returnexpression_1_retcri, returnexpression_1_retpeb, returnexpression_1_retpib,
       updateexpression_1_updcle, updateexpression_1_updcli, updateexpression_1_updcre,
       updateexpression_1_updcri, updateexpression_1_updexp, updateexpression_1_updstackclear,
       updatepointerleft_1_updcle, updatepointerleft_1_updcli, updatepointerleft_1_updcre,
       updatepointerleft_1_updcri, updatepointerleft_1_updexp, updatepointerright_1_updcle,
       updatepointerright_1_updcli, updatepointerright_1_updcre, updatepointerright_1_updcri,
       updatepointerright_1_updexp;
  wire [2:0] not_1_out, xor_1_out;
  wire [7:0] comparevalue_1_cli_2, comparevalue_1_cri_2, comparevalue_1_pib_2, controlled_buffer_1_out,
       controlled_buffer_2_out, controlled_buffer_20_out, controlled_buffer_40_out, nullification_1_cli,
       nullification_1_cri, preparefortransformationasdecendantinput_1_cli_2,
       preparefortransformationasdecendantinput_1_cri_2, preparefortransformationasdecendantinput_1_output,
       preparefortransformationasdecendantinput_1_pib_2, returnexpression_1_cli_2, returnexpression_1_cri_2,
       returnexpression_1_pib_2, updateexpression_1_cli, updateexpression_1_cri, updatepointerleft_1_cli,
       updatepointerleft_1_cri, updatepointerright_1_cli, updatepointerright_1_cri;
  wire [11:0] branchchop_1_newvalue, comparevalue_1_cle, comparevalue_1_cre, controlled_buffer_3_out,
       controlled_buffer_4_out, controlled_buffer_6_out, controlled_buffer_19_out, nullification_1_newvalue,
       preparefortransformationasdecendantinput_1_cle, preparefortransformationasdecendantinput_1_cre,
       preparefortransformationasdecendantinput_1_newexpression, returnexpression_1_peb,
       updateexpression_1_cle, updateexpression_1_cre, updateexpression_1_newvalue, updatepointerleft_1_cle,
       updatepointerleft_1_cre, updatepointerleft_1_newvalue, updatepointerright_1_cli_2,
       updatepointerright_1_cri_2, updatepointerright_1_newvalue;

  Decoder #(.select(4)) decoder_1 (
    .out1(decoder_1_out1), .out2(decoder_1_out2), .out3(decoder_1_out3), .out4(decoder_1_out4),
    .out5(decoder_1_out5), .out6(decoder_1_out6), .out9(decoder_1_out9), .sel(PIB[7:4]));  // open: out0, out7, out8, out10, out11, out12, out13, out14, out15, en
  Nullification nullification_1 (
    .ActivationSignal(decoder_1_out1), .Clock(Clock), .NullCLI(nullification_1_nullcli),
    .NullCRI(nullification_1_nullcri), .NullStackClear(nullification_1_nullstackclear),
    .NullEXP(nullification_1_nullexp), .CRI(nullification_1_cri), .CLI(nullification_1_cli),
    .NewValue(nullification_1_newvalue));
  assign controlled_buffer_1_out = nullification_1_nullcli ? nullification_1_cri : 8'bz;  // Controlled_Buffer controlled_buffer_1
  assign controlled_buffer_2_out = nullification_1_nullcri ? nullification_1_cli : 8'bz;  // Controlled_Buffer controlled_buffer_2
  assign controlled_buffer_3_out = nullification_1_nullexp ? nullification_1_newvalue : 12'bz;  // Controlled_Buffer controlled_buffer_3
  UpdateExpression updateexpression_1 (
    .ActivationSignal(decoder_1_out2), .Clock(Clock), .UniqueNodeID(UniqueNodeID), .PIB(PIB), .PEB(PEB),
    .UpdCLE(updateexpression_1_updcle), .UpdCRE(updateexpression_1_updcre),
    .UpdCLI(updateexpression_1_updcli), .UpdCRI(updateexpression_1_updcri),
    .UpdStackClear(updateexpression_1_updstackclear), .UpdEXP(updateexpression_1_updexp),
    .CRI(updateexpression_1_cri), .CLI(updateexpression_1_cli), .CRE(updateexpression_1_cre),
    .CLE(updateexpression_1_cle), .NewValue(updateexpression_1_newvalue));
  assign xor_1_out = InternalExpression[10:8] ^ 3'b010;  // XOR_Gate xor_1, 3 bits wide
  assign not_1_out = ~xor_1_out;  // NOT_Gate not_1, 3 bits wide
  or or_1 (or_1_out, nullification_1_nullexp, updateexpression_1_updexp);
  assign controlled_buffer_4_out = updateexpression_1_updcre ? updateexpression_1_cre : 12'bz;  // Controlled_Buffer controlled_buffer_4
  or or_2 (or_2_out, nullification_1_nullcli, updateexpression_1_updcri);
  assign controlled_buffer_1_out = updateexpression_1_updcri ? updateexpression_1_cri : 8'bz;  // Controlled_Buffer controlled_buffer_5
  assign controlled_buffer_6_out = updateexpression_1_updcle ? updateexpression_1_cle : 12'bz;  // Controlled_Buffer controlled_buffer_6
  or or_3 (or_3_out, nullification_1_nullcri, updateexpression_1_updcli);
  assign controlled_buffer_2_out = updateexpression_1_updcli ? updateexpression_1_cli : 8'bz;  // Controlled_Buffer controlled_buffer_7
  or or_4 (or_4_out, nullification_1_nullexp, updateexpression_1_updexp);
  assign controlled_buffer_3_out = updateexpression_1_updexp ? updateexpression_1_newvalue : 12'bz;  // Controlled_Buffer controlled_buffer_8
  or or_5 (or_5_out, nullification_1_nullstackclear, updateexpression_1_updstackclear);
  and and_1 (and_1_out, not_1_out[0], not_1_out[1], not_1_out[2]);
  UpdatePointerLeft updatepointerleft_1 (
    .ActivationSignal(decoder_1_out3), .Clock(Clock), .UniqueNodeID(UniqueNodeID), .PIB(PIB),
    .InternalExpression(InternalExpression), .PEB(PEB), .UpdCLE(updatepointerleft_1_updcle),
    .UpdCRE(updatepointerleft_1_updcre), .UpdCLI(updatepointerleft_1_updcli),
    .UpdCRI(updatepointerleft_1_updcri), .UpdEXP(updatepointerleft_1_updexp), .CRI(updatepointerleft_1_cri),
    .CLI(updatepointerleft_1_cli), .CRE(updatepointerleft_1_cre), .CLE(updatepointerleft_1_cle),
    .NewValue(updatepointerleft_1_newvalue));
  or or_6 (or_6_out, or_1_out, updatepointerleft_1_updexp);
  or or_7 (or_7_out, updateexpression_1_updcre, updatepointerleft_1_updcre);
  assign controlled_buffer_4_out = updatepointerleft_1_updcre ? updatepointerleft_1_cre : 12'bz;  // Controlled_Buffer controlled_buffer_9
  or or_8 (or_8_out, or_2_out, updatepointerleft_1_updcri);
  assign controlled_buffer_1_out = updatepointerleft_1_updcri ? updatepointerleft_1_cri : 8'bz;  // Controlled_Buffer controlled_buffer_10
  or or_9 (or_9_out, updateexpression_1_updcle, updatepointerleft_1_updcle);
  assign controlled_buffer_6_out = updatepointerleft_1_updcle ? updatepointerleft_1_cle : 12'bz;  // Controlled_Buffer controlled_buffer_11
  or or_10 (or_10_out, or_3_out, updatepointerleft_1_updcli);
  assign controlled_buffer_2_out = updatepointerleft_1_updcli ? updatepointerleft_1_cli : 8'bz;  // Controlled_Buffer controlled_buffer_12
  or or_11 (or_11_out, or_4_out, updatepointerleft_1_updexp);
  assign controlled_buffer_3_out = updatepointerleft_1_updexp ? updatepointerleft_1_newvalue : 12'bz;  // Controlled_Buffer controlled_buffer_13
  UpdatePointerRight updatepointerright_1 (
    .ActivationSignal(decoder_1_out4), .Clock(Clock), .UniqueNodeID(UniqueNodeID), .PIB(PIB),
    .InternalExpression(InternalExpression), .PEB(PEB), .UpdCLE(updatepointerright_1_updcle),
    .UpdCRE(updatepointerright_1_updcre), .UpdCLI(updatepointerright_1_updcli),
    .UpdCRI(updatepointerright_1_updcri), .UpdEXP(updatepointerright_1_updexp),
    .CRI(updatepointerright_1_cri), .CLI(updatepointerright_1_cli), .CRI_2(updatepointerright_1_cri_2),
    .CLI_2(updatepointerright_1_cli_2), .NewValue(updatepointerright_1_newvalue));
  or or_12 (or_12_out, or_6_out, updatepointerright_1_updexp);
  or or_13 (or_13_out, or_7_out, updatepointerright_1_updcre);
  assign controlled_buffer_4_out = updatepointerright_1_updcre ? updatepointerright_1_cri_2 : 12'bz;  // Controlled_Buffer controlled_buffer_14
  or or_14 (or_14_out, or_8_out, updatepointerright_1_updcri);
  assign controlled_buffer_1_out = updatepointerright_1_updcri ? updatepointerright_1_cri : 8'bz;  // Controlled_Buffer controlled_buffer_15
  or or_15 (or_15_out, or_9_out, updatepointerright_1_updcle);
  assign controlled_buffer_6_out = updatepointerright_1_updcle ? updatepointerright_1_cli_2 : 12'bz;  // Controlled_Buffer controlled_buffer_16
  or or_16 (or_16_out, or_10_out, updatepointerright_1_updcli);
  assign controlled_buffer_2_out = updatepointerright_1_updcli ? updatepointerright_1_cli : 8'bz;  // Controlled_Buffer controlled_buffer_17
  or or_17 (or_17_out, or_11_out, updatepointerright_1_updexp);
  assign controlled_buffer_3_out = updatepointerright_1_updexp ? updatepointerright_1_newvalue : 12'bz;  // Controlled_Buffer controlled_buffer_18
  assign controlled_buffer_19_out = returnexpression_1_retpeb ? returnexpression_1_peb : 12'bz;  // Controlled_Buffer controlled_buffer_19
  assign controlled_buffer_20_out = returnexpression_1_retpib ? returnexpression_1_pib_2 : 8'bz;  // Controlled_Buffer controlled_buffer_20
  or or_18 (or_18_out, or_14_out, returnexpression_1_retcri);
  assign controlled_buffer_1_out = returnexpression_1_retcri ? returnexpression_1_cri_2 : 8'bz;  // Controlled_Buffer controlled_buffer_21
  ReturnExpression returnexpression_1 (
    .ActivationSignal(decoder_1_out5), .UniqueNodeID(UniqueNodeID), .PIB(PIB), .CLI(CLI), .CRI(CRI),
    .CRE(CRE), .CLE(CLE), .InternalExpression(InternalExpression), .RetCLI(returnexpression_1_retcli),
    .RetCRI(returnexpression_1_retcri), .RetPIB(returnexpression_1_retpib),
    .RetPEB(returnexpression_1_retpeb), .CRI_2(returnexpression_1_cri_2), .CLI_2(returnexpression_1_cli_2),
    .PEB(returnexpression_1_peb), .PIB_2(returnexpression_1_pib_2));
  or or_19 (or_19_out, or_16_out, returnexpression_1_retcli);
  assign controlled_buffer_2_out = returnexpression_1_retcli ? returnexpression_1_cli_2 : 8'bz;  // Controlled_Buffer controlled_buffer_22
  CompareValue comparevalue_1 (
    .ActivationSignal(decoder_1_out6), .Clock(Clock),
    .Clear(preparefortransformationasdecendantinput_1_ptdstackclear), .InternalValue(InternalExpression),
    .PEB(PEB), .PIB(PIB), .CRI(CRI), .CLI(CLI), .ComCLI(comparevalue_1_comcli),
    .ComCLE(comparevalue_1_comcle), .ComCRI(comparevalue_1_comcri), .ComCRE(comparevalue_1_comcre),
    .ComPIB(comparevalue_1_compib), .MarkForTransformation(comparevalue_1_markfortransformation),
    .CLI_2(comparevalue_1_cli_2), .CRI_2(comparevalue_1_cri_2), .CLE(comparevalue_1_cle),
    .CRE(comparevalue_1_cre), .PIB_2(comparevalue_1_pib_2));
  or or_20 (or_20_out, returnexpression_1_retpib, comparevalue_1_compib);
  assign controlled_buffer_20_out = comparevalue_1_compib ? comparevalue_1_pib_2 : 8'bz;  // Controlled_Buffer controlled_buffer_23
  or or_21 (or_21_out, or_13_out, comparevalue_1_comcre);
  assign controlled_buffer_4_out = comparevalue_1_comcre ? comparevalue_1_cre : 12'bz;  // Controlled_Buffer controlled_buffer_24
  or or_22 (or_22_out, or_18_out, comparevalue_1_comcri);
  assign controlled_buffer_1_out = comparevalue_1_comcri ? comparevalue_1_cri_2 : 8'bz;  // Controlled_Buffer controlled_buffer_25
  or or_23 (or_23_out, or_15_out, comparevalue_1_comcle);
  assign controlled_buffer_6_out = comparevalue_1_comcle ? comparevalue_1_cle : 12'bz;  // Controlled_Buffer controlled_buffer_26
  or or_24 (or_24_out, or_19_out, comparevalue_1_comcli);
  assign controlled_buffer_2_out = comparevalue_1_comcli ? comparevalue_1_cli_2 : 8'bz;  // Controlled_Buffer controlled_buffer_27
  or or_25 (or_25_out, or_12_out, preparefortransformationasdecendantinput_1_ptdexp);
  or or_26 (or_26_out, or_20_out, preparefortransformationasdecendantinput_1_ptdpib);
  assign controlled_buffer_20_out = preparefortransformationasdecendantinput_1_ptdpib ? preparefortransformationasdecendantinput_1_pib_2 : 8'bz;  // Controlled_Buffer controlled_buffer_28
  or or_27 (or_27_out, or_21_out, preparefortransformationasdecendantinput_1_ptdcre);
  assign controlled_buffer_4_out = preparefortransformationasdecendantinput_1_ptdcre ? preparefortransformationasdecendantinput_1_cre : 12'bz;  // Controlled_Buffer controlled_buffer_29
  PrepareForTransformationAsDecendantInput preparefortransformationasdecendantinput_1 (
    .ActivationSignal(decoder_1_out9), .Clock(Clock), .TransformMark(comparevalue_1_markfortransformation),
    .InExp(InternalExpression), .SFS(SFS), .SBS(SBS), .UniqueNodeID(UniqueNodeID), .RAM(RAM),
    .NewNodeID(NewNodeID), .PIB(PIB), .Buffer(Buffer), .PEB(PEB), .CLI(CLI), .CRI(CRI),
    .ptdCLC(preparefortransformationasdecendantinput_1_ptdclc),
    .ptdRAM(preparefortransformationasdecendantinput_1_ptdram),
    .ptdSFS(preparefortransformationasdecendantinput_1_ptdsfs),
    .ptdSEL(preparefortransformationasdecendantinput_1_ptdsel),
    .ptdNEW(preparefortransformationasdecendantinput_1_ptdnew),
    .PtdBUF(preparefortransformationasdecendantinput_1_ptdbuf),
    .ptdCRI(preparefortransformationasdecendantinput_1_ptdcri),
    .ptdCLI(preparefortransformationasdecendantinput_1_ptdcli),
    .ptdCRE(preparefortransformationasdecendantinput_1_ptdcre),
    .ptdCLE(preparefortransformationasdecendantinput_1_ptdcle),
    .PtdEXP(preparefortransformationasdecendantinput_1_ptdexp),
    .ptdSBS(preparefortransformationasdecendantinput_1_ptdsbs),
    .ptdPIB(preparefortransformationasdecendantinput_1_ptdpib),
    .ptdCompareValueClear(preparefortransformationasdecendantinput_1_ptdcomparevalueclear),
    .ptdStackclear(preparefortransformationasdecendantinput_1_ptdstackclear),
    .Output(preparefortransformationasdecendantinput_1_output),
    .CLI_2(preparefortransformationasdecendantinput_1_cli_2),
    .CLE(preparefortransformationasdecendantinput_1_cle),
    .CRI_2(preparefortransformationasdecendantinput_1_cri_2),
    .CRE(preparefortransformationasdecendantinput_1_cre),
    .PIB_2(preparefortransformationasdecendantinput_1_pib_2),
    .NewExpression(preparefortransformationasdecendantinput_1_newexpression));  // open: PtdToggleChildren
  assign RamSelect = and_1_out ? preparefortransformationasdecendantinput_1_ptdsel : 1'bz;  // Controlled_Buffer controlled_buffer_30
  assign BackStack = and_1_out ? preparefortransformationasdecendantinput_1_ptdsbs : 1'bz;  // Controlled_Buffer controlled_buffer_31
  assign FrontStack = and_1_out ? preparefortransformationasdecendantinput_1_ptdsfs : 1'bz;  // Controlled_Buffer controlled_buffer_32
  assign RAMwrite = and_1_out ? preparefortransformationasdecendantinput_1_ptdram : 1'bz;  // Controlled_Buffer controlled_buffer_33
  assign EXPWrite = and_1_out ? or_25_out : 1'bz;  // Controlled_Buffer controlled_buffer_34
  assign NewNode = and_1_out ? preparefortransformationasdecendantinput_1_ptdnew : 1'bz;  // Controlled_Buffer controlled_buffer_35
  or or_28 (or_28_out, or_22_out, preparefortransformationasdecendantinput_1_ptdcri);
  assign controlled_buffer_1_out = preparefortransformationasdecendantinput_1_ptdcri ? preparefortransformationasdecendantinput_1_cri_2 : 8'bz;  // Controlled_Buffer controlled_buffer_36
  or or_29 (or_29_out, or_23_out, preparefortransformationasdecendantinput_1_ptdcle);
  assign controlled_buffer_6_out = preparefortransformationasdecendantinput_1_ptdcle ? preparefortransformationasdecendantinput_1_cle : 12'bz;  // Controlled_Buffer controlled_buffer_37
  or or_30 (or_30_out, or_24_out, preparefortransformationasdecendantinput_1_ptdcli);
  assign controlled_buffer_2_out = preparefortransformationasdecendantinput_1_ptdcli ? preparefortransformationasdecendantinput_1_cli_2 : 8'bz;  // Controlled_Buffer controlled_buffer_38
  or or_31 (or_31_out, or_17_out, preparefortransformationasdecendantinput_1_ptdexp);
  assign controlled_buffer_3_out = preparefortransformationasdecendantinput_1_ptdexp ? preparefortransformationasdecendantinput_1_newexpression : 12'bz;  // Controlled_Buffer controlled_buffer_39
  or or_32 (or_32_out, or_5_out, preparefortransformationasdecendantinput_1_ptdcomparevalueclear);
  or or_33 (or_33_out, preparefortransformationasdecendantinput_1_ptdram, preparefortransformationasdecendantinput_1_ptdsfs, preparefortransformationasdecendantinput_1_ptdsbs, preparefortransformationasdecendantinput_1_ptdbuf);
  assign controlled_buffer_40_out = or_33_out ? preparefortransformationasdecendantinput_1_output : 8'bz;  // Controlled_Buffer controlled_buffer_40
  BranchChop branchchop_1 (
    .Clock(Clock), .CLI(CLI), .CRI(CRI), .InternalExpression(InternalExpression),
    .BraNew(branchchop_1_branew), .NewValue(branchchop_1_newvalue));
  or or_34 (or_34_out, or_31_out, branchchop_1_branew);
  assign controlled_buffer_3_out = branchchop_1_branew ? branchchop_1_newvalue : 12'bz;  // Controlled_Buffer controlled_buffer_41
  not not_2 (not_2_out, returnexpression_1_retpeb);
  assign controlled_buffer_19_out = not_2_out ? CLE : 12'bz;  // Controlled_Buffer controlled_buffer_42
  not not_3 (not_3_out, or_26_out);
  assign controlled_buffer_20_out = not_3_out ? CRI : 8'bz;  // Controlled_Buffer controlled_buffer_43
  not not_4 (not_4_out, or_27_out);
  assign controlled_buffer_4_out = not_4_out ? PEB : 12'bz;  // Controlled_Buffer controlled_buffer_44
  not not_5 (not_5_out, or_28_out);
  assign controlled_buffer_1_out = not_5_out ? CLI : 8'bz;  // Controlled_Buffer controlled_buffer_45
  not not_6 (not_6_out, or_29_out);
  assign controlled_buffer_6_out = not_6_out ? CRE : 12'bz;  // Controlled_Buffer controlled_buffer_46
  not not_7 (not_7_out, or_30_out);
  assign controlled_buffer_2_out = not_7_out ? PIB : 8'bz;  // Controlled_Buffer controlled_buffer_47
  not not_8 (not_8_out, or_34_out);
  assign controlled_buffer_3_out = not_8_out ? {12{1'b0}} : 12'bz;  // Controlled_Buffer controlled_buffer_48
  not not_9 (not_9_out, or_33_out);
  assign controlled_buffer_40_out = not_9_out ? {8{1'b0}} : 8'bz;  // Controlled_Buffer controlled_buffer_49
  assign ClearChidlren = and_1_out ? preparefortransformationasdecendantinput_1_ptdclc : 1'bz;  // Controlled_Buffer controlled_buffer_50
  assign PEB_2 = and_1_out ? controlled_buffer_19_out : 12'bz;  // Controlled_Buffer controlled_buffer_51
  assign PIB_2 = and_1_out ? controlled_buffer_20_out : 8'bz;  // Controlled_Buffer controlled_buffer_52
  assign CRE_2 = and_1_out ? controlled_buffer_4_out : 12'bz;  // Controlled_Buffer controlled_buffer_53
  assign CRI_2 = and_1_out ? controlled_buffer_1_out : 8'bz;  // Controlled_Buffer controlled_buffer_54
  assign CLE_2 = and_1_out ? controlled_buffer_6_out : 12'bz;  // Controlled_Buffer controlled_buffer_55
  assign CLI_2 = and_1_out ? controlled_buffer_2_out : 8'bz;  // Controlled_Buffer controlled_buffer_56
  assign NewNode_2 = and_1_out ? controlled_buffer_3_out : 12'bz;  // Controlled_Buffer controlled_buffer_57
  assign GeneralOutput = and_1_out ? controlled_buffer_40_out : 8'bz;  // Controlled_Buffer controlled_buffer_58
  assign StackClear = and_1_out ? or_32_out : 1'bz;  // Controlled_Buffer controlled_buffer_59

  // Notes on the sheet:
  //   Input
  //   0 == Backstack / 1 == Frontstack
  //   Output
endmodule

module FunctionExpression (
  input  [11:0] PEB,
  input  [7:0] PIB,
  input  [11:0] CRE,
  input  [7:0] CRI,
  input  [11:0] CLE,
  input  [7:0] CLI,
  input  [3:0] SFS,
  input  [3:0] SBS,
  input  [3:0] RAM,
  input  [11:0] InternalExpression,
  input  UnreduceFlag,
  input  Clock,
  input  [3:0] NewNodeID,
  input  [3:0] UniqueNodeID,
  output EXPWrite,
  output RamSelect,
  output FrontStack,
  output BackStack,
  output RAMwrite,
  output NewNode,
  output [11:0] PEB_2,
  output [7:0] PIB_2,
  output [11:0] CRE_2,
  output [7:0] CRI_2,
  output [11:0] CLE_2,
  output [7:0] CLI_2,
  output [11:0] NewNode_2,
  output [7:0] GeneralOutput,
  output ResolveFlagOveride,
  output ClearChidlren,
  output StackClear
);

  wire and_1_out, and_2_out, decoder_1_out0, decoder_1_out1, decoder_1_out2, decoder_1_out3, decoder_1_out4,
       decoder_1_out5, decoder_1_out7, decoder_1_out8, functioncorelogic_1_corecli,
       functioncorelogic_1_corecre, functioncorelogic_1_corecri, functioncorelogic_1_coreexp,
       functioncorelogic_1_corepib, immediateresolution_1_immpib, not_2_out, not_4_out, not_5_out, not_6_out,
       not_7_out, not_8_out, not_9_out, not_10_out, not_11_out, nullification_1_nullcli,
       nullification_1_nullcri, nullification_1_nullexp, nullification_1_nullstackclear, or_1_out, or_2_out,
       or_3_out, or_4_out, or_5_out, or_6_out, or_7_out, or_8_out, or_9_out, or_10_out, or_11_out, or_12_out,
       or_13_out, or_14_out, or_15_out, or_16_out, or_17_out, or_18_out, or_19_out, or_20_out, or_21_out,
       or_22_out, or_23_out, or_24_out, or_25_out, or_26_out, or_27_out, or_28_out, or_29_out, or_30_out,
       or_31_out, or_32_out, preparefortransformationasancestorinput_1_ptacli,
       preparefortransformationasancestorinput_1_ptacri, preparefortransformationasancestorinput_1_ptapeb,
       preparefortransformationasancestorinput_1_ptapib, preparefortransformationasancestorinput_1_ptaram,
       preparefortransformationasancestorinput_1_ptasbs, preparefortransformationasancestorinput_1_ptasel,
       preparefortransformationasancestorinput_1_ptasfs,
       preparefortransformationasancestorinput_1_ptastackclear, returnexpression_1_retcli,
       returnexpression_1_retcri, returnexpression_1_retpeb, returnexpression_1_retpib,
       updateexpression_1_updcle, updateexpression_1_updcli, updateexpression_1_updcre,
       updateexpression_1_updcri, updateexpression_1_updexp, updateexpression_1_updstackclear,
       updatepointerleft_1_updcle, updatepointerleft_1_updcli, updatepointerleft_1_updcre,
       updatepointerleft_1_updcri, updatepointerleft_1_updexp, updatepointerright_1_updcle,
       updatepointerright_1_updcli, updatepointerright_1_updcre, updatepointerright_1_updcri,
       updatepointerright_1_updexp;
  wire [2:0] not_1_out, xor_1_out;
  wire [7:0] controlled_buffer_1_out, controlled_buffer_3_out, controlled_buffer_4_out,
       controlled_buffer_46_out, functioncorelogic_1_cli, functioncorelogic_1_cri_2, functioncorelogic_1_pib,
       immediateresolution_1_out_3, nullification_1_cli, nullification_1_cri,
       preparefortransformationasancestorinput_1_cli_2, preparefortransformationasancestorinput_1_cri_2,
       preparefortransformationasancestorinput_1_generalouput, preparefortransformationasancestorinput_1_pib,
       returnexpression_1_cli_2, returnexpression_1_cri_2, returnexpression_1_pib_2, updateexpression_1_cli,
       updateexpression_1_cri, updatepointerleft_1_cli, updatepointerleft_1_cri, updatepointerright_1_cli,
       updatepointerright_1_cri;
  wire [11:0] controlled_buffer_2_out, controlled_buffer_5_out, controlled_buffer_11_out,
       controlled_buffer_24_out, functioncorelogic_1_cre_2, functioncorelogic_1_new,
       nullification_1_newvalue, preparefortransformationasancestorinput_1_peb, returnexpression_1_peb,
       updateexpression_1_cle, updateexpression_1_cre, updateexpression_1_newvalue, updatepointerleft_1_cle,
       updatepointerleft_1_cre, updatepointerleft_1_newvalue, updatepointerright_1_cli_2,
       updatepointerright_1_cri_2, updatepointerright_1_newvalue;

  Decoder #(.select(4)) decoder_1 (
    .out0(decoder_1_out0), .out1(decoder_1_out1), .out2(decoder_1_out2), .out3(decoder_1_out3),
    .out4(decoder_1_out4), .out5(decoder_1_out5), .out7(decoder_1_out7), .out8(decoder_1_out8), .sel(PIB[7:4]));  // open: out6, out9, out10, out11, out12, out13, out14, out15, en
  FunctionCoreLogic functioncorelogic_1 (
    .ActivationSignal(decoder_1_out0), .UnreduceableFlag(UnreduceFlag), .Clock(Clock), .PEB(PEB),
    .InternalExpression(InternalExpression), .CRE(CRE), .CLE(CLE), .CRI(CRI),
    .CoreCRI(functioncorelogic_1_corecri), .CoreCRE(functioncorelogic_1_corecre),
    .CorePIB(functioncorelogic_1_corepib), .CoreExp(functioncorelogic_1_coreexp),
    .CoreCLI(functioncorelogic_1_corecli), .CRE_2(functioncorelogic_1_cre_2),
    .CRI_2(functioncorelogic_1_cri_2), .PIB(functioncorelogic_1_pib), .CLI(functioncorelogic_1_cli),
    .New(functioncorelogic_1_new));
  assign xor_1_out = InternalExpression[10:8] ^ 3'b011;  // XOR_Gate xor_1, 3 bits wide
  assign controlled_buffer_1_out = functioncorelogic_1_corepib ? functioncorelogic_1_pib : 8'bz;  // Controlled_Buffer controlled_buffer_1
  assign controlled_buffer_2_out = functioncorelogic_1_corecre ? functioncorelogic_1_cre_2 : 12'bz;  // Controlled_Buffer controlled_buffer_2
  assign controlled_buffer_3_out = functioncorelogic_1_corecri ? functioncorelogic_1_cri_2 : 8'bz;  // Controlled_Buffer controlled_buffer_3
  assign controlled_buffer_4_out = functioncorelogic_1_corecli ? functioncorelogic_1_cli : 8'bz;  // Controlled_Buffer controlled_buffer_4
  assign controlled_buffer_5_out = functioncorelogic_1_coreexp ? functioncorelogic_1_new : 12'bz;  // Controlled_Buffer controlled_buffer_5
  assign not_1_out = ~xor_1_out;  // NOT_Gate not_1, 3 bits wide
  or or_1 (or_1_out, functioncorelogic_1_coreexp, nullification_1_nullexp);
  or or_2 (or_2_out, functioncorelogic_1_corecri, nullification_1_nullcli);
  assign controlled_buffer_3_out = nullification_1_nullcli ? nullification_1_cri : 8'bz;  // Controlled_Buffer controlled_buffer_6
  Nullification nullification_1 (
    .ActivationSignal(decoder_1_out1), .Clock(Clock), .NullCLI(nullification_1_nullcli),
    .NullCRI(nullification_1_nullcri), .NullStackClear(nullification_1_nullstackclear),
    .NullEXP(nullification_1_nullexp), .CRI(nullification_1_cri), .CLI(nullification_1_cli),
    .NewValue(nullification_1_newvalue));
  and and_1 (and_1_out, not_1_out[0], not_1_out[1], not_1_out[2]);
  or or_3 (or_3_out, functioncorelogic_1_corecli, nullification_1_nullcri);
  assign controlled_buffer_4_out = nullification_1_nullcri ? nullification_1_cli : 8'bz;  // Controlled_Buffer controlled_buffer_7
  or or_4 (or_4_out, functioncorelogic_1_coreexp, nullification_1_nullexp);
  assign controlled_buffer_5_out = nullification_1_nullexp ? nullification_1_newvalue : 12'bz;  // Controlled_Buffer controlled_buffer_8
  or or_5 (or_5_out, or_1_out, updateexpression_1_updexp);
  or or_6 (or_6_out, functioncorelogic_1_corecre, updateexpression_1_updcre);
  assign controlled_buffer_2_out = updateexpression_1_updcre ? updateexpression_1_cre : 12'bz;  // Controlled_Buffer controlled_buffer_9
  or or_7 (or_7_out, or_2_out, updateexpression_1_updcri);
  assign controlled_buffer_3_out = updateexpression_1_updcri ? updateexpression_1_cri : 8'bz;  // Controlled_Buffer controlled_buffer_10
  UpdateExpression updateexpression_1 (
    .ActivationSignal(decoder_1_out2), .Clock(Clock), .UniqueNodeID(UniqueNodeID), .PIB(PIB), .PEB(PEB),
    .UpdCLE(updateexpression_1_updcle), .UpdCRE(updateexpression_1_updcre),
    .UpdCLI(updateexpression_1_updcli), .UpdCRI(updateexpression_1_updcri),
    .UpdStackClear(updateexpression_1_updstackclear), .UpdEXP(updateexpression_1_updexp),
    .CRI(updateexpression_1_cri), .CLI(updateexpression_1_cli), .CRE(updateexpression_1_cre),
    .CLE(updateexpression_1_cle), .NewValue(updateexpression_1_newvalue));
  assign controlled_buffer_11_out = updateexpression_1_updcle ? updateexpression_1_cle : 12'bz;  // Controlled_Buffer controlled_buffer_11
  or or_8 (or_8_out, or_3_out, updateexpression_1_updcli);
  assign controlled_buffer_4_out = updateexpression_1_updcli ? updateexpression_1_cli : 8'bz;  // Controlled_Buffer controlled_buffer_12
  or or_9 (or_9_out, or_4_out, updateexpression_1_updexp);
  assign controlled_buffer_5_out = updateexpression_1_updexp ? updateexpression_1_newvalue : 12'bz;  // Controlled_Buffer controlled_buffer_13
  or or_10 (or_10_out, nullification_1_nullstackclear, updateexpression_1_updstackclear);
  or or_11 (or_11_out, or_5_out, updatepointerleft_1_updexp);
  assign controlled_buffer_2_out = updatepointerleft_1_updcre ? updatepointerleft_1_cre : 12'bz;  // Controlled_Buffer controlled_buffer_14
  UpdatePointerLeft updatepointerleft_1 (
    .ActivationSignal(decoder_1_out3), .Clock(Clock), .UniqueNodeID(UniqueNodeID), .PIB(PIB),
    .InternalExpression(InternalExpression), .PEB(PEB), .UpdCLE(updatepointerleft_1_updcle),
    .UpdCRE(updatepointerleft_1_updcre), .UpdCLI(updatepointerleft_1_updcli),
    .UpdCRI(updatepointerleft_1_updcri), .UpdEXP(updatepointerleft_1_updexp), .CRI(updatepointerleft_1_cri),
    .CLI(updatepointerleft_1_cli), .CRE(updatepointerleft_1_cre), .CLE(updatepointerleft_1_cle),
    .NewValue(updatepointerleft_1_newvalue));
  or or_12 (or_12_out, or_6_out, updatepointerleft_1_updcre);
  or or_13 (or_13_out, or_7_out, updatepointerleft_1_updcri);
  assign controlled_buffer_3_out = updatepointerleft_1_updcri ? updatepointerleft_1_cri : 8'bz;  // Controlled_Buffer controlled_buffer_15
  or or_14 (or_14_out, updateexpression_1_updcle, updatepointerleft_1_updcle);
  assign controlled_buffer_11_out = updatepointerleft_1_updcle ? updatepointerleft_1_cle : 12'bz;  // Controlled_Buffer controlled_buffer_16
  or or_15 (or_15_out, or_8_out, updatepointerleft_1_updcli);
  assign controlled_buffer_4_out = updatepointerleft_1_updcli ? updatepointerleft_1_cli : 8'bz;  // Controlled_Buffer controlled_buffer_17
  or or_16 (or_16_out, or_9_out, updatepointerleft_1_updexp);
  assign controlled_buffer_5_out = updatepointerleft_1_updexp ? updatepointerleft_1_newvalue : 12'bz;  // Controlled_Buffer controlled_buffer_18
  UpdatePointerRight updatepointerright_1 (
    .ActivationSignal(decoder_1_out4), .Clock(Clock), .UniqueNodeID(UniqueNodeID), .PIB(PIB),
    .InternalExpression(InternalExpression), .PEB(PEB), .UpdCLE(updatepointerright_1_updcle),
    .UpdCRE(updatepointerright_1_updcre), .UpdCLI(updatepointerright_1_updcli),
    .UpdCRI(updatepointerright_1_updcri), .UpdEXP(updatepointerright_1_updexp),
    .CRI(updatepointerright_1_cri), .CLI(updatepointerright_1_cli), .CRI_2(updatepointerright_1_cri_2),
    .CLI_2(updatepointerright_1_cli_2), .NewValue(updatepointerright_1_newvalue));
  or or_17 (or_17_out, or_11_out, updatepointerright_1_updexp);
  or or_18 (or_18_out, or_12_out, updatepointerright_1_updcre);
  assign controlled_buffer_2_out = updatepointerright_1_updcre ? updatepointerright_1_cri_2 : 12'bz;  // Controlled_Buffer controlled_buffer_19
  or or_19 (or_19_out, or_13_out, updatepointerright_1_updcri);
  assign controlled_buffer_3_out = updatepointerright_1_updcri ? updatepointerright_1_cri : 8'bz;  // Controlled_Buffer controlled_buffer_20
  or or_20 (or_20_out, or_14_out, updatepointerright_1_updcle);
  assign controlled_buffer_11_out = updatepointerright_1_updcle ? updatepointerright_1_cli_2 : 12'bz;  // Controlled_Buffer controlled_buffer_21
  or or_21 (or_21_out, or_15_out, updatepointerright_1_updcli);
  assign controlled_buffer_4_out = updatepointerright_1_updcli ? updatepointerright_1_cli : 8'bz;  // Controlled_Buffer controlled_buffer_22
  or or_22 (or_22_out, or_16_out, updatepointerright_1_updexp);
  assign controlled_buffer_5_out = updatepointerright_1_updexp ? updatepointerright_1_newvalue : 12'bz;  // Controlled_Buffer controlled_buffer_23
  ReturnExpression returnexpression_1 (
    .ActivationSignal(decoder_1_out5), .UniqueNodeID(UniqueNodeID), .PIB(PIB), .CLI(CLI), .CRI(CRI),
    .CRE(CRE), .CLE(CLE), .InternalExpression(InternalExpression), .RetCLI(returnexpression_1_retcli),
    .RetCRI(returnexpression_1_retcri), .RetPIB(returnexpression_1_retpib),
    .RetPEB(returnexpression_1_retpeb), .CRI_2(returnexpression_1_cri_2), .CLI_2(returnexpression_1_cli_2),
    .PEB(returnexpression_1_peb), .PIB_2(returnexpression_1_pib_2));
  assign controlled_buffer_24_out = returnexpression_1_retpeb ? returnexpression_1_peb : 12'bz;  // Controlled_Buffer controlled_buffer_24
  or or_23 (or_23_out, functioncorelogic_1_corepib, returnexpression_1_retpib);
  assign controlled_buffer_1_out = returnexpression_1_retpib ? returnexpression_1_pib_2 : 8'bz;  // Controlled_Buffer controlled_buffer_25
  or or_24 (or_24_out, or_19_out, returnexpression_1_retcri);
  assign controlled_buffer_3_out = returnexpression_1_retcri ? returnexpression_1_cri_2 : 8'bz;  // Controlled_Buffer controlled_buffer_26
  or or_25 (or_25_out, or_21_out, returnexpression_1_retcli);
  assign controlled_buffer_4_out = returnexpression_1_retcli ? returnexpression_1_cli_2 : 8'bz;  // Controlled_Buffer controlled_buffer_27
  or or_26 (or_26_out, or_23_out, immediateresolution_1_immpib);
  assign controlled_buffer_1_out = immediateresolution_1_immpib ? immediateresolution_1_out_3 : 8'bz;  // Controlled_Buffer controlled_buffer_28
  ImmediateResolution immediateresolution_1 (
    .ActivationSignal(decoder_1_out7), .ImmPIB(immediateresolution_1_immpib),
    .out_3(immediateresolution_1_out_3));
  assign RamSelect = and_1_out ? preparefortransformationasancestorinput_1_ptasel : 1'bz;  // Controlled_Buffer controlled_buffer_29
  assign BackStack = and_1_out ? preparefortransformationasancestorinput_1_ptasbs : 1'bz;  // Controlled_Buffer controlled_buffer_30
  assign FrontStack = and_1_out ? preparefortransformationasancestorinput_1_ptasfs : 1'bz;  // Controlled_Buffer controlled_buffer_31
  assign RAMwrite = and_1_out ? preparefortransformationasancestorinput_1_ptaram : 1'bz;  // Controlled_Buffer controlled_buffer_32
  assign EXPWrite = and_1_out ? or_17_out : 1'bz;  // Controlled_Buffer controlled_buffer_33
  assign NewNode = and_1_out ? 1'b0 : 1'bz;  // Controlled_Buffer controlled_buffer_34
  PrepareForTransformationAsAncestorInput preparefortransformationasancestorinput_1 (
    .ActivationSignal(decoder_1_out8), .Clock(Clock), .SFS(SFS), .SBS(SBS), .RAM(RAM),
    .UniqueNodeID(UniqueNodeID), .CLI(CLI), .CRI(CRI), .CLE(CLE), .CRE(CRE),
    .InternalExpression(InternalExpression), .ptaRAM(preparefortransformationasancestorinput_1_ptaram),
    .ptaSFS(preparefortransformationasancestorinput_1_ptasfs),
    .ptaCLI(preparefortransformationasancestorinput_1_ptacli),
    .ptaCRI(preparefortransformationasancestorinput_1_ptacri),
    .ptaPEB(preparefortransformationasancestorinput_1_ptapeb),
    .ptaSEL(preparefortransformationasancestorinput_1_ptasel),
    .ptaSBS(preparefortransformationasancestorinput_1_ptasbs),
    .ptaStackClear(preparefortransformationasancestorinput_1_ptastackclear),
    .ptaPIB(preparefortransformationasancestorinput_1_ptapib),
    .GeneralOuput(preparefortransformationasancestorinput_1_generalouput),
    .PEB(preparefortransformationasancestorinput_1_peb),
    .CLI_2(preparefortransformationasancestorinput_1_cli_2),
    .CRI_2(preparefortransformationasancestorinput_1_cri_2),
    .PIB(preparefortransformationasancestorinput_1_pib));
  or or_27 (or_27_out, returnexpression_1_retpeb, preparefortransformationasancestorinput_1_ptapeb);
  assign controlled_buffer_24_out = preparefortransformationasancestorinput_1_ptapeb ? preparefortransformationasancestorinput_1_peb : 12'bz;  // Controlled_Buffer controlled_buffer_35
  or or_28 (or_28_out, or_26_out, preparefortransformationasancestorinput_1_ptapib);
  assign controlled_buffer_1_out = preparefortransformationasancestorinput_1_ptapib ? preparefortransformationasancestorinput_1_pib : 8'bz;  // Controlled_Buffer controlled_buffer_36
  or or_29 (or_29_out, or_24_out, preparefortransformationasancestorinput_1_ptacri);
  assign controlled_buffer_3_out = preparefortransformationasancestorinput_1_ptacri ? preparefortransformationasancestorinput_1_cri_2 : 8'bz;  // Controlled_Buffer controlled_buffer_37
  or or_30 (or_30_out, or_25_out, preparefortransformationasancestorinput_1_ptacli);
  assign controlled_buffer_4_out = preparefortransformationasancestorinput_1_ptacli ? preparefortransformationasancestorinput_1_cli_2 : 8'bz;  // Controlled_Buffer controlled_buffer_38
  not not_2 (not_2_out, UnreduceFlag);
  and and_2 (and_2_out, and_1_out, not_2_out);
  not not_3 (ResolveFlagOveride, and_2_out);
  not not_4 (not_4_out, or_27_out);
  assign controlled_buffer_24_out = not_4_out ? InternalExpression : 12'bz;  // Controlled_Buffer controlled_buffer_39
  not not_5 (not_5_out, or_28_out);
  assign controlled_buffer_1_out = not_5_out ? {8{1'b0}} : 8'bz;  // Controlled_Buffer controlled_buffer_40
  not not_6 (not_6_out, or_18_out);
  assign controlled_buffer_2_out = not_6_out ? {12{1'b0}} : 12'bz;  // Controlled_Buffer controlled_buffer_41
  not not_7 (not_7_out, or_29_out);
  assign controlled_buffer_3_out = not_7_out ? {8{1'b0}} : 8'bz;  // Controlled_Buffer controlled_buffer_42
  not not_8 (not_8_out, or_20_out);
  assign controlled_buffer_11_out = not_8_out ? {12{1'b0}} : 12'bz;  // Controlled_Buffer controlled_buffer_43
  not not_9 (not_9_out, or_30_out);
  assign controlled_buffer_4_out = not_9_out ? {8{1'b0}} : 8'bz;  // Controlled_Buffer controlled_buffer_44
  not not_10 (not_10_out, or_22_out);
  assign controlled_buffer_5_out = not_10_out ? {12{1'b0}} : 12'bz;  // Controlled_Buffer controlled_buffer_45
  assign controlled_buffer_46_out = or_32_out ? preparefortransformationasancestorinput_1_generalouput : 8'bz;  // Controlled_Buffer controlled_buffer_46
  or or_31 (or_31_out, or_10_out, preparefortransformationasancestorinput_1_ptastackclear);
  or or_32 (or_32_out, preparefortransformationasancestorinput_1_ptaram, preparefortransformationasancestorinput_1_ptasfs, preparefortransformationasancestorinput_1_ptasbs);
  not not_11 (not_11_out, or_32_out);
  assign ClearChidlren = and_1_out ? 1'b0 : 1'bz;  // Controlled_Buffer controlled_buffer_47
  assign PEB_2 = and_1_out ? controlled_buffer_24_out : 12'bz;  // Controlled_Buffer controlled_buffer_48
  assign PIB_2 = and_1_out ? controlled_buffer_1_out : 8'bz;  // Controlled_Buffer controlled_buffer_49
  assign CRE_2 = and_1_out ? controlled_buffer_2_out : 12'bz;  // Controlled_Buffer controlled_buffer_50
  assign CRI_2 = and_1_out ? controlled_buffer_3_out : 8'bz;  // Controlled_Buffer controlled_buffer_51
  assign CLE_2 = and_1_out ? controlled_buffer_11_out : 12'bz;  // Controlled_Buffer controlled_buffer_52
  assign CLI_2 = and_1_out ? controlled_buffer_4_out : 8'bz;  // Controlled_Buffer controlled_buffer_53
  assign NewNode_2 = and_1_out ? controlled_buffer_5_out : 12'bz;  // Controlled_Buffer controlled_buffer_54
  assign controlled_buffer_46_out = not_11_out ? {8{1'b0}} : 8'bz;  // Controlled_Buffer controlled_buffer_55
  assign GeneralOutput = and_1_out ? controlled_buffer_46_out : 8'bz;  // Controlled_Buffer controlled_buffer_56
  assign StackClear = and_1_out ? or_31_out : 1'bz;  // Controlled_Buffer controlled_buffer_57

  // Notes on the sheet:
  //   Input
  //   0 == Backstack / 1 == Frontstack
  //   Output
endmodule

module Nullification (
  input  ActivationSignal,
  input  Clock,
  output NullCLI,
  output NullStackClear,
  output NullCRI,
  output NullEXP,
  output [7:0] CRI,
  output [7:0] CLI,
  output [11:0] NewValue
);

  wire and_1_out, d_ff_1_q, not_1_out, or_2_out;

  or or_1 (NullCLI, and_1_out, NullEXP);
  not not_1 (not_1_out, NullEXP);
  D_Flip_Flop d_ff_1 (.D(and_1_out), .clk(Clock), .Q(d_ff_1_q));  // open: Qn, preset, reset
  and and_1 (and_1_out, ActivationSignal, not_1_out);
  or or_2 (or_2_out, and_1_out, NullEXP);
  assign CLI = or_2_out ? 8'h10 : 8'bz;  // Controlled_Buffer controlled_buffer_1
  and and_2 (NullEXP, ActivationSignal, d_ff_1_q);
  assign NewValue = NullEXP ? {12{1'b0}} : 12'bz;  // Controlled_Buffer controlled_buffer_2

  assign CRI = CLI;
  assign NullCRI = NullCLI;
  assign NullStackClear = NullEXP;
endmodule

module UpdateExpression (
  input  ActivationSignal,
  input  Clock,
  input  [3:0] UniqueNodeID,
  input  [7:0] PIB,
  input  [11:0] PEB,
  output UpdCLE,
  output UpdStackClear,
  output UpdCRE,
  output UpdEXP,
  output UpdCLI,
  output UpdCRI,
  output [7:0] CRI,
  output [7:0] CLI,
  output [11:0] CRE,
  output [11:0] CLE,
  output [11:0] NewValue
);

  wire and_1_out, and_3_out;
  wire [3:0] not_1_out, xor_1_out;

  assign CLI = ActivationSignal ? PIB : 8'bz;  // Controlled_Buffer controlled_buffer_1
  assign CLE = ActivationSignal ? PEB : 12'bz;  // Controlled_Buffer controlled_buffer_2
  assign xor_1_out = UniqueNodeID ^ PIB[3:0];  // XOR_Gate xor_1, 4 bits wide
  and and_1 (and_1_out, not_1_out[0], not_1_out[1], not_1_out[2], not_1_out[3]);
  assign not_1_out = ~xor_1_out;  // NOT_Gate not_1, 4 bits wide
  and and_2 (UpdEXP, and_1_out, ActivationSignal);
  and and_3 (and_3_out, and_1_out, ActivationSignal);
  assign NewValue = and_3_out ? {1'b0, PEB[10:0]} : 12'bz;  // Controlled_Buffer controlled_buffer_3

  assign CRE = CLE;
  assign CRI = CLI;
  assign UpdCLE = ActivationSignal;
  assign UpdCLI = ActivationSignal;
  assign UpdCRE = ActivationSignal;
  assign UpdCRI = ActivationSignal;
  assign UpdStackClear = UpdEXP;
endmodule

module UpdatePointerLeft (
  input  ActivationSignal,
  input  Clock,
  input  [3:0] UniqueNodeID,
  input  [7:0] PIB,
  input  [11:0] InternalExpression,
  input  [11:0] PEB,
  output UpdCLE,
  output UpdCRE,
  output UpdCLI,
  output UpdEXP,
  output UpdCRI,
  output [7:0] CRI,
  output [7:0] CLI,
  output [11:0] CRE,
  output [11:0] CLE,
  output [11:0] NewValue
);

  wire and_1_out, and_3_out;
  wire [3:0] not_1_out, xor_1_out;

  assign CLI = ActivationSignal ? PIB : 8'bz;  // Controlled_Buffer controlled_buffer_1
  assign CLE = ActivationSignal ? PEB : 12'bz;  // Controlled_Buffer controlled_buffer_2
  assign xor_1_out = UniqueNodeID ^ PIB[3:0];  // XOR_Gate xor_1, 4 bits wide
  and and_1 (and_1_out, not_1_out[0], not_1_out[1], not_1_out[2], not_1_out[3]);
  assign not_1_out = ~xor_1_out;  // NOT_Gate not_1, 4 bits wide
  and and_2 (UpdEXP, and_1_out, ActivationSignal);
  and and_3 (and_3_out, and_1_out, ActivationSignal);
  assign NewValue = and_3_out ? {InternalExpression[11:8], PEB[7:4], InternalExpression[3:0]} : 12'bz;  // Controlled_Buffer controlled_buffer_3

  assign CRE = CLE;
  assign CRI = CLI;
  assign UpdCLE = ActivationSignal;
  assign UpdCLI = ActivationSignal;
  assign UpdCRE = ActivationSignal;
  assign UpdCRI = ActivationSignal;
endmodule

module UpdatePointerRight (
  input  ActivationSignal,
  input  Clock,
  input  [3:0] UniqueNodeID,
  input  [7:0] PIB,
  input  [11:0] InternalExpression,
  input  [11:0] PEB,
  output UpdCLE,
  output UpdCRE,
  output UpdCLI,
  output UpdEXP,
  output UpdCRI,
  output [7:0] CRI,
  output [7:0] CLI,
  output [11:0] CRI_2,
  output [11:0] CLI_2,
  output [11:0] NewValue
);

  wire and_1_out, and_3_out;
  wire [3:0] not_1_out, xor_1_out;

  assign CLI = ActivationSignal ? PIB : 8'bz;  // Controlled_Buffer controlled_buffer_1
  assign CLI_2 = ActivationSignal ? PEB : 12'bz;  // Controlled_Buffer controlled_buffer_2
  assign xor_1_out = UniqueNodeID ^ PIB[3:0];  // XOR_Gate xor_1, 4 bits wide
  and and_1 (and_1_out, not_1_out[0], not_1_out[1], not_1_out[2], not_1_out[3]);
  assign not_1_out = ~xor_1_out;  // NOT_Gate not_1, 4 bits wide
  and and_2 (UpdEXP, and_1_out, ActivationSignal);
  and and_3 (and_3_out, and_1_out, ActivationSignal);
  assign NewValue = and_3_out ? {InternalExpression[11:4], PEB[3:0]} : 12'bz;  // Controlled_Buffer controlled_buffer_3

  assign CRI = CLI;
  assign CRI_2 = CLI_2;
  assign UpdCLE = ActivationSignal;
  assign UpdCLI = ActivationSignal;
  assign UpdCRE = ActivationSignal;
  assign UpdCRI = ActivationSignal;
endmodule

module ReturnExpression (
  input  ActivationSignal,
  input  [3:0] UniqueNodeID,
  input  [7:0] PIB,
  input  [7:0] CLI,
  input  [7:0] CRI,
  input  [11:0] CRE,
  input  [11:0] CLE,
  input  [11:0] InternalExpression,
  output RetPIB,
  output RetCLI,
  output RetPEB,
  output RetCRI,
  output [7:0] CRI_2,
  output [7:0] CLI_2,
  output [11:0] PEB,
  output [7:0] PIB_2
);

  wire and_1_out, and_2_out, and_3_out, and_5_out, and_6_out, and_7_out, or_1_out, or_2_out;
  wire [3:0] not_1_out, not_2_out, not_3_out, xor_1_out, xor_2_out, xor_3_out;

  assign not_1_out = ~xor_1_out;  // NOT_Gate not_1, 4 bits wide
  assign xor_1_out = UniqueNodeID ^ PIB[3:0];  // XOR_Gate xor_1, 4 bits wide
  assign CLI_2 = ActivationSignal ? PIB : 8'bz;  // Controlled_Buffer controlled_buffer_1
  assign xor_2_out = 4'b0011 ^ CLI[7:4];  // XOR_Gate xor_2, 4 bits wide
  assign not_2_out = ~xor_2_out;  // NOT_Gate not_2, 4 bits wide
  assign not_3_out = ~xor_3_out;  // NOT_Gate not_3, 4 bits wide
  assign xor_3_out = 4'b0011 ^ CRI[7:4];  // XOR_Gate xor_3, 4 bits wide
  and and_1 (and_1_out, not_1_out[0], not_1_out[1], not_1_out[2], not_1_out[3]);
  and and_2 (and_2_out, not_2_out[0], not_2_out[1], not_2_out[2], not_2_out[3]);
  and and_3 (and_3_out, not_3_out[0], not_3_out[1], not_3_out[2], not_3_out[3]);
  and and_4 (RetPEB, or_1_out, ActivationSignal);
  or or_1 (or_1_out, and_1_out, and_2_out, and_3_out);
  and and_5 (and_5_out, and_1_out, ActivationSignal);
  and and_6 (and_6_out, and_2_out, ActivationSignal);
  and and_7 (and_7_out, and_3_out, ActivationSignal);
  assign PEB = and_6_out ? CLE : 12'bz;  // Controlled_Buffer controlled_buffer_2
  assign PEB = and_5_out ? InternalExpression : 12'bz;  // Controlled_Buffer controlled_buffer_3
  assign PEB = and_7_out ? CRE : 12'bz;  // Controlled_Buffer controlled_buffer_4
  or or_2 (or_2_out, and_5_out, and_6_out, and_7_out);
  assign PIB_2 = or_2_out ? 8'h30 : 8'bz;  // Controlled_Buffer controlled_buffer_5

  assign CRI_2 = CLI_2;
  assign RetCLI = ActivationSignal;
  assign RetCRI = ActivationSignal;
  assign RetPIB = RetPEB;

  // Notes on the sheet:
  //   Marker Signal is 0011
  //   Marker Signal is 0011
endmodule

module BranchChop (
  input  Clock,
  input  [7:0] CLI,
  input  [7:0] CRI,
  input  [11:0] InternalExpression,
  output BraNew,
  output [11:0] NewValue
);

  wire and_1_out, and_2_out, or_1_out;
  wire [3:0] not_1_out, not_2_out, xor_1_out, xor_2_out;

  assign xor_1_out = CLI[7:4] ^ 4'b0001;  // XOR_Gate xor_1, 4 bits wide
  assign xor_2_out = CRI[7:4] ^ 4'b0001;  // XOR_Gate xor_2, 4 bits wide
  assign not_1_out = ~xor_1_out;  // NOT_Gate not_1, 4 bits wide
  assign not_2_out = ~xor_2_out;  // NOT_Gate not_2, 4 bits wide
  D_Flip_Flop d_ff_1 (.D(or_1_out), .clk(Clock), .Q(BraNew));  // open: Qn, preset, reset
  or or_1 (or_1_out, and_2_out, and_1_out);
  and and_1 (and_1_out, not_1_out[0], not_1_out[1], not_1_out[2], not_1_out[3]);
  and and_2 (and_2_out, not_2_out[0], not_2_out[1], not_2_out[2], not_2_out[3]);
  assign NewValue = and_2_out ? {4'b0000, InternalExpression[7:4], 3'b100, InternalExpression[0]} : 12'bz;  // Controlled_Buffer controlled_buffer_1
  assign NewValue = and_1_out ? {4'b0000, InternalExpression[11:8], 3'b100, InternalExpression[0]} : 12'bz;  // Controlled_Buffer controlled_buffer_2
endmodule

module CompareValue (
  input  ActivationSignal,
  input  Clock,
  input  Clear,
  input  [11:0] InternalValue,
  input  [11:0] PEB,
  input  [7:0] PIB,
  input  [7:0] CRI,
  input  [7:0] CLI,
  output ComCLI,
  output ComCLE,
  output ComCRI,
  output ComCRE,
  output ComPIB,
  output MarkForTransformation,
  output [7:0] CLI_2,
  output [7:0] CRI_2,
  output [11:0] CLE,
  output [11:0] CRE,
  output [7:0] PIB_2
);

  wire and_1_out, and_2_out, and_3_out, and_4_out, and_5_out, and_6_out, and_8_out, and_9_out, and_10_out,
       not_4_out, not_6_out, not_7_out, not_8_out, not_9_out, or_2_out;
  wire [2:0] not_1_out, xor_1_out;
  wire [3:0] not_2_out, not_5_out, xor_2_out, xor_4_out;
  wire [7:0] controlled_buffer_1_out, controlled_buffer_5_out, not_3_out, xor_3_out;

  assign not_1_out = ~xor_1_out;  // NOT_Gate not_1, 3 bits wide
  assign xor_1_out = 3'b010 ^ InternalValue[10:8];  // XOR_Gate xor_1, 3 bits wide
  assign xor_2_out = 4'b0100 ^ CRI[7:4];  // XOR_Gate xor_2, 4 bits wide
  assign not_2_out = ~xor_2_out;  // NOT_Gate not_2, 4 bits wide
  and and_1 (and_1_out, not_1_out[0], not_1_out[1], not_1_out[2]);
  assign xor_3_out = InternalValue[7:0] ^ PEB[7:0];  // XOR_Gate xor_3, 8 bits wide
  assign not_3_out = ~xor_3_out;  // NOT_Gate not_3, 8 bits wide
  and and_2 (and_2_out, not_2_out[0], not_2_out[1], not_2_out[2], not_2_out[3]);
  not not_4 (not_4_out, and_1_out);
  and and_3 (and_3_out, not_3_out[0], not_3_out[1], not_3_out[2], not_3_out[3], not_3_out[4], not_3_out[5], not_3_out[6], not_3_out[7]);
  assign controlled_buffer_1_out = and_2_out ? CRI : 8'bz;  // Controlled_Buffer controlled_buffer_1
  assign xor_4_out = 4'b0100 ^ CLI[7:4];  // XOR_Gate xor_4, 4 bits wide
  and and_4 (and_4_out, not_4_out, and_3_out);
  assign not_5_out = ~xor_4_out;  // NOT_Gate not_5, 4 bits wide
  assign controlled_buffer_1_out = and_5_out ? CLI : 8'bz;  // Controlled_Buffer controlled_buffer_2
  and and_5 (and_5_out, not_5_out[0], not_5_out[1], not_5_out[2], not_5_out[3]);
  not not_6 (not_6_out, and_2_out);
  and and_6 (and_6_out, not_6_out, not_7_out);
  not not_7 (not_7_out, and_5_out);
  or or_1 (ComPIB, ComCLE, and_8_out);
  and and_7 (ComCLE, and_1_out, ActivationSignal);
  not not_8 (not_8_out, and_1_out);
  assign CLI_2 = and_1_out ? PIB : 8'bz;  // Controlled_Buffer controlled_buffer_3
  assign CLE = and_1_out ? PEB : 12'bz;  // Controlled_Buffer controlled_buffer_4
  assign controlled_buffer_5_out = and_1_out ? controlled_buffer_1_out : 8'bz;  // Controlled_Buffer controlled_buffer_5
  assign controlled_buffer_1_out = and_6_out ? {8{1'b0}} : 8'bz;  // Controlled_Buffer controlled_buffer_6
  and and_8 (and_8_out, not_8_out, ActivationSignal);
  and and_9 (and_9_out, ActivationSignal, and_4_out);
  not not_9 (not_9_out, and_4_out);
  and and_10 (and_10_out, not_8_out, not_9_out);
  assign controlled_buffer_5_out = and_4_out ? 8'h40 : 8'bz;  // Controlled_Buffer controlled_buffer_7
  assign controlled_buffer_5_out = and_10_out ? {8{1'b0}} : 8'bz;  // Controlled_Buffer controlled_buffer_8
  or or_2 (or_2_out, MarkForTransformation, and_9_out);
  assign PIB_2 = ActivationSignal ? controlled_buffer_5_out : 8'bz;  // Controlled_Buffer controlled_buffer_9
  D_Flip_Flop d_ff_1 (.D(or_2_out), .clk(Clock), .Q(MarkForTransformation), .reset(Clear));  // open: Qn, preset

  assign ComCLI = ComCLE;
  assign ComCRE = ComCLE;
  assign ComCRI = ComCLE;
  assign CRE = CLE;
  assign CRI_2 = CLI_2;
endmodule

module ImmediateResolution (
  input  ActivationSignal,
  output ImmPIB,
  output [7:0] out_3
);

  assign out_3 = ActivationSignal ? 8'h10 : 8'bz;  // Controlled_Buffer controlled_buffer_1

  assign ImmPIB = ActivationSignal;
endmodule

module PrepareForTransformationAsAncestorInput (
  input  ActivationSignal,
  input  Clock,
  input  [3:0] SFS,
  input  [3:0] SBS,
  input  [3:0] RAM,
  input  [3:0] UniqueNodeID,
  input  [7:0] CLI,
  input  [7:0] CRI,
  input  [11:0] CLE,
  input  [11:0] CRE,
  input  [11:0] InternalExpression,
  output ptaSEL,
  output ptaPEB,
  output ptaStackClear,
  output ptaRAM,
  output ptaSFS,
  output ptaSBS,
  output ptaCLI,
  output ptaPIB,
  output ptaCRI,
  output [7:0] GeneralOuput,
  output [11:0] PEB,
  output [7:0] CLI_2,
  output [7:0] CRI_2,
  output [7:0] PIB
);

  wire and_1_out, and_2_out, and_3_out, and_4_out, and_5_out, and_6_out, and_7_out, and_8_out, and_9_out,
       and_10_out, and_11_out, and_12_out, and_14_out, and_15_out, and_16_out, and_17_out, and_18_out,
       and_19_out, and_20_out, and_21_out, and_22_out, and_23_out, and_24_out, and_25_out, and_27_out,
       and_29_out, and_30_out, d_ff_1_q, d_ff_2_q, d_ff_3_q, d_ff_4_q, d_ff_5_q, d_ff_6_q, d_ff_7_q,
       d_ff_8_q, d_ff_9_q, d_ff_10_q, d_ff_11_q, not_1_out, not_7_out, not_10_out, not_11_out, or_1_out,
       or_4_out, or_5_out, or_6_out, or_8_out, or_9_out, or_10_out, or_11_out, or_13_out, or_14_out,
       or_15_out, or_16_out, or_17_out, or_18_out, or_19_out, or_20_out, or_21_out, or_22_out, or_23_out,
       or_24_out, or_25_out, or_26_out, or_27_out, or_28_out, or_29_out, or_30_out, or_31_out, or_32_out,
       or_33_out;
  wire [2:0] not_8_out, not_9_out, xor_6_out, xor_7_out;
  wire [3:0] adder_1_out, adder_2_out, not_2_out, not_3_out, not_4_out, not_5_out, not_6_out, xor_1_out,
       xor_2_out, xor_3_out, xor_4_out, xor_5_out;
  wire [11:0] controlled_buffer_2_out, register_1_q;

  not not_1 (not_1_out, or_1_out);
  assign xor_1_out = 4'b0011 ^ CLI[7:4];  // XOR_Gate xor_1, 4 bits wide
  assign xor_2_out = 4'b0011 ^ CRI[7:4];  // XOR_Gate xor_2, 4 bits wide
  D_Flip_Flop d_ff_1 (.D(and_1_out), .clk(Clock), .Q(d_ff_1_q));  // open: Qn, preset, reset
  and and_1 (and_1_out, ActivationSignal, not_1_out);
  assign xor_3_out = 4'b0000 ^ SBS;  // XOR_Gate xor_3, 4 bits wide
  assign not_2_out = ~xor_3_out;  // NOT_Gate not_2, 4 bits wide
  assign xor_4_out = 4'b0000 ^ SBS;  // XOR_Gate xor_4, 4 bits wide
  assign not_3_out = ~xor_4_out;  // NOT_Gate not_3, 4 bits wide
  Adder #(.width(4)) adder_1 (.a(4'b0001), .b(SFS), .out(adder_1_out));  // open: cin, cout
  Adder #(.width(4)) adder_2 (.a(4'b0001), .b(SBS), .out(adder_2_out));  // open: cin, cout
  assign not_4_out = ~xor_5_out;  // NOT_Gate not_4, 4 bits wide
  assign xor_5_out = SFS ^ SBS;  // XOR_Gate xor_5, 4 bits wide
  assign not_5_out = ~xor_1_out;  // NOT_Gate not_5, 4 bits wide
  assign not_6_out = ~xor_2_out;  // NOT_Gate not_6, 4 bits wide
  and and_2 (and_2_out, and_3_out, and_4_out);
  or or_1 (or_1_out, and_3_out, or_4_out);
  and and_3 (and_3_out, ActivationSignal, d_ff_1_q);
  and and_4 (and_4_out, not_2_out[0], not_2_out[1], not_2_out[2], not_2_out[3]);
  and and_5 (and_5_out, not_3_out[0], not_3_out[1], not_3_out[2], not_3_out[3]);
  and and_6 (and_6_out, and_3_out, and_4_out);
  and and_7 (and_7_out, not_4_out[0], not_4_out[1], not_4_out[2], not_4_out[3]);
  and and_8 (and_8_out, not_5_out[0], not_5_out[1], not_5_out[2], not_5_out[3]);
  and and_9 (and_9_out, not_6_out[0], not_6_out[1], not_6_out[2], not_6_out[3]);
  or or_2 (ptaRAM, and_2_out, or_10_out);
  D_Flip_Flop d_ff_2 (.D(and_3_out), .clk(Clock), .Q(d_ff_2_q));  // open: Qn, preset, reset
  assign GeneralOuput = and_6_out ? {4'b0000, UniqueNodeID} : 8'bz;  // Controlled_Buffer controlled_buffer_1
  assign controlled_buffer_2_out = and_8_out ? CLE : 12'bz;  // Controlled_Buffer controlled_buffer_2
  assign controlled_buffer_2_out = and_9_out ? CRE : 12'bz;  // Controlled_Buffer controlled_buffer_3
  assign controlled_buffer_2_out = and_5_out ? InternalExpression : 12'bz;  // Controlled_Buffer controlled_buffer_4
  or or_3 (ptaSFS, and_10_out, or_15_out);
  and and_10 (and_10_out, and_11_out, and_4_out);
  or or_4 (or_4_out, and_11_out, or_5_out);
  and and_11 (and_11_out, ActivationSignal, d_ff_2_q);
  and and_12 (and_12_out, and_11_out, and_4_out);
  assign GeneralOuput = and_12_out ? {4'b0000, adder_1_out} : 8'bz;  // Controlled_Buffer controlled_buffer_5
  or or_5 (or_5_out, ptaCLI, or_11_out);
  D_Flip_Flop d_ff_3 (.D(and_11_out), .clk(Clock), .Q(d_ff_3_q));  // open: Qn, preset, reset
  not not_7 (not_7_out, and_4_out);
  or or_6 (or_6_out, and_3_out, and_11_out);
  or or_7 (ptaPEB, or_8_out, or_9_out);
  or or_8 (or_8_out, and_14_out, ptaCLI);
  and and_13 (ptaCLI, ActivationSignal, d_ff_3_q);
  Register #(.width(12)) register_1 (
    .D(controlled_buffer_2_out), .en(ptaCLI), .clk(Clock), .Q(register_1_q));  // open: clr
  and and_14 (and_14_out, not_7_out, or_6_out);
  assign PEB = ptaCLI ? register_1_q : 12'bz;  // Controlled_Buffer controlled_buffer_6
  assign CLI_2 = ptaCLI ? {4'b0101, RAM} : 8'bz;  // Controlled_Buffer controlled_buffer_7
  assign CRI_2 = ptaCLI ? {4'b0101, RAM} : 8'bz;  // Controlled_Buffer controlled_buffer_8
  or or_9 (or_9_out, or_14_out, and_16_out);
  or or_10 (or_10_out, and_22_out, and_15_out);
  or or_11 (or_11_out, and_16_out, or_16_out);
  D_Flip_Flop d_ff_4 (.D(ptaCLI), .clk(Clock), .Q(d_ff_4_q));  // open: Qn, preset, reset
  assign not_8_out = ~xor_6_out;  // NOT_Gate not_8, 3 bits wide
  assign xor_6_out = 3'b101 ^ register_1_q[10:8];  // XOR_Gate xor_6, 3 bits wide
  assign not_9_out = ~xor_7_out;  // NOT_Gate not_9, 3 bits wide
  assign xor_7_out = 3'b001 ^ register_1_q[10:8];  // XOR_Gate xor_7, 3 bits wide
  or or_12 (ptaSEL, and_16_out, or_13_out);
  and and_15 (and_15_out, and_16_out, and_20_out);
  and and_16 (and_16_out, ActivationSignal, d_ff_4_q);
  assign GeneralOuput = and_16_out ? {4'b0000, register_1_q[7:4]} : 8'bz;  // Controlled_Buffer controlled_buffer_9
  assign PEB = and_16_out ? register_1_q : 12'bz;  // Controlled_Buffer controlled_buffer_10
  not not_10 (not_10_out, and_17_out);
  and and_17 (and_17_out, not_8_out[0], not_8_out[1], not_8_out[2]);
  and and_18 (and_18_out, not_9_out[0], not_9_out[1], not_9_out[2]);
  or or_13 (or_13_out, or_22_out, and_21_out);
  or or_14 (or_14_out, or_19_out, and_21_out);
  or or_15 (or_15_out, and_24_out, and_19_out);
  and and_19 (and_19_out, and_20_out, and_21_out);
  D_Flip_Flop d_ff_5 (.D(and_16_out), .clk(Clock), .Q(d_ff_5_q));  // open: Qn, preset, reset
  and and_20 (and_20_out, not_10_out, not_11_out);
  or or_16 (or_16_out, and_21_out, or_20_out);
  and and_21 (and_21_out, ActivationSignal, d_ff_5_q);
  or or_17 (or_17_out, and_14_out, and_21_out);
  or or_18 (or_18_out, or_17_out, or_21_out);
  or or_19 (or_19_out, or_23_out, and_23_out);
  or or_20 (or_20_out, and_23_out, or_24_out);
  D_Flip_Flop d_ff_6 (.D(and_21_out), .clk(Clock), .Q(d_ff_6_q));  // open: Qn, preset, reset
  or or_21 (or_21_out, and_23_out, or_25_out);
  assign GeneralOuput = and_19_out ? {4'b0000, adder_1_out} : 8'bz;  // Controlled_Buffer controlled_buffer_11
  assign PEB = or_18_out ? register_1_q : 12'bz;  // Controlled_Buffer controlled_buffer_12
  or or_22 (or_22_out, and_24_out, and_22_out);
  and and_22 (and_22_out, not_11_out, and_23_out);
  and and_23 (and_23_out, ActivationSignal, d_ff_6_q);
  not not_11 (not_11_out, and_18_out);
  or or_23 (or_23_out, or_26_out, and_25_out);
  D_Flip_Flop d_ff_7 (.D(and_23_out), .clk(Clock), .Q(d_ff_7_q));  // open: Qn, preset, reset
  assign GeneralOuput = and_22_out ? {4'b0000, register_1_q[3:0]} : 8'bz;  // Controlled_Buffer controlled_buffer_13
  and and_24 (and_24_out, not_11_out, and_25_out);
  or or_24 (or_24_out, and_25_out, or_27_out);
  and and_25 (and_25_out, ActivationSignal, d_ff_7_q);
  or or_25 (or_25_out, and_25_out, or_28_out);
  assign GeneralOuput = and_25_out ? {4'b0000, adder_1_out} : 8'bz;  // Controlled_Buffer controlled_buffer_14
  or or_26 (or_26_out, or_29_out, ptaSBS);
  or or_27 (or_27_out, ptaSBS, or_30_out);
  D_Flip_Flop d_ff_8 (.D(and_25_out), .clk(Clock), .Q(d_ff_8_q));  // open: Qn, preset, reset
  or or_28 (or_28_out, ptaSBS, or_31_out);
  D_Flip_Flop d_ff_9 (.D(ptaSBS), .clk(Clock), .Q(d_ff_9_q));  // open: Qn, preset, reset
  and and_26 (ptaSBS, ActivationSignal, d_ff_8_q);
  assign GeneralOuput = ptaSBS ? {4'b0000, adder_2_out} : 8'bz;  // Controlled_Buffer controlled_buffer_15
  or or_29 (or_29_out, d_ff_9_q, or_32_out);
  or or_30 (or_30_out, d_ff_9_q, and_29_out);
  or or_31 (or_31_out, d_ff_9_q, or_33_out);
  D_Flip_Flop d_ff_10 (.D(and_27_out), .clk(Clock), .Q(d_ff_10_q));  // open: Qn, preset, reset
  and and_27 (and_27_out, ActivationSignal, d_ff_9_q);
  and and_28 (ptaPIB, and_29_out, and_7_out);
  or or_32 (or_32_out, and_29_out, and_30_out);
  and and_29 (and_29_out, ActivationSignal, d_ff_10_q);
  or or_33 (or_33_out, and_29_out, and_30_out);
  D_Flip_Flop d_ff_11 (.D(and_29_out), .clk(Clock), .Q(d_ff_11_q));  // open: Qn, preset, reset
  assign PIB = ptaPIB ? 8'h10 : 8'bz;  // Controlled_Buffer controlled_buffer_16
  and and_30 (and_30_out, ActivationSignal, d_ff_11_q);

  assign ptaCRI = ptaCLI;
  assign ptaStackClear = ptaPIB;

  // Notes on the sheet:
  //   New SFS
  //   New SBS
  //   RAM on == Write
  //   off == Read
  //   SEL off == SBS
  //   on == SFS
endmodule

module PrepareForTransformationAsDecendantInput (
  input  ActivationSignal,
  input  Clock,
  input  TransformMark,
  input  [11:0] InExp,
  input  [3:0] SFS,
  input  [3:0] SBS,
  input  [3:0] UniqueNodeID,
  input  [3:0] RAM,
  input  [3:0] NewNodeID,
  input  [7:0] PIB,
  input  [2:0] Buffer,
  input  [11:0] PEB,
  input  [7:0] CLI,
  input  [7:0] CRI,
  output ptdPIB,
  output ptdSEL,
  output ptdNEW,
  output PtdBUF,
  output ptdCRI,
  output PtdEXP,
  output ptdCompareValueClear,
  output ptdCLC,
  output ptdRAM,
  output ptdSFS,
  output PtdToggleChildren,
  output ptdSBS,
  output ptdCLI,
  output ptdStackclear,
  output ptdCRE,
  output ptdCLE,
  output [7:0] Output,
  output [7:0] CLI_2,
  output [11:0] CLE,
  output [7:0] CRI_2,
  output [11:0] CRE,
  output [7:0] PIB_2,
  output [11:0] NewExpression
);

  wire and_1_out, and_2_out, and_3_out, and_4_out, and_6_out, and_7_out, and_8_out, and_9_out, and_10_out,
       and_11_out, and_12_out, and_13_out, and_14_out, and_15_out, and_16_out, and_17_out, and_18_out,
       and_19_out, and_20_out, and_21_out, and_22_out, and_23_out, and_25_out, and_26_out, and_27_out,
       and_28_out, and_29_out, and_30_out, and_31_out, and_32_out, and_33_out, and_34_out, and_35_out,
       and_36_out, and_37_out, and_38_out, and_39_out, and_40_out, and_41_out, and_42_out, and_43_out,
       and_44_out, and_45_out, and_46_out, and_47_out, and_48_out, and_49_out, and_50_out, and_52_out,
       controlled_buffer_1_out, d_ff_1_q, d_ff_2_q, d_ff_3_q, d_ff_4_q, d_ff_5_q, d_ff_6_q, d_ff_7_q,
       d_ff_8_q, d_ff_9_q, d_ff_10_q, not_2_out, not_3_out, not_12_out, not_13_out, not_14_out, not_17_out,
       not_18_out, not_19_out, not_20_out, not_21_out, not_22_out, not_23_out, not_24_out, not_25_out,
       not_26_out, or_1_out, or_3_out, or_5_out, or_6_out, or_7_out, or_10_out, or_12_out, or_13_out,
       or_14_out, or_16_out, or_17_out, or_18_out, or_19_out, or_20_out, or_21_out, or_22_out, or_23_out,
       or_24_out, or_25_out;
  wire [2:0] not_1_out, not_6_out, not_7_out, not_10_out, not_11_out, xor_1_out, xor_3_out, xor_4_out,
       xor_8_out, xor_9_out;
  wire [3:0] adder_1_out, adder_2_out, controlled_buffer_14_out, controlled_buffer_23_out, not_4_out,
       not_5_out, not_16_out, register_1_q, xor_2_out, xor_7_out, xor_10_out;
  wire [7:0] controlled_buffer_4_out, not_8_out, not_9_out, xor_5_out, xor_6_out;
  wire [11:0] controlled_buffer_6_out;

  assign xor_1_out = 3'b010 ^ InExp[10:8];  // XOR_Gate xor_1, 3 bits wide
  assign not_1_out = ~xor_1_out;  // NOT_Gate not_1, 3 bits wide
  and and_1 (and_1_out, ActivationSignal, TransformMark);
  and and_2 (and_2_out, not_1_out[0], not_1_out[1], not_1_out[2]);
  and and_3 (and_3_out, and_2_out, ActivationSignal);
  not not_2 (not_2_out, and_3_out);
  not not_3 (not_3_out, or_1_out);
  assign controlled_buffer_1_out = not_2_out ? and_1_out : 1'bz;  // Controlled_Buffer controlled_buffer_1
  assign xor_2_out = 4'b0000 ^ SFS;  // XOR_Gate xor_2, 4 bits wide
  assign xor_3_out = 3'b001 ^ Buffer;  // XOR_Gate xor_3, 3 bits wide
  assign xor_4_out = 3'b001 ^ PEB[10:8];  // XOR_Gate xor_4, 3 bits wide
  assign xor_5_out = 8'h20 ^ CLI;  // XOR_Gate xor_5, 8 bits wide
  assign xor_6_out = 8'h20 ^ CRI;  // XOR_Gate xor_6, 8 bits wide
  D_Flip_Flop d_ff_1 (.D(and_4_out), .clk(Clock), .Q(d_ff_1_q));  // open: Qn, preset, reset
  and and_4 (and_4_out, controlled_buffer_1_out, not_3_out);
  assign not_4_out = ~xor_2_out;  // NOT_Gate not_4, 4 bits wide
  Adder #(.width(4)) adder_1 (.a(4'b0001), .b(SFS), .out(adder_1_out));  // open: cin, cout
  Adder #(.width(4)) adder_2 (.a(4'b0001), .b(SBS), .out(adder_2_out));  // open: cin, cout
  assign xor_7_out = SFS ^ SBS;  // XOR_Gate xor_7, 4 bits wide
  assign not_5_out = ~xor_7_out;  // NOT_Gate not_5, 4 bits wide
  assign not_6_out = ~xor_3_out;  // NOT_Gate not_6, 3 bits wide
  assign not_7_out = ~xor_4_out;  // NOT_Gate not_7, 3 bits wide
  assign not_8_out = ~xor_5_out;  // NOT_Gate not_8, 8 bits wide
  assign not_9_out = ~xor_6_out;  // NOT_Gate not_9, 8 bits wide
  and and_5 (ptdCLC, and_6_out, and_7_out);
  or or_1 (or_1_out, and_6_out, or_5_out);
  and and_6 (and_6_out, controlled_buffer_1_out, d_ff_1_q);
  and and_7 (and_7_out, not_4_out[0], not_4_out[1], not_4_out[2], not_4_out[3]);
  and and_8 (and_8_out, and_6_out, and_7_out);
  and and_9 (and_9_out, not_5_out[0], not_5_out[1], not_5_out[2], not_5_out[3]);
  and and_10 (and_10_out, not_6_out[0], not_6_out[1], not_6_out[2]);
  and and_11 (and_11_out, not_7_out[0], not_7_out[1], not_7_out[2]);
  and and_12 (and_12_out, not_8_out[0], not_8_out[1], not_8_out[2], not_8_out[3], not_8_out[4], not_8_out[5], not_8_out[6], not_8_out[7]);
  and and_13 (and_13_out, not_9_out[0], not_9_out[1], not_9_out[2], not_9_out[3], not_9_out[4], not_9_out[5], not_9_out[6], not_9_out[7]);
  or or_2 (ptdRAM, ptdCLC, or_13_out);
  D_Flip_Flop d_ff_2 (.D(and_6_out), .clk(Clock), .Q(d_ff_2_q));  // open: Qn, preset, reset
  assign Output = and_8_out ? {4'b0000, UniqueNodeID} : 8'bz;  // Controlled_Buffer controlled_buffer_2
  assign xor_8_out = 3'b000 ^ Buffer;  // XOR_Gate xor_8, 3 bits wide
  assign not_10_out = ~xor_8_out;  // NOT_Gate not_10, 3 bits wide
  assign not_11_out = ~xor_9_out;  // NOT_Gate not_11, 3 bits wide
  assign xor_9_out = 3'b101 ^ PEB[10:8];  // XOR_Gate xor_9, 3 bits wide
  or or_3 (or_3_out, and_12_out, and_13_out);
  or or_4 (ptdSFS, and_14_out, or_19_out);
  and and_14 (and_14_out, and_15_out, and_7_out);
  or or_5 (or_5_out, and_15_out, or_6_out);
  and and_15 (and_15_out, controlled_buffer_1_out, d_ff_2_q);
  and and_16 (and_16_out, and_15_out, and_7_out);
  assign Output = and_16_out ? {4'b0000, adder_1_out} : 8'bz;  // Controlled_Buffer controlled_buffer_3
  and and_17 (and_17_out, not_10_out[0], not_10_out[1], not_10_out[2]);
  not not_12 (not_12_out, and_11_out);
  not not_13 (not_13_out, and_18_out);
  and and_18 (and_18_out, not_11_out[0], not_11_out[1], not_11_out[2]);
  assign controlled_buffer_4_out = not_14_out ? {8{1'b0}} : 8'bz;  // Controlled_Buffer controlled_buffer_4
  not not_14 (not_14_out, or_3_out);
  or or_6 (or_6_out, and_20_out, or_10_out);
  D_Flip_Flop d_ff_3 (.D(and_15_out), .clk(Clock), .Q(d_ff_3_q));  // open: Qn, preset, reset
  and and_19 (and_19_out, not_12_out, not_13_out);
  assign controlled_buffer_4_out = or_3_out ? 8'h20 : 8'bz;  // Controlled_Buffer controlled_buffer_5
  and and_20 (and_20_out, controlled_buffer_1_out, d_ff_3_q);
  Register #(.width(4)) register_1 (.D(RAM), .en(and_20_out), .clk(Clock), .Q(register_1_q));  // open: clr
  not not_15 (PtdToggleChildren, or_7_out);
  or or_7 (or_7_out, and_10_out, and_17_out);
  or or_8 (ptdSEL, and_22_out, or_17_out);
  D_Flip_Flop d_ff_4 (.D(and_20_out), .clk(Clock), .Q(d_ff_4_q));  // open: Qn, preset, reset
  assign xor_10_out = register_1_q ^ UniqueNodeID;  // XOR_Gate xor_10, 4 bits wide
  assign not_16_out = ~xor_10_out;  // NOT_Gate not_16, 4 bits wide
  assign controlled_buffer_6_out = not_17_out ? {1'b0, PEB[10:8], {8{1'b0}}} : 12'bz;  // Controlled_Buffer controlled_buffer_6
  not not_17 (not_17_out, and_11_out);
  or or_9 (ptdNEW, and_21_out, and_35_out);
  and and_21 (and_21_out, and_22_out, and_19_out);
  or or_10 (or_10_out, and_22_out, or_14_out);
  and and_22 (and_22_out, controlled_buffer_1_out, d_ff_4_q);
  and and_23 (and_23_out, not_16_out[0], not_16_out[1], not_16_out[2], not_16_out[3]);
  assign controlled_buffer_6_out = and_11_out ? {1'b0, PEB[10:0]} : 12'bz;  // Controlled_Buffer controlled_buffer_7
  or or_11 (ptdCLE, or_12_out, or_16_out);
  or or_12 (or_12_out, and_3_out, and_25_out);
  and and_24 (PtdBUF, and_23_out, and_22_out);
  and and_25 (and_25_out, not_18_out, and_22_out);
  not not_18 (not_18_out, and_23_out);
  not not_19 (not_19_out, and_23_out);
  and and_26 (and_26_out, and_23_out, and_22_out);
  and and_27 (and_27_out, not_19_out, and_22_out);
  assign Output = and_26_out ? {{5{1'b0}}, PEB[10:8]} : 8'bz;  // Controlled_Buffer controlled_buffer_8
  D_Flip_Flop d_ff_5 (.D(and_22_out), .clk(Clock), .Q(d_ff_5_q));  // open: Qn, preset, reset
  assign CLI_2 = and_27_out ? {4'b0010, register_1_q} : 8'bz;  // Controlled_Buffer controlled_buffer_9
  assign CLE = and_27_out ? controlled_buffer_6_out : 12'bz;  // Controlled_Buffer controlled_buffer_10
  assign CRI_2 = and_27_out ? {4'b0010, register_1_q} : 8'bz;  // Controlled_Buffer controlled_buffer_11
  assign CRE = and_27_out ? controlled_buffer_6_out : 12'bz;  // Controlled_Buffer controlled_buffer_12
  assign NewExpression = and_27_out ? {1'b0, PEB[10:8], {8{1'b0}}} : 12'bz;  // Controlled_Buffer controlled_buffer_13
  not not_20 (not_20_out, and_11_out);
  or or_13 (or_13_out, and_41_out, and_31_out);
  or or_14 (or_14_out, and_28_out, or_20_out);
  and and_28 (and_28_out, controlled_buffer_1_out, d_ff_5_q);
  assign controlled_buffer_14_out = not_21_out ? NewNodeID : 4'bz;  // Controlled_Buffer controlled_buffer_14
  not not_21 (not_21_out, or_7_out);
  assign controlled_buffer_14_out = or_7_out ? PEB[7:4] : 4'bz;  // Controlled_Buffer controlled_buffer_15
  or or_15 (PtdEXP, and_30_out, or_21_out);
  or or_16 (or_16_out, and_44_out, and_29_out);
  or or_17 (or_17_out, or_18_out, and_28_out);
  and and_29 (and_29_out, not_22_out, and_32_out);
  and and_30 (and_30_out, and_23_out, and_28_out);
  and and_31 (and_31_out, and_19_out, and_28_out);
  not not_22 (not_22_out, and_23_out);
  and and_32 (and_32_out, and_19_out, and_28_out);
  not not_23 (not_23_out, and_23_out);
  and and_33 (and_33_out, and_23_out, and_28_out);
  and and_34 (and_34_out, not_23_out, and_32_out);
  assign NewExpression = and_33_out ? {InExp[11:8], controlled_buffer_14_out, InExp[3:0]} : 12'bz;  // Controlled_Buffer controlled_buffer_16
  assign CLI_2 = and_34_out ? {4'b0011, register_1_q} : 8'bz;  // Controlled_Buffer controlled_buffer_17
  assign CLE = and_34_out ? {4'b0000, PEB[7:4], 4'b0000} : 12'bz;  // Controlled_Buffer controlled_buffer_18
  assign CRI_2 = and_34_out ? {4'b0011, register_1_q} : 8'bz;  // Controlled_Buffer controlled_buffer_19
  assign CRE = and_34_out ? {4'b0000, PEB[7:4], 4'b0000} : 12'bz;  // Controlled_Buffer controlled_buffer_20
  or or_18 (or_18_out, or_23_out, and_36_out);
  or or_19 (or_19_out, and_46_out, and_37_out);
  D_Flip_Flop d_ff_6 (.D(and_28_out), .clk(Clock), .Q(d_ff_6_q));  // open: Qn, preset, reset
  assign Output = and_28_out ? {4'b0000, NewNodeID} : 8'bz;  // Controlled_Buffer controlled_buffer_21
  and and_35 (and_35_out, and_36_out, not_20_out);
  or or_20 (or_20_out, and_36_out, or_22_out);
  and and_36 (and_36_out, controlled_buffer_1_out, d_ff_6_q);
  and and_37 (and_37_out, and_19_out, and_36_out);
  D_Flip_Flop d_ff_7 (.D(and_36_out), .clk(Clock), .Q(d_ff_7_q));  // open: Qn, preset, reset
  and and_38 (and_38_out, and_19_out, and_36_out);
  assign Output = and_38_out ? {4'b0000, adder_1_out} : 8'bz;  // Controlled_Buffer controlled_buffer_22
  or or_21 (or_21_out, ptdCompareValueClear, and_40_out);
  or or_22 (or_22_out, and_39_out, or_24_out);
  and and_39 (and_39_out, controlled_buffer_1_out, d_ff_7_q);
  assign controlled_buffer_23_out = not_24_out ? NewNodeID : 4'bz;  // Controlled_Buffer controlled_buffer_23
  not not_24 (not_24_out, or_7_out);
  assign controlled_buffer_23_out = or_7_out ? PEB[3:0] : 4'bz;  // Controlled_Buffer controlled_buffer_24
  and and_40 (and_40_out, and_23_out, and_39_out);
  and and_41 (and_41_out, not_20_out, and_39_out);
  not not_25 (not_25_out, and_23_out);
  and and_42 (and_42_out, not_20_out, and_39_out);
  not not_26 (not_26_out, and_23_out);
  and and_43 (and_43_out, and_23_out, and_39_out);
  assign NewExpression = and_43_out ? {InExp[11:4], controlled_buffer_23_out} : 12'bz;  // Controlled_Buffer controlled_buffer_25
  or or_23 (or_23_out, and_47_out, and_39_out);
  and and_44 (and_44_out, not_25_out, and_42_out);
  and and_45 (and_45_out, not_26_out, and_42_out);
  assign CLI_2 = and_45_out ? {4'b0100, register_1_q} : 8'bz;  // Controlled_Buffer controlled_buffer_26
  assign CLE = and_45_out ? {4'b0000, PEB[3:0], 4'b0000} : 12'bz;  // Controlled_Buffer controlled_buffer_27
  assign CRI_2 = and_45_out ? {4'b0100, register_1_q} : 8'bz;  // Controlled_Buffer controlled_buffer_28
  assign CRE = and_45_out ? {4'b0000, PEB[3:0], 4'b0000} : 12'bz;  // Controlled_Buffer controlled_buffer_29
  D_Flip_Flop d_ff_8 (.D(and_39_out), .clk(Clock), .Q(d_ff_8_q));  // open: Qn, preset, reset
  assign Output = and_39_out ? {4'b0000, NewNodeID} : 8'bz;  // Controlled_Buffer controlled_buffer_30
  or or_24 (or_24_out, and_47_out, or_25_out);
  and and_46 (and_46_out, not_20_out, and_47_out);
  D_Flip_Flop d_ff_9 (.D(and_47_out), .clk(Clock), .Q(d_ff_9_q));  // open: Qn, preset, reset
  and and_47 (and_47_out, controlled_buffer_1_out, d_ff_8_q);
  and and_48 (and_48_out, not_20_out, and_47_out);
  assign Output = and_48_out ? {4'b0000, adder_1_out} : 8'bz;  // Controlled_Buffer controlled_buffer_31
  or or_25 (or_25_out, and_49_out, and_50_out);
  or or_26 (ptdSBS, and_3_out, and_49_out);
  D_Flip_Flop d_ff_10 (.D(and_49_out), .clk(Clock), .Q(d_ff_10_q));  // open: Qn, preset, reset
  and and_49 (and_49_out, controlled_buffer_1_out, d_ff_9_q);
  assign Output = and_49_out ? {4'b0000, adder_2_out} : 8'bz;  // Controlled_Buffer controlled_buffer_32
  and and_50 (and_50_out, controlled_buffer_1_out, d_ff_10_q);
  and and_51 (ptdCompareValueClear, and_50_out, and_9_out);
  and and_52 (and_52_out, d_ff_10_q, and_9_out);
  D_Flip_Flop d_ff_11 (.D(and_52_out), .clk(Clock), .Q(ptdStackclear));  // open: Qn, preset, reset
  assign PIB_2 = ptdCompareValueClear ? 8'h10 : 8'bz;  // Controlled_Buffer controlled_buffer_33
  assign PIB_2 = and_3_out ? controlled_buffer_4_out : 8'bz;  // Controlled_Buffer controlled_buffer_34
  assign NewExpression = ptdCompareValueClear ? {1'b0, Buffer, InExp[7:0]} : 12'bz;  // Controlled_Buffer controlled_buffer_35
  assign CLI_2 = and_3_out ? PIB : 8'bz;  // Controlled_Buffer controlled_buffer_36
  assign CRI_2 = and_3_out ? PIB : 8'bz;  // Controlled_Buffer controlled_buffer_37
  assign CLE = and_3_out ? PEB : 12'bz;  // Controlled_Buffer controlled_buffer_38
  assign CRE = and_3_out ? PEB : 12'bz;  // Controlled_Buffer controlled_buffer_39

  assign ptdCLI = ptdCLE;
  assign ptdCRE = ptdCLE;
  assign ptdCRI = ptdCLE;
  assign ptdPIB = ptdCompareValueClear;

  // Notes on the sheet:
  //   Clear Children
  //   New SFS
  //   New SBS
  //   RAM on == Write
  //   off == Read
endmodule

module FunctionCoreLogic (
  input  ActivationSignal,
  input  UnreduceableFlag,
  input  Clock,
  input  [11:0] PEB,
  input  [11:0] InternalExpression,
  input  [11:0] CRE,
  input  [11:0] CLE,
  input  [7:0] CRI,
  output CoreExp,
  output CoreCRI,
  output CorePIB,
  output CoreCLI,
  output CoreCRE,
  output [11:0] CRE_2,
  output [7:0] CRI_2,
  output [7:0] PIB,
  output [7:0] CLI,
  output [11:0] New
);

  wire and_1_out, and_2_out, and_3_out, and_4_out, and_5_out, and_6_out, and_7_out, and_8_out, and_9_out,
       and_10_out, and_11_out, and_12_out, and_13_out, and_14_out, d_ff_1_q, d_ff_2_q, d_ff_3_q, d_ff_4_q,
       d_ff_5_q, not_1_out, not_3_out, not_5_out, not_6_out, or_1_out, or_3_out, or_4_out, or_5_out,
       or_6_out, or_8_out;
  wire [3:0] not_2_out, not_4_out, xor_1_out, xor_2_out;

  not not_1 (not_1_out, UnreduceableFlag);
  and and_1 (and_1_out, CRE[11], CLE[11]);
  and and_2 (and_2_out, PEB[11], and_1_out);
  assign xor_1_out = 4'b0100 ^ CRI[7:4];  // XOR_Gate xor_1, 4 bits wide
  assign not_2_out = ~xor_1_out;  // NOT_Gate not_2, 4 bits wide
  not not_3 (not_3_out, or_1_out);
  D_Flip_Flop d_ff_1 (.D(and_4_out), .clk(Clock), .Q(d_ff_1_q));  // open: Qn, preset, reset
  and and_3 (and_3_out, ActivationSignal, not_1_out, and_2_out);
  and and_4 (and_4_out, not_3_out, and_3_out);
  and and_5 (and_5_out, not_2_out[0], not_2_out[1], not_2_out[2], not_2_out[3]);
  or or_1 (or_1_out, or_4_out, and_6_out);
  and and_6 (and_6_out, ActivationSignal, d_ff_1_q);
  assign not_4_out = ~xor_2_out;  // NOT_Gate not_4, 4 bits wide
  assign xor_2_out = 4'b0001 ^ CRI[7:4];  // XOR_Gate xor_2, 4 bits wide
  or or_2 (CoreCRE, and_6_out, and_8_out, and_12_out);
  D_Flip_Flop d_ff_2 (.D(and_6_out), .clk(Clock), .Q(d_ff_2_q));  // open: Qn, preset, reset
  or or_3 (or_3_out, and_6_out, and_8_out);
  and and_7 (and_7_out, not_4_out[0], not_4_out[1], not_4_out[2], not_4_out[3]);
  or or_4 (or_4_out, or_5_out, and_8_out);
  and and_8 (and_8_out, ActivationSignal, d_ff_2_q);
  assign CRE_2 = or_3_out ? CLE : 12'bz;  // Controlled_Buffer controlled_buffer_1
  assign CRI_2 = or_3_out ? 8'h60 : 8'bz;  // Controlled_Buffer controlled_buffer_2
  or or_5 (or_5_out, CoreCLI, and_13_out, and_12_out);
  and and_9 (and_9_out, and_8_out, and_5_out);
  not not_5 (not_5_out, and_7_out);
  and and_10 (and_10_out, and_8_out, not_6_out);
  not not_6 (not_6_out, and_5_out);
  and and_11 (and_11_out, and_12_out, not_5_out);
  or or_6 (or_6_out, and_11_out, and_9_out);
  D_Flip_Flop d_ff_3 (.D(or_6_out), .clk(Clock), .Q(d_ff_3_q));  // open: Qn, preset, reset
  D_Flip_Flop d_ff_4 (.D(and_10_out), .clk(Clock), .Q(d_ff_4_q));  // open: Qn, preset, reset
  and and_12 (and_12_out, ActivationSignal, d_ff_3_q);
  and and_13 (and_13_out, ActivationSignal, d_ff_4_q);
  or or_7 (CorePIB, and_12_out, and_13_out);
  and and_14 (and_14_out, and_12_out, and_7_out);
  assign CRE_2 = and_12_out ? PEB : 12'bz;  // Controlled_Buffer controlled_buffer_3
  assign CRI_2 = and_12_out ? 8'h90 : 8'bz;  // Controlled_Buffer controlled_buffer_4
  assign PIB = and_12_out ? 8'h80 : 8'bz;  // Controlled_Buffer controlled_buffer_5
  D_Flip_Flop d_ff_5 (.D(or_8_out), .clk(Clock), .Q(d_ff_5_q));  // open: Qn, preset, reset
  or or_8 (or_8_out, and_14_out, and_13_out);
  assign PIB = and_13_out ? 8'h70 : 8'bz;  // Controlled_Buffer controlled_buffer_6
  and and_15 (CoreCLI, ActivationSignal, d_ff_5_q);
  assign CLI = CoreCLI ? 8'h10 : 8'bz;  // Controlled_Buffer controlled_buffer_7
  assign New = CoreCLI ? {PEB[11], 7'b1000000, InternalExpression[3:0]} : 12'bz;  // Controlled_Buffer controlled_buffer_8

  assign CoreCRI = CoreCRE;
  assign CoreExp = CoreCLI;
endmodule
module NewNodeTracker (
  input  N0Request,
  input  N1Request,
  input  N2Request,
  input  N3Request,
  input  N4Request,
  input  N5Request,
  input  N6Request,
  input  N7Request,
  input  N8Request,
  input  N9Request,
  input  NaRequest,
  input  NbRequest,
  input  NcRequest,
  input  NdRequest,
  input  NeRequest,
  input  NfRequest,
  input  N0Clear,
  input  N1Clear,
  input  N2Clear,
  input  N3Clear,
  input  N4Clear,
  input  N5Clear,
  input  N6Clear,
  input  N7Clear,
  input  N8Clear,
  input  N9Clear,
  input  NaClear,
  input  NbClear,
  input  NcClear,
  input  NdClear,
  input  NeClear,
  input  NfClear,
  input  Clock,
  input  [2:0] N1Exp,
  input  [2:0] N2Exp,
  input  [2:0] N3Exp,
  input  [2:0] N4Exp,
  input  [2:0] N5Exp,
  input  [2:0] N6Exp,
  input  [2:0] N7Exp,
  input  [2:0] N8Exp,
  input  [2:0] N9Exp,
  input  [2:0] NaExp,
  input  [2:0] NbExp,
  input  [2:0] NcExp,
  input  [2:0] NdExp,
  input  [2:0] NeExp,
  input  [2:0] NfExp,
  output [3:0] NewNode
);

  wire and_1_out, and_2_out, and_3_out, and_4_out, and_5_out, and_6_out, and_7_out, and_8_out, and_9_out,
       and_10_out, and_11_out, and_12_out, and_13_out, and_14_out, and_15_out, and_16_out, and_17_out,
       and_18_out, and_19_out, and_20_out, and_21_out, and_22_out, and_23_out, and_24_out, and_25_out,
       and_26_out, and_27_out, and_28_out, and_29_out, and_30_out, and_31_out, and_32_out, and_33_out,
       and_34_out, and_35_out, and_36_out, and_37_out, and_38_out, and_39_out, and_40_out, and_41_out,
       and_42_out, and_43_out, and_44_out, and_45_out, and_46_out, and_47_out, and_48_out, and_49_out,
       and_50_out, and_51_out, and_52_out, and_53_out, and_54_out, and_55_out, and_56_out, and_57_out,
       and_58_out, and_59_out, and_60_out, and_61_out, and_62_out, and_63_out, and_64_out, and_65_out,
       and_66_out, and_67_out, and_68_out, and_69_out, and_70_out, and_71_out, and_72_out, and_73_out,
       and_74_out, and_75_out, and_76_out, and_77_out, and_78_out, and_79_out, and_80_out, and_81_out,
       and_82_out, and_83_out, and_84_out, and_85_out, and_86_out, and_87_out, and_88_out, and_89_out,
       and_90_out, and_91_out, and_92_out, and_93_out, and_94_out, and_95_out, and_96_out, and_97_out,
       and_98_out, and_99_out, and_100_out, and_101_out, and_102_out, and_103_out, and_104_out, and_105_out,
       and_106_out, and_107_out, and_108_out, and_109_out, and_110_out, and_111_out, and_112_out,
       and_113_out, and_114_out, and_115_out, and_116_out, and_117_out, and_118_out, and_119_out,
       and_120_out, and_121_out, and_122_out, and_123_out, and_124_out, and_125_out, and_126_out,
       and_127_out, and_128_out, and_129_out, and_130_out, and_131_out, and_132_out, and_133_out,
       and_134_out, and_135_out, and_136_out, and_137_out, and_138_out, and_139_out, and_140_out,
       and_141_out, and_142_out, and_143_out, and_144_out, and_145_out, and_146_out, and_147_out,
       and_148_out, and_149_out, and_150_out, and_151_out, and_152_out, and_153_out, and_154_out,
       and_155_out, and_156_out, and_157_out, and_158_out, and_159_out, and_160_out, and_161_out,
       and_162_out, and_163_out, and_164_out, and_165_out, and_166_out, and_167_out, and_168_out,
       and_169_out, and_170_out, and_171_out, and_172_out, and_173_out, and_174_out, and_175_out,
       and_176_out, and_177_out, and_178_out, and_179_out, and_180_out, and_181_out, and_182_out,
       and_183_out, and_184_out, and_185_out, and_186_out, and_187_out, and_188_out, and_189_out,
       and_190_out, and_191_out, and_192_out, and_193_out, and_194_out, and_195_out, and_196_out,
       and_197_out, and_198_out, and_199_out, and_200_out, and_201_out, and_202_out, and_203_out,
       and_204_out, and_205_out, and_206_out, and_207_out, and_208_out, and_209_out, and_210_out,
       and_211_out, and_212_out, and_213_out, and_214_out, and_215_out, and_216_out, and_217_out,
       and_218_out, and_219_out, and_220_out, and_221_out, and_222_out, and_223_out, and_224_out,
       and_225_out, and_226_out, and_227_out, and_228_out, and_229_out, and_230_out, and_231_out,
       and_232_out, and_233_out, and_234_out, and_235_out, and_236_out, and_237_out, and_238_out,
       and_239_out, and_240_out, and_241_out, and_242_out, and_243_out, and_244_out, and_245_out,
       and_246_out, and_247_out, and_248_out, and_249_out, and_250_out, and_251_out, and_252_out,
       and_253_out, and_254_out, and_255_out, and_256_out, and_257_out, and_258_out, and_259_out,
       and_260_out, and_261_out, and_262_out, and_263_out, and_264_out, and_265_out, and_266_out,
       and_267_out, and_268_out, and_269_out, and_270_out, and_271_out, and_272_out, and_273_out,
       and_274_out, and_275_out, and_276_out, and_277_out, and_278_out, and_279_out, and_280_out,
       and_281_out, and_282_out, and_283_out, and_284_out, and_285_out, and_286_out, and_287_out,
       and_288_out, and_289_out, and_290_out, and_291_out, and_292_out, and_293_out, and_294_out,
       and_295_out, and_296_out, and_297_out, and_298_out, and_299_out, and_300_out, and_301_out,
       and_302_out, and_303_out, and_304_out, and_305_out, and_306_out, and_307_out, and_308_out,
       and_309_out, and_310_out, and_311_out, and_312_out, and_313_out, and_314_out, and_315_out,
       and_316_out, and_317_out, and_318_out, and_319_out, and_320_out, and_321_out, and_322_out,
       and_323_out, and_324_out, and_325_out, and_326_out, and_327_out, and_328_out, and_329_out,
       and_330_out, and_331_out, and_332_out, and_333_out, and_334_out, and_335_out, and_336_out,
       and_337_out, and_338_out, and_339_out, and_340_out, and_341_out, and_342_out, and_343_out,
       and_344_out, and_345_out, and_346_out, and_347_out, and_348_out, and_349_out, and_350_out,
       and_351_out, and_352_out, and_353_out, and_354_out, and_355_out, and_356_out, and_357_out,
       and_358_out, and_359_out, and_360_out, and_361_out, and_362_out, and_363_out, and_364_out,
       and_365_out, and_366_out, and_367_out, and_368_out, and_369_out, and_370_out, and_371_out,
       and_372_out, and_373_out, and_374_out, and_375_out, and_376_out, and_377_out, and_378_out,
       and_379_out, and_380_out, and_381_out, and_382_out, and_383_out, and_384_out, and_385_out,
       and_386_out, and_387_out, and_388_out, and_389_out, and_390_out, and_391_out, and_392_out,
       and_393_out, and_394_out, and_395_out, and_396_out, and_397_out, and_398_out, and_399_out,
       and_400_out, and_401_out, and_402_out, and_403_out, and_404_out, and_405_out, and_406_out,
       and_407_out, and_408_out, and_409_out, and_410_out, and_411_out, and_412_out, and_413_out,
       and_414_out, and_415_out, and_416_out, and_417_out, and_418_out, and_419_out, and_420_out,
       and_421_out, and_422_out, and_423_out, and_424_out, and_425_out, and_426_out, and_427_out,
       and_428_out, and_429_out, and_430_out, and_431_out, and_432_out, and_433_out, and_434_out,
       and_435_out, and_436_out, and_437_out, and_438_out, and_439_out, and_440_out, and_441_out,
       and_442_out, and_443_out, and_444_out, and_445_out, and_446_out, and_447_out, and_448_out,
       and_449_out, and_450_out, and_451_out, and_452_out, and_453_out, and_454_out, and_455_out,
       and_456_out, and_457_out, and_458_out, and_459_out, and_460_out, and_461_out, and_462_out,
       and_463_out, and_464_out, and_465_out, and_466_out, and_467_out, and_468_out, and_469_out,
       and_470_out, and_471_out, and_472_out, and_473_out, and_474_out, and_475_out, and_476_out,
       and_477_out, and_478_out, and_479_out, and_480_out, and_481_out, and_482_out, and_483_out,
       and_484_out, and_485_out, and_486_out, and_487_out, and_488_out, and_489_out, and_490_out,
       and_491_out, and_492_out, and_493_out, and_494_out, and_495_out, and_496_out, and_497_out,
       and_498_out, and_499_out, and_500_out, and_501_out, and_502_out, and_503_out, and_504_out,
       and_505_out, and_506_out, and_507_out, and_508_out, and_509_out, and_510_out, and_511_out,
       and_512_out, and_513_out, and_514_out, and_515_out, and_516_out, and_517_out, and_518_out,
       and_519_out, and_520_out, and_521_out, and_522_out, and_523_out, and_524_out, and_525_out,
       and_526_out, and_527_out, and_528_out, and_529_out, and_530_out, and_531_out, and_532_out,
       and_533_out, and_534_out, and_535_out, and_536_out, and_537_out, and_538_out, and_539_out,
       and_540_out, and_541_out, and_542_out, and_543_out, and_544_out, and_545_out, and_546_out,
       and_547_out, and_548_out, and_549_out, and_550_out, and_551_out, and_552_out, and_553_out,
       and_554_out, and_555_out, and_556_out, and_557_out, and_558_out, and_559_out, and_560_out,
       and_561_out, and_562_out, and_563_out, and_564_out, and_565_out, and_566_out, and_567_out,
       and_568_out, and_569_out, and_570_out, and_571_out, and_572_out, and_573_out, and_574_out,
       and_575_out, and_576_out, and_577_out, and_578_out, and_579_out, and_580_out, and_581_out,
       and_582_out, and_583_out, and_584_out, and_585_out, and_586_out, and_587_out, and_588_out,
       and_589_out, and_590_out, and_591_out, and_592_out, and_593_out, and_594_out, and_595_out,
       and_596_out, d_ff_1_qn, d_ff_2_qn, d_ff_3_qn, d_ff_4_qn, d_ff_5_qn, d_ff_6_qn, d_ff_7_qn, d_ff_8_qn,
       d_ff_9_qn, d_ff_10_qn, d_ff_11_qn, d_ff_12_qn, d_ff_13_qn, d_ff_14_qn, d_ff_15_qn, not_1_out,
       not_3_out, not_20_out, not_21_out, not_23_out, not_40_out, not_41_out, not_43_out, not_60_out,
       not_61_out, not_63_out, not_80_out, not_81_out, not_99_out, not_100_out, not_101_out, not_103_out,
       not_120_out, not_121_out, not_139_out, not_140_out, not_141_out, not_159_out, not_177_out,
       not_195_out, not_213_out, not_231_out, not_249_out, not_267_out, or_1_out, or_2_out, or_3_out,
       or_4_out, or_5_out, or_6_out, or_7_out, or_8_out, or_9_out, or_10_out, or_11_out, or_12_out,
       or_13_out, or_14_out, or_15_out, or_16_out, or_17_out, or_18_out, or_19_out, or_20_out, or_21_out,
       or_22_out, or_23_out, or_24_out, or_25_out, or_26_out, or_27_out, or_28_out, or_29_out, or_30_out,
       or_31_out, or_32_out, or_33_out, or_34_out, or_35_out, or_36_out, or_37_out, or_38_out, or_39_out,
       or_40_out, or_41_out, or_42_out, or_43_out, or_44_out, or_45_out, or_46_out, or_47_out, or_48_out,
       or_49_out, or_50_out, or_51_out, or_52_out, or_53_out, or_54_out, or_55_out, or_56_out, or_57_out,
       or_58_out, or_59_out, or_60_out, or_61_out, or_62_out, or_63_out, or_64_out, or_65_out, or_66_out,
       or_67_out, or_68_out, or_69_out, or_70_out, or_71_out, or_72_out, or_73_out, or_74_out, or_75_out,
       or_76_out, or_77_out, or_78_out, or_79_out, or_80_out, or_81_out, or_82_out, or_83_out, or_84_out,
       or_85_out, or_86_out, or_87_out, or_88_out, or_89_out, or_90_out, or_91_out, or_92_out, or_93_out,
       or_94_out, or_95_out, or_96_out, or_97_out, or_98_out, or_99_out, or_100_out, or_101_out, or_102_out,
       or_103_out, or_104_out, or_105_out, or_106_out, or_107_out, or_108_out, or_109_out, or_110_out,
       or_111_out, or_112_out, or_113_out, or_114_out, or_115_out, or_116_out, or_117_out, or_118_out,
       or_119_out, or_120_out, or_121_out, or_122_out, or_123_out, or_124_out, or_125_out, or_126_out,
       or_127_out, or_128_out, or_129_out, or_130_out, or_131_out, or_132_out, or_133_out, or_134_out,
       or_135_out, or_136_out, or_137_out, or_138_out, or_139_out, or_140_out, or_141_out, or_142_out,
       or_143_out, or_144_out, or_145_out, or_146_out, or_147_out, or_148_out, or_149_out, or_150_out,
       or_151_out, or_152_out, or_153_out, or_154_out, or_155_out, or_156_out, or_157_out, or_158_out,
       or_159_out, or_160_out, or_161_out, or_162_out, or_163_out, or_164_out, or_165_out, or_166_out,
       or_167_out, or_168_out, or_169_out, or_170_out, or_171_out, or_172_out, or_173_out, or_174_out,
       or_175_out, or_176_out, or_177_out, or_178_out, or_179_out, or_180_out, or_181_out, or_182_out,
       or_183_out, or_184_out, or_185_out, or_186_out, or_187_out, or_188_out, or_189_out, or_190_out,
       or_191_out, or_192_out, or_193_out, or_194_out, or_195_out, or_196_out, or_197_out, or_198_out,
       or_199_out, or_200_out, or_201_out, or_202_out, or_203_out, or_204_out, or_205_out, or_206_out,
       or_207_out, or_208_out, or_209_out, or_210_out, or_211_out, or_212_out, or_213_out, or_214_out,
       or_215_out, or_216_out, or_217_out, or_218_out, or_219_out, or_220_out, or_221_out, or_222_out,
       or_223_out, or_224_out, or_225_out, or_226_out, or_227_out, or_228_out, or_229_out, or_230_out,
       or_231_out, or_232_out, or_233_out, or_234_out, or_235_out, or_236_out, or_237_out, or_238_out,
       or_239_out, or_240_out;
  wire [2:0] not_2_out, not_22_out, not_42_out, not_62_out, not_82_out, not_102_out, not_122_out,
       not_142_out, not_160_out, not_178_out, not_196_out, not_214_out, not_232_out, not_250_out,
       not_268_out, xor_1_out, xor_18_out, xor_35_out, xor_52_out, xor_69_out, xor_86_out, xor_103_out,
       xor_120_out, xor_137_out, xor_154_out, xor_171_out, xor_188_out, xor_205_out, xor_222_out, xor_239_out;
  wire [3:0] controlled_buffer_1_out, not_4_out, not_5_out, not_6_out, not_7_out, not_8_out, not_9_out,
       not_10_out, not_11_out, not_12_out, not_13_out, not_14_out, not_15_out, not_16_out, not_17_out,
       not_18_out, not_19_out, not_24_out, not_25_out, not_26_out, not_27_out, not_28_out, not_29_out,
       not_30_out, not_31_out, not_32_out, not_33_out, not_34_out, not_35_out, not_36_out, not_37_out,
       not_38_out, not_39_out, not_44_out, not_45_out, not_46_out, not_47_out, not_48_out, not_49_out,
       not_50_out, not_51_out, not_52_out, not_53_out, not_54_out, not_55_out, not_56_out, not_57_out,
       not_58_out, not_59_out, not_64_out, not_65_out, not_66_out, not_67_out, not_68_out, not_69_out,
       not_70_out, not_71_out, not_72_out, not_73_out, not_74_out, not_75_out, not_76_out, not_77_out,
       not_78_out, not_79_out, not_83_out, not_84_out, not_85_out, not_86_out, not_87_out, not_88_out,
       not_89_out, not_90_out, not_91_out, not_92_out, not_93_out, not_94_out, not_95_out, not_96_out,
       not_97_out, not_98_out, not_104_out, not_105_out, not_106_out, not_107_out, not_108_out, not_109_out,
       not_110_out, not_111_out, not_112_out, not_113_out, not_114_out, not_115_out, not_116_out,
       not_117_out, not_118_out, not_119_out, not_123_out, not_124_out, not_125_out, not_126_out,
       not_127_out, not_128_out, not_129_out, not_130_out, not_131_out, not_132_out, not_133_out,
       not_134_out, not_135_out, not_136_out, not_137_out, not_138_out, not_143_out, not_144_out,
       not_145_out, not_146_out, not_147_out, not_148_out, not_149_out, not_150_out, not_151_out,
       not_152_out, not_153_out, not_154_out, not_155_out, not_156_out, not_157_out, not_158_out,
       not_161_out, not_162_out, not_163_out, not_164_out, not_165_out, not_166_out, not_167_out,
       not_168_out, not_169_out, not_170_out, not_171_out, not_172_out, not_173_out, not_174_out,
       not_175_out, not_176_out, not_179_out, not_180_out, not_181_out, not_182_out, not_183_out,
       not_184_out, not_185_out, not_186_out, not_187_out, not_188_out, not_189_out, not_190_out,
       not_191_out, not_192_out, not_193_out, not_194_out, not_197_out, not_198_out, not_199_out,
       not_200_out, not_201_out, not_202_out, not_203_out, not_204_out, not_205_out, not_206_out,
       not_207_out, not_208_out, not_209_out, not_210_out, not_211_out, not_212_out, not_215_out,
       not_216_out, not_217_out, not_218_out, not_219_out, not_220_out, not_221_out, not_222_out,
       not_223_out, not_224_out, not_225_out, not_226_out, not_227_out, not_228_out, not_229_out,
       not_230_out, not_233_out, not_234_out, not_235_out, not_236_out, not_237_out, not_238_out,
       not_239_out, not_240_out, not_241_out, not_242_out, not_243_out, not_244_out, not_245_out,
       not_246_out, not_247_out, not_248_out, not_251_out, not_252_out, not_253_out, not_254_out,
       not_255_out, not_256_out, not_257_out, not_258_out, not_259_out, not_260_out, not_261_out,
       not_262_out, not_263_out, not_264_out, not_265_out, not_266_out, not_269_out, not_270_out,
       not_271_out, not_272_out, not_273_out, not_274_out, not_275_out, not_276_out, not_277_out,
       not_278_out, not_279_out, not_280_out, not_281_out, not_282_out, not_283_out, not_284_out,
       register_1_q, register_2_q, register_3_q, register_4_q, register_5_q, register_6_q, register_7_q,
       register_8_q, register_9_q, register_10_q, register_11_q, register_12_q, register_13_q, register_14_q,
       register_15_q, xor_2_out, xor_3_out, xor_4_out, xor_5_out, xor_6_out, xor_7_out, xor_8_out, xor_9_out,
       xor_10_out, xor_11_out, xor_12_out, xor_13_out, xor_14_out, xor_15_out, xor_16_out, xor_17_out,
       xor_19_out, xor_20_out, xor_21_out, xor_22_out, xor_23_out, xor_24_out, xor_25_out, xor_26_out,
       xor_27_out, xor_28_out, xor_29_out, xor_30_out, xor_31_out, xor_32_out, xor_33_out, xor_34_out,
       xor_36_out, xor_37_out, xor_38_out, xor_39_out, xor_40_out, xor_41_out, xor_42_out, xor_43_out,
       xor_44_out, xor_45_out, xor_46_out, xor_47_out, xor_48_out, xor_49_out, xor_50_out, xor_51_out,
       xor_53_out, xor_54_out, xor_55_out, xor_56_out, xor_57_out, xor_58_out, xor_59_out, xor_60_out,
       xor_61_out, xor_62_out, xor_63_out, xor_64_out, xor_65_out, xor_66_out, xor_67_out, xor_68_out,
       xor_70_out, xor_71_out, xor_72_out, xor_73_out, xor_74_out, xor_75_out, xor_76_out, xor_77_out,
       xor_78_out, xor_79_out, xor_80_out, xor_81_out, xor_82_out, xor_83_out, xor_84_out, xor_85_out,
       xor_87_out, xor_88_out, xor_89_out, xor_90_out, xor_91_out, xor_92_out, xor_93_out, xor_94_out,
       xor_95_out, xor_96_out, xor_97_out, xor_98_out, xor_99_out, xor_100_out, xor_101_out, xor_102_out,
       xor_104_out, xor_105_out, xor_106_out, xor_107_out, xor_108_out, xor_109_out, xor_110_out,
       xor_111_out, xor_112_out, xor_113_out, xor_114_out, xor_115_out, xor_116_out, xor_117_out,
       xor_118_out, xor_119_out, xor_121_out, xor_122_out, xor_123_out, xor_124_out, xor_125_out,
       xor_126_out, xor_127_out, xor_128_out, xor_129_out, xor_130_out, xor_131_out, xor_132_out,
       xor_133_out, xor_134_out, xor_135_out, xor_136_out, xor_138_out, xor_139_out, xor_140_out,
       xor_141_out, xor_142_out, xor_143_out, xor_144_out, xor_145_out, xor_146_out, xor_147_out,
       xor_148_out, xor_149_out, xor_150_out, xor_151_out, xor_152_out, xor_153_out, xor_155_out,
       xor_156_out, xor_157_out, xor_158_out, xor_159_out, xor_160_out, xor_161_out, xor_162_out,
       xor_163_out, xor_164_out, xor_165_out, xor_166_out, xor_167_out, xor_168_out, xor_169_out,
       xor_170_out, xor_172_out, xor_173_out, xor_174_out, xor_175_out, xor_176_out, xor_177_out,
       xor_178_out, xor_179_out, xor_180_out, xor_181_out, xor_182_out, xor_183_out, xor_184_out,
       xor_185_out, xor_186_out, xor_187_out, xor_189_out, xor_190_out, xor_191_out, xor_192_out,
       xor_193_out, xor_194_out, xor_195_out, xor_196_out, xor_197_out, xor_198_out, xor_199_out,
       xor_200_out, xor_201_out, xor_202_out, xor_203_out, xor_204_out, xor_206_out, xor_207_out,
       xor_208_out, xor_209_out, xor_210_out, xor_211_out, xor_212_out, xor_213_out, xor_214_out,
       xor_215_out, xor_216_out, xor_217_out, xor_218_out, xor_219_out, xor_220_out, xor_221_out,
       xor_223_out, xor_224_out, xor_225_out, xor_226_out, xor_227_out, xor_228_out, xor_229_out,
       xor_230_out, xor_231_out, xor_232_out, xor_233_out, xor_234_out, xor_235_out, xor_236_out,
       xor_237_out, xor_238_out, xor_240_out, xor_241_out, xor_242_out, xor_243_out, xor_244_out,
       xor_245_out, xor_246_out, xor_247_out, xor_248_out, xor_249_out, xor_250_out, xor_251_out,
       xor_252_out, xor_253_out, xor_254_out, xor_255_out;

  assign controlled_buffer_1_out = N0Request ? 4'b0000 : 4'bz;  // Controlled_Buffer controlled_buffer_1
  or or_1 (or_1_out, N0Request, or_2_out);
  not not_1 (not_1_out, N0Request);
  and and_1 (and_1_out, not_1_out, N1Request);
  assign controlled_buffer_1_out = and_1_out ? 4'b0001 : 4'bz;  // Controlled_Buffer controlled_buffer_2
  or or_2 (or_2_out, N1Request, or_18_out);
  and and_2 (and_2_out, and_39_out, or_1_out);
  Register #(.width(4), .trigger("falling")) register_1 (
    .D(controlled_buffer_1_out), .en(and_2_out), .clk(and_3_out), .Q(register_1_q), .clr(or_3_out));
  and and_3 (and_3_out, and_2_out, Clock);
  or or_3 (or_3_out, or_4_out, and_4_out);
  and and_4 (and_4_out, N0Clear, and_22_out);
  or or_4 (or_4_out, or_5_out, and_5_out);
  and and_5 (and_5_out, N1Clear, and_23_out);
  or or_5 (or_5_out, or_6_out, and_6_out);
  and and_6 (and_6_out, N2Clear, and_24_out);
  or or_6 (or_6_out, or_7_out, and_7_out);
  and and_7 (and_7_out, N3Clear, and_25_out);
  or or_7 (or_7_out, or_8_out, and_8_out);
  and and_8 (and_8_out, N4Clear, and_26_out);
  or or_8 (or_8_out, or_9_out, and_9_out);
  and and_9 (and_9_out, N5Clear, and_27_out);
  or or_9 (or_9_out, or_10_out, and_10_out);
  and and_10 (and_10_out, N6Clear, and_28_out);
  or or_10 (or_10_out, or_11_out, and_11_out);
  and and_11 (and_11_out, N7Clear, and_29_out);
  or or_11 (or_11_out, or_12_out, and_12_out);
  and and_12 (and_12_out, N8Clear, and_30_out);
  or or_12 (or_12_out, or_13_out, and_13_out);
  and and_13 (and_13_out, N9Clear, and_31_out);
  or or_13 (or_13_out, or_14_out, and_14_out);
  and and_14 (and_14_out, NaClear, and_32_out);
  or or_14 (or_14_out, or_15_out, and_15_out);
  and and_15 (and_15_out, NbClear, and_33_out);
  or or_15 (or_15_out, or_16_out, and_16_out);
  and and_16 (and_16_out, NcClear, and_34_out);
  or or_16 (or_16_out, or_17_out, and_17_out);
  and and_17 (and_17_out, NdClear, and_35_out);
  or or_17 (or_17_out, and_19_out, and_18_out);
  and and_18 (and_18_out, NeClear, and_36_out);
  and and_19 (and_19_out, NfClear, and_37_out);
  and and_20 (and_20_out, not_2_out[2], not_2_out[1], not_2_out[0]);
  assign not_2_out = ~xor_1_out;  // NOT_Gate not_2, 3 bits wide
  assign xor_1_out = 3'b000 ^ N1Exp;  // XOR_Gate xor_1, 3 bits wide
  and and_21 (and_21_out, not_1_out, not_3_out);
  not not_3 (not_3_out, N1Request);
  assign controlled_buffer_1_out = and_38_out ? 4'b0010 : 4'bz;  // Controlled_Buffer controlled_buffer_3
  D_Flip_Flop #(.trigger("falling")) d_ff_1 (
    .D(and_2_out), .clk(and_3_out), .Qn(d_ff_1_qn), .reset(or_3_out));  // open: Q, preset
  and and_22 (and_22_out, not_4_out[3], not_4_out[2], not_4_out[1], not_4_out[0]);
  assign xor_2_out = 4'b0000 ^ register_1_q;  // XOR_Gate xor_2, 4 bits wide
  assign not_4_out = ~xor_2_out;  // NOT_Gate not_4, 4 bits wide
  and and_23 (and_23_out, not_5_out[3], not_5_out[2], not_5_out[1], not_5_out[0]);
  assign xor_3_out = 4'b0001 ^ register_1_q;  // XOR_Gate xor_3, 4 bits wide
  assign not_5_out = ~xor_3_out;  // NOT_Gate not_5, 4 bits wide
  and and_24 (and_24_out, not_6_out[3], not_6_out[2], not_6_out[1], not_6_out[0]);
  assign xor_4_out = 4'b0010 ^ register_1_q;  // XOR_Gate xor_4, 4 bits wide
  assign not_6_out = ~xor_4_out;  // NOT_Gate not_6, 4 bits wide
  and and_25 (and_25_out, not_7_out[3], not_7_out[2], not_7_out[1], not_7_out[0]);
  assign xor_5_out = 4'b0011 ^ register_1_q;  // XOR_Gate xor_5, 4 bits wide
  assign not_7_out = ~xor_5_out;  // NOT_Gate not_7, 4 bits wide
  and and_26 (and_26_out, not_8_out[3], not_8_out[2], not_8_out[1], not_8_out[0]);
  assign xor_6_out = 4'b0100 ^ register_1_q;  // XOR_Gate xor_6, 4 bits wide
  assign not_8_out = ~xor_6_out;  // NOT_Gate not_8, 4 bits wide
  and and_27 (and_27_out, not_9_out[3], not_9_out[2], not_9_out[1], not_9_out[0]);
  assign xor_7_out = 4'b0101 ^ register_1_q;  // XOR_Gate xor_7, 4 bits wide
  assign not_9_out = ~xor_7_out;  // NOT_Gate not_9, 4 bits wide
  and and_28 (and_28_out, not_10_out[3], not_10_out[2], not_10_out[1], not_10_out[0]);
  assign xor_8_out = 4'b0110 ^ register_1_q;  // XOR_Gate xor_8, 4 bits wide
  assign not_10_out = ~xor_8_out;  // NOT_Gate not_10, 4 bits wide
  and and_29 (and_29_out, not_11_out[3], not_11_out[2], not_11_out[1], not_11_out[0]);
  assign xor_9_out = 4'b0111 ^ register_1_q;  // XOR_Gate xor_9, 4 bits wide
  assign not_11_out = ~xor_9_out;  // NOT_Gate not_11, 4 bits wide
  and and_30 (and_30_out, not_12_out[3], not_12_out[2], not_12_out[1], not_12_out[0]);
  assign xor_10_out = 4'b1000 ^ register_1_q;  // XOR_Gate xor_10, 4 bits wide
  assign not_12_out = ~xor_10_out;  // NOT_Gate not_12, 4 bits wide
  and and_31 (and_31_out, not_13_out[3], not_13_out[2], not_13_out[1], not_13_out[0]);
  assign xor_11_out = 4'b1001 ^ register_1_q;  // XOR_Gate xor_11, 4 bits wide
  assign not_13_out = ~xor_11_out;  // NOT_Gate not_13, 4 bits wide
  and and_32 (and_32_out, not_14_out[3], not_14_out[2], not_14_out[1], not_14_out[0]);
  assign xor_12_out = 4'b1010 ^ register_1_q;  // XOR_Gate xor_12, 4 bits wide
  assign not_14_out = ~xor_12_out;  // NOT_Gate not_14, 4 bits wide
  and and_33 (and_33_out, not_15_out[3], not_15_out[2], not_15_out[1], not_15_out[0]);
  assign xor_13_out = 4'b1011 ^ register_1_q;  // XOR_Gate xor_13, 4 bits wide
  assign not_15_out = ~xor_13_out;  // NOT_Gate not_15, 4 bits wide
  and and_34 (and_34_out, not_16_out[3], not_16_out[2], not_16_out[1], not_16_out[0]);
  assign xor_14_out = 4'b1100 ^ register_1_q;  // XOR_Gate xor_14, 4 bits wide
  assign not_16_out = ~xor_14_out;  // NOT_Gate not_16, 4 bits wide
  and and_35 (and_35_out, not_17_out[3], not_17_out[2], not_17_out[1], not_17_out[0]);
  assign xor_15_out = 4'b1101 ^ register_1_q;  // XOR_Gate xor_15, 4 bits wide
  assign not_17_out = ~xor_15_out;  // NOT_Gate not_17, 4 bits wide
  and and_36 (and_36_out, not_18_out[3], not_18_out[2], not_18_out[1], not_18_out[0]);
  assign xor_16_out = 4'b1110 ^ register_1_q;  // XOR_Gate xor_16, 4 bits wide
  assign not_18_out = ~xor_16_out;  // NOT_Gate not_18, 4 bits wide
  and and_37 (and_37_out, not_19_out[3], not_19_out[2], not_19_out[1], not_19_out[0]);
  assign xor_17_out = 4'b1111 ^ register_1_q;  // XOR_Gate xor_17, 4 bits wide
  assign not_19_out = ~xor_17_out;  // NOT_Gate not_19, 4 bits wide
  not not_20 (not_20_out, N2Request);
  and and_38 (and_38_out, and_21_out, N2Request);
  or or_18 (or_18_out, N2Request, or_19_out);
  not not_21 (not_21_out, and_39_out);
  and and_39 (and_39_out, d_ff_1_qn, and_20_out);
  assign NewNode = and_39_out ? 4'b0001 : 4'bz;  // Controlled_Buffer controlled_buffer_4
  and and_40 (and_40_out, and_21_out, not_20_out);
  assign controlled_buffer_1_out = and_44_out ? 4'b0011 : 4'bz;  // Controlled_Buffer controlled_buffer_5
  or or_19 (or_19_out, N3Request, or_35_out);
  and and_41 (and_41_out, and_79_out, or_1_out);
  and and_42 (and_42_out, and_41_out, Clock);
  or or_20 (or_20_out, or_21_out, and_45_out);
  or or_21 (or_21_out, or_22_out, and_47_out);
  or or_22 (or_22_out, or_23_out, and_49_out);
  or or_23 (or_23_out, or_24_out, and_51_out);
  or or_24 (or_24_out, or_25_out, and_53_out);
  or or_25 (or_25_out, or_26_out, and_55_out);
  or or_26 (or_26_out, or_27_out, and_57_out);
  or or_27 (or_27_out, or_28_out, and_59_out);
  or or_28 (or_28_out, or_29_out, and_61_out);
  or or_29 (or_29_out, or_30_out, and_63_out);
  or or_30 (or_30_out, or_31_out, and_65_out);
  or or_31 (or_31_out, or_32_out, and_67_out);
  or or_32 (or_32_out, or_33_out, and_69_out);
  or or_33 (or_33_out, or_34_out, and_71_out);
  or or_34 (or_34_out, and_75_out, and_73_out);
  and and_43 (and_43_out, not_22_out[2], not_22_out[1], not_22_out[0]);
  assign not_22_out = ~xor_18_out;  // NOT_Gate not_22, 3 bits wide
  assign xor_18_out = 3'b000 ^ N2Exp;  // XOR_Gate xor_18, 3 bits wide
  not not_23 (not_23_out, N3Request);
  and and_44 (and_44_out, and_40_out, N3Request);
  D_Flip_Flop #(.trigger("falling")) d_ff_2 (
    .D(and_41_out), .clk(and_42_out), .Qn(d_ff_2_qn), .reset(or_20_out));  // open: Q, preset
  Register #(.width(4)) register_2 (
    .D(controlled_buffer_1_out), .en(and_41_out), .clk(and_42_out), .Q(register_2_q), .clr(or_20_out));
  and and_45 (and_45_out, N0Clear, and_46_out);
  and and_46 (and_46_out, not_24_out[3], not_24_out[2], not_24_out[1], not_24_out[0]);
  assign xor_19_out = 4'b0000 ^ register_2_q;  // XOR_Gate xor_19, 4 bits wide
  assign not_24_out = ~xor_19_out;  // NOT_Gate not_24, 4 bits wide
  and and_47 (and_47_out, N1Clear, and_48_out);
  and and_48 (and_48_out, not_25_out[3], not_25_out[2], not_25_out[1], not_25_out[0]);
  assign xor_20_out = 4'b0001 ^ register_2_q;  // XOR_Gate xor_20, 4 bits wide
  assign not_25_out = ~xor_20_out;  // NOT_Gate not_25, 4 bits wide
  and and_49 (and_49_out, N2Clear, and_50_out);
  and and_50 (and_50_out, not_26_out[3], not_26_out[2], not_26_out[1], not_26_out[0]);
  assign xor_21_out = 4'b0010 ^ register_2_q;  // XOR_Gate xor_21, 4 bits wide
  assign not_26_out = ~xor_21_out;  // NOT_Gate not_26, 4 bits wide
  and and_51 (and_51_out, N3Clear, and_52_out);
  and and_52 (and_52_out, not_27_out[3], not_27_out[2], not_27_out[1], not_27_out[0]);
  assign xor_22_out = 4'b0011 ^ register_2_q;  // XOR_Gate xor_22, 4 bits wide
  assign not_27_out = ~xor_22_out;  // NOT_Gate not_27, 4 bits wide
  and and_53 (and_53_out, N4Clear, and_54_out);
  and and_54 (and_54_out, not_28_out[3], not_28_out[2], not_28_out[1], not_28_out[0]);
  assign xor_23_out = 4'b0100 ^ register_2_q;  // XOR_Gate xor_23, 4 bits wide
  assign not_28_out = ~xor_23_out;  // NOT_Gate not_28, 4 bits wide
  and and_55 (and_55_out, N5Clear, and_56_out);
  and and_56 (and_56_out, not_29_out[3], not_29_out[2], not_29_out[1], not_29_out[0]);
  assign xor_24_out = 4'b0101 ^ register_2_q;  // XOR_Gate xor_24, 4 bits wide
  assign not_29_out = ~xor_24_out;  // NOT_Gate not_29, 4 bits wide
  and and_57 (and_57_out, N6Clear, and_58_out);
  and and_58 (and_58_out, not_30_out[3], not_30_out[2], not_30_out[1], not_30_out[0]);
  assign xor_25_out = 4'b0110 ^ register_2_q;  // XOR_Gate xor_25, 4 bits wide
  assign not_30_out = ~xor_25_out;  // NOT_Gate not_30, 4 bits wide
  and and_59 (and_59_out, N7Clear, and_60_out);
  and and_60 (and_60_out, not_31_out[3], not_31_out[2], not_31_out[1], not_31_out[0]);
  assign xor_26_out = 4'b0111 ^ register_2_q;  // XOR_Gate xor_26, 4 bits wide
  assign not_31_out = ~xor_26_out;  // NOT_Gate not_31, 4 bits wide
  and and_61 (and_61_out, N8Clear, and_62_out);
  and and_62 (and_62_out, not_32_out[3], not_32_out[2], not_32_out[1], not_32_out[0]);
  assign xor_27_out = 4'b1000 ^ register_2_q;  // XOR_Gate xor_27, 4 bits wide
  assign not_32_out = ~xor_27_out;  // NOT_Gate not_32, 4 bits wide
  and and_63 (and_63_out, N9Clear, and_64_out);
  and and_64 (and_64_out, not_33_out[3], not_33_out[2], not_33_out[1], not_33_out[0]);
  assign xor_28_out = 4'b1001 ^ register_2_q;  // XOR_Gate xor_28, 4 bits wide
  assign not_33_out = ~xor_28_out;  // NOT_Gate not_33, 4 bits wide
  and and_65 (and_65_out, NaClear, and_66_out);
  and and_66 (and_66_out, not_34_out[3], not_34_out[2], not_34_out[1], not_34_out[0]);
  assign xor_29_out = 4'b1010 ^ register_2_q;  // XOR_Gate xor_29, 4 bits wide
  assign not_34_out = ~xor_29_out;  // NOT_Gate not_34, 4 bits wide
  and and_67 (and_67_out, NbClear, and_68_out);
  and and_68 (and_68_out, not_35_out[3], not_35_out[2], not_35_out[1], not_35_out[0]);
  assign xor_30_out = 4'b1011 ^ register_2_q;  // XOR_Gate xor_30, 4 bits wide
  assign not_35_out = ~xor_30_out;  // NOT_Gate not_35, 4 bits wide
  and and_69 (and_69_out, NcClear, and_70_out);
  and and_70 (and_70_out, not_36_out[3], not_36_out[2], not_36_out[1], not_36_out[0]);
  assign xor_31_out = 4'b1100 ^ register_2_q;  // XOR_Gate xor_31, 4 bits wide
  assign not_36_out = ~xor_31_out;  // NOT_Gate not_36, 4 bits wide
  and and_71 (and_71_out, NdClear, and_72_out);
  and and_72 (and_72_out, not_37_out[3], not_37_out[2], not_37_out[1], not_37_out[0]);
  assign xor_32_out = 4'b1101 ^ register_2_q;  // XOR_Gate xor_32, 4 bits wide
  assign not_37_out = ~xor_32_out;  // NOT_Gate not_37, 4 bits wide
  and and_73 (and_73_out, NeClear, and_74_out);
  and and_74 (and_74_out, not_38_out[3], not_38_out[2], not_38_out[1], not_38_out[0]);
  assign xor_33_out = 4'b1110 ^ register_2_q;  // XOR_Gate xor_33, 4 bits wide
  assign not_38_out = ~xor_33_out;  // NOT_Gate not_38, 4 bits wide
  and and_75 (and_75_out, NfClear, and_76_out);
  and and_76 (and_76_out, not_39_out[3], not_39_out[2], not_39_out[1], not_39_out[0]);
  assign xor_34_out = 4'b1111 ^ register_2_q;  // XOR_Gate xor_34, 4 bits wide
  assign not_39_out = ~xor_34_out;  // NOT_Gate not_39, 4 bits wide
  and and_77 (and_77_out, and_40_out, not_23_out);
  and and_78 (and_78_out, and_77_out, N4Request);
  assign controlled_buffer_1_out = and_78_out ? 4'b0100 : 4'bz;  // Controlled_Buffer controlled_buffer_6
  or or_35 (or_35_out, N4Request, or_36_out);
  and and_79 (and_79_out, not_21_out, and_80_out);
  and and_80 (and_80_out, d_ff_2_qn, and_43_out);
  assign NewNode = and_79_out ? 4'b0010 : 4'bz;  // Controlled_Buffer controlled_buffer_7
  and and_81 (and_81_out, and_77_out, not_40_out);
  not not_40 (not_40_out, N4Request);
  and and_82 (and_82_out, not_21_out, not_41_out);
  not not_41 (not_41_out, and_79_out);
  and and_83 (and_83_out, and_122_out, or_1_out);
  and and_84 (and_84_out, and_83_out, Clock);
  and and_85 (and_85_out, not_42_out[2], not_42_out[1], not_42_out[0]);
  assign not_42_out = ~xor_35_out;  // NOT_Gate not_42, 3 bits wide
  assign xor_35_out = 3'b000 ^ N3Exp;  // XOR_Gate xor_35, 3 bits wide
  and and_86 (and_86_out, and_81_out, N5Request);
  assign controlled_buffer_1_out = and_86_out ? 4'b0101 : 4'bz;  // Controlled_Buffer controlled_buffer_8
  or or_36 (or_36_out, N5Request, or_52_out);
  D_Flip_Flop #(.trigger("falling")) d_ff_3 (
    .D(and_83_out), .clk(and_84_out), .Qn(d_ff_3_qn), .reset(or_37_out));  // open: Q, preset
  Register #(.width(4)) register_3 (
    .D(controlled_buffer_1_out), .en(and_83_out), .clk(and_84_out), .Q(register_3_q), .clr(or_37_out));
  or or_37 (or_37_out, or_38_out, and_87_out);
  and and_87 (and_87_out, N0Clear, and_88_out);
  and and_88 (and_88_out, not_44_out[3], not_44_out[2], not_44_out[1], not_44_out[0]);
  or or_38 (or_38_out, or_39_out, and_89_out);
  and and_89 (and_89_out, N1Clear, and_90_out);
  and and_90 (and_90_out, not_45_out[3], not_45_out[2], not_45_out[1], not_45_out[0]);
  or or_39 (or_39_out, or_40_out, and_91_out);
  and and_91 (and_91_out, N2Clear, and_92_out);
  and and_92 (and_92_out, not_46_out[3], not_46_out[2], not_46_out[1], not_46_out[0]);
  or or_40 (or_40_out, or_41_out, and_93_out);
  and and_93 (and_93_out, N3Clear, and_94_out);
  and and_94 (and_94_out, not_47_out[3], not_47_out[2], not_47_out[1], not_47_out[0]);
  or or_41 (or_41_out, or_42_out, and_95_out);
  and and_95 (and_95_out, N4Clear, and_96_out);
  and and_96 (and_96_out, not_48_out[3], not_48_out[2], not_48_out[1], not_48_out[0]);
  or or_42 (or_42_out, or_43_out, and_97_out);
  and and_97 (and_97_out, N5Clear, and_98_out);
  and and_98 (and_98_out, not_49_out[3], not_49_out[2], not_49_out[1], not_49_out[0]);
  or or_43 (or_43_out, or_44_out, and_99_out);
  and and_99 (and_99_out, N6Clear, and_100_out);
  and and_100 (and_100_out, not_50_out[3], not_50_out[2], not_50_out[1], not_50_out[0]);
  or or_44 (or_44_out, or_45_out, and_101_out);
  and and_101 (and_101_out, N7Clear, and_102_out);
  and and_102 (and_102_out, not_51_out[3], not_51_out[2], not_51_out[1], not_51_out[0]);
  or or_45 (or_45_out, or_46_out, and_103_out);
  and and_103 (and_103_out, N8Clear, and_104_out);
  and and_104 (and_104_out, not_52_out[3], not_52_out[2], not_52_out[1], not_52_out[0]);
  or or_46 (or_46_out, or_47_out, and_105_out);
  and and_105 (and_105_out, N9Clear, and_106_out);
  and and_106 (and_106_out, not_53_out[3], not_53_out[2], not_53_out[1], not_53_out[0]);
  or or_47 (or_47_out, or_48_out, and_107_out);
  and and_107 (and_107_out, NaClear, and_108_out);
  and and_108 (and_108_out, not_54_out[3], not_54_out[2], not_54_out[1], not_54_out[0]);
  or or_48 (or_48_out, or_49_out, and_109_out);
  and and_109 (and_109_out, NbClear, and_110_out);
  and and_110 (and_110_out, not_55_out[3], not_55_out[2], not_55_out[1], not_55_out[0]);
  or or_49 (or_49_out, or_50_out, and_111_out);
  and and_111 (and_111_out, NcClear, and_112_out);
  and and_112 (and_112_out, not_56_out[3], not_56_out[2], not_56_out[1], not_56_out[0]);
  or or_50 (or_50_out, or_51_out, and_113_out);
  and and_113 (and_113_out, NdClear, and_114_out);
  and and_114 (and_114_out, not_57_out[3], not_57_out[2], not_57_out[1], not_57_out[0]);
  or or_51 (or_51_out, and_117_out, and_115_out);
  and and_115 (and_115_out, NeClear, and_116_out);
  and and_116 (and_116_out, not_58_out[3], not_58_out[2], not_58_out[1], not_58_out[0]);
  and and_117 (and_117_out, NfClear, and_118_out);
  and and_118 (and_118_out, not_59_out[3], not_59_out[2], not_59_out[1], not_59_out[0]);
  and and_119 (and_119_out, and_81_out, not_43_out);
  not not_43 (not_43_out, N5Request);
  assign controlled_buffer_1_out = and_121_out ? 4'b0110 : 4'bz;  // Controlled_Buffer controlled_buffer_9
  and and_120 (and_120_out, d_ff_3_qn, and_85_out);
  assign xor_36_out = 4'b0000 ^ register_3_q;  // XOR_Gate xor_36, 4 bits wide
  assign not_44_out = ~xor_36_out;  // NOT_Gate not_44, 4 bits wide
  assign xor_37_out = 4'b0001 ^ register_3_q;  // XOR_Gate xor_37, 4 bits wide
  assign not_45_out = ~xor_37_out;  // NOT_Gate not_45, 4 bits wide
  assign xor_38_out = 4'b0010 ^ register_3_q;  // XOR_Gate xor_38, 4 bits wide
  assign not_46_out = ~xor_38_out;  // NOT_Gate not_46, 4 bits wide
  assign xor_39_out = 4'b0011 ^ register_3_q;  // XOR_Gate xor_39, 4 bits wide
  assign not_47_out = ~xor_39_out;  // NOT_Gate not_47, 4 bits wide
  assign xor_40_out = 4'b0100 ^ register_3_q;  // XOR_Gate xor_40, 4 bits wide
  assign not_48_out = ~xor_40_out;  // NOT_Gate not_48, 4 bits wide
  assign xor_41_out = 4'b0101 ^ register_3_q;  // XOR_Gate xor_41, 4 bits wide
  assign not_49_out = ~xor_41_out;  // NOT_Gate not_49, 4 bits wide
  assign xor_42_out = 4'b0110 ^ register_3_q;  // XOR_Gate xor_42, 4 bits wide
  assign not_50_out = ~xor_42_out;  // NOT_Gate not_50, 4 bits wide
  assign xor_43_out = 4'b0111 ^ register_3_q;  // XOR_Gate xor_43, 4 bits wide
  assign not_51_out = ~xor_43_out;  // NOT_Gate not_51, 4 bits wide
  assign xor_44_out = 4'b1000 ^ register_3_q;  // XOR_Gate xor_44, 4 bits wide
  assign not_52_out = ~xor_44_out;  // NOT_Gate not_52, 4 bits wide
  assign xor_45_out = 4'b1001 ^ register_3_q;  // XOR_Gate xor_45, 4 bits wide
  assign not_53_out = ~xor_45_out;  // NOT_Gate not_53, 4 bits wide
  assign xor_46_out = 4'b1010 ^ register_3_q;  // XOR_Gate xor_46, 4 bits wide
  assign not_54_out = ~xor_46_out;  // NOT_Gate not_54, 4 bits wide
  assign xor_47_out = 4'b1011 ^ register_3_q;  // XOR_Gate xor_47, 4 bits wide
  assign not_55_out = ~xor_47_out;  // NOT_Gate not_55, 4 bits wide
  assign xor_48_out = 4'b1100 ^ register_3_q;  // XOR_Gate xor_48, 4 bits wide
  assign not_56_out = ~xor_48_out;  // NOT_Gate not_56, 4 bits wide
  assign xor_49_out = 4'b1101 ^ register_3_q;  // XOR_Gate xor_49, 4 bits wide
  assign not_57_out = ~xor_49_out;  // NOT_Gate not_57, 4 bits wide
  assign xor_50_out = 4'b1110 ^ register_3_q;  // XOR_Gate xor_50, 4 bits wide
  assign not_58_out = ~xor_50_out;  // NOT_Gate not_58, 4 bits wide
  assign xor_51_out = 4'b1111 ^ register_3_q;  // XOR_Gate xor_51, 4 bits wide
  assign not_59_out = ~xor_51_out;  // NOT_Gate not_59, 4 bits wide
  not not_60 (not_60_out, N6Request);
  and and_121 (and_121_out, and_119_out, N6Request);
  or or_52 (or_52_out, N6Request, or_53_out);
  not not_61 (not_61_out, and_122_out);
  and and_122 (and_122_out, and_82_out, and_120_out);
  assign NewNode = and_122_out ? 4'b0011 : 4'bz;  // Controlled_Buffer controlled_buffer_10
  assign not_62_out = ~xor_52_out;  // NOT_Gate not_62, 3 bits wide
  assign xor_52_out = 3'b000 ^ N4Exp;  // XOR_Gate xor_52, 3 bits wide
  and and_123 (and_123_out, and_119_out, not_60_out);
  assign controlled_buffer_1_out = and_160_out ? 4'b0111 : 4'bz;  // Controlled_Buffer controlled_buffer_11
  or or_53 (or_53_out, N7Request, or_69_out);
  and and_124 (and_124_out, and_82_out, not_61_out);
  D_Flip_Flop #(.trigger("falling")) d_ff_4 (
    .D(and_125_out), .clk(and_126_out), .Qn(d_ff_4_qn), .reset(or_54_out));  // open: Q, preset
  and and_125 (and_125_out, and_163_out, or_1_out);
  Register #(.width(4)) register_4 (
    .D(controlled_buffer_1_out), .en(and_125_out), .clk(and_126_out), .Q(register_4_q), .clr(or_54_out));
  and and_126 (and_126_out, and_125_out, Clock);
  or or_54 (or_54_out, or_55_out, and_127_out);
  and and_127 (and_127_out, N0Clear, and_128_out);
  and and_128 (and_128_out, not_64_out[3], not_64_out[2], not_64_out[1], not_64_out[0]);
  or or_55 (or_55_out, or_56_out, and_129_out);
  and and_129 (and_129_out, N1Clear, and_130_out);
  and and_130 (and_130_out, not_65_out[3], not_65_out[2], not_65_out[1], not_65_out[0]);
  or or_56 (or_56_out, or_57_out, and_131_out);
  and and_131 (and_131_out, N2Clear, and_132_out);
  and and_132 (and_132_out, not_66_out[3], not_66_out[2], not_66_out[1], not_66_out[0]);
  or or_57 (or_57_out, or_58_out, and_133_out);
  and and_133 (and_133_out, N3Clear, and_134_out);
  and and_134 (and_134_out, not_67_out[3], not_67_out[2], not_67_out[1], not_67_out[0]);
  or or_58 (or_58_out, or_59_out, and_135_out);
  and and_135 (and_135_out, N4Clear, and_136_out);
  and and_136 (and_136_out, not_68_out[3], not_68_out[2], not_68_out[1], not_68_out[0]);
  or or_59 (or_59_out, or_60_out, and_137_out);
  and and_137 (and_137_out, N5Clear, and_138_out);
  and and_138 (and_138_out, not_69_out[3], not_69_out[2], not_69_out[1], not_69_out[0]);
  or or_60 (or_60_out, or_61_out, and_139_out);
  and and_139 (and_139_out, N6Clear, and_140_out);
  and and_140 (and_140_out, not_70_out[3], not_70_out[2], not_70_out[1], not_70_out[0]);
  or or_61 (or_61_out, or_62_out, and_141_out);
  and and_141 (and_141_out, N7Clear, and_142_out);
  and and_142 (and_142_out, not_71_out[3], not_71_out[2], not_71_out[1], not_71_out[0]);
  or or_62 (or_62_out, or_63_out, and_143_out);
  and and_143 (and_143_out, N8Clear, and_144_out);
  and and_144 (and_144_out, not_72_out[3], not_72_out[2], not_72_out[1], not_72_out[0]);
  or or_63 (or_63_out, or_64_out, and_145_out);
  and and_145 (and_145_out, N9Clear, and_146_out);
  and and_146 (and_146_out, not_73_out[3], not_73_out[2], not_73_out[1], not_73_out[0]);
  or or_64 (or_64_out, or_65_out, and_147_out);
  and and_147 (and_147_out, NaClear, and_148_out);
  and and_148 (and_148_out, not_74_out[3], not_74_out[2], not_74_out[1], not_74_out[0]);
  or or_65 (or_65_out, or_66_out, and_149_out);
  and and_149 (and_149_out, NbClear, and_150_out);
  and and_150 (and_150_out, not_75_out[3], not_75_out[2], not_75_out[1], not_75_out[0]);
  or or_66 (or_66_out, or_67_out, and_151_out);
  and and_151 (and_151_out, NcClear, and_152_out);
  and and_152 (and_152_out, not_76_out[3], not_76_out[2], not_76_out[1], not_76_out[0]);
  or or_67 (or_67_out, or_68_out, and_153_out);
  and and_153 (and_153_out, NdClear, and_154_out);
  and and_154 (and_154_out, not_77_out[3], not_77_out[2], not_77_out[1], not_77_out[0]);
  or or_68 (or_68_out, and_157_out, and_155_out);
  and and_155 (and_155_out, NeClear, and_156_out);
  and and_156 (and_156_out, not_78_out[3], not_78_out[2], not_78_out[1], not_78_out[0]);
  and and_157 (and_157_out, NfClear, and_158_out);
  and and_158 (and_158_out, not_79_out[3], not_79_out[2], not_79_out[1], not_79_out[0]);
  and and_159 (and_159_out, not_62_out[2], not_62_out[1], not_62_out[0]);
  not not_63 (not_63_out, N7Request);
  and and_160 (and_160_out, and_123_out, N7Request);
  assign xor_53_out = 4'b0000 ^ register_4_q;  // XOR_Gate xor_53, 4 bits wide
  assign not_64_out = ~xor_53_out;  // NOT_Gate not_64, 4 bits wide
  assign xor_54_out = 4'b0001 ^ register_4_q;  // XOR_Gate xor_54, 4 bits wide
  assign not_65_out = ~xor_54_out;  // NOT_Gate not_65, 4 bits wide
  assign xor_55_out = 4'b0010 ^ register_4_q;  // XOR_Gate xor_55, 4 bits wide
  assign not_66_out = ~xor_55_out;  // NOT_Gate not_66, 4 bits wide
  assign xor_56_out = 4'b0011 ^ register_4_q;  // XOR_Gate xor_56, 4 bits wide
  assign not_67_out = ~xor_56_out;  // NOT_Gate not_67, 4 bits wide
  assign xor_57_out = 4'b0100 ^ register_4_q;  // XOR_Gate xor_57, 4 bits wide
  assign not_68_out = ~xor_57_out;  // NOT_Gate not_68, 4 bits wide
  assign xor_58_out = 4'b0101 ^ register_4_q;  // XOR_Gate xor_58, 4 bits wide
  assign not_69_out = ~xor_58_out;  // NOT_Gate not_69, 4 bits wide
  assign xor_59_out = 4'b0110 ^ register_4_q;  // XOR_Gate xor_59, 4 bits wide
  assign not_70_out = ~xor_59_out;  // NOT_Gate not_70, 4 bits wide
  assign xor_60_out = 4'b0111 ^ register_4_q;  // XOR_Gate xor_60, 4 bits wide
  assign not_71_out = ~xor_60_out;  // NOT_Gate not_71, 4 bits wide
  assign xor_61_out = 4'b1000 ^ register_4_q;  // XOR_Gate xor_61, 4 bits wide
  assign not_72_out = ~xor_61_out;  // NOT_Gate not_72, 4 bits wide
  assign xor_62_out = 4'b1001 ^ register_4_q;  // XOR_Gate xor_62, 4 bits wide
  assign not_73_out = ~xor_62_out;  // NOT_Gate not_73, 4 bits wide
  assign xor_63_out = 4'b1010 ^ register_4_q;  // XOR_Gate xor_63, 4 bits wide
  assign not_74_out = ~xor_63_out;  // NOT_Gate not_74, 4 bits wide
  assign xor_64_out = 4'b1011 ^ register_4_q;  // XOR_Gate xor_64, 4 bits wide
  assign not_75_out = ~xor_64_out;  // NOT_Gate not_75, 4 bits wide
  assign xor_65_out = 4'b1100 ^ register_4_q;  // XOR_Gate xor_65, 4 bits wide
  assign not_76_out = ~xor_65_out;  // NOT_Gate not_76, 4 bits wide
  assign xor_66_out = 4'b1101 ^ register_4_q;  // XOR_Gate xor_66, 4 bits wide
  assign not_77_out = ~xor_66_out;  // NOT_Gate not_77, 4 bits wide
  assign xor_67_out = 4'b1110 ^ register_4_q;  // XOR_Gate xor_67, 4 bits wide
  assign not_78_out = ~xor_67_out;  // NOT_Gate not_78, 4 bits wide
  assign xor_68_out = 4'b1111 ^ register_4_q;  // XOR_Gate xor_68, 4 bits wide
  assign not_79_out = ~xor_68_out;  // NOT_Gate not_79, 4 bits wide
  and and_161 (and_161_out, and_123_out, not_63_out);
  and and_162 (and_162_out, and_161_out, N8Request);
  assign controlled_buffer_1_out = and_162_out ? 4'b1000 : 4'bz;  // Controlled_Buffer controlled_buffer_12
  or or_69 (or_69_out, N8Request, or_70_out);
  and and_163 (and_163_out, and_124_out, and_164_out);
  and and_164 (and_164_out, d_ff_4_qn, and_159_out);
  assign NewNode = and_163_out ? 4'b0100 : 4'bz;  // Controlled_Buffer controlled_buffer_13
  and and_165 (and_165_out, and_161_out, not_80_out);
  not not_80 (not_80_out, N8Request);
  and and_166 (and_166_out, and_124_out, not_81_out);
  not not_81 (not_81_out, and_163_out);
  and and_167 (and_167_out, and_204_out, or_1_out);
  and and_168 (and_168_out, and_167_out, Clock);
  and and_169 (and_169_out, not_82_out[2], not_82_out[1], not_82_out[0]);
  assign not_82_out = ~xor_69_out;  // NOT_Gate not_82, 3 bits wide
  assign xor_69_out = 3'b000 ^ N5Exp;  // XOR_Gate xor_69, 3 bits wide
  and and_170 (and_170_out, and_165_out, N9Request);
  assign controlled_buffer_1_out = and_170_out ? 4'b1001 : 4'bz;  // Controlled_Buffer controlled_buffer_14
  or or_70 (or_70_out, N9Request, or_86_out);
  D_Flip_Flop #(.trigger("falling")) d_ff_5 (
    .D(and_167_out), .clk(and_168_out), .Qn(d_ff_5_qn), .reset(or_71_out));  // open: Q, preset
  Register #(.width(4)) register_5 (
    .D(controlled_buffer_1_out), .en(and_167_out), .clk(and_168_out), .Q(register_5_q), .clr(or_71_out));
  or or_71 (or_71_out, or_72_out, and_171_out);
  and and_171 (and_171_out, N0Clear, and_172_out);
  and and_172 (and_172_out, not_83_out[3], not_83_out[2], not_83_out[1], not_83_out[0]);
  assign xor_70_out = 4'b0000 ^ register_5_q;  // XOR_Gate xor_70, 4 bits wide
  or or_72 (or_72_out, or_73_out, and_173_out);
  assign not_83_out = ~xor_70_out;  // NOT_Gate not_83, 4 bits wide
  and and_173 (and_173_out, N1Clear, and_174_out);
  and and_174 (and_174_out, not_84_out[3], not_84_out[2], not_84_out[1], not_84_out[0]);
  assign xor_71_out = 4'b0001 ^ register_5_q;  // XOR_Gate xor_71, 4 bits wide
  or or_73 (or_73_out, or_74_out, and_175_out);
  assign not_84_out = ~xor_71_out;  // NOT_Gate not_84, 4 bits wide
  and and_175 (and_175_out, N2Clear, and_176_out);
  and and_176 (and_176_out, not_85_out[3], not_85_out[2], not_85_out[1], not_85_out[0]);
  assign xor_72_out = 4'b0010 ^ register_5_q;  // XOR_Gate xor_72, 4 bits wide
  or or_74 (or_74_out, or_75_out, and_177_out);
  assign not_85_out = ~xor_72_out;  // NOT_Gate not_85, 4 bits wide
  and and_177 (and_177_out, N3Clear, and_178_out);
  and and_178 (and_178_out, not_86_out[3], not_86_out[2], not_86_out[1], not_86_out[0]);
  assign xor_73_out = 4'b0011 ^ register_5_q;  // XOR_Gate xor_73, 4 bits wide
  or or_75 (or_75_out, or_76_out, and_179_out);
  assign not_86_out = ~xor_73_out;  // NOT_Gate not_86, 4 bits wide
  and and_179 (and_179_out, N4Clear, and_180_out);
  and and_180 (and_180_out, not_87_out[3], not_87_out[2], not_87_out[1], not_87_out[0]);
  assign xor_74_out = 4'b0100 ^ register_5_q;  // XOR_Gate xor_74, 4 bits wide
  or or_76 (or_76_out, or_77_out, and_181_out);
  assign not_87_out = ~xor_74_out;  // NOT_Gate not_87, 4 bits wide
  and and_181 (and_181_out, N5Clear, and_182_out);
  and and_182 (and_182_out, not_88_out[3], not_88_out[2], not_88_out[1], not_88_out[0]);
  assign xor_75_out = 4'b0101 ^ register_5_q;  // XOR_Gate xor_75, 4 bits wide
  or or_77 (or_77_out, or_78_out, and_183_out);
  assign not_88_out = ~xor_75_out;  // NOT_Gate not_88, 4 bits wide
  and and_183 (and_183_out, N6Clear, and_184_out);
  and and_184 (and_184_out, not_89_out[3], not_89_out[2], not_89_out[1], not_89_out[0]);
  assign xor_76_out = 4'b0110 ^ register_5_q;  // XOR_Gate xor_76, 4 bits wide
  or or_78 (or_78_out, or_79_out, and_185_out);
  assign not_89_out = ~xor_76_out;  // NOT_Gate not_89, 4 bits wide
  and and_185 (and_185_out, N7Clear, and_186_out);
  and and_186 (and_186_out, not_90_out[3], not_90_out[2], not_90_out[1], not_90_out[0]);
  assign xor_77_out = 4'b0111 ^ register_5_q;  // XOR_Gate xor_77, 4 bits wide
  or or_79 (or_79_out, or_80_out, and_187_out);
  assign not_90_out = ~xor_77_out;  // NOT_Gate not_90, 4 bits wide
  and and_187 (and_187_out, N8Clear, and_188_out);
  and and_188 (and_188_out, not_91_out[3], not_91_out[2], not_91_out[1], not_91_out[0]);
  assign xor_78_out = 4'b1000 ^ register_5_q;  // XOR_Gate xor_78, 4 bits wide
  or or_80 (or_80_out, or_81_out, and_189_out);
  assign not_91_out = ~xor_78_out;  // NOT_Gate not_91, 4 bits wide
  and and_189 (and_189_out, N9Clear, and_190_out);
  and and_190 (and_190_out, not_92_out[3], not_92_out[2], not_92_out[1], not_92_out[0]);
  assign xor_79_out = 4'b1001 ^ register_5_q;  // XOR_Gate xor_79, 4 bits wide
  or or_81 (or_81_out, or_82_out, and_191_out);
  assign not_92_out = ~xor_79_out;  // NOT_Gate not_92, 4 bits wide
  and and_191 (and_191_out, NaClear, and_192_out);
  and and_192 (and_192_out, not_93_out[3], not_93_out[2], not_93_out[1], not_93_out[0]);
  assign xor_80_out = 4'b1010 ^ register_5_q;  // XOR_Gate xor_80, 4 bits wide
  or or_82 (or_82_out, or_83_out, and_193_out);
  assign not_93_out = ~xor_80_out;  // NOT_Gate not_93, 4 bits wide
  and and_193 (and_193_out, NbClear, and_194_out);
  and and_194 (and_194_out, not_94_out[3], not_94_out[2], not_94_out[1], not_94_out[0]);
  assign xor_81_out = 4'b1011 ^ register_5_q;  // XOR_Gate xor_81, 4 bits wide
  or or_83 (or_83_out, or_84_out, and_195_out);
  assign not_94_out = ~xor_81_out;  // NOT_Gate not_94, 4 bits wide
  and and_195 (and_195_out, NcClear, and_196_out);
  and and_196 (and_196_out, not_95_out[3], not_95_out[2], not_95_out[1], not_95_out[0]);
  assign xor_82_out = 4'b1100 ^ register_5_q;  // XOR_Gate xor_82, 4 bits wide
  or or_84 (or_84_out, or_85_out, and_197_out);
  assign not_95_out = ~xor_82_out;  // NOT_Gate not_95, 4 bits wide
  and and_197 (and_197_out, NdClear, and_198_out);
  and and_198 (and_198_out, not_96_out[3], not_96_out[2], not_96_out[1], not_96_out[0]);
  assign xor_83_out = 4'b1101 ^ register_5_q;  // XOR_Gate xor_83, 4 bits wide
  or or_85 (or_85_out, and_201_out, and_199_out);
  assign not_96_out = ~xor_83_out;  // NOT_Gate not_96, 4 bits wide
  and and_199 (and_199_out, NeClear, and_200_out);
  and and_200 (and_200_out, not_97_out[3], not_97_out[2], not_97_out[1], not_97_out[0]);
  assign xor_84_out = 4'b1110 ^ register_5_q;  // XOR_Gate xor_84, 4 bits wide
  assign not_97_out = ~xor_84_out;  // NOT_Gate not_97, 4 bits wide
  and and_201 (and_201_out, NfClear, and_202_out);
  and and_202 (and_202_out, not_98_out[3], not_98_out[2], not_98_out[1], not_98_out[0]);
  assign xor_85_out = 4'b1111 ^ register_5_q;  // XOR_Gate xor_85, 4 bits wide
  assign not_98_out = ~xor_85_out;  // NOT_Gate not_98, 4 bits wide
  and and_203 (and_203_out, and_165_out, not_99_out);
  not not_99 (not_99_out, N9Request);
  assign controlled_buffer_1_out = and_206_out ? 4'b1010 : 4'bz;  // Controlled_Buffer controlled_buffer_15
  and and_204 (and_204_out, and_166_out, and_205_out);
  and and_205 (and_205_out, d_ff_5_qn, and_169_out);
  assign NewNode = and_204_out ? 4'b0101 : 4'bz;  // Controlled_Buffer controlled_buffer_16
  not not_100 (not_100_out, NaRequest);
  and and_206 (and_206_out, and_203_out, NaRequest);
  or or_86 (or_86_out, NaRequest, or_87_out);
  and and_207 (and_207_out, and_166_out, not_101_out);
  not not_101 (not_101_out, and_204_out);
  and and_208 (and_208_out, and_211_out, Clock);
  and and_209 (and_209_out, not_102_out[2], not_102_out[1], not_102_out[0]);
  assign not_102_out = ~xor_86_out;  // NOT_Gate not_102, 3 bits wide
  assign xor_86_out = 3'b000 ^ N6Exp;  // XOR_Gate xor_86, 3 bits wide
  and and_210 (and_210_out, and_203_out, not_100_out);
  assign controlled_buffer_1_out = and_244_out ? 4'b1011 : 4'bz;  // Controlled_Buffer controlled_buffer_17
  or or_87 (or_87_out, NbRequest, or_103_out);
  D_Flip_Flop #(.trigger("falling")) d_ff_6 (
    .D(and_211_out), .clk(and_208_out), .Qn(d_ff_6_qn), .reset(or_88_out));  // open: Q, preset
  and and_211 (and_211_out, and_248_out, or_1_out);
  Register #(.width(4)) register_6 (
    .D(controlled_buffer_1_out), .en(and_211_out), .clk(and_208_out), .Q(register_6_q), .clr(or_88_out));
  or or_88 (or_88_out, or_89_out, and_212_out);
  and and_212 (and_212_out, N0Clear, and_213_out);
  and and_213 (and_213_out, not_104_out[3], not_104_out[2], not_104_out[1], not_104_out[0]);
  or or_89 (or_89_out, or_90_out, and_214_out);
  and and_214 (and_214_out, N1Clear, and_215_out);
  and and_215 (and_215_out, not_105_out[3], not_105_out[2], not_105_out[1], not_105_out[0]);
  or or_90 (or_90_out, or_91_out, and_216_out);
  and and_216 (and_216_out, N2Clear, and_217_out);
  and and_217 (and_217_out, not_106_out[3], not_106_out[2], not_106_out[1], not_106_out[0]);
  or or_91 (or_91_out, or_92_out, and_218_out);
  and and_218 (and_218_out, N3Clear, and_219_out);
  and and_219 (and_219_out, not_107_out[3], not_107_out[2], not_107_out[1], not_107_out[0]);
  or or_92 (or_92_out, or_93_out, and_220_out);
  and and_220 (and_220_out, N4Clear, and_221_out);
  and and_221 (and_221_out, not_108_out[3], not_108_out[2], not_108_out[1], not_108_out[0]);
  or or_93 (or_93_out, or_94_out, and_222_out);
  and and_222 (and_222_out, N5Clear, and_223_out);
  and and_223 (and_223_out, not_109_out[3], not_109_out[2], not_109_out[1], not_109_out[0]);
  or or_94 (or_94_out, or_95_out, and_224_out);
  and and_224 (and_224_out, N6Clear, and_225_out);
  and and_225 (and_225_out, not_110_out[3], not_110_out[2], not_110_out[1], not_110_out[0]);
  or or_95 (or_95_out, or_96_out, and_226_out);
  and and_226 (and_226_out, N7Clear, and_227_out);
  and and_227 (and_227_out, not_111_out[3], not_111_out[2], not_111_out[1], not_111_out[0]);
  or or_96 (or_96_out, or_97_out, and_228_out);
  and and_228 (and_228_out, N8Clear, and_229_out);
  and and_229 (and_229_out, not_112_out[3], not_112_out[2], not_112_out[1], not_112_out[0]);
  or or_97 (or_97_out, or_98_out, and_230_out);
  and and_230 (and_230_out, N9Clear, and_231_out);
  and and_231 (and_231_out, not_113_out[3], not_113_out[2], not_113_out[1], not_113_out[0]);
  or or_98 (or_98_out, or_99_out, and_232_out);
  and and_232 (and_232_out, NaClear, and_233_out);
  and and_233 (and_233_out, not_114_out[3], not_114_out[2], not_114_out[1], not_114_out[0]);
  or or_99 (or_99_out, or_100_out, and_234_out);
  and and_234 (and_234_out, NbClear, and_235_out);
  and and_235 (and_235_out, not_115_out[3], not_115_out[2], not_115_out[1], not_115_out[0]);
  or or_100 (or_100_out, or_101_out, and_236_out);
  and and_236 (and_236_out, NcClear, and_237_out);
  and and_237 (and_237_out, not_116_out[3], not_116_out[2], not_116_out[1], not_116_out[0]);
  or or_101 (or_101_out, or_102_out, and_238_out);
  and and_238 (and_238_out, NdClear, and_239_out);
  and and_239 (and_239_out, not_117_out[3], not_117_out[2], not_117_out[1], not_117_out[0]);
  or or_102 (or_102_out, and_242_out, and_240_out);
  and and_240 (and_240_out, NeClear, and_241_out);
  and and_241 (and_241_out, not_118_out[3], not_118_out[2], not_118_out[1], not_118_out[0]);
  and and_242 (and_242_out, NfClear, and_243_out);
  and and_243 (and_243_out, not_119_out[3], not_119_out[2], not_119_out[1], not_119_out[0]);
  not not_103 (not_103_out, NbRequest);
  and and_244 (and_244_out, and_210_out, NbRequest);
  and and_245 (and_245_out, d_ff_6_qn, and_209_out);
  assign xor_87_out = 4'b0000 ^ register_6_q;  // XOR_Gate xor_87, 4 bits wide
  assign not_104_out = ~xor_87_out;  // NOT_Gate not_104, 4 bits wide
  assign xor_88_out = 4'b0001 ^ register_6_q;  // XOR_Gate xor_88, 4 bits wide
  assign not_105_out = ~xor_88_out;  // NOT_Gate not_105, 4 bits wide
  assign xor_89_out = 4'b0010 ^ register_6_q;  // XOR_Gate xor_89, 4 bits wide
  assign not_106_out = ~xor_89_out;  // NOT_Gate not_106, 4 bits wide
  assign xor_90_out = 4'b0011 ^ register_6_q;  // XOR_Gate xor_90, 4 bits wide
  assign not_107_out = ~xor_90_out;  // NOT_Gate not_107, 4 bits wide
  assign xor_91_out = 4'b0100 ^ register_6_q;  // XOR_Gate xor_91, 4 bits wide
  assign not_108_out = ~xor_91_out;  // NOT_Gate not_108, 4 bits wide
  assign xor_92_out = 4'b0101 ^ register_6_q;  // XOR_Gate xor_92, 4 bits wide
  assign not_109_out = ~xor_92_out;  // NOT_Gate not_109, 4 bits wide
  assign xor_93_out = 4'b0110 ^ register_6_q;  // XOR_Gate xor_93, 4 bits wide
  assign not_110_out = ~xor_93_out;  // NOT_Gate not_110, 4 bits wide
  assign xor_94_out = 4'b0111 ^ register_6_q;  // XOR_Gate xor_94, 4 bits wide
  assign not_111_out = ~xor_94_out;  // NOT_Gate not_111, 4 bits wide
  assign xor_95_out = 4'b1000 ^ register_6_q;  // XOR_Gate xor_95, 4 bits wide
  assign not_112_out = ~xor_95_out;  // NOT_Gate not_112, 4 bits wide
  assign xor_96_out = 4'b1001 ^ register_6_q;  // XOR_Gate xor_96, 4 bits wide
  assign not_113_out = ~xor_96_out;  // NOT_Gate not_113, 4 bits wide
  assign xor_97_out = 4'b1010 ^ register_6_q;  // XOR_Gate xor_97, 4 bits wide
  assign not_114_out = ~xor_97_out;  // NOT_Gate not_114, 4 bits wide
  assign xor_98_out = 4'b1011 ^ register_6_q;  // XOR_Gate xor_98, 4 bits wide
  assign not_115_out = ~xor_98_out;  // NOT_Gate not_115, 4 bits wide
  assign xor_99_out = 4'b1100 ^ register_6_q;  // XOR_Gate xor_99, 4 bits wide
  assign not_116_out = ~xor_99_out;  // NOT_Gate not_116, 4 bits wide
  assign xor_100_out = 4'b1101 ^ register_6_q;  // XOR_Gate xor_100, 4 bits wide
  assign not_117_out = ~xor_100_out;  // NOT_Gate not_117, 4 bits wide
  assign xor_101_out = 4'b1110 ^ register_6_q;  // XOR_Gate xor_101, 4 bits wide
  assign not_118_out = ~xor_101_out;  // NOT_Gate not_118, 4 bits wide
  assign xor_102_out = 4'b1111 ^ register_6_q;  // XOR_Gate xor_102, 4 bits wide
  assign not_119_out = ~xor_102_out;  // NOT_Gate not_119, 4 bits wide
  and and_246 (and_246_out, and_210_out, not_103_out);
  and and_247 (and_247_out, and_246_out, NcRequest);
  assign controlled_buffer_1_out = and_247_out ? 4'b1100 : 4'bz;  // Controlled_Buffer controlled_buffer_18
  or or_103 (or_103_out, NcRequest, or_119_out);
  not not_120 (not_120_out, and_248_out);
  and and_248 (and_248_out, and_207_out, and_245_out);
  assign NewNode = and_248_out ? 4'b0110 : 4'bz;  // Controlled_Buffer controlled_buffer_19
  and and_249 (and_249_out, and_246_out, not_121_out);
  not not_121 (not_121_out, NcRequest);
  and and_250 (and_250_out, and_207_out, not_120_out);
  and and_251 (and_251_out, and_288_out, or_1_out);
  Register #(.width(4)) register_7 (
    .D(controlled_buffer_1_out), .en(and_251_out), .clk(and_252_out), .Q(register_7_q), .clr(or_104_out));
  and and_252 (and_252_out, and_251_out, Clock);
  or or_104 (or_104_out, or_105_out, and_253_out);
  and and_253 (and_253_out, N0Clear, and_271_out);
  or or_105 (or_105_out, or_106_out, and_254_out);
  and and_254 (and_254_out, N1Clear, and_272_out);
  or or_106 (or_106_out, or_107_out, and_255_out);
  and and_255 (and_255_out, N2Clear, and_273_out);
  or or_107 (or_107_out, or_108_out, and_256_out);
  and and_256 (and_256_out, N3Clear, and_274_out);
  or or_108 (or_108_out, or_109_out, and_257_out);
  and and_257 (and_257_out, N4Clear, and_275_out);
  or or_109 (or_109_out, or_110_out, and_258_out);
  and and_258 (and_258_out, N5Clear, and_276_out);
  or or_110 (or_110_out, or_111_out, and_259_out);
  and and_259 (and_259_out, N6Clear, and_277_out);
  or or_111 (or_111_out, or_112_out, and_260_out);
  and and_260 (and_260_out, N7Clear, and_278_out);
  or or_112 (or_112_out, or_113_out, and_261_out);
  and and_261 (and_261_out, N8Clear, and_279_out);
  or or_113 (or_113_out, or_114_out, and_262_out);
  and and_262 (and_262_out, N9Clear, and_280_out);
  or or_114 (or_114_out, or_115_out, and_263_out);
  and and_263 (and_263_out, NaClear, and_281_out);
  or or_115 (or_115_out, or_116_out, and_264_out);
  and and_264 (and_264_out, NbClear, and_282_out);
  or or_116 (or_116_out, or_117_out, and_265_out);
  and and_265 (and_265_out, NcClear, and_283_out);
  or or_117 (or_117_out, or_118_out, and_266_out);
  and and_266 (and_266_out, NdClear, and_284_out);
  or or_118 (or_118_out, and_268_out, and_267_out);
  and and_267 (and_267_out, NeClear, and_285_out);
  and and_268 (and_268_out, NfClear, and_286_out);
  and and_269 (and_269_out, not_122_out[2], not_122_out[1], not_122_out[0]);
  assign not_122_out = ~xor_103_out;  // NOT_Gate not_122, 3 bits wide
  assign xor_103_out = 3'b000 ^ N7Exp;  // XOR_Gate xor_103, 3 bits wide
  and and_270 (and_270_out, and_249_out, NdRequest);
  assign controlled_buffer_1_out = and_270_out ? 4'b1101 : 4'bz;  // Controlled_Buffer controlled_buffer_20
  or or_119 (or_119_out, NdRequest, or_120_out);
  D_Flip_Flop #(.trigger("falling")) d_ff_7 (
    .D(and_251_out), .clk(and_252_out), .Qn(d_ff_7_qn), .reset(or_104_out));  // open: Q, preset
  and and_271 (and_271_out, not_123_out[3], not_123_out[2], not_123_out[1], not_123_out[0]);
  assign xor_104_out = 4'b0000 ^ register_7_q;  // XOR_Gate xor_104, 4 bits wide
  assign not_123_out = ~xor_104_out;  // NOT_Gate not_123, 4 bits wide
  and and_272 (and_272_out, not_124_out[3], not_124_out[2], not_124_out[1], not_124_out[0]);
  assign xor_105_out = 4'b0001 ^ register_7_q;  // XOR_Gate xor_105, 4 bits wide
  assign not_124_out = ~xor_105_out;  // NOT_Gate not_124, 4 bits wide
  and and_273 (and_273_out, not_125_out[3], not_125_out[2], not_125_out[1], not_125_out[0]);
  assign xor_106_out = 4'b0010 ^ register_7_q;  // XOR_Gate xor_106, 4 bits wide
  assign not_125_out = ~xor_106_out;  // NOT_Gate not_125, 4 bits wide
  and and_274 (and_274_out, not_126_out[3], not_126_out[2], not_126_out[1], not_126_out[0]);
  assign xor_107_out = 4'b0011 ^ register_7_q;  // XOR_Gate xor_107, 4 bits wide
  assign not_126_out = ~xor_107_out;  // NOT_Gate not_126, 4 bits wide
  and and_275 (and_275_out, not_127_out[3], not_127_out[2], not_127_out[1], not_127_out[0]);
  assign xor_108_out = 4'b0100 ^ register_7_q;  // XOR_Gate xor_108, 4 bits wide
  assign not_127_out = ~xor_108_out;  // NOT_Gate not_127, 4 bits wide
  and and_276 (and_276_out, not_128_out[3], not_128_out[2], not_128_out[1], not_128_out[0]);
  assign xor_109_out = 4'b0101 ^ register_7_q;  // XOR_Gate xor_109, 4 bits wide
  assign not_128_out = ~xor_109_out;  // NOT_Gate not_128, 4 bits wide
  and and_277 (and_277_out, not_129_out[3], not_129_out[2], not_129_out[1], not_129_out[0]);
  assign xor_110_out = 4'b0110 ^ register_7_q;  // XOR_Gate xor_110, 4 bits wide
  assign not_129_out = ~xor_110_out;  // NOT_Gate not_129, 4 bits wide
  and and_278 (and_278_out, not_130_out[3], not_130_out[2], not_130_out[1], not_130_out[0]);
  assign xor_111_out = 4'b0111 ^ register_7_q;  // XOR_Gate xor_111, 4 bits wide
  assign not_130_out = ~xor_111_out;  // NOT_Gate not_130, 4 bits wide
  and and_279 (and_279_out, not_131_out[3], not_131_out[2], not_131_out[1], not_131_out[0]);
  assign xor_112_out = 4'b1000 ^ register_7_q;  // XOR_Gate xor_112, 4 bits wide
  assign not_131_out = ~xor_112_out;  // NOT_Gate not_131, 4 bits wide
  and and_280 (and_280_out, not_132_out[3], not_132_out[2], not_132_out[1], not_132_out[0]);
  assign xor_113_out = 4'b1001 ^ register_7_q;  // XOR_Gate xor_113, 4 bits wide
  assign not_132_out = ~xor_113_out;  // NOT_Gate not_132, 4 bits wide
  and and_281 (and_281_out, not_133_out[3], not_133_out[2], not_133_out[1], not_133_out[0]);
  assign xor_114_out = 4'b1010 ^ register_7_q;  // XOR_Gate xor_114, 4 bits wide
  assign not_133_out = ~xor_114_out;  // NOT_Gate not_133, 4 bits wide
  and and_282 (and_282_out, not_134_out[3], not_134_out[2], not_134_out[1], not_134_out[0]);
  assign xor_115_out = 4'b1011 ^ register_7_q;  // XOR_Gate xor_115, 4 bits wide
  assign not_134_out = ~xor_115_out;  // NOT_Gate not_134, 4 bits wide
  and and_283 (and_283_out, not_135_out[3], not_135_out[2], not_135_out[1], not_135_out[0]);
  assign xor_116_out = 4'b1100 ^ register_7_q;  // XOR_Gate xor_116, 4 bits wide
  assign not_135_out = ~xor_116_out;  // NOT_Gate not_135, 4 bits wide
  and and_284 (and_284_out, not_136_out[3], not_136_out[2], not_136_out[1], not_136_out[0]);
  assign xor_117_out = 4'b1101 ^ register_7_q;  // XOR_Gate xor_117, 4 bits wide
  assign not_136_out = ~xor_117_out;  // NOT_Gate not_136, 4 bits wide
  and and_285 (and_285_out, not_137_out[3], not_137_out[2], not_137_out[1], not_137_out[0]);
  assign xor_118_out = 4'b1110 ^ register_7_q;  // XOR_Gate xor_118, 4 bits wide
  assign not_137_out = ~xor_118_out;  // NOT_Gate not_137, 4 bits wide
  and and_286 (and_286_out, not_138_out[3], not_138_out[2], not_138_out[1], not_138_out[0]);
  assign xor_119_out = 4'b1111 ^ register_7_q;  // XOR_Gate xor_119, 4 bits wide
  assign not_138_out = ~xor_119_out;  // NOT_Gate not_138, 4 bits wide
  and and_287 (and_287_out, and_249_out, not_139_out);
  not not_139 (not_139_out, NdRequest);
  assign controlled_buffer_1_out = and_290_out ? 4'b1110 : 4'bz;  // Controlled_Buffer controlled_buffer_21
  and and_288 (and_288_out, and_250_out, and_289_out);
  and and_289 (and_289_out, d_ff_7_qn, and_269_out);
  assign NewNode = and_288_out ? 4'b0111 : 4'bz;  // Controlled_Buffer controlled_buffer_22
  not not_140 (not_140_out, NeRequest);
  and and_290 (and_290_out, and_287_out, NeRequest);
  or or_120 (or_120_out, NeRequest, NfRequest);
  and and_291 (and_291_out, and_250_out, not_141_out);
  not not_141 (not_141_out, and_288_out);
  and and_292 (and_292_out, and_330_out, or_1_out);
  and and_293 (and_293_out, and_292_out, Clock);
  and and_294 (and_294_out, not_142_out[2], not_142_out[1], not_142_out[0]);
  assign not_142_out = ~xor_120_out;  // NOT_Gate not_142, 3 bits wide
  assign xor_120_out = 3'b000 ^ N8Exp;  // XOR_Gate xor_120, 3 bits wide
  and and_295 (and_295_out, and_287_out, not_140_out);
  assign controlled_buffer_1_out = and_328_out ? 4'b1111 : 4'bz;  // Controlled_Buffer controlled_buffer_23
  D_Flip_Flop #(.trigger("falling")) d_ff_8 (
    .D(and_292_out), .clk(and_293_out), .Qn(d_ff_8_qn), .reset(or_121_out));  // open: Q, preset
  Register #(.width(4)) register_8 (
    .D(controlled_buffer_1_out), .en(and_292_out), .clk(and_293_out), .Q(register_8_q), .clr(or_121_out));
  or or_121 (or_121_out, or_122_out, and_296_out);
  and and_296 (and_296_out, N0Clear, and_297_out);
  and and_297 (and_297_out, not_143_out[3], not_143_out[2], not_143_out[1], not_143_out[0]);
  assign xor_121_out = 4'b0000 ^ register_8_q;  // XOR_Gate xor_121, 4 bits wide
  or or_122 (or_122_out, or_123_out, and_298_out);
  assign not_143_out = ~xor_121_out;  // NOT_Gate not_143, 4 bits wide
  and and_298 (and_298_out, N1Clear, and_299_out);
  and and_299 (and_299_out, not_144_out[3], not_144_out[2], not_144_out[1], not_144_out[0]);
  assign xor_122_out = 4'b0001 ^ register_8_q;  // XOR_Gate xor_122, 4 bits wide
  or or_123 (or_123_out, or_124_out, and_300_out);
  assign not_144_out = ~xor_122_out;  // NOT_Gate not_144, 4 bits wide
  and and_300 (and_300_out, N2Clear, and_301_out);
  and and_301 (and_301_out, not_145_out[3], not_145_out[2], not_145_out[1], not_145_out[0]);
  assign xor_123_out = 4'b0010 ^ register_8_q;  // XOR_Gate xor_123, 4 bits wide
  or or_124 (or_124_out, or_125_out, and_302_out);
  assign not_145_out = ~xor_123_out;  // NOT_Gate not_145, 4 bits wide
  and and_302 (and_302_out, N3Clear, and_303_out);
  and and_303 (and_303_out, not_146_out[3], not_146_out[2], not_146_out[1], not_146_out[0]);
  assign xor_124_out = 4'b0011 ^ register_8_q;  // XOR_Gate xor_124, 4 bits wide
  or or_125 (or_125_out, or_126_out, and_304_out);
  assign not_146_out = ~xor_124_out;  // NOT_Gate not_146, 4 bits wide
  and and_304 (and_304_out, N4Clear, and_305_out);
  and and_305 (and_305_out, not_147_out[3], not_147_out[2], not_147_out[1], not_147_out[0]);
  assign xor_125_out = 4'b0100 ^ register_8_q;  // XOR_Gate xor_125, 4 bits wide
  or or_126 (or_126_out, or_127_out, and_306_out);
  assign not_147_out = ~xor_125_out;  // NOT_Gate not_147, 4 bits wide
  and and_306 (and_306_out, N5Clear, and_307_out);
  and and_307 (and_307_out, not_148_out[3], not_148_out[2], not_148_out[1], not_148_out[0]);
  assign xor_126_out = 4'b0101 ^ register_8_q;  // XOR_Gate xor_126, 4 bits wide
  or or_127 (or_127_out, or_128_out, and_308_out);
  assign not_148_out = ~xor_126_out;  // NOT_Gate not_148, 4 bits wide
  and and_308 (and_308_out, N6Clear, and_309_out);
  and and_309 (and_309_out, not_149_out[3], not_149_out[2], not_149_out[1], not_149_out[0]);
  assign xor_127_out = 4'b0110 ^ register_8_q;  // XOR_Gate xor_127, 4 bits wide
  or or_128 (or_128_out, or_129_out, and_310_out);
  assign not_149_out = ~xor_127_out;  // NOT_Gate not_149, 4 bits wide
  and and_310 (and_310_out, N7Clear, and_311_out);
  and and_311 (and_311_out, not_150_out[3], not_150_out[2], not_150_out[1], not_150_out[0]);
  assign xor_128_out = 4'b0111 ^ register_8_q;  // XOR_Gate xor_128, 4 bits wide
  or or_129 (or_129_out, or_130_out, and_312_out);
  assign not_150_out = ~xor_128_out;  // NOT_Gate not_150, 4 bits wide
  and and_312 (and_312_out, N8Clear, and_313_out);
  and and_313 (and_313_out, not_151_out[3], not_151_out[2], not_151_out[1], not_151_out[0]);
  assign xor_129_out = 4'b1000 ^ register_8_q;  // XOR_Gate xor_129, 4 bits wide
  or or_130 (or_130_out, or_131_out, and_314_out);
  assign not_151_out = ~xor_129_out;  // NOT_Gate not_151, 4 bits wide
  and and_314 (and_314_out, N9Clear, and_315_out);
  and and_315 (and_315_out, not_152_out[3], not_152_out[2], not_152_out[1], not_152_out[0]);
  assign xor_130_out = 4'b1001 ^ register_8_q;  // XOR_Gate xor_130, 4 bits wide
  or or_131 (or_131_out, or_132_out, and_316_out);
  assign not_152_out = ~xor_130_out;  // NOT_Gate not_152, 4 bits wide
  and and_316 (and_316_out, NaClear, and_317_out);
  and and_317 (and_317_out, not_153_out[3], not_153_out[2], not_153_out[1], not_153_out[0]);
  assign xor_131_out = 4'b1010 ^ register_8_q;  // XOR_Gate xor_131, 4 bits wide
  or or_132 (or_132_out, or_133_out, and_318_out);
  assign not_153_out = ~xor_131_out;  // NOT_Gate not_153, 4 bits wide
  and and_318 (and_318_out, NbClear, and_319_out);
  and and_319 (and_319_out, not_154_out[3], not_154_out[2], not_154_out[1], not_154_out[0]);
  assign xor_132_out = 4'b1011 ^ register_8_q;  // XOR_Gate xor_132, 4 bits wide
  or or_133 (or_133_out, or_134_out, and_320_out);
  assign not_154_out = ~xor_132_out;  // NOT_Gate not_154, 4 bits wide
  and and_320 (and_320_out, NcClear, and_321_out);
  and and_321 (and_321_out, not_155_out[3], not_155_out[2], not_155_out[1], not_155_out[0]);
  assign xor_133_out = 4'b1100 ^ register_8_q;  // XOR_Gate xor_133, 4 bits wide
  or or_134 (or_134_out, or_135_out, and_322_out);
  assign not_155_out = ~xor_133_out;  // NOT_Gate not_155, 4 bits wide
  and and_322 (and_322_out, NdClear, and_323_out);
  and and_323 (and_323_out, not_156_out[3], not_156_out[2], not_156_out[1], not_156_out[0]);
  assign xor_134_out = 4'b1101 ^ register_8_q;  // XOR_Gate xor_134, 4 bits wide
  or or_135 (or_135_out, and_326_out, and_324_out);
  assign not_156_out = ~xor_134_out;  // NOT_Gate not_156, 4 bits wide
  and and_324 (and_324_out, NeClear, and_325_out);
  and and_325 (and_325_out, not_157_out[3], not_157_out[2], not_157_out[1], not_157_out[0]);
  assign xor_135_out = 4'b1110 ^ register_8_q;  // XOR_Gate xor_135, 4 bits wide
  assign not_157_out = ~xor_135_out;  // NOT_Gate not_157, 4 bits wide
  and and_326 (and_326_out, NfClear, and_327_out);
  and and_327 (and_327_out, not_158_out[3], not_158_out[2], not_158_out[1], not_158_out[0]);
  assign xor_136_out = 4'b1111 ^ register_8_q;  // XOR_Gate xor_136, 4 bits wide
  assign not_158_out = ~xor_136_out;  // NOT_Gate not_158, 4 bits wide
  and and_328 (and_328_out, and_295_out, NfRequest);
  and and_329 (and_329_out, d_ff_8_qn, and_294_out);
  assign NewNode = and_330_out ? 4'b1000 : 4'bz;  // Controlled_Buffer controlled_buffer_24
  not not_159 (not_159_out, and_330_out);
  and and_330 (and_330_out, and_291_out, and_329_out);
  and and_331 (and_331_out, and_333_out, Clock);
  assign not_160_out = ~xor_137_out;  // NOT_Gate not_160, 3 bits wide
  assign xor_137_out = 3'b000 ^ N9Exp;  // XOR_Gate xor_137, 3 bits wide
  and and_332 (and_332_out, and_291_out, not_159_out);
  and and_333 (and_333_out, and_368_out, or_1_out);
  D_Flip_Flop #(.trigger("falling")) d_ff_9 (
    .D(and_333_out), .clk(and_331_out), .Qn(d_ff_9_qn), .reset(or_136_out));  // open: Q, preset
  Register #(.width(4)) register_9 (
    .D(controlled_buffer_1_out), .en(and_333_out), .clk(and_331_out), .Q(register_9_q), .clr(or_136_out));
  or or_136 (or_136_out, or_137_out, and_334_out);
  and and_334 (and_334_out, N0Clear, and_335_out);
  and and_335 (and_335_out, not_161_out[3], not_161_out[2], not_161_out[1], not_161_out[0]);
  or or_137 (or_137_out, or_138_out, and_336_out);
  and and_336 (and_336_out, N1Clear, and_337_out);
  and and_337 (and_337_out, not_162_out[3], not_162_out[2], not_162_out[1], not_162_out[0]);
  or or_138 (or_138_out, or_139_out, and_338_out);
  and and_338 (and_338_out, N2Clear, and_339_out);
  and and_339 (and_339_out, not_163_out[3], not_163_out[2], not_163_out[1], not_163_out[0]);
  or or_139 (or_139_out, or_140_out, and_340_out);
  and and_340 (and_340_out, N3Clear, and_341_out);
  and and_341 (and_341_out, not_164_out[3], not_164_out[2], not_164_out[1], not_164_out[0]);
  or or_140 (or_140_out, or_141_out, and_342_out);
  and and_342 (and_342_out, N4Clear, and_343_out);
  and and_343 (and_343_out, not_165_out[3], not_165_out[2], not_165_out[1], not_165_out[0]);
  or or_141 (or_141_out, or_142_out, and_344_out);
  and and_344 (and_344_out, N5Clear, and_345_out);
  and and_345 (and_345_out, not_166_out[3], not_166_out[2], not_166_out[1], not_166_out[0]);
  or or_142 (or_142_out, or_143_out, and_346_out);
  and and_346 (and_346_out, N6Clear, and_347_out);
  and and_347 (and_347_out, not_167_out[3], not_167_out[2], not_167_out[1], not_167_out[0]);
  or or_143 (or_143_out, or_144_out, and_348_out);
  and and_348 (and_348_out, N7Clear, and_349_out);
  and and_349 (and_349_out, not_168_out[3], not_168_out[2], not_168_out[1], not_168_out[0]);
  or or_144 (or_144_out, or_145_out, and_350_out);
  and and_350 (and_350_out, N8Clear, and_351_out);
  and and_351 (and_351_out, not_169_out[3], not_169_out[2], not_169_out[1], not_169_out[0]);
  or or_145 (or_145_out, or_146_out, and_352_out);
  and and_352 (and_352_out, N9Clear, and_353_out);
  and and_353 (and_353_out, not_170_out[3], not_170_out[2], not_170_out[1], not_170_out[0]);
  or or_146 (or_146_out, or_147_out, and_354_out);
  and and_354 (and_354_out, NaClear, and_355_out);
  and and_355 (and_355_out, not_171_out[3], not_171_out[2], not_171_out[1], not_171_out[0]);
  or or_147 (or_147_out, or_148_out, and_356_out);
  and and_356 (and_356_out, NbClear, and_357_out);
  and and_357 (and_357_out, not_172_out[3], not_172_out[2], not_172_out[1], not_172_out[0]);
  or or_148 (or_148_out, or_149_out, and_358_out);
  and and_358 (and_358_out, NcClear, and_359_out);
  and and_359 (and_359_out, not_173_out[3], not_173_out[2], not_173_out[1], not_173_out[0]);
  or or_149 (or_149_out, or_150_out, and_360_out);
  and and_360 (and_360_out, NdClear, and_361_out);
  and and_361 (and_361_out, not_174_out[3], not_174_out[2], not_174_out[1], not_174_out[0]);
  or or_150 (or_150_out, and_364_out, and_362_out);
  and and_362 (and_362_out, NeClear, and_363_out);
  and and_363 (and_363_out, not_175_out[3], not_175_out[2], not_175_out[1], not_175_out[0]);
  and and_364 (and_364_out, NfClear, and_365_out);
  and and_365 (and_365_out, not_176_out[3], not_176_out[2], not_176_out[1], not_176_out[0]);
  and and_366 (and_366_out, not_160_out[2], not_160_out[1], not_160_out[0]);
  and and_367 (and_367_out, d_ff_9_qn, and_366_out);
  assign xor_138_out = 4'b0000 ^ register_9_q;  // XOR_Gate xor_138, 4 bits wide
  assign not_161_out = ~xor_138_out;  // NOT_Gate not_161, 4 bits wide
  assign xor_139_out = 4'b0001 ^ register_9_q;  // XOR_Gate xor_139, 4 bits wide
  assign not_162_out = ~xor_139_out;  // NOT_Gate not_162, 4 bits wide
  assign xor_140_out = 4'b0010 ^ register_9_q;  // XOR_Gate xor_140, 4 bits wide
  assign not_163_out = ~xor_140_out;  // NOT_Gate not_163, 4 bits wide
  assign xor_141_out = 4'b0011 ^ register_9_q;  // XOR_Gate xor_141, 4 bits wide
  assign not_164_out = ~xor_141_out;  // NOT_Gate not_164, 4 bits wide
  assign xor_142_out = 4'b0100 ^ register_9_q;  // XOR_Gate xor_142, 4 bits wide
  assign not_165_out = ~xor_142_out;  // NOT_Gate not_165, 4 bits wide
  assign xor_143_out = 4'b0101 ^ register_9_q;  // XOR_Gate xor_143, 4 bits wide
  assign not_166_out = ~xor_143_out;  // NOT_Gate not_166, 4 bits wide
  assign xor_144_out = 4'b0110 ^ register_9_q;  // XOR_Gate xor_144, 4 bits wide
  assign not_167_out = ~xor_144_out;  // NOT_Gate not_167, 4 bits wide
  assign xor_145_out = 4'b0111 ^ register_9_q;  // XOR_Gate xor_145, 4 bits wide
  assign not_168_out = ~xor_145_out;  // NOT_Gate not_168, 4 bits wide
  assign xor_146_out = 4'b1000 ^ register_9_q;  // XOR_Gate xor_146, 4 bits wide
  assign not_169_out = ~xor_146_out;  // NOT_Gate not_169, 4 bits wide
  assign xor_147_out = 4'b1001 ^ register_9_q;  // XOR_Gate xor_147, 4 bits wide
  assign not_170_out = ~xor_147_out;  // NOT_Gate not_170, 4 bits wide
  assign xor_148_out = 4'b1010 ^ register_9_q;  // XOR_Gate xor_148, 4 bits wide
  assign not_171_out = ~xor_148_out;  // NOT_Gate not_171, 4 bits wide
  assign xor_149_out = 4'b1011 ^ register_9_q;  // XOR_Gate xor_149, 4 bits wide
  assign not_172_out = ~xor_149_out;  // NOT_Gate not_172, 4 bits wide
  assign xor_150_out = 4'b1100 ^ register_9_q;  // XOR_Gate xor_150, 4 bits wide
  assign not_173_out = ~xor_150_out;  // NOT_Gate not_173, 4 bits wide
  assign xor_151_out = 4'b1101 ^ register_9_q;  // XOR_Gate xor_151, 4 bits wide
  assign not_174_out = ~xor_151_out;  // NOT_Gate not_174, 4 bits wide
  assign xor_152_out = 4'b1110 ^ register_9_q;  // XOR_Gate xor_152, 4 bits wide
  assign not_175_out = ~xor_152_out;  // NOT_Gate not_175, 4 bits wide
  assign xor_153_out = 4'b1111 ^ register_9_q;  // XOR_Gate xor_153, 4 bits wide
  assign not_176_out = ~xor_153_out;  // NOT_Gate not_176, 4 bits wide
  not not_177 (not_177_out, and_368_out);
  and and_368 (and_368_out, and_332_out, and_367_out);
  assign NewNode = and_368_out ? 4'b1001 : 4'bz;  // Controlled_Buffer controlled_buffer_25
  and and_369 (and_369_out, and_332_out, not_177_out);
  and and_370 (and_370_out, and_405_out, or_1_out);
  and and_371 (and_371_out, and_370_out, Clock);
  or or_151 (or_151_out, or_152_out, and_373_out);
  or or_152 (or_152_out, or_153_out, and_375_out);
  or or_153 (or_153_out, or_154_out, and_377_out);
  or or_154 (or_154_out, or_155_out, and_379_out);
  or or_155 (or_155_out, or_156_out, and_381_out);
  or or_156 (or_156_out, or_157_out, and_383_out);
  or or_157 (or_157_out, or_158_out, and_385_out);
  or or_158 (or_158_out, or_159_out, and_387_out);
  or or_159 (or_159_out, or_160_out, and_389_out);
  or or_160 (or_160_out, or_161_out, and_391_out);
  or or_161 (or_161_out, or_162_out, and_393_out);
  or or_162 (or_162_out, or_163_out, and_395_out);
  or or_163 (or_163_out, or_164_out, and_397_out);
  or or_164 (or_164_out, or_165_out, and_399_out);
  or or_165 (or_165_out, and_403_out, and_401_out);
  and and_372 (and_372_out, not_178_out[2], not_178_out[1], not_178_out[0]);
  assign not_178_out = ~xor_154_out;  // NOT_Gate not_178, 3 bits wide
  assign xor_154_out = 3'b000 ^ NaExp;  // XOR_Gate xor_154, 3 bits wide
  D_Flip_Flop #(.trigger("falling")) d_ff_10 (
    .D(and_370_out), .clk(and_371_out), .Qn(d_ff_10_qn), .reset(or_151_out));  // open: Q, preset
  Register #(.width(4)) register_10 (
    .D(controlled_buffer_1_out), .en(and_370_out), .clk(and_371_out), .Q(register_10_q), .clr(or_151_out));
  and and_373 (and_373_out, N0Clear, and_374_out);
  and and_374 (and_374_out, not_179_out[3], not_179_out[2], not_179_out[1], not_179_out[0]);
  assign xor_155_out = 4'b0000 ^ register_10_q;  // XOR_Gate xor_155, 4 bits wide
  assign not_179_out = ~xor_155_out;  // NOT_Gate not_179, 4 bits wide
  and and_375 (and_375_out, N1Clear, and_376_out);
  and and_376 (and_376_out, not_180_out[3], not_180_out[2], not_180_out[1], not_180_out[0]);
  assign xor_156_out = 4'b0001 ^ register_10_q;  // XOR_Gate xor_156, 4 bits wide
  assign not_180_out = ~xor_156_out;  // NOT_Gate not_180, 4 bits wide
  and and_377 (and_377_out, N2Clear, and_378_out);
  and and_378 (and_378_out, not_181_out[3], not_181_out[2], not_181_out[1], not_181_out[0]);
  assign xor_157_out = 4'b0010 ^ register_10_q;  // XOR_Gate xor_157, 4 bits wide
  assign not_181_out = ~xor_157_out;  // NOT_Gate not_181, 4 bits wide
  and and_379 (and_379_out, N3Clear, and_380_out);
  and and_380 (and_380_out, not_182_out[3], not_182_out[2], not_182_out[1], not_182_out[0]);
  assign xor_158_out = 4'b0011 ^ register_10_q;  // XOR_Gate xor_158, 4 bits wide
  assign not_182_out = ~xor_158_out;  // NOT_Gate not_182, 4 bits wide
  and and_381 (and_381_out, N4Clear, and_382_out);
  and and_382 (and_382_out, not_183_out[3], not_183_out[2], not_183_out[1], not_183_out[0]);
  assign xor_159_out = 4'b0100 ^ register_10_q;  // XOR_Gate xor_159, 4 bits wide
  assign not_183_out = ~xor_159_out;  // NOT_Gate not_183, 4 bits wide
  and and_383 (and_383_out, N5Clear, and_384_out);
  and and_384 (and_384_out, not_184_out[3], not_184_out[2], not_184_out[1], not_184_out[0]);
  assign xor_160_out = 4'b0101 ^ register_10_q;  // XOR_Gate xor_160, 4 bits wide
  assign not_184_out = ~xor_160_out;  // NOT_Gate not_184, 4 bits wide
  and and_385 (and_385_out, N6Clear, and_386_out);
  and and_386 (and_386_out, not_185_out[3], not_185_out[2], not_185_out[1], not_185_out[0]);
  assign xor_161_out = 4'b0110 ^ register_10_q;  // XOR_Gate xor_161, 4 bits wide
  assign not_185_out = ~xor_161_out;  // NOT_Gate not_185, 4 bits wide
  and and_387 (and_387_out, N7Clear, and_388_out);
  and and_388 (and_388_out, not_186_out[3], not_186_out[2], not_186_out[1], not_186_out[0]);
  assign xor_162_out = 4'b0111 ^ register_10_q;  // XOR_Gate xor_162, 4 bits wide
  assign not_186_out = ~xor_162_out;  // NOT_Gate not_186, 4 bits wide
  and and_389 (and_389_out, N8Clear, and_390_out);
  and and_390 (and_390_out, not_187_out[3], not_187_out[2], not_187_out[1], not_187_out[0]);
  assign xor_163_out = 4'b1000 ^ register_10_q;  // XOR_Gate xor_163, 4 bits wide
  assign not_187_out = ~xor_163_out;  // NOT_Gate not_187, 4 bits wide
  and and_391 (and_391_out, N9Clear, and_392_out);
  and and_392 (and_392_out, not_188_out[3], not_188_out[2], not_188_out[1], not_188_out[0]);
  assign xor_164_out = 4'b1001 ^ register_10_q;  // XOR_Gate xor_164, 4 bits wide
  assign not_188_out = ~xor_164_out;  // NOT_Gate not_188, 4 bits wide
  and and_393 (and_393_out, NaClear, and_394_out);
  and and_394 (and_394_out, not_189_out[3], not_189_out[2], not_189_out[1], not_189_out[0]);
  assign xor_165_out = 4'b1010 ^ register_10_q;  // XOR_Gate xor_165, 4 bits wide
  assign not_189_out = ~xor_165_out;  // NOT_Gate not_189, 4 bits wide
  and and_395 (and_395_out, NbClear, and_396_out);
  and and_396 (and_396_out, not_190_out[3], not_190_out[2], not_190_out[1], not_190_out[0]);
  assign xor_166_out = 4'b1011 ^ register_10_q;  // XOR_Gate xor_166, 4 bits wide
  assign not_190_out = ~xor_166_out;  // NOT_Gate not_190, 4 bits wide
  and and_397 (and_397_out, NcClear, and_398_out);
  and and_398 (and_398_out, not_191_out[3], not_191_out[2], not_191_out[1], not_191_out[0]);
  assign xor_167_out = 4'b1100 ^ register_10_q;  // XOR_Gate xor_167, 4 bits wide
  assign not_191_out = ~xor_167_out;  // NOT_Gate not_191, 4 bits wide
  and and_399 (and_399_out, NdClear, and_400_out);
  and and_400 (and_400_out, not_192_out[3], not_192_out[2], not_192_out[1], not_192_out[0]);
  assign xor_168_out = 4'b1101 ^ register_10_q;  // XOR_Gate xor_168, 4 bits wide
  assign not_192_out = ~xor_168_out;  // NOT_Gate not_192, 4 bits wide
  and and_401 (and_401_out, NeClear, and_402_out);
  and and_402 (and_402_out, not_193_out[3], not_193_out[2], not_193_out[1], not_193_out[0]);
  assign xor_169_out = 4'b1110 ^ register_10_q;  // XOR_Gate xor_169, 4 bits wide
  assign not_193_out = ~xor_169_out;  // NOT_Gate not_193, 4 bits wide
  and and_403 (and_403_out, NfClear, and_404_out);
  and and_404 (and_404_out, not_194_out[3], not_194_out[2], not_194_out[1], not_194_out[0]);
  assign xor_170_out = 4'b1111 ^ register_10_q;  // XOR_Gate xor_170, 4 bits wide
  assign not_194_out = ~xor_170_out;  // NOT_Gate not_194, 4 bits wide
  and and_405 (and_405_out, and_369_out, and_406_out);
  and and_406 (and_406_out, d_ff_10_qn, and_372_out);
  assign NewNode = and_405_out ? 4'b1010 : 4'bz;  // Controlled_Buffer controlled_buffer_26
  and and_407 (and_407_out, and_369_out, not_195_out);
  not not_195 (not_195_out, and_405_out);
  and and_408 (and_408_out, and_444_out, or_1_out);
  and and_409 (and_409_out, and_408_out, Clock);
  and and_410 (and_410_out, not_196_out[2], not_196_out[1], not_196_out[0]);
  assign not_196_out = ~xor_171_out;  // NOT_Gate not_196, 3 bits wide
  assign xor_171_out = 3'b000 ^ NbExp;  // XOR_Gate xor_171, 3 bits wide
  D_Flip_Flop #(.trigger("falling")) d_ff_11 (
    .D(and_408_out), .clk(and_409_out), .Qn(d_ff_11_qn), .reset(or_166_out));  // open: Q, preset
  Register #(.width(4)) register_11 (
    .D(controlled_buffer_1_out), .en(and_408_out), .clk(and_409_out), .Q(register_11_q), .clr(or_166_out));
  or or_166 (or_166_out, or_167_out, and_411_out);
  and and_411 (and_411_out, N0Clear, and_412_out);
  and and_412 (and_412_out, not_197_out[3], not_197_out[2], not_197_out[1], not_197_out[0]);
  or or_167 (or_167_out, or_168_out, and_413_out);
  and and_413 (and_413_out, N1Clear, and_414_out);
  and and_414 (and_414_out, not_198_out[3], not_198_out[2], not_198_out[1], not_198_out[0]);
  or or_168 (or_168_out, or_169_out, and_415_out);
  and and_415 (and_415_out, N2Clear, and_416_out);
  and and_416 (and_416_out, not_199_out[3], not_199_out[2], not_199_out[1], not_199_out[0]);
  or or_169 (or_169_out, or_170_out, and_417_out);
  and and_417 (and_417_out, N3Clear, and_418_out);
  and and_418 (and_418_out, not_200_out[3], not_200_out[2], not_200_out[1], not_200_out[0]);
  or or_170 (or_170_out, or_171_out, and_419_out);
  and and_419 (and_419_out, N4Clear, and_420_out);
  and and_420 (and_420_out, not_201_out[3], not_201_out[2], not_201_out[1], not_201_out[0]);
  or or_171 (or_171_out, or_172_out, and_421_out);
  and and_421 (and_421_out, N5Clear, and_422_out);
  and and_422 (and_422_out, not_202_out[3], not_202_out[2], not_202_out[1], not_202_out[0]);
  or or_172 (or_172_out, or_173_out, and_423_out);
  and and_423 (and_423_out, N6Clear, and_424_out);
  and and_424 (and_424_out, not_203_out[3], not_203_out[2], not_203_out[1], not_203_out[0]);
  or or_173 (or_173_out, or_174_out, and_425_out);
  and and_425 (and_425_out, N7Clear, and_426_out);
  and and_426 (and_426_out, not_204_out[3], not_204_out[2], not_204_out[1], not_204_out[0]);
  or or_174 (or_174_out, or_175_out, and_427_out);
  and and_427 (and_427_out, N8Clear, and_428_out);
  and and_428 (and_428_out, not_205_out[3], not_205_out[2], not_205_out[1], not_205_out[0]);
  or or_175 (or_175_out, or_176_out, and_429_out);
  and and_429 (and_429_out, N9Clear, and_430_out);
  and and_430 (and_430_out, not_206_out[3], not_206_out[2], not_206_out[1], not_206_out[0]);
  or or_176 (or_176_out, or_177_out, and_431_out);
  and and_431 (and_431_out, NaClear, and_432_out);
  and and_432 (and_432_out, not_207_out[3], not_207_out[2], not_207_out[1], not_207_out[0]);
  or or_177 (or_177_out, or_178_out, and_433_out);
  and and_433 (and_433_out, NbClear, and_434_out);
  and and_434 (and_434_out, not_208_out[3], not_208_out[2], not_208_out[1], not_208_out[0]);
  or or_178 (or_178_out, or_179_out, and_435_out);
  and and_435 (and_435_out, NcClear, and_436_out);
  and and_436 (and_436_out, not_209_out[3], not_209_out[2], not_209_out[1], not_209_out[0]);
  or or_179 (or_179_out, or_180_out, and_437_out);
  and and_437 (and_437_out, NdClear, and_438_out);
  and and_438 (and_438_out, not_210_out[3], not_210_out[2], not_210_out[1], not_210_out[0]);
  or or_180 (or_180_out, and_441_out, and_439_out);
  and and_439 (and_439_out, NeClear, and_440_out);
  and and_440 (and_440_out, not_211_out[3], not_211_out[2], not_211_out[1], not_211_out[0]);
  and and_441 (and_441_out, NfClear, and_442_out);
  and and_442 (and_442_out, not_212_out[3], not_212_out[2], not_212_out[1], not_212_out[0]);
  and and_443 (and_443_out, d_ff_11_qn, and_410_out);
  assign xor_172_out = 4'b0000 ^ register_11_q;  // XOR_Gate xor_172, 4 bits wide
  assign not_197_out = ~xor_172_out;  // NOT_Gate not_197, 4 bits wide
  assign xor_173_out = 4'b0001 ^ register_11_q;  // XOR_Gate xor_173, 4 bits wide
  assign not_198_out = ~xor_173_out;  // NOT_Gate not_198, 4 bits wide
  assign xor_174_out = 4'b0010 ^ register_11_q;  // XOR_Gate xor_174, 4 bits wide
  assign not_199_out = ~xor_174_out;  // NOT_Gate not_199, 4 bits wide
  assign xor_175_out = 4'b0011 ^ register_11_q;  // XOR_Gate xor_175, 4 bits wide
  assign not_200_out = ~xor_175_out;  // NOT_Gate not_200, 4 bits wide
  assign xor_176_out = 4'b0100 ^ register_11_q;  // XOR_Gate xor_176, 4 bits wide
  assign not_201_out = ~xor_176_out;  // NOT_Gate not_201, 4 bits wide
  assign xor_177_out = 4'b0101 ^ register_11_q;  // XOR_Gate xor_177, 4 bits wide
  assign not_202_out = ~xor_177_out;  // NOT_Gate not_202, 4 bits wide
  assign xor_178_out = 4'b0110 ^ register_11_q;  // XOR_Gate xor_178, 4 bits wide
  assign not_203_out = ~xor_178_out;  // NOT_Gate not_203, 4 bits wide
  assign xor_179_out = 4'b0111 ^ register_11_q;  // XOR_Gate xor_179, 4 bits wide
  assign not_204_out = ~xor_179_out;  // NOT_Gate not_204, 4 bits wide
  assign xor_180_out = 4'b1000 ^ register_11_q;  // XOR_Gate xor_180, 4 bits wide
  assign not_205_out = ~xor_180_out;  // NOT_Gate not_205, 4 bits wide
  assign xor_181_out = 4'b1001 ^ register_11_q;  // XOR_Gate xor_181, 4 bits wide
  assign not_206_out = ~xor_181_out;  // NOT_Gate not_206, 4 bits wide
  assign xor_182_out = 4'b1010 ^ register_11_q;  // XOR_Gate xor_182, 4 bits wide
  assign not_207_out = ~xor_182_out;  // NOT_Gate not_207, 4 bits wide
  assign xor_183_out = 4'b1011 ^ register_11_q;  // XOR_Gate xor_183, 4 bits wide
  assign not_208_out = ~xor_183_out;  // NOT_Gate not_208, 4 bits wide
  assign xor_184_out = 4'b1100 ^ register_11_q;  // XOR_Gate xor_184, 4 bits wide
  assign not_209_out = ~xor_184_out;  // NOT_Gate not_209, 4 bits wide
  assign xor_185_out = 4'b1101 ^ register_11_q;  // XOR_Gate xor_185, 4 bits wide
  assign not_210_out = ~xor_185_out;  // NOT_Gate not_210, 4 bits wide
  assign xor_186_out = 4'b1110 ^ register_11_q;  // XOR_Gate xor_186, 4 bits wide
  assign not_211_out = ~xor_186_out;  // NOT_Gate not_211, 4 bits wide
  assign xor_187_out = 4'b1111 ^ register_11_q;  // XOR_Gate xor_187, 4 bits wide
  assign not_212_out = ~xor_187_out;  // NOT_Gate not_212, 4 bits wide
  not not_213 (not_213_out, and_444_out);
  and and_444 (and_444_out, and_407_out, and_443_out);
  assign NewNode = and_444_out ? 4'b1011 : 4'bz;  // Controlled_Buffer controlled_buffer_27
  assign not_214_out = ~xor_188_out;  // NOT_Gate not_214, 3 bits wide
  assign xor_188_out = 3'b000 ^ NcExp;  // XOR_Gate xor_188, 3 bits wide
  and and_445 (and_445_out, and_407_out, not_213_out);
  and and_446 (and_446_out, and_481_out, or_1_out);
  D_Flip_Flop #(.trigger("falling")) d_ff_12 (
    .D(and_446_out), .clk(and_447_out), .Qn(d_ff_12_qn), .reset(or_181_out));  // open: Q, preset
  Register #(.width(4)) register_12 (
    .D(controlled_buffer_1_out), .en(and_446_out), .clk(and_447_out), .Q(register_12_q), .clr(or_181_out));
  and and_447 (and_447_out, and_446_out, Clock);
  or or_181 (or_181_out, or_182_out, and_448_out);
  and and_448 (and_448_out, N0Clear, and_449_out);
  and and_449 (and_449_out, not_215_out[3], not_215_out[2], not_215_out[1], not_215_out[0]);
  or or_182 (or_182_out, or_183_out, and_450_out);
  and and_450 (and_450_out, N1Clear, and_451_out);
  and and_451 (and_451_out, not_216_out[3], not_216_out[2], not_216_out[1], not_216_out[0]);
  or or_183 (or_183_out, or_184_out, and_452_out);
  and and_452 (and_452_out, N2Clear, and_453_out);
  and and_453 (and_453_out, not_217_out[3], not_217_out[2], not_217_out[1], not_217_out[0]);
  or or_184 (or_184_out, or_185_out, and_454_out);
  and and_454 (and_454_out, N3Clear, and_455_out);
  and and_455 (and_455_out, not_218_out[3], not_218_out[2], not_218_out[1], not_218_out[0]);
  or or_185 (or_185_out, or_186_out, and_456_out);
  and and_456 (and_456_out, N4Clear, and_457_out);
  and and_457 (and_457_out, not_219_out[3], not_219_out[2], not_219_out[1], not_219_out[0]);
  or or_186 (or_186_out, or_187_out, and_458_out);
  and and_458 (and_458_out, N5Clear, and_459_out);
  and and_459 (and_459_out, not_220_out[3], not_220_out[2], not_220_out[1], not_220_out[0]);
  or or_187 (or_187_out, or_188_out, and_460_out);
  and and_460 (and_460_out, N6Clear, and_461_out);
  and and_461 (and_461_out, not_221_out[3], not_221_out[2], not_221_out[1], not_221_out[0]);
  or or_188 (or_188_out, or_189_out, and_462_out);
  and and_462 (and_462_out, N7Clear, and_463_out);
  and and_463 (and_463_out, not_222_out[3], not_222_out[2], not_222_out[1], not_222_out[0]);
  or or_189 (or_189_out, or_190_out, and_464_out);
  and and_464 (and_464_out, N8Clear, and_465_out);
  and and_465 (and_465_out, not_223_out[3], not_223_out[2], not_223_out[1], not_223_out[0]);
  or or_190 (or_190_out, or_191_out, and_466_out);
  and and_466 (and_466_out, N9Clear, and_467_out);
  and and_467 (and_467_out, not_224_out[3], not_224_out[2], not_224_out[1], not_224_out[0]);
  or or_191 (or_191_out, or_192_out, and_468_out);
  and and_468 (and_468_out, NaClear, and_469_out);
  and and_469 (and_469_out, not_225_out[3], not_225_out[2], not_225_out[1], not_225_out[0]);
  or or_192 (or_192_out, or_193_out, and_470_out);
  and and_470 (and_470_out, NbClear, and_471_out);
  and and_471 (and_471_out, not_226_out[3], not_226_out[2], not_226_out[1], not_226_out[0]);
  or or_193 (or_193_out, or_194_out, and_472_out);
  and and_472 (and_472_out, NcClear, and_473_out);
  and and_473 (and_473_out, not_227_out[3], not_227_out[2], not_227_out[1], not_227_out[0]);
  or or_194 (or_194_out, or_195_out, and_474_out);
  and and_474 (and_474_out, NdClear, and_475_out);
  and and_475 (and_475_out, not_228_out[3], not_228_out[2], not_228_out[1], not_228_out[0]);
  or or_195 (or_195_out, and_478_out, and_476_out);
  and and_476 (and_476_out, NeClear, and_477_out);
  and and_477 (and_477_out, not_229_out[3], not_229_out[2], not_229_out[1], not_229_out[0]);
  and and_478 (and_478_out, NfClear, and_479_out);
  and and_479 (and_479_out, not_230_out[3], not_230_out[2], not_230_out[1], not_230_out[0]);
  and and_480 (and_480_out, not_214_out[2], not_214_out[1], not_214_out[0]);
  assign xor_189_out = 4'b0000 ^ register_12_q;  // XOR_Gate xor_189, 4 bits wide
  assign not_215_out = ~xor_189_out;  // NOT_Gate not_215, 4 bits wide
  assign xor_190_out = 4'b0001 ^ register_12_q;  // XOR_Gate xor_190, 4 bits wide
  assign not_216_out = ~xor_190_out;  // NOT_Gate not_216, 4 bits wide
  assign xor_191_out = 4'b0010 ^ register_12_q;  // XOR_Gate xor_191, 4 bits wide
  assign not_217_out = ~xor_191_out;  // NOT_Gate not_217, 4 bits wide
  assign xor_192_out = 4'b0011 ^ register_12_q;  // XOR_Gate xor_192, 4 bits wide
  assign not_218_out = ~xor_192_out;  // NOT_Gate not_218, 4 bits wide
  assign xor_193_out = 4'b0100 ^ register_12_q;  // XOR_Gate xor_193, 4 bits wide
  assign not_219_out = ~xor_193_out;  // NOT_Gate not_219, 4 bits wide
  assign xor_194_out = 4'b0101 ^ register_12_q;  // XOR_Gate xor_194, 4 bits wide
  assign not_220_out = ~xor_194_out;  // NOT_Gate not_220, 4 bits wide
  assign xor_195_out = 4'b0110 ^ register_12_q;  // XOR_Gate xor_195, 4 bits wide
  assign not_221_out = ~xor_195_out;  // NOT_Gate not_221, 4 bits wide
  assign xor_196_out = 4'b0111 ^ register_12_q;  // XOR_Gate xor_196, 4 bits wide
  assign not_222_out = ~xor_196_out;  // NOT_Gate not_222, 4 bits wide
  assign xor_197_out = 4'b1000 ^ register_12_q;  // XOR_Gate xor_197, 4 bits wide
  assign not_223_out = ~xor_197_out;  // NOT_Gate not_223, 4 bits wide
  assign xor_198_out = 4'b1001 ^ register_12_q;  // XOR_Gate xor_198, 4 bits wide
  assign not_224_out = ~xor_198_out;  // NOT_Gate not_224, 4 bits wide
  assign xor_199_out = 4'b1010 ^ register_12_q;  // XOR_Gate xor_199, 4 bits wide
  assign not_225_out = ~xor_199_out;  // NOT_Gate not_225, 4 bits wide
  assign xor_200_out = 4'b1011 ^ register_12_q;  // XOR_Gate xor_200, 4 bits wide
  assign not_226_out = ~xor_200_out;  // NOT_Gate not_226, 4 bits wide
  assign xor_201_out = 4'b1100 ^ register_12_q;  // XOR_Gate xor_201, 4 bits wide
  assign not_227_out = ~xor_201_out;  // NOT_Gate not_227, 4 bits wide
  assign xor_202_out = 4'b1101 ^ register_12_q;  // XOR_Gate xor_202, 4 bits wide
  assign not_228_out = ~xor_202_out;  // NOT_Gate not_228, 4 bits wide
  assign xor_203_out = 4'b1110 ^ register_12_q;  // XOR_Gate xor_203, 4 bits wide
  assign not_229_out = ~xor_203_out;  // NOT_Gate not_229, 4 bits wide
  assign xor_204_out = 4'b1111 ^ register_12_q;  // XOR_Gate xor_204, 4 bits wide
  assign not_230_out = ~xor_204_out;  // NOT_Gate not_230, 4 bits wide
  and and_481 (and_481_out, and_445_out, and_482_out);
  and and_482 (and_482_out, d_ff_12_qn, and_480_out);
  assign NewNode = and_481_out ? 4'b1100 : 4'bz;  // Controlled_Buffer controlled_buffer_28
  and and_483 (and_483_out, and_445_out, not_231_out);
  not not_231 (not_231_out, and_481_out);
  and and_484 (and_484_out, and_519_out, or_1_out);
  and and_485 (and_485_out, and_484_out, Clock);
  and and_486 (and_486_out, not_232_out[2], not_232_out[1], not_232_out[0]);
  assign not_232_out = ~xor_205_out;  // NOT_Gate not_232, 3 bits wide
  assign xor_205_out = 3'b000 ^ NdExp;  // XOR_Gate xor_205, 3 bits wide
  D_Flip_Flop #(.trigger("falling")) d_ff_13 (
    .D(and_484_out), .clk(and_485_out), .Qn(d_ff_13_qn), .reset(or_196_out));  // open: Q, preset
  Register #(.width(4)) register_13 (
    .D(controlled_buffer_1_out), .en(and_484_out), .clk(and_485_out), .Q(register_13_q), .clr(or_196_out));
  or or_196 (or_196_out, or_197_out, and_487_out);
  and and_487 (and_487_out, N0Clear, and_488_out);
  and and_488 (and_488_out, not_233_out[3], not_233_out[2], not_233_out[1], not_233_out[0]);
  assign xor_206_out = 4'b0000 ^ register_13_q;  // XOR_Gate xor_206, 4 bits wide
  or or_197 (or_197_out, or_198_out, and_489_out);
  assign not_233_out = ~xor_206_out;  // NOT_Gate not_233, 4 bits wide
  and and_489 (and_489_out, N1Clear, and_490_out);
  and and_490 (and_490_out, not_234_out[3], not_234_out[2], not_234_out[1], not_234_out[0]);
  assign xor_207_out = 4'b0001 ^ register_13_q;  // XOR_Gate xor_207, 4 bits wide
  or or_198 (or_198_out, or_199_out, and_491_out);
  assign not_234_out = ~xor_207_out;  // NOT_Gate not_234, 4 bits wide
  and and_491 (and_491_out, N2Clear, and_492_out);
  and and_492 (and_492_out, not_235_out[3], not_235_out[2], not_235_out[1], not_235_out[0]);
  assign xor_208_out = 4'b0010 ^ register_13_q;  // XOR_Gate xor_208, 4 bits wide
  or or_199 (or_199_out, or_200_out, and_493_out);
  assign not_235_out = ~xor_208_out;  // NOT_Gate not_235, 4 bits wide
  and and_493 (and_493_out, N3Clear, and_494_out);
  and and_494 (and_494_out, not_236_out[3], not_236_out[2], not_236_out[1], not_236_out[0]);
  assign xor_209_out = 4'b0011 ^ register_13_q;  // XOR_Gate xor_209, 4 bits wide
  or or_200 (or_200_out, or_201_out, and_495_out);
  assign not_236_out = ~xor_209_out;  // NOT_Gate not_236, 4 bits wide
  and and_495 (and_495_out, N4Clear, and_496_out);
  and and_496 (and_496_out, not_237_out[3], not_237_out[2], not_237_out[1], not_237_out[0]);
  assign xor_210_out = 4'b0100 ^ register_13_q;  // XOR_Gate xor_210, 4 bits wide
  or or_201 (or_201_out, or_202_out, and_497_out);
  assign not_237_out = ~xor_210_out;  // NOT_Gate not_237, 4 bits wide
  and and_497 (and_497_out, N5Clear, and_498_out);
  and and_498 (and_498_out, not_238_out[3], not_238_out[2], not_238_out[1], not_238_out[0]);
  assign xor_211_out = 4'b0101 ^ register_13_q;  // XOR_Gate xor_211, 4 bits wide
  or or_202 (or_202_out, or_203_out, and_499_out);
  assign not_238_out = ~xor_211_out;  // NOT_Gate not_238, 4 bits wide
  and and_499 (and_499_out, N6Clear, and_500_out);
  and and_500 (and_500_out, not_239_out[3], not_239_out[2], not_239_out[1], not_239_out[0]);
  assign xor_212_out = 4'b0110 ^ register_13_q;  // XOR_Gate xor_212, 4 bits wide
  or or_203 (or_203_out, or_204_out, and_501_out);
  assign not_239_out = ~xor_212_out;  // NOT_Gate not_239, 4 bits wide
  and and_501 (and_501_out, N7Clear, and_502_out);
  and and_502 (and_502_out, not_240_out[3], not_240_out[2], not_240_out[1], not_240_out[0]);
  assign xor_213_out = 4'b0111 ^ register_13_q;  // XOR_Gate xor_213, 4 bits wide
  or or_204 (or_204_out, or_205_out, and_503_out);
  assign not_240_out = ~xor_213_out;  // NOT_Gate not_240, 4 bits wide
  and and_503 (and_503_out, N8Clear, and_504_out);
  and and_504 (and_504_out, not_241_out[3], not_241_out[2], not_241_out[1], not_241_out[0]);
  assign xor_214_out = 4'b1000 ^ register_13_q;  // XOR_Gate xor_214, 4 bits wide
  or or_205 (or_205_out, or_206_out, and_505_out);
  assign not_241_out = ~xor_214_out;  // NOT_Gate not_241, 4 bits wide
  and and_505 (and_505_out, N9Clear, and_506_out);
  and and_506 (and_506_out, not_242_out[3], not_242_out[2], not_242_out[1], not_242_out[0]);
  assign xor_215_out = 4'b1001 ^ register_13_q;  // XOR_Gate xor_215, 4 bits wide
  or or_206 (or_206_out, or_207_out, and_507_out);
  assign not_242_out = ~xor_215_out;  // NOT_Gate not_242, 4 bits wide
  and and_507 (and_507_out, NaClear, and_508_out);
  and and_508 (and_508_out, not_243_out[3], not_243_out[2], not_243_out[1], not_243_out[0]);
  assign xor_216_out = 4'b1010 ^ register_13_q;  // XOR_Gate xor_216, 4 bits wide
  or or_207 (or_207_out, or_208_out, and_509_out);
  assign not_243_out = ~xor_216_out;  // NOT_Gate not_243, 4 bits wide
  and and_509 (and_509_out, NbClear, and_510_out);
  and and_510 (and_510_out, not_244_out[3], not_244_out[2], not_244_out[1], not_244_out[0]);
  assign xor_217_out = 4'b1011 ^ register_13_q;  // XOR_Gate xor_217, 4 bits wide
  or or_208 (or_208_out, or_209_out, and_511_out);
  assign not_244_out = ~xor_217_out;  // NOT_Gate not_244, 4 bits wide
  and and_511 (and_511_out, NcClear, and_512_out);
  and and_512 (and_512_out, not_245_out[3], not_245_out[2], not_245_out[1], not_245_out[0]);
  assign xor_218_out = 4'b1100 ^ register_13_q;  // XOR_Gate xor_218, 4 bits wide
  or or_209 (or_209_out, or_210_out, and_513_out);
  assign not_245_out = ~xor_218_out;  // NOT_Gate not_245, 4 bits wide
  and and_513 (and_513_out, NdClear, and_514_out);
  and and_514 (and_514_out, not_246_out[3], not_246_out[2], not_246_out[1], not_246_out[0]);
  assign xor_219_out = 4'b1101 ^ register_13_q;  // XOR_Gate xor_219, 4 bits wide
  or or_210 (or_210_out, and_517_out, and_515_out);
  assign not_246_out = ~xor_219_out;  // NOT_Gate not_246, 4 bits wide
  and and_515 (and_515_out, NeClear, and_516_out);
  and and_516 (and_516_out, not_247_out[3], not_247_out[2], not_247_out[1], not_247_out[0]);
  assign xor_220_out = 4'b1110 ^ register_13_q;  // XOR_Gate xor_220, 4 bits wide
  assign not_247_out = ~xor_220_out;  // NOT_Gate not_247, 4 bits wide
  and and_517 (and_517_out, NfClear, and_518_out);
  and and_518 (and_518_out, not_248_out[3], not_248_out[2], not_248_out[1], not_248_out[0]);
  assign xor_221_out = 4'b1111 ^ register_13_q;  // XOR_Gate xor_221, 4 bits wide
  assign not_248_out = ~xor_221_out;  // NOT_Gate not_248, 4 bits wide
  and and_519 (and_519_out, and_483_out, and_520_out);
  and and_520 (and_520_out, d_ff_13_qn, and_486_out);
  assign NewNode = and_519_out ? 4'b1101 : 4'bz;  // Controlled_Buffer controlled_buffer_29
  and and_521 (and_521_out, and_483_out, not_249_out);
  not not_249 (not_249_out, and_519_out);
  and and_522 (and_522_out, and_524_out, Clock);
  and and_523 (and_523_out, not_250_out[2], not_250_out[1], not_250_out[0]);
  assign not_250_out = ~xor_222_out;  // NOT_Gate not_250, 3 bits wide
  assign xor_222_out = 3'b000 ^ NeExp;  // XOR_Gate xor_222, 3 bits wide
  and and_524 (and_524_out, and_558_out, or_1_out);
  D_Flip_Flop #(.trigger("falling")) d_ff_14 (
    .D(and_524_out), .clk(and_522_out), .Qn(d_ff_14_qn), .reset(or_211_out));  // open: Q, preset
  Register #(.width(4)) register_14 (
    .D(controlled_buffer_1_out), .en(and_524_out), .clk(and_522_out), .Q(register_14_q), .clr(or_211_out));
  or or_211 (or_211_out, or_212_out, and_525_out);
  and and_525 (and_525_out, N0Clear, and_526_out);
  and and_526 (and_526_out, not_251_out[3], not_251_out[2], not_251_out[1], not_251_out[0]);
  or or_212 (or_212_out, or_213_out, and_527_out);
  and and_527 (and_527_out, N1Clear, and_528_out);
  and and_528 (and_528_out, not_252_out[3], not_252_out[2], not_252_out[1], not_252_out[0]);
  or or_213 (or_213_out, or_214_out, and_529_out);
  and and_529 (and_529_out, N2Clear, and_530_out);
  and and_530 (and_530_out, not_253_out[3], not_253_out[2], not_253_out[1], not_253_out[0]);
  or or_214 (or_214_out, or_215_out, and_531_out);
  and and_531 (and_531_out, N3Clear, and_532_out);
  and and_532 (and_532_out, not_254_out[3], not_254_out[2], not_254_out[1], not_254_out[0]);
  or or_215 (or_215_out, or_216_out, and_533_out);
  and and_533 (and_533_out, N4Clear, and_534_out);
  and and_534 (and_534_out, not_255_out[3], not_255_out[2], not_255_out[1], not_255_out[0]);
  or or_216 (or_216_out, or_217_out, and_535_out);
  and and_535 (and_535_out, N5Clear, and_536_out);
  and and_536 (and_536_out, not_256_out[3], not_256_out[2], not_256_out[1], not_256_out[0]);
  or or_217 (or_217_out, or_218_out, and_537_out);
  and and_537 (and_537_out, N6Clear, and_538_out);
  and and_538 (and_538_out, not_257_out[3], not_257_out[2], not_257_out[1], not_257_out[0]);
  or or_218 (or_218_out, or_219_out, and_539_out);
  and and_539 (and_539_out, N7Clear, and_540_out);
  and and_540 (and_540_out, not_258_out[3], not_258_out[2], not_258_out[1], not_258_out[0]);
  or or_219 (or_219_out, or_220_out, and_541_out);
  and and_541 (and_541_out, N8Clear, and_542_out);
  and and_542 (and_542_out, not_259_out[3], not_259_out[2], not_259_out[1], not_259_out[0]);
  or or_220 (or_220_out, or_221_out, and_543_out);
  and and_543 (and_543_out, N9Clear, and_544_out);
  and and_544 (and_544_out, not_260_out[3], not_260_out[2], not_260_out[1], not_260_out[0]);
  or or_221 (or_221_out, or_222_out, and_545_out);
  and and_545 (and_545_out, NaClear, and_546_out);
  and and_546 (and_546_out, not_261_out[3], not_261_out[2], not_261_out[1], not_261_out[0]);
  or or_222 (or_222_out, or_223_out, and_547_out);
  and and_547 (and_547_out, NbClear, and_548_out);
  and and_548 (and_548_out, not_262_out[3], not_262_out[2], not_262_out[1], not_262_out[0]);
  or or_223 (or_223_out, or_224_out, and_549_out);
  and and_549 (and_549_out, NcClear, and_550_out);
  and and_550 (and_550_out, not_263_out[3], not_263_out[2], not_263_out[1], not_263_out[0]);
  or or_224 (or_224_out, or_225_out, and_551_out);
  and and_551 (and_551_out, NdClear, and_552_out);
  and and_552 (and_552_out, not_264_out[3], not_264_out[2], not_264_out[1], not_264_out[0]);
  or or_225 (or_225_out, and_555_out, and_553_out);
  and and_553 (and_553_out, NeClear, and_554_out);
  and and_554 (and_554_out, not_265_out[3], not_265_out[2], not_265_out[1], not_265_out[0]);
  and and_555 (and_555_out, NfClear, and_556_out);
  and and_556 (and_556_out, not_266_out[3], not_266_out[2], not_266_out[1], not_266_out[0]);
  and and_557 (and_557_out, d_ff_14_qn, and_523_out);
  assign xor_223_out = 4'b0000 ^ register_14_q;  // XOR_Gate xor_223, 4 bits wide
  assign not_251_out = ~xor_223_out;  // NOT_Gate not_251, 4 bits wide
  assign xor_224_out = 4'b0001 ^ register_14_q;  // XOR_Gate xor_224, 4 bits wide
  assign not_252_out = ~xor_224_out;  // NOT_Gate not_252, 4 bits wide
  assign xor_225_out = 4'b0010 ^ register_14_q;  // XOR_Gate xor_225, 4 bits wide
  assign not_253_out = ~xor_225_out;  // NOT_Gate not_253, 4 bits wide
  assign xor_226_out = 4'b0011 ^ register_14_q;  // XOR_Gate xor_226, 4 bits wide
  assign not_254_out = ~xor_226_out;  // NOT_Gate not_254, 4 bits wide
  assign xor_227_out = 4'b0100 ^ register_14_q;  // XOR_Gate xor_227, 4 bits wide
  assign not_255_out = ~xor_227_out;  // NOT_Gate not_255, 4 bits wide
  assign xor_228_out = 4'b0101 ^ register_14_q;  // XOR_Gate xor_228, 4 bits wide
  assign not_256_out = ~xor_228_out;  // NOT_Gate not_256, 4 bits wide
  assign xor_229_out = 4'b0110 ^ register_14_q;  // XOR_Gate xor_229, 4 bits wide
  assign not_257_out = ~xor_229_out;  // NOT_Gate not_257, 4 bits wide
  assign xor_230_out = 4'b0111 ^ register_14_q;  // XOR_Gate xor_230, 4 bits wide
  assign not_258_out = ~xor_230_out;  // NOT_Gate not_258, 4 bits wide
  assign xor_231_out = 4'b1000 ^ register_14_q;  // XOR_Gate xor_231, 4 bits wide
  assign not_259_out = ~xor_231_out;  // NOT_Gate not_259, 4 bits wide
  assign xor_232_out = 4'b1001 ^ register_14_q;  // XOR_Gate xor_232, 4 bits wide
  assign not_260_out = ~xor_232_out;  // NOT_Gate not_260, 4 bits wide
  assign xor_233_out = 4'b1010 ^ register_14_q;  // XOR_Gate xor_233, 4 bits wide
  assign not_261_out = ~xor_233_out;  // NOT_Gate not_261, 4 bits wide
  assign xor_234_out = 4'b1011 ^ register_14_q;  // XOR_Gate xor_234, 4 bits wide
  assign not_262_out = ~xor_234_out;  // NOT_Gate not_262, 4 bits wide
  assign xor_235_out = 4'b1100 ^ register_14_q;  // XOR_Gate xor_235, 4 bits wide
  assign not_263_out = ~xor_235_out;  // NOT_Gate not_263, 4 bits wide
  assign xor_236_out = 4'b1101 ^ register_14_q;  // XOR_Gate xor_236, 4 bits wide
  assign not_264_out = ~xor_236_out;  // NOT_Gate not_264, 4 bits wide
  assign xor_237_out = 4'b1110 ^ register_14_q;  // XOR_Gate xor_237, 4 bits wide
  assign not_265_out = ~xor_237_out;  // NOT_Gate not_265, 4 bits wide
  assign xor_238_out = 4'b1111 ^ register_14_q;  // XOR_Gate xor_238, 4 bits wide
  assign not_266_out = ~xor_238_out;  // NOT_Gate not_266, 4 bits wide
  not not_267 (not_267_out, and_558_out);
  and and_558 (and_558_out, and_521_out, and_557_out);
  assign NewNode = and_558_out ? 4'b1110 : 4'bz;  // Controlled_Buffer controlled_buffer_30
  and and_559 (and_559_out, and_521_out, not_267_out);
  and and_560 (and_560_out, and_595_out, or_1_out);
  Register #(.width(4)) register_15 (
    .D(controlled_buffer_1_out), .en(and_560_out), .clk(and_561_out), .Q(register_15_q), .clr(or_226_out));
  and and_561 (and_561_out, and_560_out, Clock);
  or or_226 (or_226_out, or_227_out, and_562_out);
  and and_562 (and_562_out, N0Clear, and_579_out);
  or or_227 (or_227_out, or_228_out, and_563_out);
  and and_563 (and_563_out, N1Clear, and_580_out);
  or or_228 (or_228_out, or_229_out, and_564_out);
  and and_564 (and_564_out, N2Clear, and_581_out);
  or or_229 (or_229_out, or_230_out, and_565_out);
  and and_565 (and_565_out, N3Clear, and_582_out);
  or or_230 (or_230_out, or_231_out, and_566_out);
  and and_566 (and_566_out, N4Clear, and_583_out);
  or or_231 (or_231_out, or_232_out, and_567_out);
  and and_567 (and_567_out, N5Clear, and_584_out);
  or or_232 (or_232_out, or_233_out, and_568_out);
  and and_568 (and_568_out, N6Clear, and_585_out);
  or or_233 (or_233_out, or_234_out, and_569_out);
  and and_569 (and_569_out, N7Clear, and_586_out);
  or or_234 (or_234_out, or_235_out, and_570_out);
  and and_570 (and_570_out, N8Clear, and_587_out);
  or or_235 (or_235_out, or_236_out, and_571_out);
  and and_571 (and_571_out, N9Clear, and_588_out);
  or or_236 (or_236_out, or_237_out, and_572_out);
  and and_572 (and_572_out, NaClear, and_589_out);
  or or_237 (or_237_out, or_238_out, and_573_out);
  and and_573 (and_573_out, NbClear, and_590_out);
  or or_238 (or_238_out, or_239_out, and_574_out);
  and and_574 (and_574_out, NcClear, and_591_out);
  or or_239 (or_239_out, or_240_out, and_575_out);
  and and_575 (and_575_out, NdClear, and_592_out);
  or or_240 (or_240_out, and_577_out, and_576_out);
  and and_576 (and_576_out, NeClear, and_593_out);
  and and_577 (and_577_out, NfClear, and_594_out);
  and and_578 (and_578_out, not_268_out[2], not_268_out[1], not_268_out[0]);
  assign not_268_out = ~xor_239_out;  // NOT_Gate not_268, 3 bits wide
  assign xor_239_out = 3'b000 ^ NfExp;  // XOR_Gate xor_239, 3 bits wide
  D_Flip_Flop #(.trigger("falling")) d_ff_15 (
    .D(and_560_out), .clk(and_561_out), .Qn(d_ff_15_qn), .reset(or_226_out));  // open: Q, preset
  and and_579 (and_579_out, not_269_out[3], not_269_out[2], not_269_out[1], not_269_out[0]);
  assign xor_240_out = 4'b0000 ^ register_15_q;  // XOR_Gate xor_240, 4 bits wide
  assign not_269_out = ~xor_240_out;  // NOT_Gate not_269, 4 bits wide
  and and_580 (and_580_out, not_270_out[3], not_270_out[2], not_270_out[1], not_270_out[0]);
  assign xor_241_out = 4'b0001 ^ register_15_q;  // XOR_Gate xor_241, 4 bits wide
  assign not_270_out = ~xor_241_out;  // NOT_Gate not_270, 4 bits wide
  and and_581 (and_581_out, not_271_out[3], not_271_out[2], not_271_out[1], not_271_out[0]);
  assign xor_242_out = 4'b0010 ^ register_15_q;  // XOR_Gate xor_242, 4 bits wide
  assign not_271_out = ~xor_242_out;  // NOT_Gate not_271, 4 bits wide
  and and_582 (and_582_out, not_272_out[3], not_272_out[2], not_272_out[1], not_272_out[0]);
  assign xor_243_out = 4'b0011 ^ register_15_q;  // XOR_Gate xor_243, 4 bits wide
  assign not_272_out = ~xor_243_out;  // NOT_Gate not_272, 4 bits wide
  and and_583 (and_583_out, not_273_out[3], not_273_out[2], not_273_out[1], not_273_out[0]);
  assign xor_244_out = 4'b0100 ^ register_15_q;  // XOR_Gate xor_244, 4 bits wide
  assign not_273_out = ~xor_244_out;  // NOT_Gate not_273, 4 bits wide
  and and_584 (and_584_out, not_274_out[3], not_274_out[2], not_274_out[1], not_274_out[0]);
  assign xor_245_out = 4'b0101 ^ register_15_q;  // XOR_Gate xor_245, 4 bits wide
  assign not_274_out = ~xor_245_out;  // NOT_Gate not_274, 4 bits wide
  and and_585 (and_585_out, not_275_out[3], not_275_out[2], not_275_out[1], not_275_out[0]);
  assign xor_246_out = 4'b0110 ^ register_15_q;  // XOR_Gate xor_246, 4 bits wide
  assign not_275_out = ~xor_246_out;  // NOT_Gate not_275, 4 bits wide
  and and_586 (and_586_out, not_276_out[3], not_276_out[2], not_276_out[1], not_276_out[0]);
  assign xor_247_out = 4'b0111 ^ register_15_q;  // XOR_Gate xor_247, 4 bits wide
  assign not_276_out = ~xor_247_out;  // NOT_Gate not_276, 4 bits wide
  and and_587 (and_587_out, not_277_out[3], not_277_out[2], not_277_out[1], not_277_out[0]);
  assign xor_248_out = 4'b1000 ^ register_15_q;  // XOR_Gate xor_248, 4 bits wide
  assign not_277_out = ~xor_248_out;  // NOT_Gate not_277, 4 bits wide
  and and_588 (and_588_out, not_278_out[3], not_278_out[2], not_278_out[1], not_278_out[0]);
  assign xor_249_out = 4'b1001 ^ register_15_q;  // XOR_Gate xor_249, 4 bits wide
  assign not_278_out = ~xor_249_out;  // NOT_Gate not_278, 4 bits wide
  and and_589 (and_589_out, not_279_out[3], not_279_out[2], not_279_out[1], not_279_out[0]);
  assign xor_250_out = 4'b1010 ^ register_15_q;  // XOR_Gate xor_250, 4 bits wide
  assign not_279_out = ~xor_250_out;  // NOT_Gate not_279, 4 bits wide
  and and_590 (and_590_out, not_280_out[3], not_280_out[2], not_280_out[1], not_280_out[0]);
  assign xor_251_out = 4'b1011 ^ register_15_q;  // XOR_Gate xor_251, 4 bits wide
  assign not_280_out = ~xor_251_out;  // NOT_Gate not_280, 4 bits wide
  and and_591 (and_591_out, not_281_out[3], not_281_out[2], not_281_out[1], not_281_out[0]);
  assign xor_252_out = 4'b1100 ^ register_15_q;  // XOR_Gate xor_252, 4 bits wide
  assign not_281_out = ~xor_252_out;  // NOT_Gate not_281, 4 bits wide
  and and_592 (and_592_out, not_282_out[3], not_282_out[2], not_282_out[1], not_282_out[0]);
  assign xor_253_out = 4'b1101 ^ register_15_q;  // XOR_Gate xor_253, 4 bits wide
  assign not_282_out = ~xor_253_out;  // NOT_Gate not_282, 4 bits wide
  and and_593 (and_593_out, not_283_out[3], not_283_out[2], not_283_out[1], not_283_out[0]);
  assign xor_254_out = 4'b1110 ^ register_15_q;  // XOR_Gate xor_254, 4 bits wide
  assign not_283_out = ~xor_254_out;  // NOT_Gate not_283, 4 bits wide
  and and_594 (and_594_out, not_284_out[3], not_284_out[2], not_284_out[1], not_284_out[0]);
  assign xor_255_out = 4'b1111 ^ register_15_q;  // XOR_Gate xor_255, 4 bits wide
  assign not_284_out = ~xor_255_out;  // NOT_Gate not_284, 4 bits wide
  and and_595 (and_595_out, and_559_out, and_596_out);
  and and_596 (and_596_out, d_ff_15_qn, and_578_out);
  assign NewNode = and_595_out ? 4'b1111 : 4'bz;  // Controlled_Buffer controlled_buffer_31
endmodule
