// Logisim project ListExpressionExample(Designed by Jasmine Ritchie).circ as structural Verilog: 14 circuits, main circuit main
module main (
  input  [21:0] ParentIn,
  input  [3:0] NewID,
  input  [21:0] ChildLeftIn,
  input  [21:0] ChildRightIn,
  input  [3:0] RAMIn,
  input  Clock,
  input  [3:0] UniqueNodeID,
  output CurrentResolveState,
  output NewNodeRequest,
  output [2:0] CurrentExpressionType,
  output StackClear,
  output [21:0] ParentOut,
  output RAMWrite,
  output [3:0] RAM,
  output [3:0] RAMLoc,
  output [21:0] ChildLeftOut,
  output [21:0] ChildRightOut,
  output [3:0] ChildRightPointerOut,
  output [3:0] ChildLeftPointerOut
);

  wire and_1_out, and_2_out, and_3_out, and_4_out, and_5_out, and_6_out, and_7_out, and_8_out, and_9_out,
       and_10_out, d_ff_1_q, d_ff_2_q, d_ff_3_q, not_1_out, not_2_out, not_4_out, not_8_out, not_9_out,
       or_1_out, or_3_out, or_4_out, or_5_out, undefinedexpression_1_backstack,
       undefinedexpression_1_clearchidlren, undefinedexpression_1_expwrite, undefinedexpression_1_frontstack,
       undefinedexpression_1_ramselect;
  wire [2:0] not_3_out, not_5_out, not_6_out, not_7_out, register_4_q, xor_1_out, xor_2_out, xor_3_out,
       xor_4_out;
  wire [3:0] ChildL, ChildR, NewNode, register_5_q, register_6_q;
  wire [7:4] undefinedexpression_1_generaloutput;
  wire [11:0] undefinedexpression_1_newnode_2;

  Register #(.width(4)) register_1 (
    .D(undefinedexpression_1_newnode_2[3:0]), .en(undefinedexpression_1_expwrite), .clk(Clock), .Q(ChildR),
    .clr(undefinedexpression_1_clearchidlren));
  Register #(.width(4)) register_2 (
    .D(undefinedexpression_1_newnode_2[7:4]), .en(undefinedexpression_1_expwrite), .clk(Clock), .Q(ChildL),
    .clr(undefinedexpression_1_clearchidlren));
  Register #(.width(3)) register_3 (
    .D(undefinedexpression_1_newnode_2[10:8]), .en(undefinedexpression_1_expwrite), .clk(Clock),
    .Q(CurrentExpressionType));  // open: clr
  and and_1 (and_1_out, undefinedexpression_1_expwrite, undefinedexpression_1_newnode_2[11]);
  not not_1 (not_1_out, undefinedexpression_1_expwrite);
  and and_2 (and_2_out, not_1_out, or_3_out);
  assign ChildLeftPointerOut = not_2_out ? ChildL : 4'bz;  // Controlled_Buffer controlled_buffer_1
  not not_2 (not_2_out, or_4_out);
  assign ChildLeftPointerOut = or_4_out ? 4'b0000 : 4'bz;  // Controlled_Buffer controlled_buffer_2
  assign not_3_out = ~xor_1_out;  // NOT_Gate not_3, 3 bits wide
  assign xor_1_out = 3'b011 ^ CurrentExpressionType;  // XOR_Gate xor_1, 3 bits wide
  D_Flip_Flop d_ff_1 (.D(or_1_out), .clk(Clock), .Q(d_ff_1_q));  // open: Qn, preset, reset
  or or_1 (or_1_out, and_1_out, and_2_out);
  and and_3 (and_3_out, not_3_out[0], not_3_out[1], not_3_out[2]);
  or or_2 (CurrentResolveState, and_7_out, and_4_out);
  and and_4 (and_4_out, d_ff_1_q, or_3_out);
  D_Flip_Flop d_ff_2 (.D(d_ff_2_q), .clk(Clock), .Q(d_ff_2_q), .reset(StackClear));  // open: Qn, preset
  Register #(.width(3)) register_4 (.D(RAM[2:0]), .en(1'b1), .clk(Clock), .Q(register_4_q));  // open: clr
  and and_5 (and_5_out, ChildLeftIn[20], ChildRightIn[20]);
  D_Flip_Flop d_ff_3 (.D(ParentIn[21]), .clk(Clock), .Q(d_ff_3_q));  // open: Qn, preset, reset
  or or_3 (or_3_out, and_5_out, and_6_out);
  and and_6 (and_6_out, and_9_out, ChildRightIn[20]);
  assign xor_2_out = 3'b001 ^ CurrentExpressionType;  // XOR_Gate xor_2, 3 bits wide
  and and_7 (and_7_out, not_5_out[0], not_5_out[1], not_5_out[2]);
  not not_4 (not_4_out, d_ff_2_q);
  and and_8 (and_8_out, not_4_out, and_10_out);
  or or_4 (or_4_out, and_8_out, and_9_out);
  or or_5 (or_5_out, and_3_out, ParentIn[21]);
  or or_6 (ChildRightOut[21], or_5_out, d_ff_3_q);
  assign not_5_out = ~xor_2_out;  // NOT_Gate not_5, 3 bits wide
  and and_9 (and_9_out, not_6_out[0], not_6_out[1], not_6_out[2]);
  and and_10 (and_10_out, not_7_out[0], not_7_out[1], not_7_out[2]);
  assign not_6_out = ~xor_3_out;  // NOT_Gate not_6, 3 bits wide
  assign xor_3_out = CurrentExpressionType ^ 3'b100;  // XOR_Gate xor_3, 3 bits wide
  assign not_7_out = ~xor_4_out;  // NOT_Gate not_7, 3 bits wide
  assign xor_4_out = CurrentExpressionType ^ 3'b001;  // XOR_Gate xor_4, 3 bits wide
  UndefinedExpression undefinedexpression_1 (
    .PEB(ParentIn[11:0]), .PIB(ParentIn[19:12]), .CRE(ChildRightIn[11:0]), .CRI(ChildRightIn[19:12]),
    .CLE(ChildLeftIn[11:0]), .CLI(ChildLeftIn[19:12]), .SFS(register_5_q), .SBS(register_6_q), .RAM(RAMIn),
    .InternalExpression({CurrentResolveState, CurrentExpressionType, ChildL, ChildR}), .Buffer(register_4_q),
    .EXPWrite(undefinedexpression_1_expwrite), .RamSelect(undefinedexpression_1_ramselect),
    .FrontStack(undefinedexpression_1_frontstack), .BackStack(undefinedexpression_1_backstack),
    .RAMwrite(RAMWrite), .NewNode(NewNodeRequest), .Clock(Clock), .NewNodeID(NewNode),
    .UniqueNodeID(UniqueNodeID), .ClearChidlren(undefinedexpression_1_clearchidlren),
    .StackClear(StackClear), .PEB_2(ParentOut[11:0]), .PIB_2(ParentOut[19:12]), .CRE_2(ChildRightOut[11:0]),
    .CRI_2(ChildRightOut[19:12]), .CLE_2(ChildLeftOut[11:0]), .CLI_2(ChildLeftOut[19:12]),
    .NewNode_2(undefinedexpression_1_newnode_2), .GeneralOutput({undefinedexpression_1_generaloutput, RAM}));
  ArithmeticExpression arithmeticexpression_1 (
    .PEB(ParentIn[11:0]), .PIB(ParentIn[19:12]), .CRE(ChildRightIn[11:0]), .CRI(ChildRightIn[19:12]),
    .CLE(ChildLeftIn[11:0]), .CLI(ChildLeftIn[19:12]), .SFS(register_5_q), .SBS(register_6_q), .RAM(RAMIn),
    .InternalExpression({CurrentResolveState, CurrentExpressionType, ChildL, ChildR}), .Buffer(register_4_q),
    .EXPWrite(undefinedexpression_1_expwrite), .RamSelect(undefinedexpression_1_ramselect),
    .FrontStack(undefinedexpression_1_frontstack), .BackStack(undefinedexpression_1_backstack),
    .RAMwrite(RAMWrite), .NewNode(NewNodeRequest), .Clock(Clock), .NewNodeID(NewNode),
    .UniqueNodeID(UniqueNodeID), .ClearChidlren(undefinedexpression_1_clearchidlren),
    .StackClear(StackClear), .PEB_2(ParentOut[11:0]), .PIB_2(ParentOut[19:12]), .CRE_2(ChildRightOut[11:0]),
    .CRI_2(ChildRightOut[19:12]), .CLE_2(ChildLeftOut[11:0]), .CLI_2(ChildLeftOut[19:12]),
    .NewNode_2(undefinedexpression_1_newnode_2), .GeneralOutput({undefinedexpression_1_generaloutput, RAM}));
  Register #(.width(4)) register_5 (
    .D(RAM), .en(undefinedexpression_1_frontstack), .clk(Clock), .Q(register_5_q), .clr(StackClear));
  not not_8 (not_8_out, and_8_out);
  Register #(.width(4)) NewNodeID (.D(NewID), .en(Clock), .clk(NewNodeRequest), .Q(NewNode));  // open: clr
  assign RAMLoc = undefinedexpression_1_ramselect ? register_5_q : 4'bz;  // Controlled_Buffer controlled_buffer_3
  assign ChildRightPointerOut = not_8_out ? ChildR : 4'bz;  // Controlled_Buffer controlled_buffer_4
  assign ChildRightPointerOut = and_8_out ? 4'b0000 : 4'bz;  // Controlled_Buffer controlled_buffer_5
  Register #(.width(4)) register_6 (
    .D(RAM), .en(undefinedexpression_1_backstack), .clk(Clock), .Q(register_6_q), .clr(StackClear));
  assign RAMLoc = not_9_out ? register_6_q : 4'bz;  // Controlled_Buffer controlled_buffer_6
  not not_9 (not_9_out, undefinedexpression_1_ramselect);

  assign ChildLeftOut[21:20] = 2'b00;
  assign ChildRightOut[20] = 1'b0;
  assign ParentOut[21:20] = {ChildRightOut[21], CurrentResolveState};

  // Other names for the same wires on the sheet: Expres[2:0] = CurrentExpressionType

  // Notes on the sheet:
  //   Resolve Flag
  //   Reduce Flag
  //   The node starts off as an undefiend node
  //   To simulate an arithmetic node first update the ParentIn Input Wire found left of here to
  //   Then cause one clock pulse by tuning the clock input wire on and off
  //   Note: This will currently cause errors until the Arethmetic Expression Component is finished
  //   000010
  //   00000110
  //   00010010
  //   FrontStack
  //   BackStack
endmodule

module UndefinedExpression (
  input  [11:0] PEB,
  input  [7:0] PIB,
  input  [11:0] CRE,
  input  [7:0] CRI,
  input  [11:0] CLE,
  input  [7:0] CLI,
  input  [3:0] SFS,
  input  [3:0] SBS,
  input  [3:0] RAM,
  input  [11:0] InternalExpression,
  input  [2:0] Buffer,
  input  Clock,
  input  [3:0] NewNodeID,
  input  [3:0] UniqueNodeID,
  output EXPWrite,
  output RamSelect,
  output FrontStack,
  output BackStack,
  output RAMwrite,
  output NewNode,
  output [11:0] PEB_2,
  output [7:0] PIB_2,
  output [11:0] CRE_2,
  output [7:0] CRI_2,
  output [11:0] CLE_2,
  output [7:0] CLI_2,
  output [11:0] NewNode_2,
  output [7:0] GeneralOutput,
  output ClearChidlren,
  output StackClear
);

  wire and_1_out, decoder_1_out1, decoder_1_out2, not_2_out, not_3_out, not_4_out, not_5_out, not_6_out,
       nullify_1_nullcli, nullify_1_nullcri, nullify_1_nullnewnode, or_1_out, or_2_out, or_3_out, or_4_out,
       or_5_out, or_6_out, or_7_out, updateinstruction_1_updcle, updateinstruction_1_updcli,
       updateinstruction_1_updcre, updateinstruction_1_updcri, updateinstruction_1_updexp,
       updateinstruction_1_updstackclear;
  wire [2:0] not_1_out, xor_1_out;
  wire [7:0] controlled_buffer_2_out, controlled_buffer_4_out, nullify_1_cli, nullify_1_cri,
       updateinstruction_1_cli, updateinstruction_1_cri;
  wire [11:0] controlled_buffer_1_out, controlled_buffer_3_out, controlled_buffer_5_out, nullify_1_newnode,
       updateinstruction_1_cle, updateinstruction_1_cre, updateinstruction_1_newvalue;

  Decoder #(.select(4)) decoder_1 (
    .out1(decoder_1_out1), .out2(decoder_1_out2), .sel(PIB[7:4]));  // open: out0, out3, out4, out5, out6, out7, out8, out9, out10, out11, out12, out13, out14, out15, en
  assign xor_1_out = InternalExpression[10:8] ^ 3'b000;  // XOR_Gate xor_1, 3 bits wide
  assign controlled_buffer_1_out = updateinstruction_1_updcre ? updateinstruction_1_cre : 12'bz;  // Controlled_Buffer controlled_buffer_1
  buf or_1 (or_1_out, updateinstruction_1_updcri);  // OR_Gate
  assign controlled_buffer_2_out = updateinstruction_1_updcri ? updateinstruction_1_cri : 8'bz;  // Controlled_Buffer controlled_buffer_2
  UpdateInstruction updateinstruction_1 (
    .ActivationSignal(decoder_1_out2), .Clock(Clock), .UniqueNodeID(UniqueNodeID), .PIB(PIB), .PEB(PEB),
    .UpdCLE(updateinstruction_1_updcle), .UpdCRE(updateinstruction_1_updcre),
    .UpdCLI(updateinstruction_1_updcli), .UpdCRI(updateinstruction_1_updcri),
    .UpdStackClear(updateinstruction_1_updstackclear), .UpdEXP(updateinstruction_1_updexp),
    .CRI(updateinstruction_1_cri), .CLI(updateinstruction_1_cli), .CRE(updateinstruction_1_cre),
    .CLE(updateinstruction_1_cle), .NewValue(updateinstruction_1_newvalue));
  assign not_1_out = ~xor_1_out;  // NOT_Gate not_1, 3 bits wide
  assign controlled_buffer_3_out = updateinstruction_1_updcle ? updateinstruction_1_cle : 12'bz;  // Controlled_Buffer controlled_buffer_3
  buf or_2 (or_2_out, updateinstruction_1_updcli);  // OR_Gate
  assign controlled_buffer_4_out = updateinstruction_1_updcli ? updateinstruction_1_cli : 8'bz;  // Controlled_Buffer controlled_buffer_4
  buf or_3 (or_3_out, updateinstruction_1_updexp);  // OR_Gate
  assign controlled_buffer_5_out = updateinstruction_1_updexp ? updateinstruction_1_newvalue : 12'bz;  // Controlled_Buffer controlled_buffer_5
  and and_1 (and_1_out, not_1_out[0], not_1_out[1], not_1_out[2]);
  or or_4 (or_4_out, updateinstruction_1_updexp, nullify_1_nullnewnode);
  or or_5 (or_5_out, or_2_out, nullify_1_nullcli);
  assign controlled_buffer_4_out = nullify_1_nullcli ? nullify_1_cli : 8'bz;  // Controlled_Buffer controlled_buffer_6
  Nullify nullify_1 (
    .ActivationSignal(decoder_1_out1), .PIB(PIB), .NullCli(nullify_1_nullcli), .NullCri(nullify_1_nullcri),
    .NullNewNode(nullify_1_nullnewnode), .CLI(nullify_1_cli), .CRI(nullify_1_cri), .NewNode(nullify_1_newnode));
  or or_6 (or_6_out, or_1_out, nullify_1_nullcri);
  assign controlled_buffer_2_out = nullify_1_nullcri ? nullify_1_cri : 8'bz;  // Controlled_Buffer controlled_buffer_7
  assign controlled_buffer_5_out = nullify_1_nullnewnode ? nullify_1_newnode : 12'bz;  // Controlled_Buffer controlled_buffer_8
  or or_7 (or_7_out, or_3_out, nullify_1_nullnewnode);
  assign RamSelect = and_1_out ? 1'b0 : 1'bz;  // Controlled_Buffer controlled_buffer_9
  assign BackStack = and_1_out ? 1'b0 : 1'bz;  // Controlled_Buffer controlled_buffer_10
  assign FrontStack = and_1_out ? 1'b0 : 1'bz;  // Controlled_Buffer controlled_buffer_11
  assign RAMwrite = and_1_out ? 1'b0 : 1'bz;  // Controlled_Buffer controlled_buffer_12
  assign EXPWrite = and_1_out ? or_4_out : 1'bz;  // Controlled_Buffer controlled_buffer_13
  assign NewNode = and_1_out ? 1'b0 : 1'bz;  // Controlled_Buffer controlled_buffer_14
  not not_2 (not_2_out, updateinstruction_1_updcre);
  assign controlled_buffer_1_out = not_2_out ? {12{1'b0}} : 12'bz;  // Controlled_Buffer controlled_buffer_15
  not not_3 (not_3_out, or_6_out);
  assign controlled_buffer_2_out = not_3_out ? {8{1'b0}} : 8'bz;  // Controlled_Buffer controlled_buffer_16
  not not_4 (not_4_out, updateinstruction_1_updcle);
  assign controlled_buffer_3_out = not_4_out ? {12{1'b0}} : 12'bz;  // Controlled_Buffer controlled_buffer_17
  not not_5 (not_5_out, or_5_out);
  assign controlled_buffer_4_out = not_5_out ? {8{1'b0}} : 8'bz;  // Controlled_Buffer controlled_buffer_18
  not not_6 (not_6_out, or_7_out);
  assign controlled_buffer_5_out = not_6_out ? {12{1'b0}} : 12'bz;  // Controlled_Buffer controlled_buffer_19
  assign ClearChidlren = and_1_out ? 1'b0 : 1'bz;  // Controlled_Buffer controlled_buffer_20
  assign PEB_2 = and_1_out ? {12{1'b0}} : 12'bz;  // Controlled_Buffer controlled_buffer_21
  assign PIB_2 = and_1_out ? {8{1'b0}} : 8'bz;  // Controlled_Buffer controlled_buffer_22
  assign CRE_2 = and_1_out ? controlled_buffer_1_out : 12'bz;  // Controlled_Buffer controlled_buffer_23
  assign CRI_2 = and_1_out ? controlled_buffer_2_out : 8'bz;  // Controlled_Buffer controlled_buffer_24
  assign CLE_2 = and_1_out ? controlled_buffer_3_out : 12'bz;  // Controlled_Buffer controlled_buffer_25
  assign CLI_2 = and_1_out ? controlled_buffer_4_out : 8'bz;  // Controlled_Buffer controlled_buffer_26
  assign NewNode_2 = and_1_out ? controlled_buffer_5_out : 12'bz;  // Controlled_Buffer controlled_buffer_27
  assign GeneralOutput = and_1_out ? {8{1'b0}} : 8'bz;  // Controlled_Buffer controlled_buffer_28
  assign StackClear = and_1_out ? updateinstruction_1_updstackclear : 1'bz;  // Controlled_Buffer controlled_buffer_29

  // Notes on the sheet:
  //   Input
  //   0 == Backstack / 1 == Frontstack
  //   Output
endmodule

module UpdateInstruction (
  input  ActivationSignal,
  input  Clock,
  input  [3:0] UniqueNodeID,
  input  [7:0] PIB,
  input  [11:0] PEB,
  output UpdCLE,
  output UpdStackClear,
  output UpdCRE,
  output UpdEXP,
  output UpdCLI,
  output UpdCRI,
  output [7:0] CRI,
  output [7:0] CLI,
  output [11:0] CRE,
  output [11:0] CLE,
  output [11:0] NewValue
);

  wire and_1_out, and_3_out;
  wire [3:0] not_1_out, xor_1_out;

  assign CLI = ActivationSignal ? PIB : 8'bz;  // Controlled_Buffer controlled_buffer_1
  assign CLE = ActivationSignal ? PEB : 12'bz;  // Controlled_Buffer controlled_buffer_2
  assign xor_1_out = UniqueNodeID ^ PIB[3:0];  // XOR_Gate xor_1, 4 bits wide
  and and_1 (and_1_out, not_1_out[0], not_1_out[1], not_1_out[2], not_1_out[3]);
  assign not_1_out = ~xor_1_out;  // NOT_Gate not_1, 4 bits wide
  and and_2 (UpdEXP, and_1_out, ActivationSignal);
  and and_3 (and_3_out, and_1_out, ActivationSignal);
  assign NewValue = and_3_out ? {1'b0, PEB[10:0]} : 12'bz;  // Controlled_Buffer controlled_buffer_3

  assign CRE = CLE;
  assign CRI = CLI;
  assign UpdCLE = ActivationSignal;
  assign UpdCLI = ActivationSignal;
  assign UpdCRE = ActivationSignal;
  assign UpdCRI = ActivationSignal;
  assign UpdStackClear = UpdEXP;
endmodule

module ArithmeticExpression (
  input  [11:0] PEB,
  input  [7:0] PIB,
  input  [11:0] CRE,
  input  [7:0] CRI,
  input  [11:0] CLE,
  input  [7:0] CLI,
  input  [3:0] SFS,
  input  [3:0] SBS,
  input  [3:0] RAM,
  input  [11:0] InternalExpression,
  input  [2:0] Buffer,
  input  Clock,
  input  [3:0] NewNodeID,
  input  [3:0] UniqueNodeID,
  output EXPWrite,
  output RamSelect,
  output FrontStack,
  output BackStack,
  output RAMwrite,
  output NewNode,
  output [11:0] PEB_2,
  output [7:0] PIB_2,
  output [11:0] CRE_2,
  output [7:0] CRI_2,
  output [11:0] CLE_2,
  output [7:0] CLI_2,
  output [11:0] NewNode_2,
  output [7:0] GeneralOutput,
  output ClearChidlren,
  output StackClear
);

  wire and_1_out, decoder_1_out12, decoder_1_out13, decoder_1_out14, decoder_1_out15, not_2_out, not_3_out,
       not_4_out, not_5_out, not_6_out, undriven;
  wire [2:0] not_1_out, xor_1_out;
  wire [7:0] controlled_buffer_8_out, controlled_buffer_10_out;
  wire [11:0] controlled_buffer_7_out, controlled_buffer_9_out, controlled_buffer_11_out;

  Decoder #(.select(4)) decoder_1 (
    .out12(decoder_1_out12), .out13(decoder_1_out13), .out14(decoder_1_out14), .out15(decoder_1_out15),
    .sel(PIB[7:4]));  // open: out0, out1, out2, out3, out4, out5, out6, out7, out8, out9, out10, out11, en
  assign xor_1_out = InternalExpression[10:8] ^ 3'b110;  // XOR_Gate xor_1, 3 bits wide
  assign not_1_out = ~xor_1_out;  // NOT_Gate not_1, 3 bits wide
  Subtraction subtraction_1 (.ActivationSignal(decoder_1_out13));
  Addition addition_1 (.ActivationSignal(decoder_1_out12));
  and and_1 (and_1_out, not_1_out[0], not_1_out[1], not_1_out[2]);
  Adder adder_1 ();  // open: a, b, out, cin, cout
  Division division_1 (.ActivationSignal(decoder_1_out14));
  Subtractor subtractor_1 ();  // open: a, b, out, bin, bout
  Division division_2 (.ActivationSignal(decoder_1_out15));
  Multiplier multiplier_1 ();  // open: a, b, out, cin, cout
  Divider divider_1 ();  // open: a, b, out, upper, rem
  Controlled_Buffer controlled_buffer_1 (.out(RamSelect), .en(and_1_out));  // open: in
  Controlled_Buffer controlled_buffer_2 (.out(BackStack), .en(and_1_out));  // open: in
  Controlled_Buffer controlled_buffer_3 (.out(FrontStack), .en(and_1_out));  // open: in
  Controlled_Buffer controlled_buffer_4 (.out(RAMwrite), .en(and_1_out));  // open: in
  Controlled_Buffer controlled_buffer_5 (.out(EXPWrite), .en(and_1_out));  // open: in
  Controlled_Buffer controlled_buffer_6 (.out(NewNode), .en(and_1_out));  // open: in
  not not_2 (not_2_out, undriven);
  assign controlled_buffer_7_out = not_2_out ? {12{1'b0}} : 12'bz;  // Controlled_Buffer controlled_buffer_7
  // NOT_Gate not_3 has open pins: in=open, out=not_3_out
  assign controlled_buffer_8_out = not_3_out ? {8{1'b0}} : 8'bz;  // Controlled_Buffer controlled_buffer_8
  // NOT_Gate not_4 has open pins: in=open, out=not_4_out
  assign controlled_buffer_9_out = not_4_out ? {12{1'b0}} : 12'bz;  // Controlled_Buffer controlled_buffer_9
  // NOT_Gate not_5 has open pins: in=open, out=not_5_out
  assign controlled_buffer_10_out = not_5_out ? {8{1'b0}} : 8'bz;  // Controlled_Buffer controlled_buffer_10
  // NOT_Gate not_6 has open pins: in=open, out=not_6_out
  assign controlled_buffer_11_out = not_6_out ? {12{1'b0}} : 12'bz;  // Controlled_Buffer controlled_buffer_11
  Controlled_Buffer controlled_buffer_12 (.out(ClearChidlren), .en(and_1_out));  // open: in
  assign PEB_2 = and_1_out ? controlled_buffer_7_out : 12'bz;  // Controlled_Buffer controlled_buffer_13
  assign PIB_2 = and_1_out ? controlled_buffer_8_out : 8'bz;  // Controlled_Buffer controlled_buffer_14
  assign CRE_2 = and_1_out ? controlled_buffer_9_out : 12'bz;  // Controlled_Buffer controlled_buffer_15
  assign CRI_2 = and_1_out ? controlled_buffer_10_out : 8'bz;  // Controlled_Buffer controlled_buffer_16
  assign CLE_2 = and_1_out ? controlled_buffer_11_out : 12'bz;  // Controlled_Buffer controlled_buffer_17
  Controlled_Buffer #(.width(8)) controlled_buffer_18 (.out(CLI_2), .en(and_1_out));  // open: in
  Controlled_Buffer #(.width(12)) controlled_buffer_19 (.out(NewNode_2), .en(and_1_out));  // open: in
  Controlled_Buffer #(.width(8)) controlled_buffer_20 (.out(GeneralOutput), .en(and_1_out));  // open: in
  Controlled_Buffer controlled_buffer_21 (.out(StackClear), .en(and_1_out));  // open: in

  // Notes on the sheet:
  //   Input
  //   These are your inputs you can drag wires from any input to any instruction component
  //   These signals cause the node to update various registers when outputting a 1
  //   You will not need to use alot of these for arithmetic.
  //   Make sure to output a constant 0 on any signal you dont intend to use
  //   These are the node's defaults which means without any valid
  //   instructions the node will output whatever value is on wire 2
  //   In this case 000.
  //   Currently the defaults are erroring to stop this make sure to pass
  //   a signal of a 0 onto wire 1 when no valid instruction is being 
  //   executed. If an instruction block would like to replace this signal 
  //   send a 1 signal to wire 1 and put the replacement value on wire 3.
  //   This Expression is currently empty. however to try and get you started I've created 4 instruction components for ADD/SUB/MUL and DIV 
  //   Try to update these instruction components so they update the appropriate output values for there instruction type
  //   To start with I would use the inbuilt logisim arithmetic components however your welcome to build your own or use parts of the TSE project
  //   https://github.com/DylanKrohnen/FixedPointALU/blob/main/FixedPointALU.circ
  //   1
  //   2
  //   3
  //   0 == Backstack / 1 == Frontstack
  //   Stack Clear and Clear Children are used when a Node updates Expression Type
  //   When updating an expression type make sure to send a 1 to both of these outputs
  //   Output
endmodule

module Addition (
  input  ActivationSignal
);


  // Notes on the sheet:
  //   which is a 12 bit bus split into 
  //   Bit(s) [11]
  //   [Resolve Flag State]
  //   (Make sure this is a 0)
  //   Bit(s) [10, 9 and 8]
  //   [Expression Type]
  //   Set this to be the new expression type
  //   Name == 001
  //   Use the splitter component to merge these values onto one 12 bit ouput bus
  //   Inside this component is where you put the digital logic required for addition
  //   An addition instruction requires you to update the expression type of the circuit to a Name represented by a 001
  //   And its (4-bit) children to equal the final 8 bits of CLE and CRE added together split across this nodes two 4-bit children
  //   (Ignore any carrys)
  //   To update the nodes expression you will need to pass a 1 to EXPwrite and pass the new values onto the NewNode output bus
  //   Bit(s) [7, 6, 5 and 4]
  //   [Child Left]
  //   Set this to be the leftmost four bits of the addition
  //   Bit(s) [3, 2, 1 and 0]
  //   [Child Right]
  //   Set this to be the rightmost four bits of the addition
endmodule

module Subtraction (
  input  ActivationSignal
);
endmodule

module Multiplication (
  input  ActivationSignal
);
endmodule

module Division (
  input  ActivationSignal
);
endmodule

module Nullify (
  input  ActivationSignal,
  input  [7:0] PIB,
  output NullCli,
  output NullCri,
  output NullNewNode,
  output [7:0] CLI,
  output [7:0] CRI,
  output [11:0] NewNode
);

  assign CLI = ActivationSignal ? PIB : 8'bz;  // Controlled_Buffer controlled_buffer_1
  assign NewNode = ActivationSignal ? {12{1'b0}} : 12'bz;  // Controlled_Buffer controlled_buffer_2

  assign CRI = CLI;
  assign NullCli = ActivationSignal;
  assign NullCri = ActivationSignal;
  assign NullNewNode = ActivationSignal;
endmodule

module ListExpression (
  input  [11:0] PEB,
  input  [7:0] PIB,
  input  [11:0] CRE,
  input  [7:0] CRI,
  input  [11:0] CLE,
  input  [7:0] CLI,
  input  [3:0] SFS,
  input  [3:0] SBS,
  input  [3:0] RAM,
  input  [11:0] InternalExpression,
  input  [2:0] Buffer,
  input  Clock,
  input  [3:0] NewNodeID,
  input  [3:0] UniqueNodeID,
  output EXPWrite,
  output RamSelect,
  output FrontStack,
  output BackStack,
  output RAMwrite,
  output NewNode,
  output [11:0] PEBOut,
  output [7:0] PIBOut,
  output [11:0] CREOut,
  output [7:0] CRIOut,
  output [11:0] CLE_2,
  output [7:0] CLI_2,
  output [11:0] NewNode_2,
  output [7:0] GeneralOutput,
  output ClearChidlren,
  output StackClear
);

  wire addbottomnode_1_creupdate, addbottomnode_1_criupdate, addbottomnode_1_expwrite,
       addbottomnode_1_requestnewnode, and_1_out, and_2_out, decoder_1_out1, decoder_1_out2, decoder_1_out10,
       decoder_1_out11, decoder_1_out12, decoder_1_out13, not_3_out, not_4_out, not_5_out, not_6_out,
       not_7_out, not_8_out, nullify_1_nullcli, nullify_1_nullcri, nullify_1_nullnewnode, or_1_out, or_2_out,
       or_3_out, or_4_out, or_5_out, or_6_out, or_7_out, or_8_out, or_9_out, or_10_out, or_11_out,
       removebottomnode_1_removecri, removebottomnode_1_removeexp, returndepth_1_criflag,
       returndepth_1_pebflag, updatedepth_1_updatedepthcri, updatedepth_1_updatedepthexp,
       updateinstruction_1_updcle, updateinstruction_1_updcli, updateinstruction_1_updcre,
       updateinstruction_1_updcri, updateinstruction_1_updexp, updateinstruction_1_updstackclear;
  wire [2:0] not_2_out, xor_2_out;
  wire [3:0] adder_1_out, not_1_out, xor_1_out;
  wire [7:0] addbottomnode_1_criout, controlled_buffer_1_out, controlled_buffer_2_out,
       controlled_buffer_23_out, nullify_1_cli, nullify_1_cri, removebottomnode_1_criout,
       returndepth_1_cri_2, updatedepth_1_criout, updateinstruction_1_cli, updateinstruction_1_cri;
  wire [11:0] addbottomnode_1_creout, addbottomnode_1_expwrite_2, controlled_buffer_3_out,
       controlled_buffer_4_out, controlled_buffer_6_out, controlled_buffer_19_out, controlled_buffer_22_out,
       nullify_1_newnode, removebottomnode_1_newexp, returndepth_1_peb, updatedepth_1_newexp,
       updateinstruction_1_cle, updateinstruction_1_cre, updateinstruction_1_newvalue;

  assign not_1_out = ~xor_1_out;  // NOT_Gate not_1, 4 bits wide
  assign xor_1_out = 4'b0000 ^ InternalExpression[3:0];  // XOR_Gate xor_1, 4 bits wide
  and and_1 (and_1_out, not_1_out[0], not_1_out[1], not_1_out[2], not_1_out[3]);
  Adder #(.width(4)) adder_1 (.a(CRI[3:0]), .b(4'b0001), .out(adder_1_out));  // open: cin, cout
  Decoder #(.select(4)) decoder_1 (
    .out1(decoder_1_out1), .out2(decoder_1_out2), .out10(decoder_1_out10), .out11(decoder_1_out11),
    .out12(decoder_1_out12), .out13(decoder_1_out13), .sel(PIB[7:4]));  // open: out0, out3, out4, out5, out6, out7, out8, out9, out14, out15, en
  assign xor_2_out = InternalExpression[10:8] ^ 3'b110;  // XOR_Gate xor_2, 3 bits wide
  assign controlled_buffer_1_out = nullify_1_nullcri ? nullify_1_cri : 8'bz;  // Controlled_Buffer controlled_buffer_1
  assign controlled_buffer_2_out = nullify_1_nullcli ? nullify_1_cli : 8'bz;  // Controlled_Buffer controlled_buffer_2
  assign controlled_buffer_3_out = nullify_1_nullnewnode ? nullify_1_newnode : 12'bz;  // Controlled_Buffer controlled_buffer_3
  Nullify nullify_1 (
    .ActivationSignal(decoder_1_out1), .PIB(PIB), .NullCli(nullify_1_nullcli), .NullCri(nullify_1_nullcri),
    .NullNewNode(nullify_1_nullnewnode), .CLI(nullify_1_cli), .CRI(nullify_1_cri), .NewNode(nullify_1_newnode));
  assign not_2_out = ~xor_2_out;  // NOT_Gate not_2, 3 bits wide
  UpdateInstruction updateinstruction_1 (
    .ActivationSignal(decoder_1_out2), .Clock(Clock), .UniqueNodeID(UniqueNodeID), .PIB(PIB), .PEB(PEB),
    .UpdCLE(updateinstruction_1_updcle), .UpdCRE(updateinstruction_1_updcre),
    .UpdCLI(updateinstruction_1_updcli), .UpdCRI(updateinstruction_1_updcri),
    .UpdStackClear(updateinstruction_1_updstackclear), .UpdEXP(updateinstruction_1_updexp),
    .CRI(updateinstruction_1_cri), .CLI(updateinstruction_1_cli), .CRE(updateinstruction_1_cre),
    .CLE(updateinstruction_1_cle), .NewValue(updateinstruction_1_newvalue));
  and and_2 (and_2_out, not_2_out[0], not_2_out[1], not_2_out[2]);
  or or_1 (or_1_out, nullify_1_nullnewnode, updateinstruction_1_updexp);
  assign controlled_buffer_4_out = updateinstruction_1_updcre ? updateinstruction_1_cre : 12'bz;  // Controlled_Buffer controlled_buffer_4
  or or_2 (or_2_out, nullify_1_nullcri, updateinstruction_1_updcri);
  assign controlled_buffer_1_out = updateinstruction_1_updcri ? updateinstruction_1_cri : 8'bz;  // Controlled_Buffer controlled_buffer_5
  assign controlled_buffer_6_out = updateinstruction_1_updcle ? updateinstruction_1_cle : 12'bz;  // Controlled_Buffer controlled_buffer_6
  or or_3 (or_3_out, nullify_1_nullcli, updateinstruction_1_updcli);
  assign controlled_buffer_2_out = updateinstruction_1_updcli ? updateinstruction_1_cli : 8'bz;  // Controlled_Buffer controlled_buffer_7
  assign controlled_buffer_3_out = updateinstruction_1_updexp ? updateinstruction_1_newvalue : 12'bz;  // Controlled_Buffer controlled_buffer_8
  UpdateDepth updatedepth_1 (
    .ActivationSignal(decoder_1_out10), .PIB(PIB), .CRIIn(CRI), .InternalValue(InternalExpression),
    .PEB(PEB), .UpdateDepthCRI(updatedepth_1_updatedepthcri), .UpdateDepthEXP(updatedepth_1_updatedepthexp),
    .CRIOut(updatedepth_1_criout), .NewEXP(updatedepth_1_newexp));
  or or_4 (or_4_out, or_1_out, updatedepth_1_updatedepthexp);
  or or_5 (or_5_out, or_2_out, updatedepth_1_updatedepthcri);
  assign controlled_buffer_1_out = updatedepth_1_updatedepthcri ? updatedepth_1_criout : 8'bz;  // Controlled_Buffer controlled_buffer_9
  assign controlled_buffer_3_out = updatedepth_1_updatedepthexp ? updatedepth_1_newexp : 12'bz;  // Controlled_Buffer controlled_buffer_10
  or or_6 (or_6_out, or_4_out, removebottomnode_1_removeexp);
  or or_7 (or_7_out, or_5_out, removebottomnode_1_removecri);
  assign controlled_buffer_1_out = removebottomnode_1_removecri ? removebottomnode_1_criout : 8'bz;  // Controlled_Buffer controlled_buffer_11
  RemoveBottomNode removebottomnode_1 (
    .ActivationSignal(decoder_1_out12), .Clock(Clock), .CRI(CRI), .PIB(PIB),
    .InternalValue(InternalExpression), .RemoveCRI(removebottomnode_1_removecri),
    .RemoveEXP(removebottomnode_1_removeexp), .CRIOut(removebottomnode_1_criout),
    .NewEXP(removebottomnode_1_newexp));
  or or_8 (or_8_out, or_6_out, addbottomnode_1_expwrite);
  assign controlled_buffer_3_out = removebottomnode_1_removeexp ? removebottomnode_1_newexp : 12'bz;  // Controlled_Buffer controlled_buffer_12
  ReturnDepth returndepth_1 (
    .ActivationSignal(decoder_1_out11), .PIB(PIB), .CRI(CRI), .InternalValue(InternalExpression),
    .CRIFlag(returndepth_1_criflag), .PEBFlag(returndepth_1_pebflag), .CRI_2(returndepth_1_cri_2),
    .PEB(returndepth_1_peb));
  assign RamSelect = and_2_out ? 1'b0 : 1'bz;  // Controlled_Buffer controlled_buffer_13
  assign BackStack = and_2_out ? 1'b0 : 1'bz;  // Controlled_Buffer controlled_buffer_14
  assign FrontStack = and_2_out ? 1'b0 : 1'bz;  // Controlled_Buffer controlled_buffer_15
  assign RAMwrite = and_2_out ? 1'b0 : 1'bz;  // Controlled_Buffer controlled_buffer_16
  assign EXPWrite = and_2_out ? or_8_out : 1'bz;  // Controlled_Buffer controlled_buffer_17
  assign NewNode = and_2_out ? addbottomnode_1_requestnewnode : 1'bz;  // Controlled_Buffer controlled_buffer_18
  assign controlled_buffer_19_out = returndepth_1_pebflag ? returndepth_1_peb : 12'bz;  // Controlled_Buffer controlled_buffer_19
  or or_9 (or_9_out, or_7_out, returndepth_1_criflag);
  assign controlled_buffer_1_out = returndepth_1_criflag ? returndepth_1_cri_2 : 8'bz;  // Controlled_Buffer controlled_buffer_20
  or or_10 (or_10_out, updateinstruction_1_updcre, addbottomnode_1_creupdate);
  assign controlled_buffer_4_out = addbottomnode_1_creupdate ? addbottomnode_1_creout : 12'bz;  // Controlled_Buffer controlled_buffer_21
  AddBottomNode addbottomnode_1 (
    .ActivationSignal(decoder_1_out13), .Clock(Clock), .CRI(CRI), .PIB(PIB), .NewNodeSignal(NewNodeID),
    .InternalValue(InternalExpression), .PEB(PEB), .CREUpdate(addbottomnode_1_creupdate),
    .RequestNewNode(addbottomnode_1_requestnewnode), .EXPWrite(addbottomnode_1_expwrite),
    .CRIUpdate(addbottomnode_1_criupdate), .CRIOut(addbottomnode_1_criout),
    .ExpWrite_2(addbottomnode_1_expwrite_2), .CREOut(addbottomnode_1_creout));
  assign controlled_buffer_22_out = and_1_out ? InternalExpression : 12'bz;  // Controlled_Buffer controlled_buffer_22
  assign controlled_buffer_23_out = and_1_out ? 8'h1 : 8'bz;  // Controlled_Buffer controlled_buffer_23
  or or_11 (or_11_out, or_9_out, addbottomnode_1_criupdate);
  assign controlled_buffer_1_out = addbottomnode_1_criupdate ? addbottomnode_1_criout : 8'bz;  // Controlled_Buffer controlled_buffer_24
  assign controlled_buffer_3_out = addbottomnode_1_expwrite ? addbottomnode_1_expwrite_2 : 12'bz;  // Controlled_Buffer controlled_buffer_25
  not not_3 (not_3_out, returndepth_1_pebflag);
  assign controlled_buffer_19_out = not_3_out ? controlled_buffer_22_out : 12'bz;  // Controlled_Buffer controlled_buffer_26
  assign controlled_buffer_22_out = not_4_out ? CRE : 12'bz;  // Controlled_Buffer controlled_buffer_27
  not not_4 (not_4_out, and_1_out);
  assign controlled_buffer_23_out = not_4_out ? {4'b0000, adder_1_out} : 8'bz;  // Controlled_Buffer controlled_buffer_28
  not not_5 (not_5_out, or_10_out);
  assign controlled_buffer_4_out = not_5_out ? {12{1'b0}} : 12'bz;  // Controlled_Buffer controlled_buffer_29
  not not_6 (not_6_out, or_11_out);
  assign controlled_buffer_1_out = not_6_out ? {8{1'b0}} : 8'bz;  // Controlled_Buffer controlled_buffer_30
  not not_7 (not_7_out, updateinstruction_1_updcle);
  assign controlled_buffer_6_out = not_7_out ? {12{1'b0}} : 12'bz;  // Controlled_Buffer controlled_buffer_31
  not not_8 (not_8_out, or_3_out);
  assign controlled_buffer_2_out = not_8_out ? {8{1'b0}} : 8'bz;  // Controlled_Buffer controlled_buffer_32
  assign ClearChidlren = and_2_out ? 1'b0 : 1'bz;  // Controlled_Buffer controlled_buffer_33
  assign PEBOut = and_2_out ? controlled_buffer_19_out : 12'bz;  // Controlled_Buffer controlled_buffer_34
  assign PIBOut = and_2_out ? controlled_buffer_23_out : 8'bz;  // Controlled_Buffer controlled_buffer_35
  assign CREOut = and_2_out ? controlled_buffer_4_out : 12'bz;  // Controlled_Buffer controlled_buffer_36
  assign CRIOut = and_2_out ? controlled_buffer_1_out : 8'bz;  // Controlled_Buffer controlled_buffer_37
  assign CLE_2 = and_2_out ? controlled_buffer_6_out : 12'bz;  // Controlled_Buffer controlled_buffer_38
  assign CLI_2 = and_2_out ? controlled_buffer_2_out : 8'bz;  // Controlled_Buffer controlled_buffer_39
  assign NewNode_2 = and_2_out ? controlled_buffer_3_out : 12'bz;  // Controlled_Buffer controlled_buffer_40
  Controlled_Buffer #(.width(8)) controlled_buffer_41 (.out(GeneralOutput), .en(and_2_out));  // open: in
  assign StackClear = and_2_out ? updateinstruction_1_updstackclear : 1'bz;  // Controlled_Buffer controlled_buffer_42

  // Notes on the sheet:
  //   Input
  //   This component was designed and implemented by Jasmine Ritchie
  //   Output
endmodule

module UpdateDepth (
  input  ActivationSignal,
  input  [7:0] PIB,
  input  [7:0] CRIIn,
  input  [11:0] InternalValue,
  input  [11:0] PEB,
  output UpdateDepthCRI,
  output UpdateDepthEXP,
  output [7:0] CRIOut,
  output [11:0] NewEXP
);

  wire and_1_out;
  wire [3:0] not_1_out, xor_1_out;

  assign xor_1_out = PIB[3:0] ^ CRIIn[3:0];  // XOR_Gate xor_1, 4 bits wide
  assign not_1_out = ~xor_1_out;  // NOT_Gate not_1, 4 bits wide
  and and_1 (and_1_out, not_1_out[0], not_1_out[1], not_1_out[2], not_1_out[3]);
  and and_2 (UpdateDepthEXP, and_1_out, ActivationSignal);
  assign NewEXP = and_1_out ? {InternalValue[11:8], PEB[7:4], InternalValue[3:0]} : 12'bz;  // Controlled_Buffer controlled_buffer_1

  assign CRIOut = PIB;
  assign UpdateDepthCRI = ActivationSignal;
endmodule

module ReturnDepth (
  input  ActivationSignal,
  input  [7:0] PIB,
  input  [7:0] CRI,
  input  [11:0] InternalValue,
  output PEBFlag,
  output CRIFlag,
  output [7:0] CRI_2,
  output [11:0] PEB
);

  wire and_2_out;
  wire [3:0] not_1_out, xor_1_out;

  assign not_1_out = ~xor_1_out;  // NOT_Gate not_1, 4 bits wide
  assign xor_1_out = PIB[3:0] ^ CRI[3:0];  // XOR_Gate xor_1, 4 bits wide
  and and_1 (PEBFlag, and_2_out, ActivationSignal);
  and and_2 (and_2_out, not_1_out[0], not_1_out[1], not_1_out[2], not_1_out[3]);
  assign PEB = and_2_out ? InternalValue : 12'bz;  // Controlled_Buffer controlled_buffer_1

  assign CRI_2 = PIB;
  assign CRIFlag = ActivationSignal;
endmodule

module RemoveBottomNode (
  input  ActivationSignal,
  input  Clock,
  input  [7:0] CRI,
  input  [7:0] PIB,
  input  [11:0] InternalValue,
  output RemoveCRI,
  output RemoveEXP,
  output [7:0] CRIOut,
  output [11:0] NewEXP
);

  wire and_1_out, and_2_out, d_ff_1_q, d_ff_2_q, not_1_out, not_3_out, or_2_out;
  wire [3:0] not_2_out, xor_1_out;

  or or_1 (RemoveCRI, d_ff_1_q, d_ff_2_q);
  not not_1 (not_1_out, or_2_out);
  and and_1 (and_1_out, not_1_out, ActivationSignal);
  or or_2 (or_2_out, d_ff_2_q, d_ff_1_q);
  D_Flip_Flop d_ff_1 (.D(and_1_out), .clk(Clock), .Q(d_ff_1_q));  // open: Qn, preset, reset
  assign xor_1_out = CRI[3:0] ^ 4'b0001;  // XOR_Gate xor_1, 4 bits wide
  D_Flip_Flop d_ff_2 (.D(d_ff_1_q), .clk(Clock), .Q(d_ff_2_q));  // open: Qn, preset, reset
  assign not_2_out = ~xor_1_out;  // NOT_Gate not_2, 4 bits wide
  and and_2 (and_2_out, not_2_out[0], not_2_out[1], not_2_out[2], not_2_out[3]);
  not not_3 (not_3_out, and_2_out);
  and and_3 (RemoveEXP, d_ff_2_q, and_2_out);
  assign CRIOut = not_3_out ? PIB : 8'bz;  // Controlled_Buffer controlled_buffer_1
  assign NewEXP = RemoveEXP ? {InternalValue[11:4], 4'b0000} : 12'bz;  // Controlled_Buffer controlled_buffer_2
  assign CRIOut = and_2_out ? 8'h10 : 8'bz;  // Controlled_Buffer controlled_buffer_3
endmodule

module AddBottomNode (
  input  ActivationSignal,
  input  Clock,
  input  [7:0] CRI,
  input  [7:0] PIB,
  input  [3:0] NewNodeSignal,
  input  [11:0] InternalValue,
  input  [11:0] PEB,
  output CREUpdate,
  output CRIUpdate,
  output RequestNewNode,
  output EXPWrite,
  output [7:0] CRIOut,
  output [11:0] ExpWrite_2,
  output [11:0] CREOut
);

  wire and_1_out, and_2_out, and_3_out, and_5_out, and_7_out, d_ff_1_q, d_ff_2_q, d_ff_3_q, not_2_out,
       not_3_out, not_4_out, or_1_out, or_2_out, or_3_out;
  wire [3:0] not_1_out, xor_1_out;

  assign xor_1_out = CRI[3:0] ^ 4'b0000;  // XOR_Gate xor_1, 4 bits wide
  and and_1 (and_1_out, ActivationSignal, not_2_out);
  assign not_1_out = ~xor_1_out;  // NOT_Gate not_1, 4 bits wide
  not not_2 (not_2_out, or_1_out);
  and and_2 (and_2_out, not_1_out[0], not_1_out[1], not_1_out[2], not_1_out[3]);
  or or_1 (or_1_out, or_3_out, d_ff_1_q);
  D_Flip_Flop d_ff_1 (.D(and_1_out), .clk(Clock), .Q(d_ff_1_q));  // open: Qn, preset, reset
  and and_3 (and_3_out, and_2_out, d_ff_2_q);
  assign CREOut = ActivationSignal ? PEB : 12'bz;  // Controlled_Buffer controlled_buffer_1
  and and_4 (RequestNewNode, d_ff_1_q, and_2_out);
  not not_3 (not_3_out, and_2_out);
  and and_5 (and_5_out, not_4_out, and_2_out);
  or or_2 (or_2_out, not_3_out, and_5_out);
  assign CRIOut = or_2_out ? PIB : 8'bz;  // Controlled_Buffer controlled_buffer_2
  assign ExpWrite_2 = and_3_out ? {InternalValue[11:4], NewNodeSignal} : 12'bz;  // Controlled_Buffer controlled_buffer_3
  or or_3 (or_3_out, d_ff_3_q, d_ff_2_q);
  D_Flip_Flop d_ff_2 (.D(d_ff_1_q), .clk(Clock), .Q(d_ff_2_q));  // open: Qn, preset, reset
  not not_4 (not_4_out, d_ff_3_q);
  and and_6 (EXPWrite, d_ff_2_q, and_2_out);
  and and_7 (and_7_out, and_2_out, d_ff_3_q);
  assign CRIOut = and_7_out ? {4'b0010, NewNodeSignal} : 8'bz;  // Controlled_Buffer controlled_buffer_4
  D_Flip_Flop d_ff_3 (.D(d_ff_2_q), .clk(Clock), .Q(d_ff_3_q));  // open: Qn, preset, reset

  assign CREUpdate = ActivationSignal;
  assign CRIUpdate = ActivationSignal;
endmodule
